// Logisim project 74_series_computer_schematic.circ as structural Verilog: 18 circuits, main circuit main
module main (
  input  in_1,
  input  in_2,
  input  [7:0] in_3
);

  wire ALU_add_sub, ALU_output_enable, button_1_out, carry, clear, clock, finished_user_input, halt,
       instruction_decoder_1_alu_op_0, instruction_decoder_1_alu_op_1, instruction_decoder_1_alu_op_2,
       instruction_decoder_1_alu_op_3, instruction_decoder_1_alu_output_enable, instruction_decoder_1_halt,
       instruction_decoder_1_instruction_register_input_enable,
       instruction_decoder_1_memory_address_register_input_enable,
       instruction_decoder_1_program_counter_increment, instruction_decoder_1_program_counter_input_enable,
       instruction_decoder_1_program_counter_output_enable, instruction_decoder_1_ram_input_enable,
       instruction_decoder_1_ram_output_enable, instruction_decoder_1_register_a_input_enable,
       instruction_decoder_1_register_a_output_enable, instruction_decoder_1_register_b_input_enable,
       instruction_decoder_1_register_b_output_enable, instruction_decoder_1_register_c_input_enable,
       instruction_decoder_1_register_c_output_enable, instruction_decoder_1_register_d_input_enable,
       instruction_decoder_1_register_d_output_enable, instruction_register_input_enable, manual_clock_pulse,
       memory_address_register_input_enable, memory_map_controller_1_mmd_0_input_enable,
       memory_map_controller_1_mmd_0_output_enable, memory_map_controller_1_mmd_1_output_enable,
       memory_map_controller_1_mmd_2_input_enable, memory_map_controller_1_mmd_2_output_enable,
       memory_map_controller_1_output_ram_input_enable, memory_map_controller_1_output_ram_output_enable,
       program_counter_increment, program_counter_input_enable, program_counter_output_enable,
       ram_input_enable, ram_output_enable, register_A_input_enable, register_A_output_enable,
       register_B_input_enable, register_B_output_enable, waiting_for_user_input;
  wire [2:0] microcode_step;
  wire [7:0] A_register_contents, ALU_result, B_register_contents, bus, D_register_contents, display_content,
       instruction_register_contents, memory_address_register_contents, program_counter_contents;

  Button button_1 (.out(button_1_out));
  Button button_2 (.out(clear));
  Button button_3 (.out(finished_user_input));
  or or_1 (manual_clock_pulse, in_1, button_1_out);
  // Probe on register_A_input_enable
  // Probe on register_A_output_enable
  // Probe on register_B_input_enable
  // Probe on register_B_output_enable
  // Probe on ALU_output_enable
  // Probe on ALU_add_sub
  // Probe on memory_address_register_input_enable
  // Probe on ram_input_enable
  // Probe on ram_output_enable
  // Probe on program_counter_input_enable
  // Probe on program_counter_output_enable
  // Probe on program_counter_increment
  // Probe on instruction_register_input_enable
  // Probe on halt
  instruction_decoder instruction_decoder_1 (
    .register_A_input_enable(instruction_decoder_1_register_a_input_enable),
    .register_A_output_enable(instruction_decoder_1_register_a_output_enable),
    .register_B_input_enable(instruction_decoder_1_register_b_input_enable),
    .register_B_output_enable(instruction_decoder_1_register_b_output_enable),
    .alu_output_enable(instruction_decoder_1_alu_output_enable), .alu_op_0(instruction_decoder_1_alu_op_0),
    .memory_address_register_input_enable(instruction_decoder_1_memory_address_register_input_enable),
    .ram_input_enable(instruction_decoder_1_ram_input_enable),
    .ram_output_enable(instruction_decoder_1_ram_output_enable),
    .program_counter_input_enable(instruction_decoder_1_program_counter_input_enable),
    .program_counter_output_enable(instruction_decoder_1_program_counter_output_enable),
    .program_counter_increment(instruction_decoder_1_program_counter_increment),
    .instruction_register_input_enable(instruction_decoder_1_instruction_register_input_enable),
    .halt(instruction_decoder_1_halt),
    .register_C_input_enable(instruction_decoder_1_register_c_input_enable),
    .register_C_output_enable(instruction_decoder_1_register_c_output_enable),
    .register_D_input_enable(instruction_decoder_1_register_d_input_enable),
    .register_D_output_enable(instruction_decoder_1_register_d_output_enable),
    .alu_op_1(instruction_decoder_1_alu_op_1), .alu_op_2(instruction_decoder_1_alu_op_2),
    .alu_op_3(instruction_decoder_1_alu_op_3));  // open: clock, clear, alu_signal, instruction_byte, microcode_step
  // Probe on clock
  // Probe on carry
  // Probe on bus
  // Probe on program_counter_contents
  // Probe on A_register_contents
  // Probe on ALU_result
  // Probe on B_register_contents
  // Probe on memory_address_register_contents
  // Probe on instruction_register_contents
  // Probe on microcode_step
  // Probe on microcode_step
  // Probe on bus
  // Probe on program_counter_contents
  // Probe on A_register_contents
  // Probe on ALU_result
  // Probe on B_register_contents
  // Probe on memory_address_register_contents
  // Probe on instruction_register_contents
  // Probe on microcode_step
  // Probe on bus
  // Probe on program_counter_contents
  // Probe on A_register_contents
  // Probe on ALU_result
  // Probe on B_register_contents
  // Probe on memory_address_register_contents
  // Probe on instruction_register_contents
  // OR_Gate or_2 is placed but not wired
  clock u_CLOCK (.manual_clock(manual_clock_pulse), .clock_out(clock), .auto_manual_step(in_2));  // open: halt
  program_counter PROGRAM_COUNTER (
    .buffered_input(bus), .increment(instruction_decoder_1_program_counter_increment), .clock(clock),
    .clear(clear), .output_enable(instruction_decoder_1_program_counter_output_enable),
    .buffered_output(bus), .input_enable(instruction_decoder_1_program_counter_input_enable),
    .contents(program_counter_contents));
  register_L A_REGISTER (
    .\input (bus), .buffered_output(bus), .content(A_register_contents),
    .input_enable(instruction_decoder_1_register_a_input_enable), .clock(clock), .clear(clear),
    .output_enable(instruction_decoder_1_register_a_output_enable));
  register_L B_REGISTER (
    .\input (bus), .buffered_output(bus), .content(B_register_contents),
    .input_enable(instruction_decoder_1_register_b_input_enable), .clock(clock), .clear(clear),
    .output_enable(instruction_decoder_1_register_b_output_enable));
  register_L C_REGISTER (
    .\input (bus), .buffered_output(bus), .content(B_register_contents),
    .input_enable(instruction_decoder_1_register_c_input_enable), .clock(clock), .clear(clear),
    .output_enable(instruction_decoder_1_register_c_output_enable));
  register_L D_REGISTER (
    .\input (bus), .buffered_output(bus), .content(D_register_contents),
    .input_enable(instruction_decoder_1_register_d_input_enable), .clock(clock), .clear(clear),
    .output_enable(instruction_decoder_1_register_d_output_enable));
  register_L MEMORY_ADDRESS_REGISTER (
    .\input (bus), .buffered_output(bus), .content(memory_address_register_contents), .clock(clock),
    .clear(clear));  // open: input_enable, output_enable
  register_L INSTRUCTION_REGISTER (
    .\input (bus), .buffered_output(bus), .content(instruction_register_contents),
    .input_enable(instruction_decoder_1_instruction_register_input_enable), .clock(clock), .clear(clear));  // open: output_enable
  RAM RAM (
    .input_enable(memory_map_controller_1_output_ram_input_enable),
    .address(memory_address_register_contents),
    .output_enable(memory_map_controller_1_output_ram_output_enable), .buffered_input(bus), .clock(clock),
    .buffered_output(bus));
  request_user_input REQUEST_USER_INPUT (
    .user_finished(finished_user_input), .buffered_input(bus),
    .input_enable(memory_map_controller_1_mmd_0_input_enable), .buffered_output(bus), .clear(clear),
    .output_enable(memory_map_controller_1_mmd_0_output_enable),
    .waiting_for_user_input(waiting_for_user_input));
  user_input USER_INPUT (
    .user_input(in_3), .buffered_output(bus), .output_enable(memory_map_controller_1_mmd_1_output_enable));
  register_R DISPLAY (
    .\input (bus), .content(display_content), .input_enable(memory_map_controller_1_mmd_2_input_enable),
    .clock(clock), .clear(clear), .output_enable(memory_map_controller_1_mmd_2_output_enable));  // open: buffered_output
  memory_map_controller memory_map_controller_1 (
    .address(memory_address_register_contents),
    .output_ram_input_enable(memory_map_controller_1_output_ram_input_enable),
    .output_ram_output_enable(memory_map_controller_1_output_ram_output_enable),
    .MMD_0_input_enable(memory_map_controller_1_mmd_0_input_enable),
    .MMD_0_output_enable(memory_map_controller_1_mmd_0_output_enable),
    .MMD_1_output_enable(memory_map_controller_1_mmd_1_output_enable),
    .MMD_2_input_enable(memory_map_controller_1_mmd_2_input_enable),
    .MMD_2_output_enable(memory_map_controller_1_mmd_2_output_enable));  // open: input_ram_input_enable, input_ram_output_enable, MMD_1_input_enable

  // Other names for the same wires on the sheet: auto_manual_clock = in_2; user_input[7:0] = in_3

  // Notes on the sheet:
  //   this is needed for getting rid of strange startup error condiitions in logisim
endmodule

module ALU (
  input  [3:0] operation,
  input  [7:0] A_input,
  input  [7:0] B_input,
  input  output_enable,
  output [7:0] buffered_output,
  output signal
);

  wire adder_subtractor_1_carry_out, bit_shift_left_1_overflow, bit_shift_right_1_overflow, decoder_1_out0,
       decoder_1_out1, decoder_1_out2, decoder_1_out3, decoder_1_out4, or_1_out, or_2_out,
       zero_check_1_is_zero;
  wire [7:0] adder_subtractor_1_buffered_output, adder_subtractor_1_unbuffered_output,
       bit_shift_left_1_output, buffer_1_out, buffer_2_out;

  Decoder #(.select(4)) decoder_1 (
    .out0(decoder_1_out0), .out1(decoder_1_out1), .out2(decoder_1_out2), .out3(decoder_1_out3),
    .out4(decoder_1_out4), .sel(operation), .en(1'b1));  // open: out5, out6, out7, out8, out9, out10, out11, out12, out13, out14, out15
  or or_1 (or_1_out, decoder_1_out2, decoder_1_out1);
  or or_2 (or_2_out, bit_shift_right_1_overflow, bit_shift_left_1_overflow, adder_subtractor_1_carry_out, zero_check_1_is_zero);
  zero_check zero_check_1 (.\input (buffer_1_out), .is_zero(zero_check_1_is_zero), .enable(decoder_1_out0));
  adder_subtractor adder_subtractor_1 (
    .add_sub(decoder_1_out2), .buffered_output(adder_subtractor_1_buffered_output), .A_input(buffer_1_out),
    .enable(or_1_out), .B_input(buffer_2_out), .carry_out(adder_subtractor_1_carry_out),
    .unbuffered_output(adder_subtractor_1_unbuffered_output));
  bit_shift_left bit_shift_left_1 (
    .\input (buffer_1_out), .\output (bit_shift_left_1_output),
    .buffered_output(adder_subtractor_1_buffered_output), .overflow(bit_shift_left_1_overflow),
    .enable(decoder_1_out3));
  bit_shift_right bit_shift_right_1 (
    .\input (buffer_1_out), .buffered_output(adder_subtractor_1_buffered_output),
    .overflow(bit_shift_right_1_overflow), .enable(decoder_1_out4));  // open: output
  assign buffer_1_out = A_input;  // Buffer buffer_1, 8 bits wide
  assign buffer_2_out = B_input;  // Buffer buffer_2, 8 bits wide
  assign buffered_output = output_enable ? adder_subtractor_1_buffered_output : 8'bz;  // Controlled_Buffer controlled_buffer_1
endmodule

module zero_check (
  input  [7:0] \input ,
  input  enable,
  output is_zero
);

  wire nor_1_out;

  nor nor_1 (nor_1_out, \input [0], \input [1], \input [2], \input [3], \input [4], \input [5], \input [6], \input [7]);
  and and_1 (is_zero, nor_1_out, enable);
endmodule

module adder_subtractor (
  input  [7:0] A_input,
  input  enable,
  input  add_sub,
  input  [7:0] B_input,
  output [7:0] buffered_output,
  output [7:0] unbuffered_output,
  output carry_out
);

  wire adder_1_cout;
  wire [7:0] xor_1_out;

  assign xor_1_out = {8{add_sub}} ^ B_input;  // XOR_Gate xor_1, 8 bits wide
  Adder adder_1 (.a(A_input), .b(xor_1_out), .out(unbuffered_output), .cin(add_sub), .cout(adder_1_cout));
  and and_1 (carry_out, adder_1_cout, enable);
  assign buffered_output = enable ? unbuffered_output : 8'bz;  // Controlled_Buffer controlled_buffer_1
endmodule

module bit_shift_left (
  input  [7:0] \input ,
  input  enable,
  output [7:0] \output ,
  output [7:0] buffered_output,
  output overflow
);

  and and_1 (overflow, \input [7], enable);
  assign buffered_output = enable ? {\input [6:0], 1'b0} : 8'bz;  // Controlled_Buffer controlled_buffer_1

  assign \output  = {\input [6:0], 1'b0};
endmodule

module bit_shift_right (
  input  [7:0] \input ,
  input  enable,
  output [7:0] \output ,
  output [7:0] buffered_output,
  output overflow
);

  and and_1 (overflow, \input [0], enable);
  assign buffered_output = enable ? {1'b0, \input [7:1]} : 8'bz;  // Controlled_Buffer controlled_buffer_1

  assign \output  = {1'b0, \input [7:1]};
endmodule

module register_L (
  input  [7:0] \input ,
  input  input_enable,
  input  clock,
  input  clear,
  input  output_enable,
  output [7:0] content,
  output [7:0] buffered_output
);

  wire and_1_out;

  Register register_1 (.D(\input ), .en(1'b1), .Q(content), .clk(and_1_out), .clr(clear));
  and and_1 (and_1_out, input_enable, clock);
  assign buffered_output = output_enable ? content : 8'bz;  // Controlled_Buffer controlled_buffer_1
endmodule

module register_R (
  input  [7:0] \input ,
  input  input_enable,
  input  clock,
  input  clear,
  input  output_enable,
  output [7:0] content,
  output [7:0] buffered_output
);

  wire and_1_out;

  Register register_1 (.D(\input ), .en(1'b1), .Q(content), .clk(and_1_out), .clr(clear));
  and and_1 (and_1_out, input_enable, clock);
  assign buffered_output = output_enable ? content : 8'bz;  // Controlled_Buffer controlled_buffer_1
endmodule

module clock (
  input  manual_clock,
  input  auto_manual_step,
  input  halt,
  output clock_out
);

  wire auto_clock_out, multiplexer_1_out, not_1_out;

  Clock auto_clock (.out(auto_clock_out));
  Multiplexer multiplexer_1 (
    .in0(auto_clock_out), .in1(manual_clock), .out(multiplexer_1_out), .sel(auto_manual_step), .en(1'b1));
  not not_1 (not_1_out, halt);
  and and_1 (clock_out, multiplexer_1_out, not_1_out);
endmodule

module RAM (
  input  [7:0] buffered_input,
  input  input_enable,
  input  [7:0] address,
  input  clock,
  input  output_enable,
  output [7:0] buffered_output
);

  wire not_1_out;
  wire [7:0] ram_1_data;

  RAM_part ram_1 (.addr(address), .data(ram_1_data), .sel(1'b1), .clk(clock), .ld(not_1_out), .clr(1'b0));
  not not_1 (not_1_out, input_enable);
  assign ram_1_data = input_enable ? buffered_input : 8'bz;  // Controlled_Buffer controlled_buffer_1
  assign buffered_output = output_enable ? ram_1_data : 8'bz;  // Controlled_Buffer controlled_buffer_2
endmodule

module program_counter (
  input  input_enable,
  input  output_enable,
  input  [7:0] buffered_input,
  input  increment,
  input  clock,
  input  clear,
  output [7:0] buffered_output,
  output [7:0] contents
);

  wire [7:0] controlled_buffer_1_out;

  assign controlled_buffer_1_out = input_enable ? buffered_input : 8'bz;  // Controlled_Buffer controlled_buffer_1
  Counter counter_1 (
    .load(input_enable), .D(controlled_buffer_1_out), .count(increment), .Q(contents), .clk(clock),
    .clr(clear));  // open: carry
  assign buffered_output = output_enable ? contents : 8'bz;  // Controlled_Buffer controlled_buffer_2
endmodule

module instruction_decoder (
  input  [7:0] instruction_byte,
  input  clock,
  input  clear,
  input  alu_signal,
  output register_A_input_enable,
  output register_A_output_enable,
  output register_B_input_enable,
  output register_B_output_enable,
  output register_C_input_enable,
  output register_C_output_enable,
  output [2:0] microcode_step,
  output register_D_input_enable,
  output register_D_output_enable,
  output alu_output_enable,
  output alu_op_0,
  output alu_op_1,
  output alu_op_2,
  output alu_op_3,
  output memory_address_register_input_enable,
  output ram_input_enable,
  output ram_output_enable,
  output program_counter_input_enable,
  output program_counter_output_enable,
  output program_counter_increment,
  output instruction_register_input_enable,
  output halt
);

  wire not_1_out, or_1_out;
  wire [7:5] rom_3_data;

  not not_1 (not_1_out, clock);
  or or_1 (or_1_out, clear, rom_3_data[5]);
  Counter #(.width(3), .max('h7)) counter_1 (
    .load(1'b0), .D(3'b000), .count(1'b1), .Q(microcode_step), .clk(not_1_out), .clr(or_1_out));  // open: carry
  ROM #(.addrWidth(13)) rom_1 (
    .addr({1'b0, alu_signal, microcode_step, instruction_byte}),
    .data({register_D_output_enable, register_D_input_enable, register_C_output_enable, register_C_input_enable, register_B_output_enable, register_B_input_enable, register_A_output_enable, register_A_input_enable}),
    .sel(1'b1));
  ROM #(.addrWidth(13)) rom_2 (
    .addr({1'b0, alu_signal, microcode_step, instruction_byte}),
    .data({ram_output_enable, ram_input_enable, memory_address_register_input_enable, alu_op_3, alu_op_2, alu_op_1, alu_op_0, alu_output_enable}),
    .sel(1'b1));
  ROM #(.addrWidth(13)) rom_3 (
    .addr({1'b0, alu_signal, microcode_step, instruction_byte}),
    .data({rom_3_data, halt, instruction_register_input_enable, program_counter_increment, program_counter_output_enable, program_counter_input_enable}),
    .sel(1'b1));

  // Notes on the sheet:
  //   microcode 0
  //   microcode 1
  //   microcode 2
  //   contents of rom_1 (hex, n*v repeats v):
  //   4*10 4*c 4*10 4*8 4*0 4*2 72*0 4*10 4*c 4*0 4*2 16*0 4*10 4*c 4*0 4*2 80*0 4*10 4*c 4*10 4*8 4*0 4*2
  //   200*0 4*10 4*c 8 10 8 10 2 20 2 20 0 2 0 2 108*0 4*10 4*c 4*2 20*0 4*10 4*c 4*1
  //   contents of rom_2 (hex, n*v repeats v):
  //   4*4 4*1 4*4 4*5 4*1 76*0 4*4 4*1 4*20 20*0 4*4 4*1 4*10 84*0 4*4 4*1 4*4 4*5 4*81 204*0 4*4 4*1 0 4
  //   0 4 0 1 0 1 112*0 4*4 4*1 24*0 4*4 4*1
  //   contents of rom_3 (hex, n*v repeats v):
  //   16*0 4*2 84*0 4*1 28*0 4*2
endmodule

module memory_map_controller (
  input  input_ram_input_enable,
  input  input_ram_output_enable,
  input  [7:0] address,
  output output_ram_input_enable,
  output output_ram_output_enable,
  output MMD_0_input_enable,
  output MMD_0_output_enable,
  output MMD_1_input_enable,
  output MMD_1_output_enable,
  output MMD_2_input_enable,
  output MMD_2_output_enable
);

  ROM #(.addrWidth(10)) rom_1 (
    .addr({input_ram_input_enable, input_ram_output_enable, address}),
    .data({MMD_2_output_enable, MMD_2_input_enable, MMD_1_output_enable, MMD_1_input_enable, MMD_0_output_enable, MMD_0_input_enable, output_ram_output_enable, output_ram_input_enable}),
    .sel(1'b1));
endmodule

module request_user_input (
  input  user_finished,
  input  clear,
  input  output_enable,
  input  [7:0] buffered_input,
  input  input_enable,
  output waiting_for_user_input,
  output [7:0] buffered_output
);

  wire and_1_out, or_1_out;
  wire [0:0] not_1_out;
  wire [7:0] controlled_buffer_1_out;

  assign controlled_buffer_1_out = input_enable ? buffered_input : 8'bz;  // Controlled_Buffer controlled_buffer_1
  Pull_Resistor pull_resistor_1 (.node(controlled_buffer_1_out));
  and and_1 (and_1_out, waiting_for_user_input, user_finished);
  or or_1 (or_1_out, and_1_out, controlled_buffer_1_out[0]);
  J_K_Flip_Flop j_k_ff_1 (
    .J(1'b1), .clk(or_1_out), .K(1'b1), .Q(waiting_for_user_input), .preset(1'b0), .en(1'b1), .reset(clear));  // open: Qn
  not not_1 (not_1_out[0], waiting_for_user_input);
  assign buffered_output = output_enable ? {{7{1'b0}}, not_1_out[0]} : 8'bz;  // Controlled_Buffer controlled_buffer_2
endmodule

module user_input (
  input  [7:0] user_input,
  input  output_enable,
  output [7:0] buffered_output
);

  assign buffered_output = output_enable ? user_input : 8'bz;  // Controlled_Buffer controlled_buffer_1
endmodule

module user_input_old (
  input  output_enable,
  input  [7:0] user_input,
  input  user_finished,
  input  request_user_input,
  input  clear,
  output [7:0] buffered_output,
  output user_input_ready
);

  wire and_1_out, j_k_ff_1_q, or_1_out;

  and and_1 (and_1_out, j_k_ff_1_q, user_finished);
  assign buffered_output = output_enable ? user_input : 8'bz;  // Controlled_Buffer controlled_buffer_1
  or or_1 (or_1_out, and_1_out, request_user_input);
  J_K_Flip_Flop j_k_ff_1 (
    .J(1'b1), .clk(or_1_out), .K(1'b1), .Q(j_k_ff_1_q), .preset(1'b0), .en(1'b1), .reset(clear));  // open: Qn
  not not_1 (user_input_ready, j_k_ff_1_q);
endmodule

module RAM_old (
  input  [7:0] buffered_input,
  input  input_enable,
  input  [7:0] address,
  input  clock,
  input  output_enable,
  output [7:0] buffered_output
);

  wire not_1_out;
  wire [7:0] ram_1_data;

  RAM_part ram_1 (.addr(address), .data(ram_1_data), .sel(1'b1), .clk(clock), .ld(not_1_out), .clr(1'b0));
  not not_1 (not_1_out, input_enable);
  assign ram_1_data = input_enable ? buffered_input : 8'bz;  // Controlled_Buffer controlled_buffer_1
  assign buffered_output = output_enable ? ram_1_data : 8'bz;  // Controlled_Buffer controlled_buffer_2
endmodule

module subtraction_test (
  input  in_1,
  input  [7:0] in_2,
  input  in_3,
  input  [7:0] in_4,
  input  in_5,
  input  [7:0] in_6,
  input  in_7,
  input  [7:0] in_8,
  input  [7:0] A,
  input  in_10,
  input  [7:0] B,
  input  in_12,
  input  add_sub,
  output [7:0] out_14,
  output [7:0] out_15
);

  wire adder_subtractor_1_carry_out, adder_subtractor_2_carry_out, adder_subtractor_3_carry_out, undriven;
  wire [7:0] adder_subtractor_4_buffered_output, multiplexer_1_out;

  LED led_1 (.in(adder_subtractor_1_carry_out));
  LED led_2 (.in(adder_subtractor_2_carry_out));
  LED led_3 (.in(adder_subtractor_3_carry_out));
  adder_subtractor adder_subtractor_1 (
    .add_sub(in_1), .A_input(in_2), .enable(in_3), .B_input(in_4), .carry_out(adder_subtractor_1_carry_out),
    .unbuffered_output(out_14));  // open: buffered_output
  adder_subtractor adder_subtractor_2 (
    .add_sub(in_5), .A_input(in_6), .enable(in_7), .B_input(in_8), .carry_out(adder_subtractor_2_carry_out),
    .unbuffered_output(out_15));  // open: buffered_output
  adder_subtractor adder_subtractor_3 (
    .add_sub(in_10), .A_input(A), .enable(in_12), .B_input(multiplexer_1_out),
    .carry_out(adder_subtractor_3_carry_out));  // open: buffered_output, unbuffered_output
  adder_subtractor adder_subtractor_4 (
    .add_sub(1'b1), .buffered_output(adder_subtractor_4_buffered_output), .A_input({8{1'b0}}), .enable(1'b1),
    .B_input(B));  // open: carry_out, unbuffered_output
  // Probe on undriven
  Multiplexer #(.width(8)) multiplexer_1 (
    .in0(B), .in1(adder_subtractor_4_buffered_output), .out(multiplexer_1_out), .sel(add_sub));  // open: en
  // Probe on multiplexer_1_out
  // Probe on adder_subtractor_4_buffered_output
  RAM_part ram_1 ();  // open: addr, data, sel, clk, ld, clr
endmodule
