# Fritzing sketch RAM (saved by Fritzing 0.9.3b)
breadboards: 4

parts:
  IC1 = DIP - 24 pins [chip_label=6116SA15TPG package="DIP (Dual Inline) [THT]"]
  IC2 = 74HCT245 [chip_label=74HCT245 package="DIP (Dual Inline) [THT]"]
  BUS = female pin header, 8 pins [form="♀ (female)"]
  IC3 = 74HCT245 [chip_label=74HCT245 package="DIP (Dual Inline) [THT]"]
  LED9 = LED - 5mm [color="Red (633nm)" package="5 mm [THT]"]
  LED10 = LED - 5mm [color="Red (633nm)" package="5 mm [THT]"]
  LED11 = LED - 5mm [color="Red (633nm)" package="5 mm [THT]"]
  LED12 = LED - 5mm [color="Red (633nm)" package="5 mm [THT]"]
  LED13 = LED - 5mm [color="Red (633nm)" package="5 mm [THT]"]
  LED14 = LED - 5mm [color="Red (633nm)" package="5 mm [THT]"]
  LED15 = LED - 5mm [color="Red (633nm)" package="5 mm [THT]"]
  LED16 = LED - 5mm [color="Red (633nm)" package="5 mm [THT]"]
  R22 = Resistor [tolerance=±5% resistance=1k package=THT]
  R23 = Resistor [tolerance=±5% resistance=1k package=THT]
  R24 = Resistor [tolerance=±5% resistance=1k package=THT]
  R25 = Resistor [tolerance=±5% resistance=1k package=THT]
  R26 = Resistor [tolerance=±5% resistance=1k package=THT]
  R27 = Resistor [tolerance=±5% resistance=1k package=THT]
  R28 = Resistor [tolerance=±5% resistance=1k package=THT]
  R29 = Resistor [tolerance=±5% resistance=1k package=THT]
  IC4 = DIP - 16 pins [chip_label=74HCT157 package="DIP (Dual Inline) [THT]"]
  IC6 = DIP - 14 pins [chip_label=74HCT14 package="DIP (Dual Inline) [THT]"]
  IC7 = 74HCT377 [chip_label=74HCT377 package="DIP (Dual Inline) [THT]"]
  MAR_DATA_OUT = female pin header, 8 pins [form="♀ (female)"]
  BUS_2 = female pin header, 8 pins [form="♀ (female)"]
  IC8 = DIP - 16 pins [chip_label=74HCT157 package="DIP (Dual Inline) [THT]"]
  A = female pin header, 8 pins [form="♀ (female)"]
  IC9 = DIP - 16 pins [chip_label=74HCT157 package="DIP (Dual Inline) [THT]"]
  OUT = female pin header, 8 pins [form="♀ (female)"]
  CLOCK = female pin header, 2 pins [form="♀ (female)"]
  RAM_IN = female pin header, 2 pins [form="♀ (female)"]
  SETUP_CLOCK = female pin header, 2 pins [form="♀ (female)"]
  C/U_P/D = female pin header, 2 pins [form="♀ (female)"]
  SETUP_P/D = female pin header, 2 pins [form="♀ (female)"]
  SETUP/RUN = female pin header, 2 pins [form="♀ (female)"]
  C1 = Ceramic Capacitor [capacitance=100nF package="100 mil [THT, multilayer]"]
  R30 = Resistor [tolerance=±5% resistance=220 package=THT]
  IC10 = DIP - 14 pins [chip_label=74HCT32 package="DIP (Dual Inline) [THT]"]
  MAR_IN = female pin header, 2 pins [form="♀ (female)"]
  LED17 = LED - 5mm [color="Red (633nm)" package="5 mm [THT]"]
  LED18 = LED - 5mm [color="Red (633nm)" package="5 mm [THT]"]
  LED19 = LED - 5mm [color="Red (633nm)" package="5 mm [THT]"]
  LED20 = LED - 5mm [color="Red (633nm)" package="5 mm [THT]"]
  LED21 = LED - 5mm [color="Red (633nm)" package="5 mm [THT]"]
  LED22 = LED - 5mm [color="Red (633nm)" package="5 mm [THT]"]
  LED23 = LED - 5mm [color="Red (633nm)" package="5 mm [THT]"]
  LED24 = LED - 5mm [color="Red (633nm)" package="5 mm [THT]"]
  B = female pin header, 8 pins [form="♀ (female)"]
  R32 = Resistor [tolerance=±5% resistance=1k package=THT]
  R33 = Resistor [tolerance=±5% resistance=1k package=THT]
  R34 = Resistor [tolerance=±5% resistance=1k package=THT]
  R35 = Resistor [tolerance=±5% resistance=1k package=THT]
  R36 = Resistor [tolerance=±5% resistance=1k package=THT]
  R37 = Resistor [tolerance=±5% resistance=1k package=THT]
  R38 = Resistor [tolerance=±5% resistance=1k package=THT]
  R39 = Resistor [tolerance=±5% resistance=1k package=THT]
  LED25 = LED - 5mm [color="Red (633nm)" package="5 mm [THT]"]
  LED26 = LED - 5mm [color="Red (633nm)" package="5 mm [THT]"]
  LED27 = LED - 5mm [color="Red (633nm)" package="5 mm [THT]"]
  LED28 = LED - 5mm [color="Red (633nm)" package="5 mm [THT]"]
  LED29 = LED - 5mm [color="Red (633nm)" package="5 mm [THT]"]
  LED30 = LED - 5mm [color="Red (633nm)" package="5 mm [THT]"]
  LED31 = LED - 5mm [color="Red (633nm)" package="5 mm [THT]"]
  LED32 = LED - 5mm [color="Red (633nm)" package="5 mm [THT]"]
  R40 = Resistor [tolerance=±5% resistance=1k package=THT]
  R41 = Resistor [tolerance=±5% resistance=1k package=THT]
  R42 = Resistor [tolerance=±5% resistance=1k package=THT]
  R43 = Resistor [tolerance=±5% resistance=1k package=THT]
  R44 = Resistor [tolerance=±5% resistance=1k package=THT]
  R45 = Resistor [tolerance=±5% resistance=1k package=THT]
  R46 = Resistor [tolerance=±5% resistance=1k package=THT]
  R47 = Resistor [tolerance=±5% resistance=1k package=THT]
  A2 = female pin header, 8 pins [form="♀ (female)"]
  OUT2 = female pin header, 8 pins [form="♀ (female)"]
  B3 = female pin header, 8 pins [form="♀ (female)"]
  IC17 = DIP - 16 pins [chip_label=74HCT157 package="DIP (Dual Inline) [THT]"]
  IC18 = DIP - 16 pins [chip_label=74HCT157 package="DIP (Dual Inline) [THT]"]
  R72 = Resistor [tolerance=±5% resistance=1k package=THT]
  R73 = Resistor [tolerance=±5% resistance=1k package=THT]
  R74 = Resistor [tolerance=±5% resistance=1k package=THT]
  R75 = Resistor [tolerance=±5% resistance=1k package=THT]
  R76 = Resistor [tolerance=±5% resistance=1k package=THT]
  R77 = Resistor [tolerance=±5% resistance=1k package=THT]
  R78 = Resistor [tolerance=±5% resistance=1k package=THT]
  R79 = Resistor [tolerance=±5% resistance=1k package=THT]
  OUT3 = female pin header, 8 pins [form="♀ (female)"]
  LED49 = LED - 5mm [color="Red (633nm)" package="5 mm [THT]"]
  LED50 = LED - 5mm [color="Red (633nm)" package="5 mm [THT]"]
  LED51 = LED - 5mm [color="Red (633nm)" package="5 mm [THT]"]
  LED52 = LED - 5mm [color="Red (633nm)" package="5 mm [THT]"]
  LED53 = LED - 5mm [color="Red (633nm)" package="5 mm [THT]"]
  LED54 = LED - 5mm [color="Red (633nm)" package="5 mm [THT]"]
  LED55 = LED - 5mm [color="Red (633nm)" package="5 mm [THT]"]
  LED56 = LED - 5mm [color="Red (633nm)" package="5 mm [THT]"]

nets:
  N1: IC1.I/O0, IC2.A8, IC3.A8, LED13.anode
  N2: IC1.I/O1, IC2.A7, IC3.A7, LED15.anode
  N3: IC1.I/O2, IC2.A6, IC3.A6, LED16.anode
  GND: IC1.GND, IC2.DIR, IC2.GND, IC3.GND
  N4: IC1.I/O3, IC2.A5, IC3.A5, LED14.anode
  N5: IC1.I/O4, IC2.A4, IC3.A4, LED11.anode
  N6: IC1.I/O5, IC2.A3, IC3.A3, LED12.anode
  N7: IC1.I/O6, IC2.A2, IC3.A2, LED9.anode
  N8: IC1.I/O7, IC2.A1, IC3.A1, LED10.anode
  N9: IC1._CS, IC1.A10, IC1._OE, IC1.A9, R22.Pin_1, R23.Pin_1, R24.Pin_1, R25.Pin_1, R27.Pin_1, R28.Pin_1, R29.Pin_1
  N10: IC1._WE, IC10.3Y
  N11: IC1.A8, IC4.2Y
  VCC: IC1.VCC, IC2.VCC, IC3.VCC
  N12: IC2._OE, IC10.1Y
  N13: BUS.pin1, IC3.B1
  N14: BUS.pin2, IC3.B2
  N15: BUS.pin3, IC3.B3
  N16: BUS.pin4, IC3.B4
  N17: BUS.pin5, IC3.B5
  N18: BUS.pin6, IC3.B6
  N19: BUS.pin7, IC3.B7
  N20: BUS.pin8, IC3.B8
  N21: LED9.cathode, R29.Pin_0
  N22: LED10.cathode, R28.Pin_0
  N23: LED11.cathode, R24.Pin_0
  N24: LED12.cathode, R25.Pin_0
  N25: LED13.cathode, R26.Pin_0
  N26: LED14.cathode, R23.Pin_0
  N27: LED15.cathode, R22.Pin_0
  N28: LED16.cathode, R27.Pin_0
  N29: IC4._A/B, SETUP/RUN.pin1, SETUP/RUN.pin2
  GND_2: IC4.1A, IC4.1B, IC4.GND, IC6.GND, IC7.GND, IC10.GND, R40.Pin_0, R41.Pin_0, R42.Pin_0, R43.Pin_0, R44.Pin_0, R45.Pin_0, R46.Pin_0, R47.Pin_0
  N30: IC4.2A, C/U_P/D.pin1, C/U_P/D.pin2
  N31: IC4.2B, SETUP_P/D.pin1, SETUP_P/D.pin2
  N32: IC4.3Y, IC6.3A, C1.0
  N33: IC4.3B, SETUP_CLOCK.pin1, SETUP_CLOCK.pin2
  N34: IC4.3A, CLOCK.pin1, CLOCK.pin2
  N35: IC4.4Y, IC6.6A
  VCC_2: IC4.4B, IC4.VCC, IC6.VCC, IC7.VCC, IC10.VCC
  N36: IC4.4A, RAM_IN.pin1, RAM_IN.pin2
  N37: IC4._G, R30.Pin_1
  N38: IC6.1A, IC6.2Y
  N39: IC6.1Y, IC10.2A
  N40: IC6.2A, IC6.3Y
  N41: IC6.4Y, IC10.2B, IC10.4A, IC10.4B
  N42: IC6.4A, C1.1, R30.Pin_0
  N43: IC6.5Y, IC7._CLKEN
  N44: IC6.5A, MAR_IN.pin1, MAR_IN.pin2
  N45: IC6.6Y, IC10.1B, IC10.3A
  N46: IC7.1Q, MAR_DATA_OUT.pin8, LED25.anode
  N47: IC7.1D, BUS_2.pin8
  N48: IC7.2D, BUS_2.pin7
  N49: IC7.2Q, MAR_DATA_OUT.pin7, LED26.anode
  N50: IC7.3Q, MAR_DATA_OUT.pin6, LED27.anode
  N51: IC7.3D, BUS_2.pin6
  N52: IC7.4D, BUS_2.pin5
  N53: IC7.4Q, MAR_DATA_OUT.pin5, LED28.anode
  N54: IC7.5Q, MAR_DATA_OUT.pin4, LED29.anode
  N55: IC7.5D, BUS_2.pin4
  N56: IC7.6D, BUS_2.pin3
  N57: IC7.6Q, MAR_DATA_OUT.pin3, LED30.anode
  N58: IC7.7Q, MAR_DATA_OUT.pin2, LED31.anode
  N59: IC7.7D, BUS_2.pin2
  N60: IC7.8D, BUS_2.pin1
  N61: IC7.8Q, MAR_DATA_OUT.pin1, LED32.anode
  N62: IC8._A/B, IC9._A/B
  N63: IC8.1A, A.pin4
  N64: IC8.1B, B.pin4
  N65: IC8.1Y, OUT.pin4, LED21.anode
  N66: IC8.2A, A.pin3
  N67: IC8.2B, B.pin3
  N68: IC8.2Y, OUT.pin3, LED22.anode
  GND_3: IC8.GND, IC9.GND
  N69: IC8.3Y, OUT.pin2, LED23.anode
  N70: IC8.3B, B.pin2
  N71: IC8.3A, A.pin2
  N72: IC8.4Y, OUT.pin1, LED24.anode
  N73: IC8.4B, B.pin1
  N74: IC8.4A, A.pin1
  VCC_3: IC8._G, IC8.VCC, IC9._G, IC9.VCC
  N75: A.pin5, IC9.4A
  N76: A.pin6, IC9.3A
  N77: A.pin7, IC9.2A
  N78: A.pin8, IC9.1A
  N79: IC9.1B, B.pin8
  N80: IC9.1Y, OUT.pin8, LED17.anode
  N81: IC9.2B, B.pin7
  N82: IC9.2Y, OUT.pin7, LED18.anode
  N83: IC9.3Y, OUT.pin6, LED19.anode
  N84: IC9.3B, B.pin6
  N85: IC9.4Y, OUT.pin5, LED20.anode
  N86: IC9.4B, B.pin5
  N87: IC10.1A, IC10.2Y
  N88: IC10.3B, IC10.4Y
  N89: LED17.cathode, R39.Pin_1
  N90: LED18.cathode, R38.Pin_1
  N91: LED19.cathode, R37.Pin_1
  N92: LED20.cathode, R36.Pin_1
  N93: LED21.cathode, R35.Pin_1
  N94: LED22.cathode, R34.Pin_1
  N95: LED23.cathode, R33.Pin_1
  N96: LED24.cathode, R32.Pin_1
  N97: R32.Pin_0, R33.Pin_0, R34.Pin_0, R35.Pin_0, R36.Pin_0, R37.Pin_0, R38.Pin_0, R39.Pin_0
  N98: LED25.cathode, R40.Pin_1
  N99: LED26.cathode, R45.Pin_1
  N100: LED27.cathode, R42.Pin_1
  N101: LED28.cathode, R43.Pin_1
  N102: LED29.cathode, R41.Pin_1
  N103: LED30.cathode, R44.Pin_1
  N104: LED31.cathode, R47.Pin_1
  N105: LED32.cathode, R46.Pin_1
  N106: A2.pin1, IC17._G, IC18._G
  N107: A2.pin2, IC17.3A
  N108: A2.pin3, IC17.2A
  N109: A2.pin4, IC17.1A
  N110: A2.pin5, IC18.4A
  N111: A2.pin6, IC18.3A
  N112: A2.pin7, IC18.2A
  N113: A2.pin8, IC18.1A
  N114: OUT2.pin1, IC17.4Y
  N115: OUT2.pin2, IC17.3Y
  N116: OUT2.pin3, IC17.2Y
  N117: OUT2.pin4, IC17.1Y
  N118: OUT2.pin5, IC18.4Y
  N119: OUT2.pin6, IC18.3Y
  N120: OUT2.pin7, IC18.2Y
  N121: OUT2.pin8, IC18.1Y
  N122: B3.pin1, IC17.4B
  N123: B3.pin2, IC17.3B
  N124: B3.pin3, IC17.2B
  N125: B3.pin4, IC17.1B
  N126: B3.pin5, IC18.4B
  N127: B3.pin6, IC18.3B
  N128: B3.pin7, IC18.2B
  N129: B3.pin8, IC18.1B
  N130: IC17._A/B, IC18._A/B
  GND_4: IC17.GND, IC18.GND
  VCC_4: IC17.VCC, IC18.VCC
  N131: R72.Pin_0, R73.Pin_0, R74.Pin_0, R75.Pin_0, R76.Pin_0, R77.Pin_0, R78.Pin_0, R79.Pin_0
  N132: R72.Pin_1, LED49.cathode
  N133: R73.Pin_1, LED50.cathode
  N134: R74.Pin_1, LED51.cathode
  N135: R75.Pin_1, LED52.cathode
  N136: R76.Pin_1, LED53.cathode
  N137: R77.Pin_1, LED54.cathode
  N138: R78.Pin_1, LED55.cathode
  N139: R79.Pin_1, LED56.cathode
  N140: OUT3.pin1, LED56.anode
  N141: OUT3.pin2, LED55.anode
  N142: OUT3.pin3, LED54.anode
  N143: OUT3.pin4, LED53.anode
  N144: OUT3.pin5, LED52.anode
  N145: OUT3.pin6, LED51.anode
  N146: OUT3.pin7, LED50.anode
  N147: OUT3.pin8, LED49.anode

custom parts:
  DIP - 24 pins: 2K SRAM (16K x 8-bit)
  74HCT245: Octal Tri state buffer
  DIP - 16 pins: Quad 2 line to one line data selectors
  DIP - 14 pins: Hex Schmitt trigger inverters
  74HCT377: Octal D-Type flip flops with clock enable 8 bit register
  DIP - 14 pins: Quad OR gate
