# Fritzing sketch alu (saved by Fritzing 0.9.3b)
breadboards: 3

parts:
  IC11 = DIP - 24 pins [chip_label=74LS181 package="DIP (Dual Inline) [THT]"]
  IC12 = DIP - 24 pins [chip_label=74LS181 package="DIP (Dual Inline) [THT]"]
  A = female pin header, 8 pins [form="♀ (female)"]
  RESULT = female pin header, 8 pins [form="♀ (female)"]
  B = female pin header, 8 pins [form="♀ (female)"]
  IC13 = IC, DIP package, 14 pins [chip_label=74HCT00]
  IC16 = IC, DIP package, 16 pins [chip_label=74HCT173]
  LED2 = LED - 5mm [color="Green (555nm)" package="5 mm [THT]"]
  LED3 = LED - 5mm [color="Green (555nm)" package="5 mm [THT]"]
  LED4 = LED - 5mm [color="Green (555nm)" package="5 mm [THT]"]
  LED5 = LED - 5mm [color="Green (555nm)" package="5 mm [THT]"]
  R1 = Resistor [tolerance=±5% resistance=220 package=THT]
  R2 = Resistor [tolerance=±5% resistance=220 package=THT]
  R3 = Resistor [tolerance=±5% resistance=220 package=THT]
  R4 = Resistor [tolerance=±5% resistance=220 package=THT]
  IC17 = DIP - 14 pins [chip_label=74HCT04 package="DIP (Dual Inline) [THT]"]
  result_live = female pin header, 8 pins [form="♀ (female)"]
  LED9 = LED - 5mm [color="Red (633nm)" package="5 mm [THT]"]
  LED10 = LED - 5mm [color="Red (633nm)" package="5 mm [THT]"]
  LED11 = LED - 5mm [color="Red (633nm)" package="5 mm [THT]"]
  LED12 = LED - 5mm [color="Red (633nm)" package="5 mm [THT]"]
  LED13 = LED - 5mm [color="Red (633nm)" package="5 mm [THT]"]
  LED14 = LED - 5mm [color="Red (633nm)" package="5 mm [THT]"]
  LED15 = LED - 5mm [color="Red (633nm)" package="5 mm [THT]"]
  LED16 = LED - 5mm [color="Red (633nm)" package="5 mm [THT]"]
  R5 = Resistor [tolerance=±5% resistance=220 package=THT]
  R13 = Resistor [tolerance=±5% resistance=220 package=THT]
  R14 = Resistor [tolerance=±5% resistance=220 package=THT]
  R15 = Resistor [tolerance=±5% resistance=220 package=THT]
  R16 = Resistor [tolerance=±5% resistance=220 package=THT]
  LED17 = LED - 5mm [color="Green (555nm)" package="5 mm [THT]"]
  LED18 = LED - 5mm [color="Green (555nm)" package="5 mm [THT]"]
  LED19 = LED - 5mm [color="Green (555nm)" package="5 mm [THT]"]
  LED20 = LED - 5mm [color="Green (555nm)" package="5 mm [THT]"]
  store_flags = female pin header, 2 pins [form="♀ (female)"]
  IC24 = DIP - 14 pins [chip_label=74HCT32 package="DIP (Dual Inline) [THT]"]
  IC25 = DIP - 14 pins [chip_label=74HCT32 package="DIP (Dual Inline) [THT]"]
  result_live_2 = female pin header, 8 pins [form="♀ (female)"]
  R40 = Resistor [tolerance=±5% resistance=220 package=THT]
  R41 = Resistor [tolerance=±5% resistance=220 package=THT]
  R42 = Resistor [tolerance=±5% resistance=220 package=THT]
  R43 = Resistor [tolerance=±5% resistance=220 package=THT]
  R44 = Resistor [tolerance=±5% resistance=220 package=THT]
  R45 = Resistor [tolerance=±5% resistance=220 package=THT]
  R46 = Resistor [tolerance=±5% resistance=220 package=THT]
  IC26 = DIP - 14 pins [chip_label=74HCT04 package="DIP (Dual Inline) [THT]"]
  IC27 = 74HCT245 [chip_label=74HCT245 package="DIP (Dual Inline) [THT]"]
  IC28 = 74HCT377 [chip_label=74HCT377 package="DIP (Dual Inline) [THT]"]
  R47 = Resistor [tolerance=±5% resistance=1k package=THT]
  R48 = Resistor [tolerance=±5% resistance=1k package=THT]
  R49 = Resistor [tolerance=±5% resistance=1k package=THT]
  R50 = Resistor [tolerance=±5% resistance=1k package=THT]
  R51 = Resistor [tolerance=±5% resistance=1k package=THT]
  R52 = Resistor [tolerance=±5% resistance=1k package=THT]
  R53 = Resistor [tolerance=±5% resistance=1k package=THT]
  R54 = Resistor [tolerance=±5% resistance=1k package=THT]
  LED30 = LED - 5mm [color="Red (633nm)" package="5 mm [THT]"]
  LED31 = LED - 5mm [color="Red (633nm)" package="5 mm [THT]"]
  LED32 = LED - 5mm [color="Red (633nm)" package="5 mm [THT]"]
  LED33 = LED - 5mm [color="Red (633nm)" package="5 mm [THT]"]
  LED34 = LED - 5mm [color="Red (633nm)" package="5 mm [THT]"]
  LED35 = LED - 5mm [color="Red (633nm)" package="5 mm [THT]"]
  LED36 = LED - 5mm [color="Red (633nm)" package="5 mm [THT]"]
  LED37 = LED - 5mm [color="Red (633nm)" package="5 mm [THT]"]
  INPUT1 = female pin header, 2 pins [form="♀ (female)"]
  CLOCK = female pin header, 2 pins [form="♀ (female)"]
  OUTPUT1 = female pin header, 2 pins [form="♀ (female)"]
  S0-3 = female pin header, 4 pins [form="♀ (female)"]
  R55 = Resistor [tolerance=±5% resistance=10k package=THT]
  R56 = Resistor [tolerance=±5% resistance=10k package=THT]
  C1 = Ceramic Capacitor [capacitance=100nF package="100 mil [THT, multilayer]"]
  C2 = Ceramic Capacitor [capacitance=100nF package="100 mil [THT, multilayer]"]
  A=B = female pin header, 2 pins [form="♀ (female)"]
  carry_borrow_out = female pin header, 2 pins [form="♀ (female)"]
  M = female pin header, 2 pins [form="♀ (female)"]
  carry_borrow_in = female pin header, 2 pins [form="♀ (female)"]
  carry_borrow_in_2 = female pin header, 2 pins [form="♀ (female)"]
  carry_borrow_in_3 = female pin header, 2 pins [form="♀ (female)"]
  A=B_2 = female pin header, 2 pins [form="♀ (female)"]
  carry_borrow_out_2 = female pin header, 2 pins [form="♀ (female)"]
  negative = female pin header, 2 pins [form="♀ (female)"]
  A=B1 = female pin header, 2 pins [form="♀ (female)"]
  flags = female pin header, 4 pins [form="♀ (female)"]
  C3 = Ceramic Capacitor [capacitance=100nF package="100 mil [THT, multilayer]"]
  C4 = Ceramic Capacitor [capacitance=100nF package="100 mil [THT, multilayer]"]
  result_live_3 = female pin header, 8 pins [form="♀ (female)"]
  result_stored = female pin header, 8 pins [form="♀ (female)"]
  clock = female pin header, 2 pins [form="♀ (female)"]
  C5 = Ceramic Capacitor [capacitance=100nF package="100 mil [THT, multilayer]"]
  C6 = Ceramic Capacitor [capacitance=100nF package="100 mil [THT, multilayer]"]

nets:
  N1: IC11.B0, B.pin4
  N2: IC11.A0, A.pin4
  N3: IC11.S3, IC12.S3, S0-3.pin1
  N4: IC11.S2, IC12.S2, S0-3.pin2
  N5: IC11.S1, IC12.S1, S0-3.pin3
  N6: IC11.S0, IC12.S0, S0-3.pin4
  N7: IC11._CN, IC12._CN+4
  N8: IC11.M, IC12.M, M.pin1, M.pin2
  N9: IC11.F0, RESULT.pin4
  N10: IC11.F1, RESULT.pin3
  N11: IC11.F2, RESULT.pin2
  GND: IC11.GND, IC12.GND, IC13.pin1, IC13.pin2, IC13.pin7, C1.0, C2.1
  N12: IC11.F3, RESULT.pin1, A=B1.pin1, A=B1.pin2
  N13: IC11.A=B, IC13.pin10, R55.Pin_0
  N14: IC11._CN+4, IC13.pin4, IC13.pin5
  N15: IC11.B3, B.pin1
  N16: IC11.A3, A.pin1
  N17: IC11.B2, B.pin2
  N18: IC11.A2, A.pin2
  N19: IC11.B1, B.pin3
  N20: IC11.A1, A.pin3
  VCC: IC11.VCC, IC12.VCC, IC13.pin14, R55.Pin_1, R56.Pin_1, C1.1, C2.0
  N21: IC12.B0, B.pin8
  N22: IC12.A0, A.pin8
  N23: IC12._CN, carry_borrow_in.pin1, carry_borrow_in.pin2
  N24: IC12.F0, RESULT.pin8
  N25: IC12.F1, RESULT.pin7
  N26: IC12.F2, RESULT.pin6
  N27: IC12.F3, RESULT.pin5
  N28: IC12.A=B, IC13.pin9, R56.Pin_0
  N29: IC12.B3, B.pin5
  N30: IC12.A3, A.pin5
  N31: IC12.B2, B.pin6
  N32: IC12.A2, A.pin6
  N33: IC12.B1, B.pin7
  N34: IC12.A1, A.pin7
  N35: IC13.pin6, carry_borrow_out.pin1, carry_borrow_out.pin2
  N36: IC13.pin8, IC13.pin12, IC13.pin13
  N37: IC13.pin11, A=B.pin1, A=B.pin2
  VCC_2: IC16.pin1, IC16.pin2, IC16.pin16, IC17.VCC, IC24.VCC, IC25.VCC, C3.1, C4.0
  N38: IC16.pin3, LED2.anode, flags.pin1
  N39: IC16.pin4, LED3.anode, flags.pin2
  N40: IC16.pin5, LED4.anode, flags.pin3
  N41: IC16.pin6, LED5.anode, flags.pin4
  N42: IC16.pin7, clock.pin1, clock.pin2
  GND_2: IC16.pin8, IC16.pin10, IC16.pin15, R1.Pin_0, R2.Pin_0, R3.Pin_0, R4.Pin_0, IC17.1A, IC17.2A, IC17.3A, IC17.GND, R5.Pin_1, R13.Pin_1, R14.Pin_1, R15.Pin_1, R16.Pin_1, IC24.1A, IC24.1B, IC24.GND, IC25.GND, R40.Pin_1, R41.Pin_1, R42.Pin_1, R43.Pin_1, R44.Pin_1, R45.Pin_1, R46.Pin_1, C3.0, C4.1
  N43: IC16.pin9, IC17.6Y
  N44: IC16.pin11, IC17.5Y, LED17.anode
  N45: IC16.pin12, LED18.anode, negative.pin1, negative.pin2
  N46: IC16.pin13, LED19.anode, carry_borrow_out_2.pin1, carry_borrow_out_2.pin2
  N47: IC16.pin14, LED20.anode, A=B_2.pin1, A=B_2.pin2
  N48: LED2.cathode, R1.Pin_1
  N49: LED3.cathode, R2.Pin_1
  N50: LED4.cathode, R4.Pin_1
  N51: LED5.cathode, R3.Pin_1
  N52: IC17.4Y, carry_borrow_in_3.pin1, carry_borrow_in_3.pin2
  N53: IC17.4A, carry_borrow_in_2.pin1, carry_borrow_in_2.pin2
  N54: IC17.5A, IC24.4Y
  N55: IC17.6A, store_flags.pin1, store_flags.pin2
  N56: result_live.pin1, LED10.cathode, IC25.4B, result_live_2.pin1
  N57: result_live.pin2, LED9.cathode, IC25.4A, result_live_2.pin2
  N58: result_live.pin3, LED12.cathode, IC25.3B, result_live_2.pin3
  N59: result_live.pin4, LED11.cathode, IC25.3A, result_live_2.pin4
  N60: result_live.pin5, LED14.cathode, IC25.1A, result_live_2.pin5
  N61: result_live.pin6, LED16.cathode, IC25.1B, result_live_2.pin6
  N62: result_live.pin7, LED13.cathode, IC25.2A, result_live_2.pin7
  N63: result_live.pin8, LED15.cathode, IC25.2B, result_live_2.pin8
  N64: LED9.anode, R44.Pin_0
  N65: LED10.anode, R45.Pin_0
  N66: LED11.anode, R43.Pin_0
  N67: LED12.anode, R46.Pin_0
  N68: LED13.anode, R40.Pin_0
  N69: LED14.anode, R42.Pin_0
  N70: LED15.anode, R5.Pin_0
  N71: LED16.anode, R41.Pin_0
  N72: R13.Pin_0, LED20.cathode
  N73: R14.Pin_0, LED19.cathode
  N74: R15.Pin_0, LED18.cathode
  N75: R16.Pin_0, LED17.cathode
  N76: IC24.2A, IC25.2Y
  N77: IC24.2B, IC25.1Y
  N78: IC24.2Y, IC24.4A
  N79: IC24.3Y, IC24.4B
  N80: IC24.3A, IC25.4Y
  N81: IC24.3B, IC25.3Y
  N82: IC26.1A, INPUT1.pin1, INPUT1.pin2
  N83: IC26.1Y, IC28._CLKEN
  GND_3: IC26.2A, IC26.3A, IC26.GND, IC26.5A, IC26.6A, IC27.GND, IC28.GND, R47.Pin_1, R48.Pin_1, R49.Pin_1, R50.Pin_1, R51.Pin_1, R52.Pin_1, R53.Pin_1, R54.Pin_1, C5.1, C6.0
  N84: IC26.4Y, IC27._OE
  N85: IC26.4A, OUTPUT1.pin1, OUTPUT1.pin2
  VCC_3: IC26.VCC, IC27.DIR, IC27.VCC, IC28.VCC, C5.0, C6.1
  N86: IC27.A1, IC28.1Q, LED31.anode
  N87: IC27.A2, IC28.2Q, LED30.anode
  N88: IC27.A3, IC28.3Q, LED33.anode
  N89: IC27.A4, IC28.4Q, LED32.anode
  N90: IC27.A5, IC28.5Q, LED35.anode
  N91: IC27.A6, IC28.6Q, LED37.anode
  N92: IC27.A7, IC28.7Q, LED36.anode
  N93: IC27.A8, IC28.8Q, LED34.anode
  N94: IC27.B8, result_stored.pin8
  N95: IC27.B7, result_stored.pin7
  N96: IC27.B6, result_stored.pin6
  N97: IC27.B5, result_stored.pin5
  N98: IC27.B4, result_stored.pin4
  N99: IC27.B3, result_stored.pin3
  N100: IC27.B2, result_stored.pin2
  N101: IC27.B1, result_stored.pin1
  N102: IC28.1D, result_live_3.pin1
  N103: IC28.2D, result_live_3.pin2
  N104: IC28.3D, result_live_3.pin3
  N105: IC28.4D, result_live_3.pin4
  N106: IC28.CLK, CLOCK.pin1, CLOCK.pin2
  N107: IC28.5D, result_live_3.pin5
  N108: IC28.6D, result_live_3.pin6
  N109: IC28.7D, result_live_3.pin7
  N110: IC28.8D, result_live_3.pin8
  N111: R47.Pin_0, LED36.cathode
  N112: R48.Pin_0, LED35.cathode
  N113: R49.Pin_0, LED32.cathode
  N114: R50.Pin_0, LED33.cathode
  N115: R51.Pin_0, LED34.cathode
  N116: R52.Pin_0, LED37.cathode
  N117: R53.Pin_0, LED31.cathode
  N118: R54.Pin_0, LED30.cathode

notes:
  result_live
  _carry_borrow_in
  S0-3
  M
  B
  A
  A=B
  carry_borrow_out
  carry_borrow_in
  store_flags
  negative
  zero
  flags_stored
  result_stored
  flags_live is composed of these 4 flags
  clock
  output_stored_result
  store_result

custom parts:
  DIP - 24 pins: 4-bit ALU
  DIP - 14 pins: Hex Inverter
  DIP - 14 pins: Quad OR gate
  74HCT245: Octal Tri state buffer
  74HCT377: Octal D-Type flip flops with clock enable 8 bit register
