# Fritzing sketch alu2 (saved by Fritzing 0.9.3b)
breadboards: 3

parts:
  IC11 = DIP - 24 pins [chip_label=74LS181 package="DIP (Dual Inline) [THT]"]
  IC12 = DIP - 24 pins [chip_label=74LS181 package="DIP (Dual Inline) [THT]"]
  BUS = female pin header, 8 pins [form="♀ (female)"]
  RESULT = female pin header, 8 pins [form="♀ (female)"]
  B_REGISTER = female pin header, 8 pins [form="♀ (female)"]
  IC13 = IC, DIP package, 14 pins [chip_label=74HCT00]
  IC16 = IC, DIP package, 16 pins [chip_label=74HCT173]
  CARRY/BORROW_IN = female pin header, 2 pins [form="♀ (female)"]
  LED2 = LED - 5mm [color="Green (555nm)" package="5 mm [THT]"]
  LED3 = LED - 5mm [color="Green (555nm)" package="5 mm [THT]"]
  LED4 = LED - 5mm [color="Green (555nm)" package="5 mm [THT]"]
  LED5 = LED - 5mm [color="Green (555nm)" package="5 mm [THT]"]
  R1 = Resistor [tolerance=±5% resistance=220 package=THT]
  R2 = Resistor [tolerance=±5% resistance=220 package=THT]
  R3 = Resistor [tolerance=±5% resistance=220 package=THT]
  R4 = Resistor [tolerance=±5% resistance=220 package=THT]
  IC17 = DIP - 14 pins [chip_label=74HCT04 package="DIP (Dual Inline) [THT]"]
  RESULT_2 = female pin header, 8 pins [form="♀ (female)"]
  LED9 = LED - 5mm [color="Red (633nm)" package="5 mm [THT]"]
  LED10 = LED - 5mm [color="Red (633nm)" package="5 mm [THT]"]
  LED11 = LED - 5mm [color="Red (633nm)" package="5 mm [THT]"]
  LED12 = LED - 5mm [color="Red (633nm)" package="5 mm [THT]"]
  LED13 = LED - 5mm [color="Red (633nm)" package="5 mm [THT]"]
  LED14 = LED - 5mm [color="Red (633nm)" package="5 mm [THT]"]
  LED15 = LED - 5mm [color="Red (633nm)" package="5 mm [THT]"]
  LED16 = LED - 5mm [color="Red (633nm)" package="5 mm [THT]"]
  R5 = Resistor [tolerance=±5% resistance=220 package=THT]
  R13 = Resistor [tolerance=±5% resistance=220 package=THT]
  R14 = Resistor [tolerance=±5% resistance=220 package=THT]
  R15 = Resistor [tolerance=±5% resistance=220 package=THT]
  R16 = Resistor [tolerance=±5% resistance=220 package=THT]
  LED17 = LED - 5mm [color="Green (555nm)" package="5 mm [THT]"]
  LED18 = LED - 5mm [color="Green (555nm)" package="5 mm [THT]"]
  LED19 = LED - 5mm [color="Green (555nm)" package="5 mm [THT]"]
  LED20 = LED - 5mm [color="Green (555nm)" package="5 mm [THT]"]
  FLAGS_IN = female pin header, 2 pins [form="♀ (female)"]
  IC24 = DIP - 14 pins [chip_label=74HCT32 package="DIP (Dual Inline) [THT]"]
  IC25 = DIP - 14 pins [chip_label=74HCT32 package="DIP (Dual Inline) [THT]"]
  RESULT1 = female pin header, 8 pins [form="♀ (female)"]
  R40 = Resistor [tolerance=±5% resistance=220 package=THT]
  R41 = Resistor [tolerance=±5% resistance=220 package=THT]
  R42 = Resistor [tolerance=±5% resistance=220 package=THT]
  R43 = Resistor [tolerance=±5% resistance=220 package=THT]
  R44 = Resistor [tolerance=±5% resistance=220 package=THT]
  R45 = Resistor [tolerance=±5% resistance=220 package=THT]
  R46 = Resistor [tolerance=±5% resistance=220 package=THT]
  IC26 = DIP - 14 pins [chip_label=74HCT04 package="DIP (Dual Inline) [THT]"]
  IC27 = 74HCT245 [chip_label=74HCT245 package="DIP (Dual Inline) [THT]"]
  IC28 = 74HCT377 [chip_label=74HCT377 package="DIP (Dual Inline) [THT]"]
  R47 = Resistor [tolerance=±5% resistance=1k package=THT]
  R48 = Resistor [tolerance=±5% resistance=1k package=THT]
  R49 = Resistor [tolerance=±5% resistance=1k package=THT]
  R50 = Resistor [tolerance=±5% resistance=1k package=THT]
  R51 = Resistor [tolerance=±5% resistance=1k package=THT]
  R52 = Resistor [tolerance=±5% resistance=1k package=THT]
  R53 = Resistor [tolerance=±5% resistance=1k package=THT]
  R54 = Resistor [tolerance=±5% resistance=1k package=THT]
  LED30 = LED - 5mm [color="Red (633nm)" package="5 mm [THT]"]
  LED31 = LED - 5mm [color="Red (633nm)" package="5 mm [THT]"]
  LED32 = LED - 5mm [color="Red (633nm)" package="5 mm [THT]"]
  LED33 = LED - 5mm [color="Red (633nm)" package="5 mm [THT]"]
  LED34 = LED - 5mm [color="Red (633nm)" package="5 mm [THT]"]
  LED35 = LED - 5mm [color="Red (633nm)" package="5 mm [THT]"]
  LED36 = LED - 5mm [color="Red (633nm)" package="5 mm [THT]"]
  LED37 = LED - 5mm [color="Red (633nm)" package="5 mm [THT]"]
  INPUT1 = female pin header, 2 pins [form="♀ (female)"]
  CLOCK1 = female pin header, 2 pins [form="♀ (female)"]
  OUTPUT1 = female pin header, 2 pins [form="♀ (female)"]

nets:
  N1: IC11.B0, B_REGISTER.pin4
  N2: IC11.A0, BUS.pin4
  N3: IC11.S3, IC12.S3
  N4: IC11.S2, IC12.S2
  N5: IC11.S1, IC12.S1
  N6: IC11.S0, IC12.S0
  N7: IC11._CN, IC12._CN+4
  N8: IC11.M, IC12.M
  N9: IC11.F0, RESULT.pin4
  N10: IC11.F1, RESULT.pin3
  N11: IC11.F2, RESULT.pin2
  GND: IC11.GND, IC12.GND, IC13.pin1, IC13.pin2, IC13.pin7
  N12: IC11.F3, RESULT.pin1, IC16.pin12, LED18.anode
  N13: IC11.A=B, IC13.pin10
  N14: IC11._CN+4, IC13.pin4, IC13.pin5
  N15: IC11.B3, B_REGISTER.pin1
  N16: IC11.A3, BUS.pin1
  N17: IC11.B2, B_REGISTER.pin2
  N18: IC11.A2, BUS.pin2
  N19: IC11.B1, B_REGISTER.pin3
  N20: IC11.A1, BUS.pin3
  VCC: IC11.VCC, IC12.VCC, IC13.pin14
  N21: IC12.B0, B_REGISTER.pin8
  N22: IC12.A0, BUS.pin8
  N23: IC12._CN, IC17.4Y
  N24: IC12.F0, RESULT.pin8
  N25: IC12.F1, RESULT.pin7
  N26: IC12.F2, RESULT.pin6
  N27: IC12.F3, RESULT.pin5
  N28: IC12.A=B, IC13.pin9
  N29: IC12.B3, B_REGISTER.pin5
  N30: IC12.A3, BUS.pin5
  N31: IC12.B2, B_REGISTER.pin6
  N32: IC12.A2, BUS.pin6
  N33: IC12.B1, B_REGISTER.pin7
  N34: IC12.A1, BUS.pin7
  N35: IC13.pin6, IC16.pin14, LED20.anode
  N36: IC13.pin8, IC13.pin12, IC13.pin13
  N37: IC13.pin11, IC16.pin13, LED19.anode
  N38: IC16.pin1, IC16.pin2
  N39: IC16.pin3, LED2.anode
  N40: IC16.pin4, LED3.anode
  N41: IC16.pin5, LED4.anode
  N42: IC16.pin6, LED5.anode
  GND_2: IC16.pin8, R1.Pin_0, R2.Pin_0, R3.Pin_0, R4.Pin_0, IC17.1A, IC17.2A, IC17.3A, IC17.GND, IC24.1A, IC24.1B, IC24.GND, IC25.GND
  N43: IC16.pin9, IC17.6Y
  N44: IC16.pin10, IC16.pin15, IC17.6A, R5.Pin_1, R13.Pin_1, R14.Pin_1, R15.Pin_1, R16.Pin_1, FLAGS_IN.pin1, FLAGS_IN.pin2, R40.Pin_1, R41.Pin_1, R42.Pin_1, R43.Pin_1, R44.Pin_1, R45.Pin_1, R46.Pin_1
  N45: IC16.pin11, IC17.5Y, LED17.anode
  VCC_2: IC16.pin16, IC17.VCC, IC24.VCC, IC25.VCC
  N46: CARRY/BORROW_IN.pin1, CARRY/BORROW_IN.pin2, IC17.4A
  N47: LED2.cathode, R1.Pin_1
  N48: LED3.cathode, R2.Pin_1
  N49: LED4.cathode, R4.Pin_1
  N50: LED5.cathode, R3.Pin_1
  N51: IC17.5A, IC24.4Y
  N52: RESULT_2.pin1, LED10.cathode, IC25.4B, RESULT1.pin1
  N53: RESULT_2.pin2, LED9.cathode, IC25.4A, RESULT1.pin2
  N54: RESULT_2.pin3, LED12.cathode, IC25.3B, RESULT1.pin3
  N55: RESULT_2.pin4, LED11.cathode, IC25.3A, RESULT1.pin4
  N56: RESULT_2.pin5, LED14.cathode, IC25.1A, RESULT1.pin5
  N57: RESULT_2.pin6, LED16.cathode, IC25.1B, RESULT1.pin6
  N58: RESULT_2.pin7, LED15.cathode, IC25.2A, RESULT1.pin7
  N59: RESULT_2.pin8, LED13.cathode, IC25.2B, RESULT1.pin8
  N60: LED9.anode, R44.Pin_0
  N61: LED10.anode, R45.Pin_0
  N62: LED11.anode, R43.Pin_0
  N63: LED12.anode, R46.Pin_0
  N64: LED13.anode, R5.Pin_0
  N65: LED14.anode, R42.Pin_0
  N66: LED15.anode, R40.Pin_0
  N67: LED16.anode, R41.Pin_0
  N68: R13.Pin_0, LED20.cathode
  N69: R14.Pin_0, LED19.cathode
  N70: R15.Pin_0, LED18.cathode
  N71: R16.Pin_0, LED17.cathode
  N72: IC24.2A, IC25.2Y
  N73: IC24.2B, IC25.1Y
  N74: IC24.2Y, IC24.4A
  N75: IC24.3Y, IC24.4B
  N76: IC24.3A, IC25.4Y
  N77: IC24.3B, IC25.3Y
  N78: IC26.1A, INPUT1.pin1, INPUT1.pin2
  N79: IC26.1Y, IC28._CLKEN
  GND_3: IC26.2A, IC26.3A, IC26.GND, IC26.5A, IC26.6A, IC27.GND, IC28.GND, R47.Pin_1, R48.Pin_1, R49.Pin_1, R50.Pin_1, R51.Pin_1, R52.Pin_1, R53.Pin_1, R54.Pin_1
  N80: IC26.4Y, IC27._OE
  N81: IC26.4A, OUTPUT1.pin1, OUTPUT1.pin2
  VCC_3: IC26.VCC, IC27.DIR, IC27.VCC, IC28.VCC
  N82: IC27.A1, IC28.1Q, LED31.anode
  N83: IC27.A2, IC28.2Q, LED30.anode
  N84: IC27.A3, IC28.3Q, LED33.anode
  N85: IC27.A4, IC28.4Q, LED32.anode
  N86: IC27.A5, IC28.5Q, LED35.anode
  N87: IC27.A6, IC28.6Q, LED37.anode
  N88: IC27.A7, IC28.7Q, LED36.anode
  N89: IC27.A8, IC28.8Q, LED34.anode
  N90: IC28.CLK, CLOCK1.pin1, CLOCK1.pin2
  N91: R47.Pin_0, LED36.cathode
  N92: R48.Pin_0, LED35.cathode
  N93: R49.Pin_0, LED32.cathode
  N94: R50.Pin_0, LED33.cathode
  N95: R51.Pin_0, LED34.cathode
  N96: R52.Pin_0, LED37.cathode
  N97: R53.Pin_0, LED31.cathode
  N98: R54.Pin_0, LED30.cathode

custom parts:
  DIP - 24 pins: 4-bit ALU
  DIP - 14 pins: Hex Inverter
  DIP - 14 pins: Quad OR gate
  74HCT245: Octal Tri state buffer
  74HCT377: Octal D-Type flip flops with clock enable 8 bit register
