# Fritzing sketch arduino_interface (saved by Fritzing 0.9.3b)
breadboards: 1

parts:
  IC1 = 74HC165 [chip_label=74HC165 package="DIP (Dual Inline) [THT]"]
  U1 = 74HC595 [package="DIP16 [THT]"]
  U2 = 74HC595 [package="DIP16 [THT]"]
  U3 = 74HC595 [package="DIP16 [THT]"]
  IC2 = IC, DIP package, 20 pins [chip_label="GREEN BAR LED"]
  IC3 = IC, DIP package, 20 pins [chip_label="RED BAR LED"]
  LED1 = LED - 5mm [color="Green (555nm)" package="5 mm [THT]"]
  LED2 = LED - 5mm [color="Green (555nm)" package="5 mm [THT]"]
  LED3 = LED - 5mm [color="Green (555nm)" package="5 mm [THT]"]
  LED4 = LED - 5mm [color="Blue (430nm)" package="5 mm [THT]"]
  LED5 = LED - 5mm [color="Blue (430nm)" package="5 mm [THT]"]
  LED6 = LED - 5mm [color="Yellow (595nm)" package="5 mm [THT]"]

nets:
  GND: IC1.GND, U1.GND, U2.GND, U3.GND
  N1: IC1.SER, IC1.CLK_INH, U1.OE, U2.OE, U3.OE
  VCC: IC1.VCC, U1.MR, U1.VCC, U2.MR, U2.VCC, U3.MR, U3.VCC
  N2: U1.Q1, IC3.pin3
  N3: U1.Q2, IC3.pin4
  N4: U1.Q3, IC3.pin5
  N5: U1.Q4, IC3.pin6
  N6: U1.Q5, IC3.pin7
  N7: U1.Q6, IC3.pin8
  N8: U1.Q7, IC3.pin9
  N9: U1.Q7', U2.DS
  N10: U1.SH_CP, U2.SH_CP, U3.SH_CP
  N11: U1.ST_CP, U2.ST_CP, U3.ST_CP
  N12: U1.Q0, IC3.pin2
  N13: U2.Q1, IC2.pin3
  N14: U2.Q2, IC2.pin4
  N15: U2.Q3, IC2.pin5
  N16: U2.Q4, IC2.pin6
  N17: U2.Q5, IC2.pin7
  N18: U2.Q6, IC2.pin8
  N19: U2.Q7, IC2.pin9
  N20: U2.Q7', U3.DS
  N21: U2.Q0, IC2.pin2
  N22: U3.Q2, LED1.anode
  N23: U3.Q3, LED2.anode
  N24: U3.Q4, LED3.anode
  N25: U3.Q5, LED4.anode
  N26: U3.Q6, LED5.anode
  N27: U3.Q7, LED6.anode

notes:
  inputs 7-0 (MSB on left)
  SHIFT_FROM_CPU_DATA
  SHIFT_FROM_CPU_SHIFT_LOAD
  SHIFT_FROM_CPU_CLOCK
  SHIFT_TO_CPU_DATA
  SHIFT_TO_CPU_LATCHOUT
  SHIFT_TO_CPU_CLOCK
  ~PROG/DATA RAM
  ~CU/USER RAM CTL
  RAM WRITE
  RESET
  CLOCK ENABLE
  ~ARDUINO/CRYSTAL CLOCK
  RAM ENABLE ENABLE

custom parts:
  74HC165: Parallel in serial out shift register
