# Fritzing sketch clock (saved by Fritzing 0.9.3b)
breadboards: 2

parts:
  U1 = 555 Timer [package="DIP8 [THT]"]
  R1 = Resistor [tolerance=±5% resistance=220 package=THT]
  R2 = Resistor [tolerance=±5% resistance=220 package=THT]
  C1 = Electrolytic Capacitor [capacitance=1µF package="100 mil [THT, electrolytic]"]
  C2 = Ceramic Capacitor [capacitance=100nF package="100 mil [THT, multilayer]"]
  R3 = Rotary Potentiometer (Small) [maximum_resistance=100kΩ package=THT]
  IC1 = DIP - 14 pins [chip_label=74HCT14 package="DIP (Dual Inline) [THT]"]
  R4 = Resistor [tolerance=±5% resistance=220 package=THT]
  C3 = Ceramic Capacitor [capacitance=100nF package="100 mil [THT, multilayer]"]
  R5 = Resistor [tolerance=±5% resistance=220 package=THT]
  R6 = Resistor [tolerance=±5% resistance=220 package=THT]
  C4 = Ceramic Capacitor [capacitance=100nF package="100 mil [THT, multilayer]"]
  C5 = Ceramic Capacitor [capacitance=100nF package="100 mil [THT, multilayer]"]
  IC2 = DIP - 14 pins [chip_label=74HCT00 package="DIP (Dual Inline) [THT]"]
  MAN/AUTO = female pin header, 2 pins [form="♀ (female)"]
  MAN_PP = female pin header, 2 pins [form="♀ (female)"]
  MAN_MOM = female pin header, 2 pins [form="♀ (female)"]
  MAN/AUTO_DB = female pin header, 2 pins [form="♀ (female)"]
  MAN_MOM_DB = female pin header, 2 pins [form="♀ (female)"]
  MAN_PP_DB = female pin header, 2 pins [form="♀ (female)"]
  IC3 = DIP - 14 pins [chip_label=74HCT86 package="DIP (Dual Inline) [THT]"]
  IC6 = DIP - 14 pins [chip_label=74HCT00 package="DIP (Dual Inline) [THT]"]
  IC7 = IC, DIP package, 14 pins [chip_label=74HCT02]
  RESET = female pin header, 2 pins [form="♀ (female)"]
  HALT = female pin header, 2 pins [form="♀ (female)"]
  RAW_CLOCK = female pin header, 2 pins [form="♀ (female)"]
  U2 = 555 Timer [package="DIP8 [THT]"]
  R7 = Resistor [tolerance=±5% resistance=220 package=THT]
  R8 = Resistor [tolerance=±5% resistance=220 package=THT]
  C6 = Electrolytic Capacitor [capacitance=1µF package="100 mil [THT, electrolytic]"]
  C7 = Ceramic Capacitor [capacitance=100nF package="100 mil [THT, multilayer]"]
  R9 = Rotary Potentiometer (Small) [maximum_resistance=100kΩ package=THT]
  R10 = Resistor [tolerance=±5% resistance=220 package=THT]
  C8 = Ceramic Capacitor [capacitance=100nF package="100 mil [THT, multilayer]"]
  MAN/AUTO_2 = female pin header, 2 pins [form="♀ (female)"]
  RESET_2 = female pin header, 2 pins [form="♀ (female)"]
  R11 = Resistor [tolerance=±5% resistance=220 package=THT]
  C9 = Ceramic Capacitor [capacitance=100nF package="100 mil [THT, multilayer]"]
  IC11 = DIP - 14 pins [chip_label=74HCT14 package="DIP (Dual Inline) [THT]"]
  IC12 = DIP - 14 pins [chip_label=74HCT00 package="DIP (Dual Inline) [THT]"]
  R12 = Resistor [tolerance=±5% resistance=220 package=THT]
  C10 = Ceramic Capacitor [capacitance=100nF package="100 mil [THT, multilayer]"]
  MANUAL = female pin header, 2 pins [form="♀ (female)"]
  RESET_DB = female pin header, 2 pins [form="♀ (female)"]
  MANUAL_DB = female pin header, 2 pins [form="♀ (female)"]
  MAN/AUTO_DB_2 = female pin header, 2 pins [form="♀ (female)"]
  IC13 = IC, DIP package, 14 pins [chip_label=74HCT02]
  DRIVER_CLOCK = female pin header, 2 pins [form="♀ (female)"]
  HALT_2 = female pin header, 2 pins [form="♀ (female)"]
  IC14 = DIP - 14 pins [chip_label=74HCT00 package="DIP (Dual Inline) [THT]"]
  IC15 = DIP - 16 pins [chip_label=74HCT109 package="DIP (Dual Inline) [THT]"]
  IC16 = DIP - 16 pins [chip_label=74HCT109 package="DIP (Dual Inline) [THT]"]
  IC17 = DIP - 16 pins [chip_label=74HCT109 package="DIP (Dual Inline) [THT]"]

nets:
  N1: U1.Ground, C1.-, C3.1, C4.1
  N2: U1.Trigger, U1.Threshold, C1.+, R3.leg1
  N3: U1.Output, IC2.2B
  N4: U1.Control_Voltage, C2.1
  N5: U1.Discharge, R1.Pin_0, R2.Pin_0
  N6: R1.Pin_1, C2.0, C5.1
  N7: R2.Pin_1, R3.wiper
  N8: IC1.1A, R4.Pin_0, C3.0
  N9: IC1.1Y, IC1.2A
  N10: IC1.2Y, IC2.1A, IC2.1B, IC2.4A, MAN/AUTO_DB.pin2
  N11: IC1.3A, R5.Pin_0, C4.0
  N12: IC1.3Y, IC1.4A
  N13: IC1.4Y, MAN_MOM_DB.pin1, IC3.4A
  N14: IC1.5Y, MAN_PP_DB.pin1, IC3.4B
  N15: IC1.5A, IC1.6Y
  N16: IC1.6A, R6.Pin_1, C5.0
  N17: R4.Pin_1, MAN/AUTO.pin1, MAN/AUTO.pin2
  N18: R5.Pin_1, MAN_MOM.pin1, MAN_MOM.pin2
  N19: R6.Pin_0, MAN_PP.pin2
  N20: IC2.1Y, IC2.2A
  N21: IC2.2Y, IC2.3A
  N22: IC2.3Y, IC6.4A, IC7.pin11, IC7.pin12, RAW_CLOCK.pin1, RAW_CLOCK.pin2
  N23: IC2.3B, IC2.4Y
  N24: IC2.4B, IC3.4Y
  N25: IC6.3Y, IC15.1CP, IC15.2CP
  N26: IC6.3B, IC6.3A, IC6.4Y
  N27: IC6.4B, IC7.pin4, IC7.pin8
  N28: IC7.pin1, IC15._1R, IC15._2R
  N29: IC7.pin2, HALT.pin2
  N30: IC7.pin3, IC7.pin5, RESET.pin2
  N31: IC7.pin6, IC7.pin10
  N32: IC7.pin9, IC7.pin13
  GND: U2.Ground, C6.-, C8.1, IC11.GND, IC12.2A, IC12.2B, IC12.GND, C10.1, IC13.pin7, IC14.1A, IC14.1B, IC14.GND, IC16._1K, IC16.GND, IC17._1K, IC17.GND
  N33: U2.Trigger, U2.Threshold, C6.+, R9.leg1
  N34: U2.Output, IC16.1CP
  N35: U2.Reset, IC16._1R, IC16.1J, IC16._1S, IC17.1J, IC17._1S
  N36: U2.Control_Voltage, C7.1
  N37: U2.Discharge, R7.Pin_0, R8.Pin_0
  VCC: U2.Vcc_Supply_Voltage, IC11.VCC, IC12.VCC, IC13.pin14, IC14.VCC, IC16._2S, IC16.2J, IC16._2R, IC16.VCC, IC17._2S, IC17.2J, IC17.VCC
  N38: R7.Pin_1, C7.0, C9.0, IC16.2CP, IC16._2K, IC17._2K
  N39: R8.Pin_1, R9.wiper
  N40: R10.Pin_0, C8.0, IC11.3A
  N41: R10.Pin_1, MAN/AUTO_2.pin1
  N42: RESET_2.pin1, R12.Pin_1
  N43: R11.Pin_0, MANUAL.pin2
  N44: R11.Pin_1, C9.1, IC11.6A
  N45: IC11.1A, R12.Pin_0, C10.0
  N46: IC11.1Y, IC11.2A
  N47: IC11.2Y, RESET_DB.pin2, IC13.pin3, IC13.pin5
  N48: IC11.3Y, IC11.4A, IC12.1A
  N49: IC11.4Y, IC12.4A, MAN/AUTO_DB_2.pin1
  N50: IC11.5Y, IC12.4B, MANUAL_DB.pin1
  N51: IC11.5A, IC11.6Y
  N52: IC12.1B, IC16.1Q
  N53: IC12.1Y, IC12.3A
  N54: IC12.3Y, IC13.pin11, IC13.pin12, DRIVER_CLOCK.pin1, IC14.4A
  N55: IC12.3B, IC12.4Y
  N56: IC13.pin1, IC17._1R, IC17._2R
  N57: IC13.pin2, HALT_2.pin1, HALT_2.pin2
  N58: IC13.pin4, IC13.pin8, IC14.4B
  N59: IC13.pin6, IC13.pin10
  N60: IC13.pin9, IC13.pin13
  N61: IC14.2A, IC14.2B, IC14.3Y, IC17.2CP
  N62: IC14.2Y, IC17.1CP
  N63: IC14.3B, IC14.3A, IC14.4Y

custom parts:
  DIP - 14 pins: Hex Schmitt trigger inverters
  DIP - 14 pins: Quad NAND
  DIP - 14 pins: Quad XOR
  DIP - 16 pins: Dual JK flip flop with set and reset, positive edge trigger
