# Fritzing sketch clock_2 (saved by Fritzing 0.9.3b)
breadboards: 1

parts:
  IC1 = DIP - 16 pins [chip_label=74HCT109 package="DIP (Dual Inline) [THT]"]
  IC2 = DIP - 16 pins [chip_label=74HCT109 package="DIP (Dual Inline) [THT]"]
  IC3 = DIP - 14 pins [chip_label=74HCT02 package="DIP (Dual Inline) [THT]"]
  IC4 = DIP - 14 pins [chip_label=74HCT00 package="DIP (Dual Inline) [THT]"]
  IC5 = DIP - 16 pins [chip_label=74HCT157 package="DIP (Dual Inline) [THT]"]
  IC7 = DIP - 14 pins [chip_label=74HCT14 package="DIP (Dual Inline) [THT]"]
  XTAL1 = Crystal [frequency="4 MHz" package=THT]
  C1 = Ceramic Capacitor [capacitance=100n package="100 mil [THT, multilayer]"]
  C2 = Ceramic Capacitor [capacitance=100nF package="100 mil [THT, multilayer]"]
  R1 = Resistor [tolerance=±5% resistance=1M package=THT]
  R2 = Resistor [tolerance=±5% resistance=5k package=THT]
  LED1 = LED - 5mm [color="Red (633nm)" package="5 mm [THT]"]
  R3 = Resistor [tolerance=±5% resistance=220 package=THT]
  LED2 = LED - 5mm [color="Red (633nm)" package="5 mm [THT]"]
  R4 = Resistor [tolerance=±5% resistance=220 package=THT]

nets:
  N1: IC1._1R, IC1._2R, IC2._1R, IC4.3Y
  N2: IC1.1J, IC1._1S, IC2.1J, IC2._1S
  GND: IC1._1K, IC1.GND, IC2._1K, IC2.GND, IC3.GND, IC4.GND, IC5.2A, IC5.2B, IC5.GND, IC7.GND, C1.1, C2.0, R4.Pin_0
  N3: IC1.1CP, IC2._1Q
  N4: IC1.1Q, LED2.anode
  N5: IC1.2Q, LED1.anode
  VCC: IC1._2S, IC1.2J, IC1.VCC, IC2._2S, IC2.2J, IC2._2R, IC2.VCC, IC3.VCC, IC4.VCC, IC5.VCC, IC7.VCC
  N6: IC1.2CP, IC2.1Q
  N7: IC1._2K, IC2.2CP, IC2._2K, IC3.4A, IC3.4B, IC5.3B, IC5.3A, IC5.4B, IC5.4A, IC5._G, IC7.4A, IC7.5A, IC7.6A, R3.Pin_0
  N8: IC2.1CP, IC4.2Y
  N9: IC3.1Y, IC3.2A
  N10: IC3.1A, IC7.3Y
  N11: IC3.1B, IC3.2Y, IC4.1B
  N12: IC3.2B, IC4.4Y
  N13: IC3.3A, IC4.3B, IC4.3A
  N14: IC3.3Y, IC4.4A
  N15: IC4.1A, IC5.1Y, IC7.3A
  N16: IC4.1Y, IC4.2A, IC4.2B
  N17: IC5.1B, IC7.2Y
  N18: IC7.1A, XTAL1.pin_0, C1.0, R1.Pin_0
  N19: IC7.1Y, IC7.2A, R1.Pin_1, R2.Pin_1
  N20: XTAL1.pin_1, C2.1, R2.Pin_0
  N21: LED1.cathode, R3.Pin_1
  N22: LED2.cathode, R4.Pin_1

notes:
  reset
  halt
  clock_enable
  _arduino/crystal
  arduino_clock

custom parts:
  DIP - 16 pins: Dual JK flip flop with set and reset, positive edge trigger
  DIP - 14 pins: Quad NOR
  DIP - 14 pins: Quad NAND
  DIP - 16 pins: Quad 2 line to one line data selectors
  DIP - 14 pins: Hex Schmitt trigger inverters
