# Fritzing sketch control_unit (saved by Fritzing 0.9.3b)
breadboards: 5

parts:
  IC1 = DIP - 28 pins [chip_label=AT28C256 package="DIP (Dual Inline) [THT]"]
  J1 = female pin header, 7 pins [form="♀ (female)"]
  J2 = female pin header, 8 pins [form="♀ (female)"]
  J3 = female pin header, 7 pins [form="♀ (female)"]
  IC2 = DIP - 28 pins [chip_label=AT28C256 package="DIP (Dual Inline) [THT]"]
  J4 = female pin header, 8 pins [form="♀ (female)"]
  IC7 = DIP - 16 pins [chip_label=74HCT138 package="DIP (Dual Inline) [THT]"]
  LED5 = LED - 5mm [color="Green (555nm)" package="5 mm [THT]"]
  LED6 = LED - 5mm [color="Green (555nm)" package="5 mm [THT]"]
  LED7 = LED - 5mm [color="Green (555nm)" package="5 mm [THT]"]
  LED8 = LED - 5mm [color="Green (555nm)" package="5 mm [THT]"]
  LED9 = LED - 5mm [color="Green (555nm)" package="5 mm [THT]"]
  LED10 = LED - 5mm [color="Green (555nm)" package="5 mm [THT]"]
  LED11 = LED - 5mm [color="Green (555nm)" package="5 mm [THT]"]
  LED12 = LED - 5mm [color="Green (555nm)" package="5 mm [THT]"]
  LED13 = LED - 5mm [color="Green (555nm)" package="5 mm [THT]"]
  LED14 = LED - 5mm [color="Green (555nm)" package="5 mm [THT]"]
  LED15 = LED - 5mm [color="Green (555nm)" package="5 mm [THT]"]
  LED16 = LED - 5mm [color="Green (555nm)" package="5 mm [THT]"]
  LED17 = LED - 5mm [color="Green (555nm)" package="5 mm [THT]"]
  J7 = female pin header, 8 pins [form="♀ (female)"]
  J8 = female pin header, 4 pins [form="♀ (female)"]
  LED25 = LED - 5mm [color="Yellow (585nm)" package="5 mm [THT]"]
  LED26 = LED - 5mm [color="Yellow (585nm)" package="5 mm [THT]"]
  LED27 = LED - 5mm [color="Yellow (585nm)" package="5 mm [THT]"]
  LED28 = LED - 5mm [color="Yellow (585nm)" package="5 mm [THT]"]
  LED29 = LED - 5mm [color="Yellow (585nm)" package="5 mm [THT]"]
  LED30 = LED - 5mm [color="Yellow (585nm)" package="5 mm [THT]"]
  LED31 = LED - 5mm [color="Yellow (585nm)" package="5 mm [THT]"]
  LED32 = LED - 5mm [color="Yellow (585nm)" package="5 mm [THT]"]
  LED33 = LED - 5mm [color="Yellow (585nm)" package="5 mm [THT]"]
  LED34 = LED - 5mm [color="Yellow (585nm)" package="5 mm [THT]"]
  LED35 = LED - 5mm [color="Yellow (585nm)" package="5 mm [THT]"]
  LED36 = LED - 5mm [color="Yellow (585nm)" package="5 mm [THT]"]
  LED37 = LED - 5mm [color="Yellow (585nm)" package="5 mm [THT]"]
  LED38 = LED - 5mm [color="Yellow (585nm)" package="5 mm [THT]"]
  LED39 = LED - 5mm [color="Yellow (585nm)" package="5 mm [THT]"]
  LED40 = LED - 5mm [color="Yellow (585nm)" package="5 mm [THT]"]
  LED41 = LED - 5mm [color="Yellow (585nm)" package="5 mm [THT]"]
  LED42 = LED - 5mm [color="Yellow (585nm)" package="5 mm [THT]"]
  LED43 = LED - 5mm [color="Yellow (585nm)" package="5 mm [THT]"]
  LED44 = LED - 5mm [color="Yellow (585nm)" package="5 mm [THT]"]
  LED45 = LED - 5mm [color="Yellow (585nm)" package="5 mm [THT]"]
  LED46 = LED - 5mm [color="Yellow (585nm)" package="5 mm [THT]"]
  LED47 = LED - 5mm [color="Yellow (585nm)" package="5 mm [THT]"]
  LED48 = LED - 5mm [color="Yellow (585nm)" package="5 mm [THT]"]
  LED49 = LED - 5mm [color="Yellow (585nm)" package="5 mm [THT]"]
  LED51 = LED - 5mm [color="Yellow (585nm)" package="5 mm [THT]"]
  LED53 = LED - 5mm [color="Yellow (585nm)" package="5 mm [THT]"]
  LED55 = LED - 5mm [color="Yellow (585nm)" package="5 mm [THT]"]
  LED56 = LED - 5mm [color="Yellow (585nm)" package="5 mm [THT]"]
  J13 = female pin header, 8 pins [form="♀ (female)"]
  J14 = female pin header, 8 pins [form="♀ (female)"]
  J15 = female pin header, 8 pins [form="♀ (female)"]
  R1 = Resistor [tolerance=±5% resistance=220 package=THT]
  R2 = Resistor [tolerance=±5% resistance=220 package=THT]
  R3 = Resistor [tolerance=±5% resistance=220 package=THT]
  R4 = Resistor [tolerance=±5% resistance=220 package=THT]
  R5 = Resistor [tolerance=±5% resistance=220 package=THT]
  R6 = Resistor [tolerance=±5% resistance=220 package=THT]
  R7 = Resistor [tolerance=±5% resistance=220 package=THT]
  R8 = Resistor [tolerance=±5% resistance=220 package=THT]
  R9 = Resistor [tolerance=±5% resistance=220 package=THT]
  R10 = Resistor [tolerance=±5% resistance=220 package=THT]
  R11 = Resistor [tolerance=±5% resistance=220 package=THT]
  R12 = Resistor [tolerance=±5% resistance=220 package=THT]
  R13 = Resistor [tolerance=±5% resistance=220 package=THT]
  R14 = Resistor [tolerance=±5% resistance=220 package=THT]
  R15 = Resistor [tolerance=±5% resistance=220 package=THT]
  R16 = Resistor [tolerance=±5% resistance=220 package=THT]
  R17 = Resistor [tolerance=±5% resistance=220 package=THT]
  R18 = Resistor [tolerance=±5% resistance=220 package=THT]
  R19 = Resistor [tolerance=±5% resistance=220 package=THT]
  R20 = Resistor [tolerance=±5% resistance=220 package=THT]
  R21 = Resistor [tolerance=±5% resistance=220 package=THT]
  R22 = Resistor [tolerance=±5% resistance=220 package=THT]
  R23 = Resistor [tolerance=±5% resistance=220 package=THT]
  R24 = Resistor [tolerance=±5% resistance=220 package=THT]
  R25 = Resistor [tolerance=±5% resistance=220 package=THT]
  R26 = Resistor [tolerance=±5% resistance=220 package=THT]
  R27 = Resistor [tolerance=±5% resistance=220 package=THT]
  R29 = Resistor [tolerance=±5% resistance=220 package=THT]
  R31 = Resistor [tolerance=±5% resistance=220 package=THT]
  LED58 = LED - 5mm [color="Yellow (585nm)" package="5 mm [THT]"]
  R32 = Resistor [tolerance=±5% resistance=220 package=THT]
  J16 = female pin header, 6 pins [form="♀ (female)"]
  IC10 = 74HCT377 [chip_label=74HCT377 package="DIP (Dual Inline) [THT]"]
  IC11 = DIP - 16 pins [chip_label=74HCT173 package="DIP (Dual Inline) [THT]"]
  IC12 = DIP - 14 pins [chip_label=74HCT04 package="DIP (Dual Inline) [THT]"]
  IC13 = DIP - 16 pins [chip_label=74HCT161 package="DIP (Dual Inline) [THT]"]
  LED59 = LED - 5mm [color="Green (555nm)" package="5 mm [THT]"]
  LED60 = LED - 5mm [color="Green (555nm)" package="5 mm [THT]"]
  LED61 = LED - 5mm [color="Green (555nm)" package="5 mm [THT]"]
  MASTER_RESET = female pin header, 2 pins [form="♀ (female)"]
  C/U_TIMER_RESET3 = female pin header, 2 pins [form="♀ (female)"]
  J17 = female pin header, 8 pins [form="♀ (female)"]
  J18 = female pin header, 8 pins [form="♀ (female)"]
  C/U_TIMER_RESET4 = female pin header, 2 pins [form="♀ (female)"]
  J23 = female pin header, 3 pins [form="♀ (female)"]
  C1 = Ceramic Capacitor [capacitance=100nF package="100 mil [THT, multilayer]"]
  C2 = Ceramic Capacitor [capacitance=100nF package="100 mil [THT, multilayer]"]
  J24 = female pin header, 3 pins [form="♀ (female)"]
  J25 = female pin header, 3 pins [form="♀ (female)"]
  J26 = female pin header, 4 pins [form="♀ (female)"]
  J27 = female pin header, 8 pins [form="♀ (female)"]
  R33 = Resistor [tolerance=±5% resistance=220 package=THT]
  R34 = Resistor [tolerance=±5% resistance=220 package=THT]
  R35 = Resistor [tolerance=±5% resistance=220 package=THT]
  R36 = Resistor [tolerance=±5% resistance=220 package=THT]
  R37 = Resistor [tolerance=±5% resistance=220 package=THT]
  R38 = Resistor [tolerance=±5% resistance=220 package=THT]
  R39 = Resistor [tolerance=±5% resistance=220 package=THT]
  R40 = Resistor [tolerance=±5% resistance=220 package=THT]
  R41 = Resistor [tolerance=±5% resistance=220 package=THT]
  R42 = Resistor [tolerance=±5% resistance=220 package=THT]
  R43 = Resistor [tolerance=±5% resistance=220 package=THT]
  R44 = Resistor [tolerance=±5% resistance=220 package=THT]
  LED62 = LED - 5mm [color="Green (555nm)" package="5 mm [THT]"]
  LED63 = LED - 5mm [color="Green (555nm)" package="5 mm [THT]"]
  LED64 = LED - 5mm [color="Green (555nm)" package="5 mm [THT]"]
  LED65 = LED - 5mm [color="Green (555nm)" package="5 mm [THT]"]
  LED66 = LED - 5mm [color="Green (555nm)" package="5 mm [THT]"]
  LED67 = LED - 5mm [color="Green (555nm)" package="5 mm [THT]"]
  LED68 = LED - 5mm [color="Green (555nm)" package="5 mm [THT]"]
  R45 = Resistor [tolerance=±5% resistance=220 package=THT]
  R46 = Resistor [tolerance=±5% resistance=220 package=THT]
  R47 = Resistor [tolerance=±5% resistance=220 package=THT]
  R48 = Resistor [tolerance=±5% resistance=220 package=THT]
  R49 = Resistor [tolerance=±5% resistance=220 package=THT]
  R51 = Resistor [tolerance=±5% resistance=220 package=THT]
  R52 = Resistor [tolerance=±5% resistance=220 package=THT]
  R53 = Resistor [tolerance=±5% resistance=220 package=THT]
  J28 = female pin header, 4 pins [form="♀ (female)"]
  J29 = female pin header, 4 pins [form="♀ (female)"]
  C3 = Ceramic Capacitor [capacitance=100nF package="100 mil [THT, multilayer]"]
  C4 = Ceramic Capacitor [capacitance=100nF package="100 mil [THT, multilayer]"]
  J30 = female pin header, 8 pins [form="♀ (female)"]
  J31 = female pin header, 8 pins [form="♀ (female)"]
  C5 = Ceramic Capacitor [capacitance=100nF package="100 mil [THT, multilayer]"]
  C6 = Ceramic Capacitor [capacitance=100nF package="100 mil [THT, multilayer]"]
  IC14 = DIP - 28 pins [chip_label=AT28C256 package="DIP (Dual Inline) [THT]"]
  J32 = female pin header, 7 pins [form="♀ (female)"]
  J33 = female pin header, 8 pins [form="♀ (female)"]
  J34 = female pin header, 7 pins [form="♀ (female)"]
  J35 = female pin header, 8 pins [form="♀ (female)"]
  IC15 = DIP - 28 pins [chip_label=AT28C256 package="DIP (Dual Inline) [THT]"]
  C7 = Ceramic Capacitor [capacitance=100nF package="100 mil [THT, multilayer]"]
  C8 = Ceramic Capacitor [capacitance=100nF package="100 mil [THT, multilayer]"]
  J36 = female pin header, 8 pins [form="♀ (female)"]
  J37 = female pin header, 8 pins [form="♀ (female)"]
  C9 = Ceramic Capacitor [capacitance=100nF package="100 mil [THT, multilayer]"]
  C10 = Ceramic Capacitor [capacitance=100nF package="100 mil [THT, multilayer]"]
  R54 = Resistor [tolerance=±5% resistance=220 package=THT]
  R55 = Resistor [tolerance=±5% resistance=220 package=THT]
  R56 = Resistor [tolerance=±5% resistance=220 package=THT]
  J38 = female pin header, 8 pins [form="♀ (female)"]
  J39 = female pin header, 8 pins [form="♀ (female)"]
  J40 = female pin header, 7 pins [form="♀ (female)"]
  J41 = female pin header, 7 pins [form="♀ (female)"]
  CONTROL_SIGNAL_0 = female pin header, 2 pins [form="♀ (female)"]
  CONTROL_SIGNAL_1 = female pin header, 2 pins [form="♀ (female)"]
  CONTROL_SIGNAL_2 = female pin header, 2 pins [form="♀ (female)"]
  CONTROL_SIGNAL_3 = female pin header, 2 pins [form="♀ (female)"]
  CONTROL_SIGNAL_4 = female pin header, 2 pins [form="♀ (female)"]
  CONTROL_SIGNAL_5 = female pin header, 2 pins [form="♀ (female)"]
  CONTROL_SIGNAL_6 = female pin header, 2 pins [form="♀ (female)"]
  CONTROL_SIGNAL_7 = female pin header, 2 pins [form="♀ (female)"]
  CONTROL_SIGNAL_8 = female pin header, 2 pins [form="♀ (female)"]
  CONTROL_SIGNAL_9 = female pin header, 2 pins [form="♀ (female)"]
  CONTROL_SIGNAL_10 = female pin header, 2 pins [form="♀ (female)"]
  CONTROL_SIGNAL_11 = female pin header, 2 pins [form="♀ (female)"]
  CONTROL_SIGNAL_12 = female pin header, 2 pins [form="♀ (female)"]
  CONTROL_SIGNAL_13 = female pin header, 2 pins [form="♀ (female)"]
  CONTROL_SIGNAL_14 = female pin header, 2 pins [form="♀ (female)"]
  CONTROL_SIGNAL_15 = female pin header, 2 pins [form="♀ (female)"]
  CONTROL_SIGNAL_16 = female pin header, 2 pins [form="♀ (female)"]
  CONTROL_SIGNAL_17 = female pin header, 2 pins [form="♀ (female)"]
  CONTROL_SIGNAL_18 = female pin header, 2 pins [form="♀ (female)"]
  CONTROL_SIGNAL_19 = female pin header, 2 pins [form="♀ (female)"]
  CONTROL_SIGNAL_20 = female pin header, 2 pins [form="♀ (female)"]
  CONTROL_SIGNAL_21 = female pin header, 2 pins [form="♀ (female)"]
  CONTROL_SIGNAL_23 = female pin header, 2 pins [form="♀ (female)"]
  CONTROL_SIGNAL_24 = female pin header, 2 pins [form="♀ (female)"]
  CONTROL_SIGNAL_25 = female pin header, 2 pins [form="♀ (female)"]
  CONTROL_SIGNAL_26 = female pin header, 2 pins [form="♀ (female)"]
  CONTROL_SIGNAL_28 = female pin header, 2 pins [form="♀ (female)"]
  CONTROL_SIGNAL_29 = female pin header, 2 pins [form="♀ (female)"]
  CONTROL_SIGNAL_30 = female pin header, 2 pins [form="♀ (female)"]
  CONTROL_SIGNAL_31 = female pin header, 2 pins [form="♀ (female)"]

nets:
  N1: IC1.A14, J1.pin1, J41.pin1
  N2: IC1.A12, J1.pin3, J41.pin3
  N3: IC1.A7, J30.pin1, J38.pin1
  N4: IC1.A6, J30.pin2, J38.pin2
  N5: IC1.A5, J30.pin3, J38.pin3
  N6: IC1.A4, J30.pin4, J38.pin4
  N7: IC1.A3, J30.pin5, J38.pin5
  N8: IC1.A2, J30.pin6, J38.pin6
  N9: IC1.A1, J30.pin7, J38.pin7
  N10: IC1.A0, J30.pin8, J38.pin8
  N11: IC1.I/O0, J2.pin8
  N12: IC1.I/O1, J2.pin7
  N13: IC1.I/O2, J2.pin6
  GND: IC1.GND, IC1._CE, IC1._OE, IC2.GND, IC2._CE, IC2._OE, C5.1, C6.0
  N14: IC1.I/O3, J2.pin5
  N15: IC1.I/O4, J2.pin4
  N16: IC1.I/O5, J2.pin3
  N17: IC1.I/O6, J2.pin2
  N18: IC1.I/O7, J2.pin1
  N19: IC1.A10, J1.pin5, J41.pin5
  N20: IC1.A11, J1.pin4, J41.pin4
  N21: IC1.A9, J1.pin6, J41.pin6
  N22: IC1.A8, J1.pin7, J41.pin7
  N23: IC1.A13, J1.pin2, J41.pin2
  VCC: IC1._WE, IC1.VCC, IC2._WE, IC2.VCC, C5.0, C6.1
  N24: J3.pin1, IC2.A14, J40.pin1
  N25: J3.pin2, IC2.A13, J40.pin2
  N26: J3.pin3, IC2.A12, J40.pin3
  N27: J3.pin4, IC2.A11, J40.pin4
  N28: J3.pin5, IC2.A10, J40.pin5
  N29: J3.pin6, IC2.A9, J40.pin6
  N30: J3.pin7, IC2.A8, J40.pin7
  N31: IC2.A7, J31.pin1, J39.pin1
  N32: IC2.A6, J31.pin2, J39.pin2
  N33: IC2.A5, J31.pin3, J39.pin3
  N34: IC2.A4, J31.pin4, J39.pin4
  N35: IC2.A3, J31.pin5, J39.pin5
  N36: IC2.A2, J31.pin6, J39.pin6
  N37: IC2.A1, J31.pin7, J39.pin7
  N38: IC2.A0, J31.pin8, J39.pin8
  N39: IC2.I/O0, J4.pin8
  N40: IC2.I/O1, J4.pin7
  N41: IC2.I/O2, J4.pin6
  N42: IC2.I/O3, J4.pin5
  N43: IC2.I/O4, J4.pin4
  N44: IC2.I/O5, J4.pin3
  N45: IC2.I/O6, J4.pin2
  N46: IC2.I/O7, J4.pin1
  N47: IC7.A, J24.pin1, J25.pin1
  N48: IC7.B, J24.pin2, J25.pin2
  N49: IC7.C, J24.pin3, J25.pin3
  N50: IC7._G2A, IC7._G2B, IC7.GND, R33.Pin_1, R34.Pin_1, R35.Pin_1, R36.Pin_1, R45.Pin_1, R46.Pin_1, R47.Pin_1, R48.Pin_1, R49.Pin_1, R51.Pin_1, R52.Pin_1, R53.Pin_1, C3.1, C4.0
  N51: IC7.G1, IC7.VCC, R37.Pin_1, R38.Pin_1, R39.Pin_1, R40.Pin_1, R41.Pin_1, R42.Pin_1, R43.Pin_1, R44.Pin_1, C3.0, C4.1
  N52: IC7.Y7, LED12.cathode
  N53: IC7.Y6, LED11.cathode
  N54: IC7.Y5, LED10.cathode
  N55: IC7.Y4, LED9.cathode
  N56: IC7.Y3, LED8.cathode
  N57: IC7.Y2, LED7.cathode
  N58: IC7.Y1, LED6.cathode
  N59: IC7.Y0, LED5.cathode
  N60: LED5.anode, R40.Pin_0
  N61: LED6.anode, R38.Pin_0
  N62: LED7.anode, R39.Pin_0
  N63: LED8.anode, R37.Pin_0
  N64: LED9.anode, R42.Pin_0
  N65: LED10.anode, R44.Pin_0
  N66: LED11.anode, R41.Pin_0
  N67: LED12.anode, R43.Pin_0
  N68: LED13.cathode, R33.Pin_0
  N69: LED13.anode, J8.pin1, J26.pin1
  N70: LED14.cathode, R34.Pin_0
  N71: LED14.anode, J8.pin2, J26.pin2
  N72: LED15.cathode, R35.Pin_0
  N73: LED15.anode, J8.pin3, J26.pin3
  N74: LED16.cathode, R36.Pin_0
  N75: LED16.anode, J8.pin4, J26.pin4
  N76: LED17.cathode, R48.Pin_0
  N77: LED17.anode, J7.pin1, J27.pin1
  N78: J7.pin2, J27.pin2, LED62.anode
  N79: J7.pin3, J27.pin3, LED63.anode
  N80: J7.pin4, J27.pin4, LED64.anode
  N81: J7.pin5, J27.pin5, LED65.anode
  N82: J7.pin6, J27.pin6, LED66.anode
  N83: J7.pin7, J27.pin7, LED68.anode
  N84: J7.pin8, J27.pin8, LED67.anode
  N85: LED25.cathode, R1.Pin_1
  N86: LED25.anode, J13.pin1, CONTROL_SIGNAL_18.pin1, CONTROL_SIGNAL_18.pin2
  N87: LED26.cathode, R2.Pin_1
  N88: LED26.anode, J13.pin2, CONTROL_SIGNAL_21.pin1, CONTROL_SIGNAL_21.pin2
  N89: LED27.cathode, R3.Pin_1
  N90: LED27.anode, J13.pin3, CONTROL_SIGNAL_16.pin1, CONTROL_SIGNAL_16.pin2
  N91: LED28.cathode, R4.Pin_1
  N92: LED28.anode, J13.pin4, CONTROL_SIGNAL_20.pin1, CONTROL_SIGNAL_20.pin2
  N93: LED29.cathode, R5.Pin_1
  N94: LED29.anode, J13.pin5, CONTROL_SIGNAL_23.pin1, CONTROL_SIGNAL_23.pin2
  N95: LED30.cathode, R7.Pin_1
  N96: LED30.anode, J13.pin7, CONTROL_SIGNAL_19.pin1, CONTROL_SIGNAL_19.pin2
  N97: LED31.cathode, R8.Pin_1
  N98: LED31.anode, J13.pin6, CONTROL_SIGNAL_31.pin1, CONTROL_SIGNAL_31.pin2
  N99: LED32.cathode, R6.Pin_1
  N100: LED32.anode, J13.pin8, CONTROL_SIGNAL_17.pin1, CONTROL_SIGNAL_17.pin2
  N101: LED33.cathode, R9.Pin_1
  N102: LED33.anode, J14.pin1, CONTROL_SIGNAL_25.pin1, CONTROL_SIGNAL_25.pin2
  N103: LED34.cathode, R14.Pin_1
  N104: LED34.anode, J14.pin7, CONTROL_SIGNAL_10.pin1, CONTROL_SIGNAL_10.pin2
  N105: LED35.cathode, R15.Pin_1
  N106: LED35.anode, J14.pin3, CONTROL_SIGNAL_29.pin1, CONTROL_SIGNAL_29.pin2
  N107: LED36.cathode, R12.Pin_1
  N108: LED36.anode, J14.pin8, CONTROL_SIGNAL_8.pin1, CONTROL_SIGNAL_8.pin2
  N109: LED37.cathode, R13.Pin_1
  N110: LED37.anode, J14.pin5, CONTROL_SIGNAL_30.pin1, CONTROL_SIGNAL_30.pin2
  N111: LED38.cathode, R16.Pin_1
  N112: LED38.anode, J14.pin6, CONTROL_SIGNAL_24.pin1, CONTROL_SIGNAL_24.pin2
  N113: LED39.cathode, R11.Pin_1
  N114: LED39.anode, J14.pin4, CONTROL_SIGNAL_28.pin1, CONTROL_SIGNAL_28.pin2
  N115: LED40.cathode, R10.Pin_1
  N116: LED40.anode, J14.pin2, CONTROL_SIGNAL_26.pin1, CONTROL_SIGNAL_26.pin2
  N117: LED41.cathode, R17.Pin_1
  N118: LED41.anode, J15.pin1, CONTROL_SIGNAL_15.pin1, CONTROL_SIGNAL_15.pin2
  N119: LED42.cathode, R22.Pin_1
  N120: LED42.anode, J15.pin7, CONTROL_SIGNAL_7.pin1, CONTROL_SIGNAL_7.pin2
  N121: LED43.cathode, R23.Pin_1
  N122: LED43.anode, J15.pin3, CONTROL_SIGNAL_11.pin1, CONTROL_SIGNAL_11.pin2
  N123: LED44.cathode, R20.Pin_1
  N124: LED44.anode, J15.pin8, CONTROL_SIGNAL_6.pin1, CONTROL_SIGNAL_6.pin2
  N125: LED45.cathode, R21.Pin_1
  N126: LED45.anode, J15.pin5, CONTROL_SIGNAL_12.pin1, CONTROL_SIGNAL_12.pin2
  N127: LED46.cathode, R24.Pin_1
  N128: LED46.anode, J15.pin6, CONTROL_SIGNAL_13.pin1, CONTROL_SIGNAL_13.pin2
  N129: LED47.cathode, R19.Pin_1
  N130: LED47.anode, J15.pin4, CONTROL_SIGNAL_14.pin1, CONTROL_SIGNAL_14.pin2
  N131: LED48.cathode, R18.Pin_1
  N132: LED48.anode, J15.pin2, CONTROL_SIGNAL_9.pin1, CONTROL_SIGNAL_9.pin2
  N133: LED49.cathode, R25.Pin_1
  N134: LED49.anode, J16.pin1, CONTROL_SIGNAL_5.pin1, CONTROL_SIGNAL_5.pin2
  N135: LED51.cathode, R31.Pin_1
  N136: LED51.anode, J16.pin3, CONTROL_SIGNAL_3.pin1, CONTROL_SIGNAL_3.pin2
  N137: LED53.cathode, R29.Pin_1
  N138: LED53.anode, J16.pin5, CONTROL_SIGNAL_1.pin1, CONTROL_SIGNAL_1.pin2
  N139: LED55.cathode, R27.Pin_1
  N140: LED55.anode, J16.pin4, CONTROL_SIGNAL_2.pin1, CONTROL_SIGNAL_2.pin2
  N141: LED56.cathode, R26.Pin_1
  N142: LED56.anode, J16.pin2, CONTROL_SIGNAL_4.pin1, CONTROL_SIGNAL_4.pin2
  N143: R1.Pin_0, R2.Pin_0, R3.Pin_0, R4.Pin_0, R5.Pin_0, R6.Pin_0, R7.Pin_0, R8.Pin_0, R9.Pin_0, R10.Pin_0, R11.Pin_0, R12.Pin_0, R13.Pin_0, R14.Pin_0, R15.Pin_0, R16.Pin_0, R17.Pin_0, R18.Pin_0, R19.Pin_0, R20.Pin_0, R21.Pin_0, R22.Pin_0, R23.Pin_0, R24.Pin_0, R25.Pin_0, R26.Pin_0, R27.Pin_0, R29.Pin_0, R31.Pin_0, R32.Pin_0, C9.0, C10.1
  N144: LED58.cathode, R32.Pin_1
  N145: LED58.anode, J16.pin6, CONTROL_SIGNAL_0.pin1, CONTROL_SIGNAL_0.pin2
  GND_2: IC10._CLKEN, IC10.GND, IC11._OE, IC11._OE2, IC11.GND, IC11._E1, IC11._E2, IC11.MR, IC12.2A, IC12.3A, IC12.GND, IC12.4A, IC12.5A, IC13.P0, IC13.P1, IC13.P2, IC13.P3, IC13.GND, C1.0, C2.1, R54.Pin_1, R55.Pin_1, R56.Pin_1
  N146: IC10.1Q, J18.pin8
  N147: IC10.1D, J17.pin8
  N148: IC10.2D, J17.pin7
  N149: IC10.2Q, J18.pin7
  N150: IC10.3Q, J18.pin6
  N151: IC10.3D, J17.pin6
  N152: IC10.4D, J17.pin5
  N153: IC10.4Q, J18.pin5
  N154: IC10.CLK, IC11.CP, IC13.CP, C/U_TIMER_RESET4.pin1, C/U_TIMER_RESET4.pin2
  N155: IC10.5Q, J18.pin4
  N156: IC10.5D, J17.pin4
  N157: IC10.6D, J17.pin3
  N158: IC10.6Q, J18.pin3
  N159: IC10.7Q, J18.pin2
  N160: IC10.7D, J17.pin2
  N161: IC10.8D, J17.pin1
  N162: IC10.8Q, J18.pin1
  VCC_2: IC10.VCC, IC11.VCC, IC12.VCC, IC13.PE, IC13.TE, IC13.VCC, C1.1, C2.0
  N163: IC11.Q0, J28.pin1
  N164: IC11.Q1, J28.pin2
  N165: IC11.Q2, J28.pin3
  N166: IC11.Q3, J28.pin4
  N167: IC11.D3, J29.pin4
  N168: IC11.D2, J29.pin3
  N169: IC11.D1, J29.pin2
  N170: IC11.D0, J29.pin1
  N171: IC12.1A, MASTER_RESET.pin1, MASTER_RESET.pin2
  N172: IC12.1Y, IC13._MR
  N173: IC12.6Y, IC13._SPE
  N174: IC12.6A, C/U_TIMER_RESET3.pin1, C/U_TIMER_RESET3.pin2
  N175: IC13.Q2, LED59.anode, J23.pin1
  N176: IC13.Q1, LED60.anode, J23.pin2
  N177: IC13.Q0, LED61.anode, J23.pin3
  N178: LED59.cathode, R56.Pin_0
  N179: LED60.cathode, R55.Pin_0
  N180: LED61.cathode, R54.Pin_0
  N181: LED62.cathode, R46.Pin_0
  N182: LED63.cathode, R47.Pin_0
  N183: LED64.cathode, R45.Pin_0
  N184: LED65.cathode, R52.Pin_0
  N185: LED66.cathode, R53.Pin_0
  N186: LED67.cathode, R49.Pin_0
  N187: LED68.cathode, R51.Pin_0
  N188: IC14.A14, J32.pin1
  N189: IC14.A12, J32.pin3
  N190: IC14.A7, J37.pin1
  N191: IC14.A6, J37.pin2
  N192: IC14.A5, J37.pin3
  N193: IC14.A4, J37.pin4
  N194: IC14.A3, J37.pin5
  N195: IC14.A2, J37.pin6
  N196: IC14.A1, J37.pin7
  N197: IC14.A0, J37.pin8
  N198: IC14.I/O0, J35.pin8
  N199: IC14.I/O1, J35.pin7
  N200: IC14.I/O2, J35.pin6
  GND_3: IC14.GND, IC14._CE, IC14._OE, IC15.GND, IC15._CE, IC15._OE, C7.0, C8.1
  N201: IC14.I/O3, J35.pin5
  N202: IC14.I/O4, J35.pin4
  N203: IC14.I/O5, J35.pin3
  N204: IC14.I/O6, J35.pin2
  N205: IC14.I/O7, J35.pin1
  N206: IC14.A10, J32.pin5
  N207: IC14.A11, J32.pin4
  N208: IC14.A9, J32.pin6
  N209: IC14.A8, J32.pin7
  N210: IC14.A13, J32.pin2
  VCC_3: IC14._WE, IC14.VCC, IC15._WE, IC15.VCC, C7.1, C8.0
  N211: J33.pin1, IC15.I/O7
  N212: J33.pin2, IC15.I/O6
  N213: J33.pin3, IC15.I/O5
  N214: J33.pin4, IC15.I/O4
  N215: J33.pin5, IC15.I/O3
  N216: J33.pin6, IC15.I/O2
  N217: J33.pin7, IC15.I/O1
  N218: J33.pin8, IC15.I/O0
  N219: J34.pin1, IC15.A14
  N220: J34.pin2, IC15.A13
  N221: J34.pin3, IC15.A12
  N222: J34.pin4, IC15.A11
  N223: J34.pin5, IC15.A10
  N224: J34.pin6, IC15.A9
  N225: J34.pin7, IC15.A8
  N226: IC15.A7, J36.pin1
  N227: IC15.A6, J36.pin2
  N228: IC15.A5, J36.pin3
  N229: IC15.A4, J36.pin4
  N230: IC15.A3, J36.pin5
  N231: IC15.A2, J36.pin6
  N232: IC15.A1, J36.pin7
  N233: IC15.A0, J36.pin8
  N234: C9.1, C10.0

notes:
  step_reset
  instruction_byte
  mirror_instruction_byte
  control_clock
  master_reset
  microcode_step
  mirror_flags
  flags
  microcode_step_and_mirror_flags
  control_signal_slice_2
  control_signal_slice_3
  control_signal_slice_0
  control_signal_slice_1

custom parts:
  DIP - 28 pins: 256kbit EEPROM
  DIP - 16 pins: 3 to 8 decoder
  74HCT377: Octal D-Type flip flops with clock enable 8 bit register
  DIP - 16 pins: 4 bit register
  DIP - 14 pins: Hex Inverter
  DIP - 16 pins: 4 bit synchronous counter with load and asynchronous clear
