# Fritzing sketch control_unit_add_IR (saved by Fritzing 0.9.3b)
breadboards: 9

parts:
  IC1 = DIP - 28 pins [chip_label=AT28C256 package="DIP (Dual Inline) [THT]"]
  J1 = female pin header, 7 pins [form="♀ (female)"]
  J2 = female pin header, 8 pins [form="♀ (female)"]
  J3 = female pin header, 7 pins [form="♀ (female)"]
  IC2 = DIP - 28 pins [chip_label=AT28C256 package="DIP (Dual Inline) [THT]"]
  J4 = female pin header, 8 pins [form="♀ (female)"]
  J5 = female pin header, 8 pins [form="♀ (female)"]
  IC3 = 74HCT377 [chip_label=74HCT377 package="DIP (Dual Inline) [THT]"]
  J6 = female pin header, 8 pins [form="♀ (female)"]
  IC4 = DIP - 16 pins [chip_label=74HCT173 package="DIP (Dual Inline) [THT]"]
  IC5 = DIP - 14 pins [chip_label=74HCT04 package="DIP (Dual Inline) [THT]"]
  IC6 = DIP - 16 pins [chip_label=74HCT161 package="DIP (Dual Inline) [THT]"]
  LED2 = LED - 5mm [color="Green (555nm)" package="5 mm [THT]"]
  LED3 = LED - 5mm [color="Green (555nm)" package="5 mm [THT]"]
  LED4 = LED - 5mm [color="Green (555nm)" package="5 mm [THT]"]
  RESET = female pin header, 2 pins [form="♀ (female)"]
  C/U_TIMER_RESET = female pin header, 2 pins [form="♀ (female)"]
  IC7 = DIP - 16 pins [chip_label=74HCT138 package="DIP (Dual Inline) [THT]"]
  C/U_TIMER_RESET1 = female pin header, 2 pins [form="♀ (female)"]
  LED5 = LED - 5mm [color="Green (555nm)" package="5 mm [THT]"]
  LED6 = LED - 5mm [color="Green (555nm)" package="5 mm [THT]"]
  LED7 = LED - 5mm [color="Green (555nm)" package="5 mm [THT]"]
  LED8 = LED - 5mm [color="Green (555nm)" package="5 mm [THT]"]
  LED9 = LED - 5mm [color="Green (555nm)" package="5 mm [THT]"]
  LED10 = LED - 5mm [color="Green (555nm)" package="5 mm [THT]"]
  LED11 = LED - 5mm [color="Green (555nm)" package="5 mm [THT]"]
  LED12 = LED - 5mm [color="Green (555nm)" package="5 mm [THT]"]
  LED13 = LED - 5mm [color="Green (555nm)" package="5 mm [THT]"]
  LED14 = LED - 5mm [color="Green (555nm)" package="5 mm [THT]"]
  LED15 = LED - 5mm [color="Green (555nm)" package="5 mm [THT]"]
  LED16 = LED - 5mm [color="Green (555nm)" package="5 mm [THT]"]
  LED17 = LED - 5mm [color="Green (555nm)" package="5 mm [THT]"]
  LED18 = LED - 5mm [color="Green (555nm)" package="5 mm [THT]"]
  LED19 = LED - 5mm [color="Green (555nm)" package="5 mm [THT]"]
  LED20 = LED - 5mm [color="Green (555nm)" package="5 mm [THT]"]
  LED21 = LED - 5mm [color="Green (555nm)" package="5 mm [THT]"]
  LED22 = LED - 5mm [color="Green (555nm)" package="5 mm [THT]"]
  LED23 = LED - 5mm [color="Green (555nm)" package="5 mm [THT]"]
  LED24 = LED - 5mm [color="Green (555nm)" package="5 mm [THT]"]
  J7 = female pin header, 8 pins [form="♀ (female)"]
  J8 = female pin header, 4 pins [form="♀ (female)"]
  IC8 = DIP - 28 pins [chip_label=AT28C256 package="DIP (Dual Inline) [THT]"]
  J9 = female pin header, 7 pins [form="♀ (female)"]
  J10 = female pin header, 7 pins [form="♀ (female)"]
  J11 = female pin header, 8 pins [form="♀ (female)"]
  J12 = female pin header, 8 pins [form="♀ (female)"]
  IC9 = DIP - 28 pins [chip_label=AT28C256 package="DIP (Dual Inline) [THT]"]
  LED25 = LED - 5mm [color="Yellow (585nm)" package="5 mm [THT]"]  # not connected
  LED26 = LED - 5mm [color="Yellow (585nm)" package="5 mm [THT]"]  # not connected
  LED27 = LED - 5mm [color="Yellow (585nm)" package="5 mm [THT]"]  # not connected
  LED28 = LED - 5mm [color="Yellow (585nm)" package="5 mm [THT]"]  # not connected
  LED29 = LED - 5mm [color="Yellow (585nm)" package="5 mm [THT]"]  # not connected
  LED30 = LED - 5mm [color="Yellow (585nm)" package="5 mm [THT]"]  # not connected
  LED31 = LED - 5mm [color="Yellow (585nm)" package="5 mm [THT]"]  # not connected
  LED32 = LED - 5mm [color="Yellow (585nm)" package="5 mm [THT]"]  # not connected
  LED33 = LED - 5mm [color="Yellow (585nm)" package="5 mm [THT]"]  # not connected
  LED34 = LED - 5mm [color="Yellow (585nm)" package="5 mm [THT]"]  # not connected
  LED35 = LED - 5mm [color="Yellow (585nm)" package="5 mm [THT]"]  # not connected
  LED36 = LED - 5mm [color="Yellow (585nm)" package="5 mm [THT]"]  # not connected
  LED37 = LED - 5mm [color="Yellow (585nm)" package="5 mm [THT]"]  # not connected
  LED38 = LED - 5mm [color="Yellow (585nm)" package="5 mm [THT]"]  # not connected
  LED39 = LED - 5mm [color="Yellow (585nm)" package="5 mm [THT]"]  # not connected
  LED40 = LED - 5mm [color="Yellow (585nm)" package="5 mm [THT]"]  # not connected
  LED41 = LED - 5mm [color="Yellow (585nm)" package="5 mm [THT]"]  # not connected
  LED42 = LED - 5mm [color="Yellow (585nm)" package="5 mm [THT]"]  # not connected
  LED43 = LED - 5mm [color="Yellow (585nm)" package="5 mm [THT]"]  # not connected
  LED44 = LED - 5mm [color="Yellow (585nm)" package="5 mm [THT]"]  # not connected
  LED45 = LED - 5mm [color="Yellow (585nm)" package="5 mm [THT]"]  # not connected
  LED46 = LED - 5mm [color="Yellow (585nm)" package="5 mm [THT]"]  # not connected
  LED47 = LED - 5mm [color="Yellow (585nm)" package="5 mm [THT]"]  # not connected
  LED48 = LED - 5mm [color="Yellow (585nm)" package="5 mm [THT]"]  # not connected
  LED49 = LED - 5mm [color="Yellow (585nm)" package="5 mm [THT]"]  # not connected
  LED51 = LED - 5mm [color="Yellow (585nm)" package="5 mm [THT]"]  # not connected
  LED53 = LED - 5mm [color="Yellow (585nm)" package="5 mm [THT]"]  # not connected
  LED55 = LED - 5mm [color="Yellow (585nm)" package="5 mm [THT]"]  # not connected
  LED56 = LED - 5mm [color="Yellow (585nm)" package="5 mm [THT]"]  # not connected
  J13 = female pin header, 8 pins [form="♀ (female)"]  # not connected
  J14 = female pin header, 8 pins [form="♀ (female)"]  # not connected
  J15 = female pin header, 8 pins [form="♀ (female)"]  # not connected
  J16 = female pin header, 5 pins [form="♀ (female)"]  # not connected
  R1 = Resistor [tolerance=±5% resistance=220 package=THT]
  R2 = Resistor [tolerance=±5% resistance=220 package=THT]
  R3 = Resistor [tolerance=±5% resistance=220 package=THT]
  R4 = Resistor [tolerance=±5% resistance=220 package=THT]
  R5 = Resistor [tolerance=±5% resistance=220 package=THT]
  R6 = Resistor [tolerance=±5% resistance=220 package=THT]
  R7 = Resistor [tolerance=±5% resistance=220 package=THT]
  R8 = Resistor [tolerance=±5% resistance=220 package=THT]
  R9 = Resistor [tolerance=±5% resistance=220 package=THT]
  R10 = Resistor [tolerance=±5% resistance=220 package=THT]
  R11 = Resistor [tolerance=±5% resistance=220 package=THT]
  R12 = Resistor [tolerance=±5% resistance=220 package=THT]
  R13 = Resistor [tolerance=±5% resistance=220 package=THT]
  R14 = Resistor [tolerance=±5% resistance=220 package=THT]
  R15 = Resistor [tolerance=±5% resistance=220 package=THT]
  R16 = Resistor [tolerance=±5% resistance=220 package=THT]
  R17 = Resistor [tolerance=±5% resistance=220 package=THT]
  R18 = Resistor [tolerance=±5% resistance=220 package=THT]
  R19 = Resistor [tolerance=±5% resistance=220 package=THT]
  R20 = Resistor [tolerance=±5% resistance=220 package=THT]
  R21 = Resistor [tolerance=±5% resistance=220 package=THT]
  R22 = Resistor [tolerance=±5% resistance=220 package=THT]
  R23 = Resistor [tolerance=±5% resistance=220 package=THT]
  R24 = Resistor [tolerance=±5% resistance=220 package=THT]
  R25 = Resistor [tolerance=±5% resistance=220 package=THT]
  R26 = Resistor [tolerance=±5% resistance=220 package=THT]
  R27 = Resistor [tolerance=±5% resistance=220 package=THT]
  R29 = Resistor [tolerance=±5% resistance=220 package=THT]
  R31 = Resistor [tolerance=±5% resistance=220 package=THT]
  IC11 = DIP - 16 pins [chip_label=74HCT138 package="DIP (Dual Inline) [THT]"]
  IC13 = DIP - 16 pins [chip_label=74HCT173 package="DIP (Dual Inline) [THT]"]
  IC14 = DIP - 14 pins [chip_label=74HCT04 package="DIP (Dual Inline) [THT]"]
  IC15 = DIP - 16 pins [chip_label=74HCT161 package="DIP (Dual Inline) [THT]"]
  LED60 = LED - 5mm [color="Green (555nm)" package="5 mm [THT]"]
  LED61 = LED - 5mm [color="Green (555nm)" package="5 mm [THT]"]
  LED65 = LED - 5mm [color="Green (555nm)" package="5 mm [THT]"]
  LED66 = LED - 5mm [color="Green (555nm)" package="5 mm [THT]"]
  LED67 = LED - 5mm [color="Green (555nm)" package="5 mm [THT]"]
  LED71 = LED - 5mm [color="Green (555nm)" package="5 mm [THT]"]
  LED72 = LED - 5mm [color="Green (555nm)" package="5 mm [THT]"]
  LED73 = LED - 5mm [color="Green (555nm)" package="5 mm [THT]"]
  LED77 = LED - 5mm [color="Green (555nm)" package="5 mm [THT]"]
  LED78 = LED - 5mm [color="Green (555nm)" package="5 mm [THT]"]
  LED79 = LED - 5mm [color="Green (555nm)" package="5 mm [THT]"]
  RESET1 = female pin header, 2 pins [form="♀ (female)"]
  C/U_TIMER_RESET2 = female pin header, 2 pins [form="♀ (female)"]
  C/U_TIMER_RESET3 = female pin header, 2 pins [form="♀ (female)"]
  IC16 = DIP - 20 pins [chip_label=74HCT574 package="DIP (Dual Inline) [THT]"]
  LED80 = LED - 5mm [color="Green (555nm)" package="5 mm [THT]"]
  LED81 = LED - 5mm [color="Green (555nm)" package="5 mm [THT]"]
  LED82 = LED - 5mm [color="Green (555nm)" package="5 mm [THT]"]
  LED83 = LED - 5mm [color="Green (555nm)" package="5 mm [THT]"]
  LED84 = LED - 5mm [color="Green (555nm)" package="5 mm [THT]"]
  LED85 = LED - 5mm [color="Green (555nm)" package="5 mm [THT]"]
  LED86 = LED - 5mm [color="Green (555nm)" package="5 mm [THT]"]
  LED87 = LED - 5mm [color="Green (555nm)" package="5 mm [THT]"]
  IC17 = DIP - 16 pins [chip_label=74HCT173 package="DIP (Dual Inline) [THT]"]
  IC18 = DIP - 14 pins [chip_label=74HCT04 package="DIP (Dual Inline) [THT]"]
  IC19 = DIP - 16 pins [chip_label=74HCT161 package="DIP (Dual Inline) [THT]"]
  LED88 = LED - 5mm [color="Green (555nm)" package="5 mm [THT]"]
  LED89 = LED - 5mm [color="Green (555nm)" package="5 mm [THT]"]
  LED90 = LED - 5mm [color="Green (555nm)" package="5 mm [THT]"]
  RESET2 = female pin header, 2 pins [form="♀ (female)"]
  C/U_TIMER_RESET4 = female pin header, 2 pins [form="♀ (female)"]
  C/U_TIMER_RESET5 = female pin header, 2 pins [form="♀ (female)"]
  IC20 = DIP - 16 pins [chip_label=74HCT173 package="DIP (Dual Inline) [THT]"]
  IC21 = DIP - 14 pins [chip_label=74HCT04 package="DIP (Dual Inline) [THT]"]
  IC22 = DIP - 16 pins [chip_label=74HCT161 package="DIP (Dual Inline) [THT]"]
  LED91 = LED - 5mm [color="Green (555nm)" package="5 mm [THT]"]
  LED92 = LED - 5mm [color="Green (555nm)" package="5 mm [THT]"]
  LED93 = LED - 5mm [color="Green (555nm)" package="5 mm [THT]"]
  RESET3 = female pin header, 2 pins [form="♀ (female)"]
  C/U_TIMER_RESET6 = female pin header, 2 pins [form="♀ (female)"]
  C/U_TIMER_RESET7 = female pin header, 2 pins [form="♀ (female)"]
  LED102 = LED - 5mm [color="Green (555nm)" package="5 mm [THT]"]
  LED103 = LED - 5mm [color="Green (555nm)" package="5 mm [THT]"]
  LED104 = LED - 5mm [color="Green (555nm)" package="5 mm [THT]"]
  LED105 = LED - 5mm [color="Green (555nm)" package="5 mm [THT]"]
  J17 = female pin header, 4 pins [form="♀ (female)"]
  IC24 = DIP - 14 pins [chip_label=74HCT08 package="DIP (Dual Inline) [THT]"]
  LED106 = LED - 5mm [color="Green (555nm)" package="5 mm [THT]"]
  LED107 = LED - 5mm [color="Green (555nm)" package="5 mm [THT]"]
  LED108 = LED - 5mm [color="Green (555nm)" package="5 mm [THT]"]
  LED109 = LED - 5mm [color="Green (555nm)" package="5 mm [THT]"]
  LED110 = LED - 5mm [color="Green (555nm)" package="5 mm [THT]"]
  LED111 = LED - 5mm [color="Green (555nm)" package="5 mm [THT]"]
  LED112 = LED - 5mm [color="Green (555nm)" package="5 mm [THT]"]
  LED113 = LED - 5mm [color="Green (555nm)" package="5 mm [THT]"]
  IC25 = DIP - 20 pins [chip_label=74HCT574 package="DIP (Dual Inline) [THT]"]
  J18 = female pin header, 4 pins [form="♀ (female)"]  # not connected
  J19 = female pin header, 4 pins [form="♀ (female)"]

nets:
  N1: IC1.A14, J1.pin1
  N2: IC1.A12, J1.pin3
  N3: IC1.I/O0, J2.pin8
  N4: IC1.I/O1, J2.pin7
  N5: IC1.I/O2, J2.pin6
  GND: IC1.GND, IC2.GND
  N6: IC1.I/O3, J2.pin5
  N7: IC1.I/O4, J2.pin4
  N8: IC1.I/O5, J2.pin3
  N9: IC1.I/O6, J2.pin2
  N10: IC1.I/O7, J2.pin1
  N11: IC1._CE, IC1._OE, IC2._CE, IC2._OE
  N12: IC1.A10, J1.pin5
  N13: IC1.A11, J1.pin4
  N14: IC1.A9, J1.pin6
  N15: IC1.A8, J1.pin7
  N16: IC1.A13, J1.pin2
  VCC: IC1._WE, IC1.VCC, IC2._WE, IC2.VCC
  N17: J3.pin1, IC2.A14
  N18: J3.pin2, IC2.A13
  N19: J3.pin3, IC2.A12
  N20: J3.pin4, IC2.A11
  N21: J3.pin5, IC2.A10
  N22: J3.pin6, IC2.A9
  N23: J3.pin7, IC2.A8
  N24: IC2.I/O0, J4.pin8
  N25: IC2.I/O1, J4.pin7
  N26: IC2.I/O2, J4.pin6
  N27: IC2.I/O3, J4.pin5
  N28: IC2.I/O4, J4.pin4
  N29: IC2.I/O5, J4.pin3
  N30: IC2.I/O6, J4.pin2
  N31: IC2.I/O7, J4.pin1
  N32: J5.pin1, IC3.8Q
  N33: J5.pin2, IC3.7Q
  N34: J5.pin3, IC3.6Q
  N35: J5.pin4, IC3.5Q
  N36: J5.pin5, IC3.4Q
  N37: J5.pin6, IC3.3Q
  N38: J5.pin7, IC3.2Q
  N39: J5.pin8, IC3.1Q
  GND_2: IC3._CLKEN, IC3.GND, IC4._OE, IC4._OE2, IC4.GND, IC5.2A, IC5.3A, IC5.GND, IC6.P0, IC6.P1, IC6.P2, IC6.P3, IC6.GND
  N40: IC3.1D, J6.pin8
  N41: IC3.2D, J6.pin7
  N42: IC3.3D, J6.pin6
  N43: IC3.4D, J6.pin5
  N44: IC3.CLK, IC4.CP, IC5.1Y, IC6.CP
  N45: IC3.5D, J6.pin4
  N46: IC3.6D, J6.pin3
  N47: IC3.7D, J6.pin2
  N48: IC3.8D, J6.pin1
  VCC_2: IC3.VCC, IC4.VCC, IC5.VCC, IC6.TE, IC6.VCC
  N49: IC4._E1, IC4._E2, IC4.MR, IC5.4A, IC5.5A
  N50: IC5.1A, C/U_TIMER_RESET1.pin1, C/U_TIMER_RESET1.pin2
  N51: IC5.6Y, IC6._SPE
  N52: IC5.6A, C/U_TIMER_RESET.pin1, C/U_TIMER_RESET.pin2
  N53: IC6._MR, RESET.pin1, RESET.pin2
  N54: IC6.Q2, LED2.anode
  N55: IC6.Q1, LED3.anode
  N56: IC6.Q0, LED4.anode
  N57: IC7._G2A, IC7._G2B, IC7.GND
  N58: IC7.Y7, LED12.cathode
  N59: IC7.Y6, LED11.cathode
  N60: IC7.Y5, LED10.cathode
  N61: IC7.Y4, LED9.cathode
  N62: IC7.Y3, LED8.cathode
  N63: IC7.Y2, LED7.cathode
  N64: IC7.Y1, LED6.cathode
  N65: IC7.Y0, LED5.cathode
  N66: LED13.cathode, J8.pin4
  N67: LED14.cathode, J8.pin3
  N68: LED15.cathode, J8.pin2
  N69: LED16.cathode, J8.pin1
  N70: LED17.cathode, J7.pin1
  N71: LED18.cathode, J7.pin5
  N72: LED19.cathode, J7.pin2
  N73: LED20.cathode, J7.pin6
  N74: LED21.cathode, J7.pin7
  N75: LED22.cathode, J7.pin3
  N76: LED23.cathode, J7.pin4
  N77: LED24.cathode, J7.pin8
  N78: IC8.A14, J10.pin1
  N79: IC8.A12, J10.pin3
  N80: IC8.I/O0, J12.pin8
  N81: IC8.I/O1, J12.pin7
  N82: IC8.I/O2, J12.pin6
  GND_3: IC8.GND, IC9.GND
  N83: IC8.I/O3, J12.pin5
  N84: IC8.I/O4, J12.pin4
  N85: IC8.I/O5, J12.pin3
  N86: IC8.I/O6, J12.pin2
  N87: IC8.I/O7, J12.pin1
  N88: IC8._CE, IC8._OE, IC9._CE, IC9._OE
  N89: IC8.A10, J10.pin5
  N90: IC8.A11, J10.pin4
  N91: IC8.A9, J10.pin6
  N92: IC8.A8, J10.pin7
  N93: IC8.A13, J10.pin2
  VCC_3: IC8._WE, IC8.VCC, IC9._WE, IC9.VCC
  N94: J9.pin1, IC9.A14
  N95: J9.pin2, IC9.A13
  N96: J9.pin3, IC9.A12
  N97: J9.pin4, IC9.A11
  N98: J9.pin5, IC9.A10
  N99: J9.pin6, IC9.A9
  N100: J9.pin7, IC9.A8
  N101: J11.pin1, IC9.I/O7
  N102: J11.pin2, IC9.I/O6
  N103: J11.pin3, IC9.I/O5
  N104: J11.pin4, IC9.I/O4
  N105: J11.pin5, IC9.I/O3
  N106: J11.pin6, IC9.I/O2
  N107: J11.pin7, IC9.I/O1
  N108: J11.pin8, IC9.I/O0
  N109: R1.Pin_0, R2.Pin_0, R3.Pin_0, R4.Pin_0, R5.Pin_0, R6.Pin_0, R7.Pin_0, R8.Pin_0, R9.Pin_0, R10.Pin_0, R11.Pin_0, R12.Pin_0, R13.Pin_0, R14.Pin_0, R15.Pin_0, R16.Pin_0, R17.Pin_0, R18.Pin_0, R19.Pin_0, R20.Pin_0, R21.Pin_0, R22.Pin_0, R23.Pin_0, R24.Pin_0, R25.Pin_0, R26.Pin_0, R27.Pin_0, R29.Pin_0, R31.Pin_0
  GND_4: IC11._G2A, IC11._G2B, IC11.GND, IC24.GND
  N110: IC11.G1, IC25.VCC
  N111: IC11.Y7, LED77.cathode
  N112: IC11.Y6, LED71.cathode
  N113: IC11.Y5, LED65.cathode
  N114: IC11.Y4, LED60.cathode
  N115: IC11.Y3, LED78.cathode
  N116: IC11.Y2, LED72.cathode
  N117: IC11.Y1, LED66.cathode
  N118: IC11.Y0, LED61.cathode
  VCC_4: IC11.VCC, IC24.VCC
  GND_5: IC13._OE, IC13._OE2, IC13.GND, IC14.2A, IC14.3A, IC14.GND, IC15.P0, IC15.P1, IC15.P2, IC15.P3, IC15.GND
  N119: IC13.CP, IC14.1Y, IC15.CP
  N120: IC13._E1, IC13._E2, IC13.MR, IC14.4A, IC14.5A
  VCC_5: IC13.VCC, IC14.VCC, IC15.TE, IC15.VCC
  N121: IC14.1A, C/U_TIMER_RESET2.pin1, C/U_TIMER_RESET2.pin2
  N122: IC14.6Y, IC15._SPE
  N123: IC14.6A, C/U_TIMER_RESET3.pin1, C/U_TIMER_RESET3.pin2
  N124: IC15._MR, RESET1.pin1, RESET1.pin2
  N125: IC15.Q2, LED67.anode
  N126: IC15.Q1, LED73.anode
  N127: IC15.Q0, LED79.anode
  N128: IC16._OE, IC16.GND, IC20._E2, IC21.4A
  N129: IC16.8Q, LED81.anode
  N130: IC16.7Q, LED83.anode
  N131: IC16.6Q, LED85.anode
  N132: IC16.5Q, LED87.anode
  N133: IC16.4Q, LED80.anode
  N134: IC16.3Q, LED82.anode
  N135: IC16.2Q, LED84.anode
  N136: IC16.1Q, LED86.anode
  N137: IC16.VCC, IC22.PE
  GND_6: IC17._OE, IC17._OE2, IC17.GND, IC18.2A, IC18.3A, IC18.GND, IC19.P0, IC19.P1, IC19.P2, IC19.P3, IC19.GND
  N138: IC17.CP, IC18.1Y, IC19.CP
  N139: IC17._E1, IC17._E2, IC17.MR, IC18.4A, IC18.5A
  VCC_6: IC17.VCC, IC18.VCC, IC19.TE, IC19.VCC
  N140: IC18.1A, C/U_TIMER_RESET4.pin1, C/U_TIMER_RESET4.pin2
  N141: IC18.6Y, IC19._SPE
  N142: IC18.6A, C/U_TIMER_RESET5.pin1, C/U_TIMER_RESET5.pin2
  N143: IC19._MR, RESET2.pin1, RESET2.pin2
  N144: IC19.Q2, LED88.anode
  N145: IC19.Q1, LED89.anode
  N146: IC19.Q0, LED90.anode
  GND_7: IC20._OE, IC21.2A, IC21.3A, IC21.GND, IC22.P0, IC22.P1, IC22.P2, IC22.GND
  N147: IC20.Q0, J19.pin1
  N148: IC20.Q1, J19.pin2
  N149: IC20.Q2, J19.pin3
  N150: IC20.Q3, J19.pin4
  N151: IC20.CP, IC21.1Y, IC22.CP
  VCC_7: IC20.VCC, IC21.VCC
  N152: IC21.1A, C/U_TIMER_RESET6.pin1, C/U_TIMER_RESET6.pin2, IC24.4B
  N153: IC21.6Y, IC22._SPE
  N154: IC21.6A, C/U_TIMER_RESET7.pin1, C/U_TIMER_RESET7.pin2
  N155: IC22._MR, RESET3.pin1, RESET3.pin2
  N156: IC22.Q2, LED91.anode
  N157: IC22.Q1, LED92.anode
  N158: IC22.Q0, LED93.anode
  N159: LED102.cathode, J17.pin4
  N160: LED103.cathode, J17.pin3
  N161: LED104.cathode, J17.pin2
  N162: LED105.cathode, J17.pin1
  N163: IC24.3A, IC24.3B, IC25._OE, IC25.GND
  N164: LED106.anode, IC25.4Q
  N165: LED107.anode, IC25.8Q
  N166: LED108.anode, IC25.3Q
  N167: LED109.anode, IC25.7Q
  N168: LED110.anode, IC25.2Q
  N169: LED111.anode, IC25.6Q
  N170: LED112.anode, IC25.1Q
  N171: LED113.anode, IC25.5Q

custom parts:
  DIP - 28 pins: 256kbit EEPROM
  74HCT377: Octal D-Type flip flops with clock enable 8 bit register
  DIP - 16 pins: 4 bit register
  DIP - 14 pins: Hex Inverter
  DIP - 16 pins: 4 bit synchronous counter with load and asynchronous clear
  DIP - 16 pins: 3 to 8 decoder
  DIP - 20 pins: 8 bit register, no clock enable, bus aligned pins
  DIP - 14 pins: Quad AND
