# Fritzing sketch debounced-debug-inputs (saved by Fritzing 0.9.3b)
breadboards: 1

parts:
  S1 = Pushbutton [package="[THT]"]
  IC1 = DIP - 14 pins [chip_label=74HCT14 package="DIP (Dual Inline) [THT]"]
  J1 = female pin header, 2 pins [form="♀ (female)"]
  R1 = Resistor [tolerance=±5% resistance=220 package=THT]
  LED1 = LED - 5mm [color="Red (633nm)" package="5 mm [THT]"]
  S2 = Pushbutton [package="[THT]"]
  J2 = female pin header, 2 pins [form="♀ (female)"]
  R2 = Resistor [tolerance=±5% resistance=220 package=THT]
  LED2 = LED - 5mm [color="Red (633nm)" package="5 mm [THT]"]
  S3 = Pushbutton [package="[THT]"]
  J3 = female pin header, 2 pins [form="♀ (female)"]
  R3 = Resistor [tolerance=±5% resistance=220 package=THT]
  LED3 = LED - 5mm [color="Red (633nm)" package="5 mm [THT]"]
  S4 = Pushbutton [package="[THT]"]
  J4 = female pin header, 2 pins [form="♀ (female)"]
  R4 = Resistor [tolerance=±5% resistance=220 package=THT]
  LED4 = LED - 5mm [color="Red (633nm)" package="5 mm [THT]"]
  S5 = Pushbutton [package="[THT]"]
  J5 = female pin header, 2 pins [form="♀ (female)"]
  R5 = Resistor [tolerance=±5% resistance=220 package=THT]
  LED5 = LED - 5mm [color="Red (633nm)" package="5 mm [THT]"]
  S6 = Pushbutton [package="[THT]"]
  J6 = female pin header, 2 pins [form="♀ (female)"]
  R6 = Resistor [tolerance=±5% resistance=220 package=THT]
  LED6 = LED - 5mm [color="Red (633nm)" package="5 mm [THT]"]
  C1 = Ceramic Capacitor [capacitance=100nF package="100 mil [THT, multilayer]"]
  R7 = Resistor [tolerance=±5% resistance=220 package=THT]  # not connected
  C2 = Ceramic Capacitor [capacitance=100nF package="100 mil [THT, multilayer]"]
  C3 = Ceramic Capacitor [capacitance=100nF package="100 mil [THT, multilayer]"]
  R8 = Resistor [tolerance=±5% resistance=220 package=THT]
  R12 = Resistor [tolerance=±5% resistance=220 package=THT]
  S7 = Pushbutton [package="[THT]"]
  J7 = female pin header, 2 pins [form="♀ (female)"]
  R13 = Resistor [tolerance=±5% resistance=220 package=THT]
  LED7 = LED - 5mm [color="Red (633nm)" package="5 mm [THT]"]
  S8 = Pushbutton [package="[THT]"]
  J8 = female pin header, 2 pins [form="♀ (female)"]
  R14 = Resistor [tolerance=±5% resistance=220 package=THT]
  LED8 = LED - 5mm [color="Red (633nm)" package="5 mm [THT]"]
  IC2 = DIP - 14 pins [chip_label=74HCT14 package="DIP (Dual Inline) [THT]"]
  C4 = Ceramic Capacitor [capacitance=100nF package="100 mil [THT, multilayer]"]
  C5 = Ceramic Capacitor [capacitance=100nF package="100 mil [THT, multilayer]"]

nets:
  N1: S1.Pin_1, S1.Pin_2, LED1.anode, C1.1, C2.1, C3.1, C4.1, C5.1
  N2: S1.Pin_3, S1.Pin_4
  N3: IC1.1A, C1.0, R12.Pin_1
  N4: IC1.2A, C2.0
  N5: IC1.3A, C3.0
  N6: J1.pin1, J1.pin2
  N7: R1.Pin_0, LED1.cathode
  N8: R1.Pin_1, R2.Pin_1, R3.Pin_1, R4.Pin_1, R5.Pin_1, R6.Pin_1, R13.Pin_1
  N9: S2.Pin_1, S2.Pin_2, LED2.anode
  N10: S2.Pin_3, S2.Pin_4
  N11: J2.pin1, J2.pin2
  N12: R2.Pin_0, LED2.cathode
  N13: S3.Pin_1, S3.Pin_2, LED3.anode
  N14: S3.Pin_3, S3.Pin_4
  N15: J3.pin1, J3.pin2
  N16: R3.Pin_0, LED3.cathode
  N17: S4.Pin_1, S4.Pin_2, LED4.anode
  N18: S4.Pin_3, S4.Pin_4
  N19: J4.pin1, J4.pin2
  N20: R4.Pin_0, LED4.cathode
  N21: S5.Pin_1, S5.Pin_2, LED5.anode
  N22: S5.Pin_3, S5.Pin_4
  N23: J5.pin1, J5.pin2
  N24: R5.Pin_0, LED5.cathode
  N25: S6.Pin_1, S6.Pin_2, LED6.anode
  N26: S6.Pin_3, S6.Pin_4
  N27: J6.pin1, J6.pin2
  N28: R6.Pin_0, LED6.cathode
  N29: R8.Pin_0, R12.Pin_0
  N30: S7.Pin_1, S7.Pin_2, LED7.anode
  N31: S7.Pin_3, S7.Pin_4
  N32: J7.pin1, J7.pin2
  N33: R13.Pin_0, LED7.cathode
  N34: S8.Pin_1, S8.Pin_2, LED8.anode
  N35: S8.Pin_3, S8.Pin_4
  N36: J8.pin1, J8.pin2
  N37: R14.Pin_0, LED8.cathode
  N38: IC2.1A, C5.0
  N39: IC2.2A, C4.0

custom parts:
  DIP - 14 pins: Hex Schmitt trigger inverters
