# Fritzing sketch decimal_display (saved by Fritzing 0.9.3b)
breadboards: 1

parts:
  U1 = 555 Timer [package="DIP8 [THT]"]
  IC1 = DIP - 28 pins [chip_label=AT28C256 package="DIP (Dual Inline) [THT]"]
  IC2 = DIP - 16 pins [chip_label=74HCT109 package="DIP (Dual Inline) [THT]"]
  IC3 = IC, DIP package, 16 pins [chip_label=74HCT139]
  C3 = Ceramic Capacitor [capacitance=100nF package="100 mil [THT, multilayer]"]
  R3 = Resistor [tolerance=±5% resistance=220 package=THT]
  R4 = Resistor [tolerance=±5% resistance=220 package=THT]
  C4 = Ceramic Capacitor [capacitance=100nF package="100 mil [THT, multilayer]"]
  S1 = Pushbutton [package="[THT]"]
  S2 = Pushbutton [package="[THT]"]
  5641AH1 = 5641AH [chip_label=5641AH package="DIP (Dual Inline) [THT]"]

nets:
  GND: U1.Ground, IC1.A14, IC1.A12, IC1.GND, IC2._1K, IC2.GND, IC3.pin2, IC3.pin3, IC3.pin8, C4.0, S2.Pin_1, S2.Pin_2
  N1: U1.Trigger, U1.Threshold, R3.Pin_0, C4.1
  N2: U1.Output, IC2.1CP
  N3: U1.Reset, IC2._1R, IC2.1J, IC2._1S, IC3.pin1, S2.Pin_3, S2.Pin_4
  N4: U1.Control_Voltage, C3.0
  N5: U1.Discharge, R3.Pin_1, R4.Pin_0
  VCC: U1.Vcc_Supply_Voltage, IC1._WE, IC1.VCC, IC2._2S, IC2.2J, IC2._2R, IC2.VCC, IC3.pin16, R4.Pin_1, S1.Pin_1, S1.Pin_2
  N6: IC1.I/O0, 5641AH1.A
  N7: IC1.I/O1, 5641AH1.B
  N8: IC1.I/O2, 5641AH1.C
  N9: IC1.I/O3, 5641AH1.D
  N10: IC1.I/O4, 5641AH1.E
  N11: IC1.I/O5, 5641AH1.F
  N12: IC1.I/O6, 5641AH1.G
  N13: IC1._CE, IC1._OE, IC1.A13, IC2._2K, IC3.pin15, C3.1, S1.Pin_3, S1.Pin_4
  N14: IC1.A9, IC2.1Q, IC3.pin13
  N15: IC1.A8, IC2.2Q, IC3.pin14
  N16: IC2._1Q, IC2.2CP
  N17: IC3.pin9, 5641AH1.DIG1
  N18: IC3.pin10, 5641AH1.DIG2
  N19: IC3.pin11, 5641AH1.DIG3
  N20: IC3.pin12, 5641AH1.DIG4

custom parts:
  DIP - 28 pins: 256kbit EEPROM
  DIP - 16 pins: Dual JK flip flop with set and reset, positive edge trigger
  5641AH: 4 number, common cathode, 7 seg display
