# Fritzing sketch eeprom_programmer (saved by Fritzing 0.9.3b)
breadboards: 1

parts:
  Part1 = Arduino Mega 2560 (Rev3)
  IC1 = DIP - 28 pins [chip_label=AT28C256 package="DIP (Dual Inline) [THT]"]
  R1 = Resistor [tolerance=±5% resistance=10k package=THT]
  R2 = Resistor [tolerance=±5% resistance=10k package=THT]
  R3 = Resistor [tolerance=±5% resistance=2k package=THT]
  R4 = Resistor [tolerance=±5% resistance=2k package=THT]
  R5 = Resistor [tolerance=±5% resistance=2k package=THT]
  R6 = Resistor [tolerance=±5% resistance=2k package=THT]
  LED1 = LED - 3mm [color="Green (555nm)" package="3 mm [THT]"]
  LED2 = LED - 3mm [color="Red (633nm)" package="3 mm [THT]"]
  LED3 = LED - 3mm [color="Red (633nm)" package="3 mm [THT]"]
  LED4 = LED - 3mm [color="Red (633nm)" package="3 mm [THT]"]
  LED5 = LED - 3mm [color="Red (633nm)" package="3 mm [THT]"]
  LED6 = LED - 3mm [color="Green (555nm)" package="3 mm [THT]"]
  S2 = Pushbutton [package="[THT]"]  # not connected
  S3 = Pushbutton [package="[THT]"]  # not connected
  S4 = Pushbutton [package="[THT]"]  # not connected
  S5 = Pushbutton [package="[THT]"]
  S6 = Pushbutton [package="[THT]"]
  S7 = Pushbutton [package="[THT]"]

nets:
  N1: Part1.A8, IC1.A4
  N2: Part1.A9, IC1.A3
  N3: Part1.A10, IC1.A2
  N4: Part1.A11, IC1.A1
  N5: Part1.A12, IC1.A0
  N6: Part1.A13, IC1.I/O0
  N7: Part1.A14, IC1.I/O1
  N8: Part1.A15, IC1.I/O2
  N9: Part1.A3, IC1.A14
  N10: Part1.A4, IC1.A12
  N11: Part1.A5, IC1.A7
  N12: Part1.A6, IC1.A6
  N13: Part1.A7, IC1.A5
  N14: Part1.D21/SCL, IC1.I/O3
  N15: Part1.D20/SDA, IC1.I/O4
  N16: Part1.D19/RX1, IC1.I/O5
  N17: Part1.D18/TX1, IC1.I/O6
  N18: Part1.D17_PWM/RX2, IC1.I/O7
  N19: Part1.D16_PWM/TX2, IC1._CE
  N20: Part1.D15/RX3, IC1.A10
  N21: Part1.D14/TX3, IC1._OE
  N22: Part1.D12_PWM, LED2.anode
  N23: Part1.D11_PWM, LED3.anode
  N24: Part1.D10_PWM, LED4.anode
  N25: Part1.D9_PWM, LED5.anode
  N26: Part1.D8_PWM, LED6.anode
  5V: Part1.5V, IC1.VCC
  GND: Part1.GND, IC1.GND, R1.Pin_1, R2.Pin_1, R3.Pin_1, R4.Pin_1, R5.Pin_1, R6.Pin_1, S5.Pin_3, S5.Pin_4, S6.Pin_3, S6.Pin_4, S7.Pin_3, S7.Pin_4
  N27: Part1.D2_PWM, IC1.A11
  N28: Part1.D3_PWM, IC1.A9
  N29: Part1.D4_PWM, IC1.A8
  N30: Part1.D5_PWM, IC1.A13
  N31: Part1.D6_PWM, IC1._WE
  N32: Part1.D7_PWM, LED1.anode
  N33: R1.Pin_0, LED1.cathode
  N34: R2.Pin_0, LED6.cathode
  N35: R3.Pin_0, LED5.cathode
  N36: R4.Pin_0, LED4.cathode
  N37: R5.Pin_0, LED3.cathode
  N38: R6.Pin_0, LED2.cathode
  N39: S5.Pin_1, S5.Pin_2
  N40: S6.Pin_1, S6.Pin_2
  N41: S7.Pin_1, S7.Pin_2

custom parts:
  DIP - 28 pins: 256kbit EEPROM
