# Fritzing sketch program_counter (saved by Fritzing 0.9.3b)
breadboards: 1

parts:
  IC2 = 74HCT245 [chip_label=74HCT245 package="DIP (Dual Inline) [THT]"]
  IC3 = DIP - 16 pins [chip_label=74HCT161 package="DIP (Dual Inline) [THT]"]
  IC4 = DIP - 16 pins [chip_label=74HCT161 package="DIP (Dual Inline) [THT]"]
  BUS = female pin header, 8 pins [form="♀ (female)"]
  LED17 = LED - 5mm [color="Red (633nm)" package="5 mm [THT]"]
  LED18 = LED - 5mm [color="Red (633nm)" package="5 mm [THT]"]
  LED19 = LED - 5mm [color="Red (633nm)" package="5 mm [THT]"]
  LED20 = LED - 5mm [color="Red (633nm)" package="5 mm [THT]"]
  LED21 = LED - 5mm [color="Red (633nm)" package="5 mm [THT]"]
  LED22 = LED - 5mm [color="Red (633nm)" package="5 mm [THT]"]
  LED23 = LED - 5mm [color="Red (633nm)" package="5 mm [THT]"]
  LED24 = LED - 5mm [color="Red (633nm)" package="5 mm [THT]"]
  CLOCK = female pin header, 2 pins [form="♀ (female)"]
  R1 = Resistor [tolerance=±5% resistance=1k package=THT]
  R2 = Resistor [tolerance=±5% resistance=1k package=THT]
  Q1 = NPN-Transistor [package="TO92 [THT]"]
  R3 = Resistor [tolerance=±5% resistance=220 package=THT]
  R4 = Resistor [tolerance=±5% resistance=220 package=THT]
  RESET = female pin header, 2 pins [form="♀ (female)"]
  R5 = Resistor [tolerance=±5% resistance=220 package=THT]
  R6 = Resistor [tolerance=±5% resistance=220 package=THT]
  Q2 = NPN-Transistor [package="TO92 [THT]"]
  LOAD = female pin header, 2 pins [form="♀ (female)"]
  R7 = Resistor [tolerance=±5% resistance=1k package=THT]
  R8 = Resistor [tolerance=±5% resistance=1k package=THT]
  R9 = Resistor [tolerance=±5% resistance=1k package=THT]
  R10 = Resistor [tolerance=±5% resistance=1k package=THT]
  R11 = Resistor [tolerance=±5% resistance=1k package=THT]
  R12 = Resistor [tolerance=±5% resistance=1k package=THT]
  COUNT = female pin header, 2 pins [form="♀ (female)"]
  R13 = Resistor [tolerance=±5% resistance=220 package=THT]
  R14 = Resistor [tolerance=±5% resistance=220 package=THT]
  Q3 = NPN-Transistor [package="TO92 [THT]"]
  OUTPUT = female pin header, 2 pins [form="♀ (female)"]

nets:
  GND: IC2.DIR, IC2.GND, IC3.GND, IC4.GND, R1.Pin_1, R2.Pin_1, Q1.E, Q2.E, R7.Pin_1, R8.Pin_1, R9.Pin_1, R10.Pin_1, R11.Pin_1, R12.Pin_1, Q3.E
  N1: IC2.A1, IC3.P3, BUS.pin1
  N2: IC2.A2, IC3.P2, BUS.pin2
  N3: IC2.A3, IC3.P1, BUS.pin3
  N4: IC2.A4, IC3.P0, BUS.pin4
  N5: IC2.A5, IC4.P3, BUS.pin5
  N6: IC2.A6, IC4.P2, BUS.pin6
  N7: IC2.A7, IC4.P1, BUS.pin7
  N8: IC2.A8, IC4.P0, BUS.pin8
  N9: IC2.B8, IC4.Q0, LED24.anode
  N10: IC2.B7, IC4.Q1, LED17.anode
  N11: IC2.B6, IC4.Q2, LED18.anode
  N12: IC2.B5, IC4.Q3, LED19.anode
  N13: IC2.B4, IC3.Q0, LED20.anode
  N14: IC2.B3, IC3.Q1, LED21.anode
  N15: IC2.B2, IC3.Q2, LED22.anode
  N16: IC2.B1, IC3.Q3, LED23.anode
  N17: IC2._OE, R14.Pin_1, Q3.C
  5V: IC2.VCC, IC3.VCC, IC4.TE, IC4.VCC, R3.Pin_0, R5.Pin_0, R14.Pin_0
  N18: IC3._MR, IC4._MR, Q1.C, R3.Pin_1
  N19: IC3.CP, IC4.CP, CLOCK.pin1, CLOCK.pin2
  N20: IC3.PE, IC4.PE, COUNT.pin1, COUNT.pin2
  N21: IC3._SPE, IC4._SPE, R5.Pin_1, Q2.C
  N22: IC3.TE, IC4.TC
  N23: LED17.cathode, R2.Pin_0
  N24: LED18.cathode, R7.Pin_0
  N25: LED19.cathode, R8.Pin_0
  N26: LED20.cathode, R9.Pin_0
  N27: LED21.cathode, R10.Pin_0
  N28: LED22.cathode, R11.Pin_0
  N29: LED23.cathode, R12.Pin_0
  N30: LED24.cathode, R1.Pin_0
  N31: Q1.B, R4.Pin_1
  N32: R4.Pin_0, RESET.pin1, RESET.pin2
  N33: R6.Pin_0, LOAD.pin1, LOAD.pin2
  N34: R6.Pin_1, Q2.B
  N35: R13.Pin_0, OUTPUT.pin1, OUTPUT.pin2
  N36: R13.Pin_1, Q3.B

custom parts:
  74HCT245: Octal Tri state buffer
  DIP - 16 pins: 4 bit synchronous counter with load and asynchronous clear
