# Fritzing sketch program_counter_2 (saved by Fritzing 0.9.3b)
breadboards: 1

parts:
  IC2 = 74HCT245 [chip_label=74HCT245 package="DIP (Dual Inline) [THT]"]
  IC3 = DIP - 16 pins [chip_label=74HCT161 package="DIP (Dual Inline) [THT]"]
  IC4 = DIP - 16 pins [chip_label=74HCT161 package="DIP (Dual Inline) [THT]"]
  BUS = female pin header, 8 pins [form="♀ (female)"]
  CLOCK = female pin header, 2 pins [form="♀ (female)"]
  RESET = female pin header, 2 pins [form="♀ (female)"]
  LOAD = female pin header, 2 pins [form="♀ (female)"]
  COUNT = female pin header, 2 pins [form="♀ (female)"]
  OUTPUT = female pin header, 2 pins [form="♀ (female)"]
  LED9 = LED - 5mm [color="Red (633nm)" package="5 mm [THT]"]
  LED10 = LED - 5mm [color="Red (633nm)" package="5 mm [THT]"]
  LED11 = LED - 5mm [color="Red (633nm)" package="5 mm [THT]"]
  LED12 = LED - 5mm [color="Red (633nm)" package="5 mm [THT]"]
  LED13 = LED - 5mm [color="Red (633nm)" package="5 mm [THT]"]
  LED14 = LED - 5mm [color="Red (633nm)" package="5 mm [THT]"]
  LED15 = LED - 5mm [color="Red (633nm)" package="5 mm [THT]"]
  LED16 = LED - 5mm [color="Red (633nm)" package="5 mm [THT]"]
  IC5 = DIP - 14 pins [chip_label=74HCT04 package="DIP (Dual Inline) [THT]"]
  R1 = Resistor [tolerance=±5% resistance=220 package=THT]
  R2 = Resistor [tolerance=±5% resistance=220 package=THT]
  R3 = Resistor [tolerance=±5% resistance=220 package=THT]
  R4 = Resistor [tolerance=±5% resistance=220 package=THT]
  R5 = Resistor [tolerance=±5% resistance=220 package=THT]
  R6 = Resistor [tolerance=±5% resistance=220 package=THT]
  R7 = Resistor [tolerance=±5% resistance=220 package=THT]
  R8 = Resistor [tolerance=±5% resistance=220 package=THT]

nets:
  GND: IC2.DIR, IC2.GND, IC3.GND, IC4.GND, IC5.2A, IC5.3A, IC5.GND, IC5.4A
  N1: IC2.A1, IC3.P3, BUS.pin1
  N2: IC2.A2, IC3.P2, BUS.pin2
  N3: IC2.A3, IC3.P1, BUS.pin3
  N4: IC2.A4, IC3.P0, BUS.pin4
  N5: IC2.A5, IC4.P3, BUS.pin5
  N6: IC2.A6, IC4.P2, BUS.pin6
  N7: IC2.A7, IC4.P1, BUS.pin7
  N8: IC2.A8, IC4.P0, BUS.pin8
  N9: IC2.B8, IC4.Q0, LED13.anode
  N10: IC2.B7, IC4.Q1, LED15.anode
  N11: IC2.B6, IC4.Q2, LED16.anode
  N12: IC2.B5, IC4.Q3, LED14.anode
  N13: IC2.B4, IC3.Q0, LED11.anode
  N14: IC2.B3, IC3.Q1, LED12.anode
  N15: IC2.B2, IC3.Q2, LED9.anode
  N16: IC2.B1, IC3.Q3, LED10.anode
  N17: IC2._OE, IC5.6Y
  5V: IC2.VCC, IC3.VCC, IC4.TE, IC4.VCC, IC5.VCC, R1.Pin_0, R2.Pin_0, R3.Pin_0, R4.Pin_0, R5.Pin_0, R6.Pin_0, R7.Pin_0, R8.Pin_0
  N18: IC3._MR, IC4._MR, IC5.1Y
  N19: IC3.CP, IC4.CP, CLOCK.pin1, CLOCK.pin2
  N20: IC3.PE, IC4.PE, COUNT.pin1, COUNT.pin2
  N21: IC3._SPE, IC4._SPE, IC5.5Y
  N22: IC3.TE, IC4.TC
  N23: RESET.pin1, RESET.pin2, IC5.1A
  N24: LOAD.pin1, LOAD.pin2, IC5.5A
  N25: OUTPUT.pin1, OUTPUT.pin2, IC5.6A
  N26: LED9.cathode, R2.Pin_1
  N27: LED10.cathode, R1.Pin_1
  N28: LED11.cathode, R3.Pin_1
  N29: LED12.cathode, R8.Pin_1
  N30: LED13.cathode, R6.Pin_1
  N31: LED14.cathode, R4.Pin_1
  N32: LED15.cathode, R5.Pin_1
  N33: LED16.cathode, R7.Pin_1

custom parts:
  74HCT245: Octal Tri state buffer
  DIP - 16 pins: 4 bit synchronous counter with load and asynchronous clear
  DIP - 14 pins: Hex Inverter
