# Fritzing sketch ram (saved by Fritzing 0.9.3b)
breadboards: 2

parts:
  IC1 = DIP - 24 pins [chip_label=6116SA15TPG package="DIP (Dual Inline) [THT]"]
  IC2 = 74HCT245 [chip_label=74HCT245 package="DIP (Dual Inline) [THT]"]
  BUS = female pin header, 8 pins [form="♀ (female)"]
  IC3 = 74HCT245 [chip_label=74HCT245 package="DIP (Dual Inline) [THT]"]
  LED9 = LED - 5mm [color="Red (633nm)" package="5 mm [THT]"]
  LED10 = LED - 5mm [color="Red (633nm)" package="5 mm [THT]"]
  LED11 = LED - 5mm [color="Red (633nm)" package="5 mm [THT]"]
  LED12 = LED - 5mm [color="Red (633nm)" package="5 mm [THT]"]
  LED13 = LED - 5mm [color="Red (633nm)" package="5 mm [THT]"]
  LED14 = LED - 5mm [color="Red (633nm)" package="5 mm [THT]"]
  LED15 = LED - 5mm [color="Red (633nm)" package="5 mm [THT]"]
  LED16 = LED - 5mm [color="Red (633nm)" package="5 mm [THT]"]
  R22 = Resistor [tolerance=±5% resistance=1k package=THT]
  R23 = Resistor [tolerance=±5% resistance=1k package=THT]
  R24 = Resistor [tolerance=±5% resistance=1k package=THT]
  R25 = Resistor [tolerance=±5% resistance=1k package=THT]
  R26 = Resistor [tolerance=±5% resistance=1k package=THT]
  R27 = Resistor [tolerance=±5% resistance=1k package=THT]
  R28 = Resistor [tolerance=±5% resistance=1k package=THT]
  R29 = Resistor [tolerance=±5% resistance=1k package=THT]
  C4 = Ceramic Capacitor [capacitance=100nF package="100 mil [THT, multilayer]"]
  input_enable1 = female pin header, 2 pins [form="♀ (female)"]
  input_enable2 = female pin header, 2 pins [form="♀ (female)"]
  input_enable3 = female pin header, 2 pins [form="♀ (female)"]
  input_enable4 = female pin header, 2 pins [form="♀ (female)"]
  BUS1 = female pin header, 8 pins [form="♀ (female)"]
  BUS2 = female pin header, 8 pins [form="♀ (female)"]
  C5 = Ceramic Capacitor [capacitance=100nF package="100 mil [THT, multilayer]"]
  C6 = Ceramic Capacitor [capacitance=100nF package="100 mil [THT, multilayer]"]
  IC16 = DIP - 16 pins [chip_label=74HCT157 package="DIP (Dual Inline) [THT]"]
  IC17 = DIP - 14 pins [chip_label=74HCT02 package="DIP (Dual Inline) [THT]"]
  IC18 = DIP - 14 pins [chip_label=74HCT08 package="DIP (Dual Inline) [THT]"]
  IC19 = DIP - 14 pins [chip_label=74HCT14 package="DIP (Dual Inline) [THT]"]
  IC20 = DIP - 14 pins [chip_label=74HCT32 package="DIP (Dual Inline) [THT]"]
  R32 = Resistor [tolerance=±5% resistance=2k package=THT]
  C7 = Ceramic Capacitor [capacitance=100nF package="100 mil [THT, multilayer]"]
  input_enable5 = female pin header, 2 pins [form="♀ (female)"]
  J12 = female pin header, 2 pins [form="♀ (female)"]
  J13 = female pin header, 2 pins [form="♀ (female)"]
  J14 = female pin header, 2 pins [form="♀ (female)"]
  J15 = female pin header, 2 pins [form="♀ (female)"]
  J16 = female pin header, 2 pins [form="♀ (female)"]
  J17 = female pin header, 2 pins [form="♀ (female)"]
  J18 = female pin header, 2 pins [form="♀ (female)"]
  J19 = female pin header, 2 pins [form="♀ (female)"]
  J20 = female pin header, 2 pins [form="♀ (female)"]
  J21 = female pin header, 2 pins [form="♀ (female)"]
  C9 = Ceramic Capacitor [capacitance=100nF package="100 mil [THT, multilayer]"]
  IC21 = 74HCT123 [chip_label=74HCT123 package="DIP (Dual Inline) [THT]"]
  R33 = Resistor [tolerance=±5% resistance=220 package=THT]  # not connected
  R34 = Resistor [tolerance=±5% resistance=2k package=THT]
  C10 = Ceramic Capacitor [capacitance=100nF package="100 mil [THT, multilayer]"]

nets:
  N1: IC1.A7, BUS2.pin1
  N2: IC1.A6, BUS2.pin2
  N3: IC1.A5, BUS2.pin3
  N4: IC1.A4, BUS2.pin4
  N5: IC1.A3, BUS2.pin5
  N6: IC1.A2, BUS2.pin6
  N7: IC1.A1, BUS2.pin7
  N8: IC1.A0, BUS2.pin8
  N9: IC1.I/O0, IC2.A8, IC3.A8, LED13.anode
  N10: IC1.I/O1, IC2.A7, IC3.A7, LED15.anode
  N11: IC1.I/O2, IC2.A6, IC3.A6, LED16.anode
  GND: IC1.GND, IC1._CS, IC1.A10, IC1._OE, IC1.A9, IC2.DIR, IC2.GND, IC3.GND, R22.Pin_1, R23.Pin_1, R24.Pin_1, R25.Pin_1, R27.Pin_1, R28.Pin_1, R29.Pin_1, C5.0, C6.1
  N12: IC1.I/O3, IC2.A5, IC3.A5, LED14.anode
  N13: IC1.I/O4, IC2.A4, IC3.A4, LED11.anode
  N14: IC1.I/O5, IC2.A3, IC3.A3, LED12.anode
  N15: IC1.I/O6, IC2.A2, IC3.A2, LED9.anode
  N16: IC1.I/O7, IC2.A1, IC3.A1, LED10.anode
  N17: IC1._WE, input_enable4.pin1, input_enable4.pin2
  N18: IC1.A8, input_enable3.pin1, input_enable3.pin2
  VCC: IC1.VCC, IC2.VCC, IC3.DIR, IC3.VCC, C5.1, C6.0
  N19: IC2.B8, BUS1.pin8
  N20: IC2.B7, BUS1.pin7
  N21: IC2.B6, BUS1.pin6
  N22: IC2.B5, BUS1.pin5
  N23: IC2.B4, BUS1.pin4
  N24: IC2.B3, BUS1.pin3
  N25: IC2.B2, BUS1.pin2
  N26: IC2.B1, BUS1.pin1
  N27: IC2._OE, input_enable1.pin1, input_enable1.pin2
  N28: BUS.pin1, IC3.B1
  N29: BUS.pin2, IC3.B2
  N30: BUS.pin3, IC3.B3
  N31: BUS.pin4, IC3.B4
  N32: BUS.pin5, IC3.B5
  N33: BUS.pin6, IC3.B6
  N34: BUS.pin7, IC3.B7
  N35: BUS.pin8, IC3.B8
  N36: IC3._OE, input_enable2.pin1, input_enable2.pin2
  N37: LED9.cathode, R29.Pin_0
  N38: LED10.cathode, R28.Pin_0
  N39: LED11.cathode, R24.Pin_0
  N40: LED12.cathode, R25.Pin_0
  N41: LED13.cathode, R26.Pin_0
  N42: LED14.cathode, R23.Pin_0
  N43: LED15.cathode, R22.Pin_0
  N44: LED16.cathode, R27.Pin_0
  VCC_2: C4.0, IC16.3B, IC16.VCC, IC17.VCC, IC18.3A, IC18.3B, IC18.VCC, IC19.VCC, IC20.VCC, R32.Pin_1, C9.1, IC21.1_RD, IC21.2_RD, IC21.VCC, R34.Pin_0
  GND_2: C4.1, IC16.GND, IC16.3Y, IC16.4B, IC16.4A, IC16._G, IC17.GND, IC18.1A, IC18.2A, IC18.2B, IC18.GND, IC19.1A, IC19.2A, IC19.GND, IC19.4A, IC20.1A, IC20.1B, IC20.2A, IC20.2B, IC20.GND, C7.0, C9.0, IC21.1_A, IC21.2CEXT, IC21.GND, IC21.2_A, IC21.1CEXT, C10.0
  N45: IC16._A/B, J20.pin1, J20.pin2
  N46: IC16.1A, J21.pin1, J21.pin2
  N47: IC16.1B, J19.pin1, J19.pin2
  N48: IC16.1Y, J16.pin1, J16.pin2
  N49: IC16.2A, J18.pin1, J18.pin2
  N50: IC16.2B, J17.pin1, J17.pin2
  N51: IC16.2Y, IC17.1A, IC17.1B, IC18.4B
  N52: IC16.3A, input_enable5.pin1, input_enable5.pin2
  N53: IC17.1Y, IC17.2A
  N54: IC17.2Y, IC17.3A
  N55: IC17.2B, IC17.3Y, IC18.4A
  N56: IC17.3B, IC17.4Y
  N57: IC17.4A, IC17.4B, IC18.1Y
  N58: IC18.4Y, IC19.6A
  N59: IC19.3A, J13.pin1, J13.pin2
  N60: IC19.3Y, J12.pin1, J12.pin2
  N61: IC19.5Y, IC21.2B
  N62: IC19.5A, IC19.6Y
  N63: IC20.3Y, J14.pin1, J14.pin2
  N64: IC20.3A, IC21.2_Q
  N65: IC20.3B, IC20.4A, IC20.4B, IC21.1_Q
  N66: IC20.4Y, J15.pin1, J15.pin2
  N67: R32.Pin_0, C7.1, IC21.2REXTCEXT
  N68: IC21.1REXTCEXT, R34.Pin_1, C10.1

notes:
  _output_enable
  input_buffer__OE
  data_in
  data_out
  address
  select_data_memory
  ram_chip__WE
  input_enable
  run/setup 0/1
  setup_clock
  control_unit_select_data_memory
  setup_select_data_memory
  output_enable
  data_clock
  safe_clock_enable_out
  ram_enable_enable

custom parts:
  DIP - 24 pins: 2K SRAM (16K x 8-bit)
  74HCT245: Octal Tri state buffer
  DIP - 16 pins: Quad 2 line to one line data selectors
  DIP - 14 pins: Quad NOR
  DIP - 14 pins: Quad AND
  DIP - 14 pins: Hex Schmitt trigger inverters
  DIP - 14 pins: Quad OR gate
  74HCT123: Dual retriggerable monostable multivibrator with reset
