# Fritzing sketch register (saved by Fritzing 0.9.3b)
breadboards: 1

parts:
  IC5 = 74HCT245 [chip_label=74HCT245 package="DIP (Dual Inline) [THT]"]
  IC6 = 74HCT377 [chip_label=74HCT377 package="DIP (Dual Inline) [THT]"]
  constant_out = female pin header, 8 pins [form="♀ (female)"]
  bus = female pin header, 8 pins [form="♀ (female)"]
  LED9 = LED - 5mm [color="Red (633nm)" package="5 mm [THT]"]
  LED10 = LED - 5mm [color="Red (633nm)" package="5 mm [THT]"]
  LED11 = LED - 5mm [color="Red (633nm)" package="5 mm [THT]"]
  LED12 = LED - 5mm [color="Red (633nm)" package="5 mm [THT]"]
  LED13 = LED - 5mm [color="Red (633nm)" package="5 mm [THT]"]
  LED14 = LED - 5mm [color="Red (633nm)" package="5 mm [THT]"]
  LED15 = LED - 5mm [color="Red (633nm)" package="5 mm [THT]"]
  LED16 = LED - 5mm [color="Red (633nm)" package="5 mm [THT]"]
  R2 = Resistor [tolerance=±5% resistance=330 package=THT]
  R3 = Resistor [tolerance=±5% resistance=330 package=THT]
  R4 = Resistor [tolerance=±5% resistance=330 package=THT]
  R5 = Resistor [tolerance=±5% resistance=330 package=THT]
  R6 = Resistor [tolerance=±5% resistance=330 package=THT]
  R7 = Resistor [tolerance=±5% resistance=330 package=THT]
  R8 = Resistor [tolerance=±5% resistance=330 package=THT]
  R9 = Resistor [tolerance=±5% resistance=330 package=THT]
  Q1 = NPN-Transistor [package="TO92 [THT]"]
  R10 = Resistor [tolerance=±5% resistance=220 package=THT]
  Q2 = NPN-Transistor [package="TO92 [THT]"]
  R11 = Resistor [tolerance=±5% resistance=220 package=THT]
  R12 = Resistor [tolerance=±5% resistance=220 package=THT]
  R13 = Resistor [tolerance=±5% resistance=220 package=THT]
  input_enable = female pin header, 2 pins [form="♀ (female)"]
  output_enable = female pin header, 2 pins [form="♀ (female)"]
  clock = female pin header, 2 pins [form="♀ (female)"]
  C1 = Ceramic Capacitor [capacitance=100nF package="100 mil [THT, multilayer]"]

nets:
  5V: IC5.DIR, IC5.VCC, IC6.VCC, R10.Pin_0, R11.Pin_0, C1.1
  N1: IC5.A1, IC6.1Q, constant_out.pin1, LED11.anode
  N2: IC5.A2, IC6.2Q, constant_out.pin2, LED9.anode
  N3: IC5.A3, IC6.3Q, constant_out.pin3, LED10.anode
  N4: IC5.A4, IC6.4Q, constant_out.pin4, LED12.anode
  N5: IC5.A5, IC6.5Q, constant_out.pin5, LED13.anode
  N6: IC5.A6, IC6.6Q, constant_out.pin6, LED14.anode
  N7: IC5.A7, IC6.7Q, constant_out.pin7, LED15.anode
  N8: IC5.A8, IC6.8Q, constant_out.pin8, LED16.anode
  GND: IC5.GND, IC6.GND, R2.Pin_1, R3.Pin_1, R4.Pin_1, R5.Pin_1, R6.Pin_1, R7.Pin_1, R8.Pin_1, R9.Pin_1, Q1.E, Q2.E, C1.0
  N9: IC5.B8, IC6.8D, bus.pin8
  N10: IC5.B7, IC6.7D, bus.pin7
  N11: IC5.B6, IC6.6D, bus.pin6
  N12: IC5.B5, IC6.5D, bus.pin5
  N13: IC5.B4, IC6.4D, bus.pin4
  N14: IC5.B3, IC6.3D, bus.pin3
  N15: IC5.B2, IC6.2D, bus.pin2
  N16: IC5.B1, IC6.1D, bus.pin1
  N17: IC5._OE, Q1.C, R10.Pin_1
  N18: IC6._CLKEN, Q2.C, R11.Pin_1
  N19: IC6.CLK, clock.pin1, clock.pin2
  N20: LED9.cathode, R3.Pin_0
  N21: LED10.cathode, R4.Pin_0
  N22: LED11.cathode, R2.Pin_0
  N23: LED12.cathode, R5.Pin_0
  N24: LED13.cathode, R6.Pin_0
  N25: LED14.cathode, R7.Pin_0
  N26: LED15.cathode, R8.Pin_0
  N27: LED16.cathode, R9.Pin_0
  N28: Q1.B, R13.Pin_1
  N29: Q2.B, R12.Pin_1
  N30: R12.Pin_0, input_enable.pin1, input_enable.pin2
  N31: R13.Pin_0, output_enable.pin1, output_enable.pin2

custom parts:
  74HCT245: Octal Tri state buffer
  74HCT377: Octal D-Type flip flops with clock enable 8 bit register
