# Fritzing sketch register_2 (saved by Fritzing 0.9.3b)
breadboards: 2

parts:
  IC1 = 74HCT245 [chip_label=74HCT245 package="DIP (Dual Inline) [THT]"]
  IC2 = 74HCT377 [chip_label=74HCT377 package="DIP (Dual Inline) [THT]"]
  R13 = Resistor [tolerance=±5% resistance=1k package=THT]
  R14 = Resistor [tolerance=±5% resistance=1k package=THT]
  R15 = Resistor [tolerance=±5% resistance=1k package=THT]
  R16 = Resistor [tolerance=±5% resistance=1k package=THT]
  R17 = Resistor [tolerance=±5% resistance=1k package=THT]
  R18 = Resistor [tolerance=±5% resistance=1k package=THT]
  R19 = Resistor [tolerance=±5% resistance=1k package=THT]
  R20 = Resistor [tolerance=±5% resistance=1k package=THT]
  Q3 = NPN-Transistor [package="TO92 [THT]"]
  R21 = Resistor [tolerance=±5% resistance=220 package=THT]
  Q4 = NPN-Transistor [package="TO92 [THT]"]
  R22 = Resistor [tolerance=±5% resistance=220 package=THT]
  R23 = Resistor [tolerance=±5% resistance=220 package=THT]
  R24 = Resistor [tolerance=±5% resistance=220 package=THT]
  OUT = female pin header, 2 pins [form="♀ (female)"]
  IN = female pin header, 2 pins [form="♀ (female)"]
  LED25 = LED - 5mm [color="Red (633nm)" package="5 mm [THT]"]
  LED27 = LED - 5mm [color="Red (633nm)" package="5 mm [THT]"]
  LED30 = LED - 5mm [color="Red (633nm)" package="5 mm [THT]"]
  LED31 = LED - 5mm [color="Red (633nm)" package="5 mm [THT]"]
  LED26 = LED - 5mm [color="Red (633nm)" package="5 mm [THT]"]
  LED28 = LED - 5mm [color="Red (633nm)" package="5 mm [THT]"]
  LED32 = LED - 5mm [color="Red (633nm)" package="5 mm [THT]"]
  LED29 = LED - 5mm [color="Red (633nm)" package="5 mm [THT]"]

nets:
  VCC: IC1.DIR, IC1.VCC, IC2.VCC, R21.Pin_0, R22.Pin_0
  N1: IC1.A1, IC2.1Q, LED31.anode
  N2: IC1.A2, IC2.2Q, LED25.anode
  N3: IC1.A3, IC2.3Q, LED26.anode
  N4: IC1.A4, IC2.4Q, LED27.anode
  N5: IC1.A5, IC2.5Q, LED28.anode
  N6: IC1.A6, IC2.6Q, LED29.anode
  N7: IC1.A7, IC2.7Q, LED30.anode
  N8: IC1.A8, IC2.8Q, LED32.anode
  GND: IC1.GND, IC2.GND, R13.Pin_1, R14.Pin_1, R15.Pin_1, R16.Pin_1, R17.Pin_1, R18.Pin_1, R19.Pin_1, R20.Pin_1, Q3.E, Q4.E
  N9: IC1.B8, IC2.8D
  N10: IC1.B7, IC2.7D
  N11: IC1.B6, IC2.6D
  N12: IC1.B5, IC2.5D
  N13: IC1.B4, IC2.4D
  N14: IC1.B3, IC2.3D
  N15: IC1.B2, IC2.2D
  N16: IC1.B1, IC2.1D
  N17: IC1._OE, Q3.C, R21.Pin_1
  N18: IC2._CLKEN, Q4.C, R22.Pin_1
  N19: R13.Pin_0, LED30.cathode
  N20: R14.Pin_0, LED28.cathode
  N21: R15.Pin_0, LED27.cathode
  N22: R16.Pin_0, LED26.cathode
  N23: R17.Pin_0, LED29.cathode
  N24: R18.Pin_0, LED31.cathode
  N25: R19.Pin_0, LED25.cathode
  N26: R20.Pin_0, LED32.cathode
  N27: Q3.B, R24.Pin_1
  N28: Q4.B, R23.Pin_1
  N29: R23.Pin_0, IN.pin1, IN.pin2
  N30: R24.Pin_0, OUT.pin1, OUT.pin2

custom parts:
  74HCT245: Octal Tri state buffer
  74HCT377: Octal D-Type flip flops with clock enable 8 bit register
