# Fritzing sketch register_3 (saved by Fritzing 0.9.3b)
breadboards: 2

parts:
  IC1 = 74HCT245 [chip_label=74HCT245 package="DIP (Dual Inline) [THT]"]
  IC2 = 74HCT377 [chip_label=74HCT377 package="DIP (Dual Inline) [THT]"]
  R13 = Resistor [tolerance=±5% resistance=1k package=THT]
  R14 = Resistor [tolerance=±5% resistance=1k package=THT]
  R15 = Resistor [tolerance=±5% resistance=1k package=THT]
  R16 = Resistor [tolerance=±5% resistance=1k package=THT]
  R17 = Resistor [tolerance=±5% resistance=1k package=THT]
  R18 = Resistor [tolerance=±5% resistance=1k package=THT]
  R19 = Resistor [tolerance=±5% resistance=1k package=THT]
  R20 = Resistor [tolerance=±5% resistance=1k package=THT]
  IC3 = IC, DIP package, 14 pins [chip_label=IC]
  LED1 = LED - 5mm [color="Red (633nm)" package="5 mm [THT]"]
  LED2 = LED - 5mm [color="Red (633nm)" package="5 mm [THT]"]
  LED3 = LED - 5mm [color="Red (633nm)" package="5 mm [THT]"]
  LED4 = LED - 5mm [color="Red (633nm)" package="5 mm [THT]"]
  LED5 = LED - 5mm [color="Red (633nm)" package="5 mm [THT]"]
  LED6 = LED - 5mm [color="Red (633nm)" package="5 mm [THT]"]
  LED7 = LED - 5mm [color="Red (633nm)" package="5 mm [THT]"]
  LED8 = LED - 5mm [color="Red (633nm)" package="5 mm [THT]"]

nets:
  VCC: IC1.DIR, IC1.VCC, IC2.VCC, IC3.pin14
  GND: IC1.GND, IC2.3Q, IC2.GND, R13.Pin_1, R14.Pin_1, R15.Pin_1, R16.Pin_1, R17.Pin_1, R18.Pin_1, R19.Pin_1, R20.Pin_1, IC3.pin7
  N1: IC1.B8, IC2.8D
  N2: IC1.B7, IC2.7D
  N3: IC1.B6, IC2.6D
  N4: IC1.B5, IC2.5D
  N5: IC1.B4, IC2.4D
  N6: IC1.B3, IC2.3D
  N7: IC1.B2, IC2.2D
  N8: IC1.B1, IC2.1D
  N9: IC2.1Q, IC3.pin1
  N10: IC2.2Q, IC3.pin4
  N11: R13.Pin_0, LED2.cathode
  N12: R14.Pin_0, LED4.cathode
  N13: R15.Pin_0, LED5.cathode
  N14: R16.Pin_0, LED7.cathode
  N15: R17.Pin_0, LED3.cathode
  N16: R18.Pin_0, LED8.cathode
  N17: R19.Pin_0, LED6.cathode
  N18: R20.Pin_0, LED1.cathode

custom parts:
  74HCT245: Octal Tri state buffer
  74HCT377: Octal D-Type flip flops with clock enable 8 bit register
