# Fritzing sketch register_4 (saved by Fritzing 0.9.3b)
breadboards: 1

parts:
  IC1 = 74HCT245 [chip_label=74HCT245 package="DIP (Dual Inline) [THT]"]
  IC2 = 74HCT377 [chip_label=74HCT377 package="DIP (Dual Inline) [THT]"]
  R14 = Resistor [tolerance=±5% resistance=1k package=THT]
  R15 = Resistor [tolerance=±5% resistance=1k package=THT]
  R16 = Resistor [tolerance=±5% resistance=1k package=THT]
  R17 = Resistor [tolerance=±5% resistance=1k package=THT]
  R18 = Resistor [tolerance=±5% resistance=1k package=THT]
  R19 = Resistor [tolerance=±5% resistance=1k package=THT]
  LED1 = LED - 5mm [color="Red (633nm)" package="5 mm [THT]"]
  LED2 = LED - 5mm [color="Red (633nm)" package="5 mm [THT]"]
  LED3 = LED - 5mm [color="Red (633nm)" package="5 mm [THT]"]
  LED4 = LED - 5mm [color="Red (633nm)" package="5 mm [THT]"]
  LED5 = LED - 5mm [color="Red (633nm)" package="5 mm [THT]"]
  LED6 = LED - 5mm [color="Red (633nm)" package="5 mm [THT]"]
  LED7 = LED - 5mm [color="Red (633nm)" package="5 mm [THT]"]
  LED8 = LED - 5mm [color="Red (633nm)" package="5 mm [THT]"]
  R20 = Resistor [tolerance=±5% resistance=1k package=THT]
  R21 = Resistor [tolerance=±5% resistance=1k package=THT]
  INPUT = female pin header, 2 pins [form="♀ (female)"]
  OUTPUT = female pin header, 2 pins [form="♀ (female)"]
  CLOCK = female pin header, 2 pins [form="♀ (female)"]
  IC3 = DIP - 14 pins [chip_label=74HCT04 package="DIP (Dual Inline) [THT]"]

nets:
  VCC: IC1.DIR, IC1.VCC, IC2.VCC, IC3.VCC
  N1: IC1.A1, IC2.1Q, LED8.anode
  N2: IC1.A2, IC2.2Q, LED6.anode
  N3: IC1.A3, IC2.3Q, LED7.anode
  N4: IC1.A4, IC2.4Q, LED5.anode
  N5: IC1.A5, IC2.5Q, LED4.anode
  N6: IC1.A6, IC2.6Q, LED3.anode
  N7: IC1.A7, IC2.7Q, LED2.anode
  N8: IC1.A8, IC2.8Q, LED1.anode
  GND: IC1.GND, IC2.GND, R14.Pin_1, R15.Pin_1, R16.Pin_1, R17.Pin_1, R18.Pin_1, R19.Pin_1, R20.Pin_1, R21.Pin_1, IC3.2A, IC3.3A, IC3.GND, IC3.5A, IC3.6A
  N9: IC1.B8, IC2.8D
  N10: IC1.B7, IC2.7D
  N11: IC1.B6, IC2.6D
  N12: IC1.B5, IC2.5D
  N13: IC1.B4, IC2.4D
  N14: IC1.B3, IC2.3D
  N15: IC1.B2, IC2.2D
  N16: IC1.B1, IC2.1D
  N17: IC1._OE, IC3.4Y
  N18: IC2._CLKEN, IC3.1Y
  N19: IC2.CLK, CLOCK.pin1, CLOCK.pin2
  N20: R14.Pin_0, LED4.cathode
  N21: R15.Pin_0, LED5.cathode
  N22: R16.Pin_0, LED7.cathode
  N23: R17.Pin_0, LED3.cathode
  N24: R18.Pin_0, LED8.cathode
  N25: R19.Pin_0, LED6.cathode
  N26: LED1.cathode, R21.Pin_0
  N27: LED2.cathode, R20.Pin_0
  N28: INPUT.pin1, INPUT.pin2, IC3.1A
  N29: OUTPUT.pin1, OUTPUT.pin2, IC3.4A

custom parts:
  74HCT245: Octal Tri state buffer
  74HCT377: Octal D-Type flip flops with clock enable 8 bit register
  DIP - 14 pins: Hex Inverter
