# Fritzing sketch register_bus_left (saved by Fritzing 0.9.3b)
breadboards: 1

parts:
  IC1 = 74HCT245 [chip_label=74HCT245 package="DIP (Dual Inline) [THT]"]
  IC2 = 74HCT377 [chip_label=74HCT377 package="DIP (Dual Inline) [THT]"]
  R14 = Resistor [tolerance=±5% resistance=1k package=THT]
  R15 = Resistor [tolerance=±5% resistance=1k package=THT]
  R16 = Resistor [tolerance=±5% resistance=1k package=THT]
  R17 = Resistor [tolerance=±5% resistance=1k package=THT]
  R18 = Resistor [tolerance=±5% resistance=1k package=THT]
  R19 = Resistor [tolerance=±5% resistance=1k package=THT]
  LED1 = LED - 5mm [color="Red (633nm)" package="5 mm [THT]"]
  LED2 = LED - 5mm [color="Red (633nm)" package="5 mm [THT]"]
  LED3 = LED - 5mm [color="Red (633nm)" package="5 mm [THT]"]
  LED4 = LED - 5mm [color="Red (633nm)" package="5 mm [THT]"]
  LED5 = LED - 5mm [color="Red (633nm)" package="5 mm [THT]"]
  LED6 = LED - 5mm [color="Red (633nm)" package="5 mm [THT]"]
  LED7 = LED - 5mm [color="Red (633nm)" package="5 mm [THT]"]
  LED8 = LED - 5mm [color="Red (633nm)" package="5 mm [THT]"]
  R20 = Resistor [tolerance=±5% resistance=1k package=THT]
  R21 = Resistor [tolerance=±5% resistance=1k package=THT]
  IC3 = DIP - 14 pins [chip_label=74HCT04 package="DIP (Dual Inline) [THT]"]
  J1 = female pin header, 8 pins [form="♀ (female)"]
  J2 = female pin header, 8 pins [form="♀ (female)"]
  C1 = Ceramic Capacitor [capacitance=100nF package="100 mil [THT, multilayer]"]
  C2 = Ceramic Capacitor [capacitance=100nF package="100 mil [THT, multilayer]"]

nets:
  VCC: IC1.DIR, IC1.VCC, IC2.VCC, IC3.VCC, C1.1, C2.0
  N1: IC1.A1, IC2.1Q, LED8.anode, J2.pin1
  N2: IC1.A2, IC2.2Q, LED6.anode, J2.pin2
  N3: IC1.A3, IC2.3Q, LED7.anode, J2.pin3
  N4: IC1.A4, IC2.4Q, LED5.anode, J2.pin4
  N5: IC1.A5, IC2.5Q, LED4.anode, J2.pin5
  N6: IC1.A6, IC2.6Q, LED3.anode, J2.pin6
  N7: IC1.A7, IC2.7Q, LED2.anode, J2.pin7
  N8: IC1.A8, IC2.8Q, LED1.anode, J2.pin8
  GND: IC1.GND, IC2.GND, R14.Pin_1, R15.Pin_1, R16.Pin_1, R17.Pin_1, R18.Pin_1, R19.Pin_1, R20.Pin_1, R21.Pin_1, IC3.2A, IC3.3A, IC3.GND, IC3.5A, IC3.6A, C1.0, C2.1
  N9: IC1.B8, IC2.8D, J1.pin8
  N10: IC1.B7, IC2.7D, J1.pin7
  N11: IC1.B6, IC2.6D, J1.pin6
  N12: IC1.B5, IC2.5D, J1.pin5
  N13: IC1.B4, IC2.4D, J1.pin4
  N14: IC1.B3, IC2.3D, J1.pin3
  N15: IC1.B2, IC2.2D, J1.pin2
  N16: IC1.B1, IC2.1D, J1.pin1
  N17: IC1._OE, IC3.4Y
  N18: IC2._CLKEN, IC3.1Y
  N19: R14.Pin_0, LED4.cathode
  N20: R15.Pin_0, LED5.cathode
  N21: R16.Pin_0, LED7.cathode
  N22: R17.Pin_0, LED3.cathode
  N23: R18.Pin_0, LED8.cathode
  N24: R19.Pin_0, LED6.cathode
  N25: LED1.cathode, R21.Pin_0
  N26: LED2.cathode, R20.Pin_0

notes:
  clock
  output_enable
  input_enable
  data
  content

custom parts:
  74HCT245: Octal Tri state buffer
  74HCT377: Octal D-Type flip flops with clock enable 8 bit register
  DIP - 14 pins: Hex Inverter
