# Fritzing sketch register_bus_right (saved by Fritzing 0.9.3b)
breadboards: 1

parts:
  IC1 = 74HCT245 [chip_label=74HCT245 package="DIP (Dual Inline) [THT]"]
  IC2 = 74HCT377 [chip_label=74HCT377 package="DIP (Dual Inline) [THT]"]
  IC3 = DIP - 14 pins [chip_label=74HCT04 package="DIP (Dual Inline) [THT]"]
  R22 = Resistor [tolerance=±5% resistance=1k package=THT]
  R23 = Resistor [tolerance=±5% resistance=1k package=THT]
  R24 = Resistor [tolerance=±5% resistance=1k package=THT]
  R25 = Resistor [tolerance=±5% resistance=1k package=THT]
  R26 = Resistor [tolerance=±5% resistance=1k package=THT]
  R27 = Resistor [tolerance=±5% resistance=1k package=THT]
  R28 = Resistor [tolerance=±5% resistance=1k package=THT]
  R29 = Resistor [tolerance=±5% resistance=1k package=THT]
  LED9 = LED - 5mm [color="Red (633nm)" package="5 mm [THT]"]
  LED11 = LED - 5mm [color="Red (633nm)" package="5 mm [THT]"]
  LED12 = LED - 5mm [color="Red (633nm)" package="5 mm [THT]"]
  LED13 = LED - 5mm [color="Red (633nm)" package="5 mm [THT]"]
  LED15 = LED - 5mm [color="Red (633nm)" package="5 mm [THT]"]
  LED10 = LED - 5mm [color="Red (633nm)" package="5 mm [THT]"]
  LED14 = LED - 5mm [color="Red (633nm)" package="5 mm [THT]"]
  LED16 = LED - 5mm [color="Red (633nm)" package="5 mm [THT]"]
  J1 = female pin header, 8 pins [form="♀ (female)"]
  J2 = female pin header, 8 pins [form="♀ (female)"]
  C1 = Ceramic Capacitor [capacitance=100nF package="100 mil [THT, multilayer]"]
  C2 = Ceramic Capacitor [capacitance=100nF package="100 mil [THT, multilayer]"]

nets:
  VCC: IC1.DIR, IC1.VCC, IC2.VCC, IC3.VCC, C1.1, C2.0
  N1: IC1.A1, IC2.1Q, LED10.anode, J2.pin1
  N2: IC1.A2, IC2.2Q, LED9.anode, J2.pin2
  N3: IC1.A3, IC2.3Q, LED12.anode, J2.pin3
  N4: IC1.A4, IC2.4Q, LED11.anode, J2.pin4
  N5: IC1.A5, IC2.5Q, LED14.anode, J2.pin5
  N6: IC1.A6, IC2.6Q, LED16.anode, J2.pin6
  N7: IC1.A7, IC2.7Q, LED15.anode, J2.pin7
  N8: IC1.A8, IC2.8Q, LED13.anode, J2.pin8
  GND: IC1.GND, IC2.GND, IC3.2A, IC3.3A, IC3.GND, IC3.5A, IC3.6A, R22.Pin_1, R23.Pin_1, R24.Pin_1, R25.Pin_1, R26.Pin_1, R27.Pin_1, R28.Pin_1, R29.Pin_1, C1.0, C2.1
  N9: IC1.B8, IC2.8D, J1.pin8
  N10: IC1.B7, IC2.7D, J1.pin7
  N11: IC1.B6, IC2.6D, J1.pin6
  N12: IC1.B5, IC2.5D, J1.pin5
  N13: IC1.B4, IC2.4D, J1.pin4
  N14: IC1.B3, IC2.3D, J1.pin3
  N15: IC1.B2, IC2.2D, J1.pin2
  N16: IC1.B1, IC2.1D, J1.pin1
  N17: IC1._OE, IC3.4Y
  N18: IC2._CLKEN, IC3.1Y
  N19: R22.Pin_0, LED15.cathode
  N20: R23.Pin_0, LED14.cathode
  N21: R24.Pin_0, LED11.cathode
  N22: R25.Pin_0, LED12.cathode
  N23: R26.Pin_0, LED13.cathode
  N24: R27.Pin_0, LED16.cathode
  N25: R28.Pin_0, LED10.cathode
  N26: R29.Pin_0, LED9.cathode

notes:
  clock
  output_enable
  input_enable
  data
  content

custom parts:
  74HCT245: Octal Tri state buffer
  74HCT377: Octal D-Type flip flops with clock enable 8 bit register
  DIP - 14 pins: Hex Inverter
