# Fritzing sketch register_input_only_right (saved by Fritzing 0.9.3b)
breadboards: 1

parts:
  IC6 = DIP - 14 pins [chip_label=74HCT14 package="DIP (Dual Inline) [THT]"]
  IC7 = 74HCT377 [chip_label=74HCT377 package="DIP (Dual Inline) [THT]"]
  MAR_DATA_OUT = female pin header, 8 pins [form="♀ (female)"]
  BUS = female pin header, 8 pins [form="♀ (female)"]
  LED25 = LED - 5mm [color="Green (555nm)" package="5 mm [THT]"]
  LED26 = LED - 5mm [color="Green (555nm)" package="5 mm [THT]"]
  LED27 = LED - 5mm [color="Green (555nm)" package="5 mm [THT]"]
  LED28 = LED - 5mm [color="Green (555nm)" package="5 mm [THT]"]
  LED29 = LED - 5mm [color="Green (555nm)" package="5 mm [THT]"]
  LED30 = LED - 5mm [color="Green (555nm)" package="5 mm [THT]"]
  LED31 = LED - 5mm [color="Green (555nm)" package="5 mm [THT]"]
  LED32 = LED - 5mm [color="Green (555nm)" package="5 mm [THT]"]
  R40 = Resistor [tolerance=±5% resistance=1k package=THT]
  R41 = Resistor [tolerance=±5% resistance=1k package=THT]
  R42 = Resistor [tolerance=±5% resistance=1k package=THT]
  R43 = Resistor [tolerance=±5% resistance=1k package=THT]
  R44 = Resistor [tolerance=±5% resistance=1k package=THT]
  R45 = Resistor [tolerance=±5% resistance=1k package=THT]
  R46 = Resistor [tolerance=±5% resistance=1k package=THT]
  R47 = Resistor [tolerance=±5% resistance=1k package=THT]
  J1 = female pin header, 2 pins [form="♀ (female)"]
  J2 = female pin header, 2 pins [form="♀ (female)"]
  C1 = Ceramic Capacitor [capacitance=100nF package="100 mil [THT, multilayer]"]
  C2 = Ceramic Capacitor [capacitance=100nF package="100 mil [THT, multilayer]"]

nets:
  N1: IC6.1A, J2.pin1, J2.pin2
  N2: IC6.1Y, IC7._CLKEN
  GND: IC6.2A, IC6.3A, IC6.GND, IC6.4A, IC6.5A, IC6.6A, IC7.GND, R40.Pin_0, R41.Pin_0, R42.Pin_0, R43.Pin_0, R44.Pin_0, R45.Pin_0, R46.Pin_0, R47.Pin_0, C1.0, C2.1
  VCC: IC6.VCC, IC7.VCC, C1.1, C2.0
  N3: IC7.1Q, MAR_DATA_OUT.pin8, LED25.anode
  N4: IC7.1D, BUS.pin8
  N5: IC7.2D, BUS.pin7
  N6: IC7.2Q, MAR_DATA_OUT.pin7, LED26.anode
  N7: IC7.3Q, MAR_DATA_OUT.pin6, LED27.anode
  N8: IC7.3D, BUS.pin6
  N9: IC7.4D, BUS.pin5
  N10: IC7.4Q, MAR_DATA_OUT.pin5, LED28.anode
  N11: IC7.CLK, J1.pin1, J1.pin2
  N12: IC7.5Q, MAR_DATA_OUT.pin4, LED29.anode
  N13: IC7.5D, BUS.pin4
  N14: IC7.6D, BUS.pin3
  N15: IC7.6Q, MAR_DATA_OUT.pin3, LED30.anode
  N16: IC7.7Q, MAR_DATA_OUT.pin2, LED31.anode
  N17: IC7.7D, BUS.pin2
  N18: IC7.8D, BUS.pin1
  N19: IC7.8Q, MAR_DATA_OUT.pin1, LED32.anode
  N20: LED25.cathode, R40.Pin_1
  N21: LED26.cathode, R45.Pin_1
  N22: LED27.cathode, R42.Pin_1
  N23: LED28.cathode, R43.Pin_1
  N24: LED29.cathode, R41.Pin_1
  N25: LED30.cathode, R44.Pin_1
  N26: LED31.cathode, R47.Pin_1
  N27: LED32.cathode, R46.Pin_1

notes:
  contents
  clock
  data
  input_enable

custom parts:
  DIP - 14 pins: Hex Schmitt trigger inverters
  74HCT377: Octal D-Type flip flops with clock enable 8 bit register
