# Fritzing sketch sixteen-bit-RAM-control (saved by Fritzing 0.9.3b)
breadboards: 1

parts:
  IC1 = IC, DIP package, 20 pins [chip_label=HC245]  # not connected
  IC2 = IC, DIP package, 16 pins [chip_label=HC123]  # not connected
  IC3 = IC, DIP package, 14 pins [chip_label="HC00 NAND"]
  IC4 = IC, DIP package, 20 pins [chip_label=HC245]  # not connected
  IC5 = IC, DIP package, 20 pins [chip_label=HC245]  # not connected
  IC6 = IC, DIP package, 20 pins [chip_label=HC245]  # not connected
  IC7 = IC, DIP package, 14 pins [chip_label="HC02 NOR"]

nets:
  N1: IC3.pin7, IC7.pin7
  N2: IC3.pin14, IC7.pin14

notes:
  clock
