# Fritzing sketch sixteen-bit-RAM (saved by Fritzing 0.9.3b)
breadboards: 2

parts:
  IC9 = IC, DIP package, 32 pins [chip_label=IC]
  J5 = female pin header, 8 pins [form="♀ (female)"]
  J6 = female pin header, 8 pins [form="♀ (female)"]
  J7 = female pin header, 8 pins [form="♀ (female)"]
  J8 = female pin header, 8 pins [form="♀ (female)"]
  J9 = female pin header, 8 pins [form="♀ (female)"]
  J10 = female pin header, 8 pins [form="♀ (female)"]
  IC10 = IC, DIP package, 32 pins [chip_label=IC]
  IC11 = IC, DIP package, 20 pins [chip_label=HC245]
  IC12 = IC, DIP package, 20 pins [chip_label=HC245]
  IC13 = IC, DIP package, 16 pins [chip_label=HC123]
  IC14 = IC, DIP package, 14 pins [chip_label="HC04 NOT"]
  IC15 = IC, DIP package, 14 pins [chip_label="HC02 NOR"]
  IC16 = IC, DIP package, 14 pins [chip_label="HC08 AND"]
  R4 = Resistor [tolerance=±5% resistance=4.7k package=THT]
  R5 = Resistor [tolerance=±5% resistance=4.7k package=THT]
  C3 = Ceramic Capacitor [capacitance=30pF package="100 mil [THT, multilayer]"]
  C4 = Ceramic Capacitor [capacitance=100nF package="100 mil [THT, multilayer]"]
  J11 = female pin header, 8 pins [form="♀ (female)"]
  J12 = female pin header, 8 pins [form="♀ (female)"]
  J13 = female pin header, 8 pins [form="♀ (female)"]
  J14 = female pin header, 8 pins [form="♀ (female)"]

nets:
  N1: IC9.pin2, IC9.pin16, IC10.pin2, IC10.pin16
  N2: IC9.pin3, J5.pin2
  N3: IC9.pin4, J5.pin4
  N4: IC9.pin5, J7.pin1
  N5: IC9.pin6, J7.pin2
  N6: IC9.pin7, J7.pin3
  N7: IC9.pin8, J7.pin4
  N8: IC9.pin9, J7.pin5
  N9: IC9.pin10, J7.pin6
  N10: IC9.pin11, J7.pin7
  N11: IC9.pin12, J7.pin8
  N12: IC9.pin13, J6.pin8
  N13: IC9.pin14, J6.pin7
  N14: IC9.pin15, J6.pin6
  N15: IC9.pin17, J6.pin5
  N16: IC9.pin18, J6.pin4
  N17: IC9.pin19, J6.pin3
  N18: IC9.pin20, J6.pin2
  N19: IC9.pin21, J6.pin1
  N20: IC9.pin22, IC9.pin30, IC9.pin32, IC10.pin22, IC10.pin30, IC10.pin32
  N21: IC9.pin24, IC10.pin24
  N22: IC9.pin29, IC10.pin29
  N23: J8.pin1, IC10.pin5
  N24: J8.pin2, IC10.pin6
  N25: J8.pin3, IC10.pin7
  N26: J8.pin4, IC10.pin8
  N27: J8.pin5, IC10.pin9
  N28: J8.pin6, IC10.pin10
  N29: J8.pin7, IC10.pin11
  N30: J8.pin8, IC10.pin12
  N31: J9.pin1, IC10.pin21
  N32: J9.pin2, IC10.pin20
  N33: J9.pin3, IC10.pin19
  N34: J9.pin4, IC10.pin18
  N35: J9.pin5, IC10.pin17
  N36: J9.pin6, IC10.pin15
  N37: J9.pin7, IC10.pin14
  N38: J9.pin8, IC10.pin13
  N39: J10.pin2, IC10.pin3
  N40: J10.pin4, IC10.pin4
  N41: IC11.pin1, IC12.pin1, IC14.pin12, IC16.pin9
  N42: IC11.pin2, J12.pin1
  N43: IC11.pin3, J12.pin2
  N44: IC11.pin4, J12.pin3
  N45: IC11.pin5, J12.pin4
  N46: IC11.pin6, J12.pin5
  N47: IC11.pin7, J12.pin6
  N48: IC11.pin8, J12.pin7
  N49: IC11.pin9, J12.pin8
  N50: IC11.pin10, IC12.pin10, IC13.pin1, IC13.pin8, IC14.pin1, IC14.pin3, IC14.pin5, IC14.pin7, IC15.pin7, IC16.pin4, IC16.pin5, IC16.pin7
  N51: IC11.pin11, J14.pin8
  N52: IC11.pin12, J14.pin7
  N53: IC11.pin13, J14.pin6
  N54: IC11.pin14, J14.pin5
  N55: IC11.pin15, J14.pin4
  N56: IC11.pin16, J14.pin3
  N57: IC11.pin17, J14.pin2
  N58: IC11.pin18, J14.pin1
  N59: IC11.pin19, IC12.pin19, IC16.pin8
  N60: IC11.pin20, IC12.pin20, IC13.pin11, IC13.pin16, IC14.pin14, IC15.pin14, IC16.pin14, R4.Pin_0
  N61: IC12.pin2, J13.pin1
  N62: IC12.pin3, J13.pin2
  N63: IC12.pin4, J13.pin3
  N64: IC12.pin5, J13.pin4
  N65: IC12.pin6, J13.pin5
  N66: IC12.pin7, J13.pin6
  N67: IC12.pin8, J13.pin7
  N68: IC12.pin9, J13.pin8
  N69: IC12.pin11, J11.pin8
  N70: IC12.pin12, J11.pin7
  N71: IC12.pin13, J11.pin6
  N72: IC12.pin14, J11.pin5
  N73: IC12.pin15, J11.pin4
  N74: IC12.pin16, J11.pin3
  N75: IC12.pin17, J11.pin2
  N76: IC12.pin18, J11.pin1
  N77: IC13.pin2, IC13.pin10, IC16.pin3
  N78: IC13.pin3, R5.Pin_1
  N79: IC13.pin6, C4.1
  N80: IC13.pin7, R5.Pin_0, C4.0
  N81: IC13.pin9, IC14.pin9
  N82: IC13.pin12, IC16.pin12
  N83: IC13.pin13, IC16.pin13
  N84: IC13.pin14, C3.1
  N85: IC13.pin15, R4.Pin_1, C3.0
  N86: IC14.pin10, IC16.pin10
  N87: IC14.pin13, IC16.pin11
  N88: IC15.pin1, IC15.pin5
  N89: IC15.pin2, IC15.pin3, IC16.pin1
  N90: IC15.pin4, IC15.pin8
  N91: IC15.pin6, IC15.pin10, IC16.pin2
  N92: IC15.pin9, IC15.pin13
  N93: IC15.pin11, IC15.pin12

notes:
  Addr bus 15-8
  Addr bus 7-0
  clock
  WTM
  (write) ~WE
  (write) Buf ~OE
  dir
  (combined) Buf ~OE
  Data bus 7-0
  RAM 7-0
  Data bus 15-8
  RAM 15-8
  RAM ~WE
  (write) Apply inputs
  (read and write) Buf ~OE
  RFM
  Safe clock
