# Fritzing sketch two_to_one_A_B_O (saved by Fritzing 0.9.3b)
breadboards: 1

parts:
  R40 = Resistor [tolerance=±5% resistance=1k package=THT]
  R41 = Resistor [tolerance=±5% resistance=1k package=THT]
  R42 = Resistor [tolerance=±5% resistance=1k package=THT]
  R43 = Resistor [tolerance=±5% resistance=1k package=THT]
  R44 = Resistor [tolerance=±5% resistance=1k package=THT]
  R45 = Resistor [tolerance=±5% resistance=1k package=THT]
  R46 = Resistor [tolerance=±5% resistance=1k package=THT]
  R47 = Resistor [tolerance=±5% resistance=1k package=THT]
  IC10 = DIP - 16 pins [chip_label=74HCT157 package="DIP (Dual Inline) [THT]"]
  IC11 = DIP - 16 pins [chip_label=74HCT157 package="DIP (Dual Inline) [THT]"]
  OUT1 = female pin header, 8 pins [form="♀ (female)"]
  B1 = female pin header, 8 pins [form="♀ (female)"]
  A1 = female pin header, 8 pins [form="♀ (female)"]
  LED25 = LED - 5mm [color="Red (633nm)" package="5 mm [THT]"]
  LED27 = LED - 5mm [color="Red (633nm)" package="5 mm [THT]"]
  LED29 = LED - 5mm [color="Red (633nm)" package="5 mm [THT]"]
  LED31 = LED - 5mm [color="Red (633nm)" package="5 mm [THT]"]
  LED33 = LED - 5mm [color="Red (633nm)" package="5 mm [THT]"]
  LED35 = LED - 5mm [color="Red (633nm)" package="5 mm [THT]"]
  LED37 = LED - 5mm [color="Red (633nm)" package="5 mm [THT]"]
  LED39 = LED - 5mm [color="Red (633nm)" package="5 mm [THT]"]
  C1 = Ceramic Capacitor [capacitance=100nF package="100 mil [THT, multilayer]"]
  C2 = Ceramic Capacitor [capacitance=100nF package="100 mil [THT, multilayer]"]

nets:
  VCC: R40.Pin_0, R41.Pin_0, R42.Pin_0, R43.Pin_0, R44.Pin_0, R45.Pin_0, R46.Pin_0, R47.Pin_0, IC10.VCC, IC11.VCC, C1.1, C2.0
  N1: R40.Pin_1, LED25.cathode
  N2: R41.Pin_1, LED27.cathode
  N3: R42.Pin_1, LED29.cathode
  N4: R43.Pin_1, LED31.cathode
  N5: R44.Pin_1, LED33.cathode
  N6: R45.Pin_1, LED35.cathode
  N7: R46.Pin_1, LED37.cathode
  N8: R47.Pin_1, LED39.cathode
  N9: IC10._A/B, IC11._A/B
  N10: IC10.1A, A1.pin8
  N11: IC10.1B, B1.pin8
  N12: IC10.1Y, OUT1.pin8, LED25.anode
  N13: IC10.2A, A1.pin7
  N14: IC10.2B, B1.pin7
  N15: IC10.2Y, OUT1.pin7, LED27.anode
  GND: IC10.GND, IC10._G, IC11.GND, IC11._G, C1.0, C2.1
  N16: IC10.3Y, OUT1.pin6, LED29.anode
  N17: IC10.3B, B1.pin6
  N18: IC10.3A, A1.pin6
  N19: IC10.4Y, OUT1.pin5, LED31.anode
  N20: IC10.4B, B1.pin5
  N21: IC10.4A, A1.pin5
  N22: IC11.1A, A1.pin4
  N23: IC11.1B, B1.pin4
  N24: IC11.1Y, OUT1.pin4, LED33.anode
  N25: IC11.2A, A1.pin3
  N26: IC11.2B, B1.pin3
  N27: IC11.2Y, OUT1.pin3, LED35.anode
  N28: IC11.3Y, OUT1.pin2, LED37.anode
  N29: IC11.3B, B1.pin2
  N30: IC11.3A, A1.pin2
  N31: IC11.4Y, OUT1.pin1, LED39.anode
  N32: IC11.4B, B1.pin1
  N33: IC11.4A, A1.pin1

notes:
  A
  B
  output
  A/B

custom parts:
  DIP - 16 pins: Quad 2 line to one line data selectors
