# Fritzing sketch two_to_one_A_O_B (saved by Fritzing 0.9.3b)
breadboards: 1

parts:
  A = female pin header, 8 pins [form="♀ (female)"]
  B = female pin header, 8 pins [form="♀ (female)"]
  IC17 = DIP - 16 pins [chip_label=74HCT157 package="DIP (Dual Inline) [THT]"]
  IC18 = DIP - 16 pins [chip_label=74HCT157 package="DIP (Dual Inline) [THT]"]
  R72 = Resistor [tolerance=±5% resistance=1k package=THT]
  R73 = Resistor [tolerance=±5% resistance=1k package=THT]
  R74 = Resistor [tolerance=±5% resistance=1k package=THT]
  R75 = Resistor [tolerance=±5% resistance=1k package=THT]
  R76 = Resistor [tolerance=±5% resistance=1k package=THT]
  R77 = Resistor [tolerance=±5% resistance=1k package=THT]
  R78 = Resistor [tolerance=±5% resistance=1k package=THT]
  R79 = Resistor [tolerance=±5% resistance=1k package=THT]
  OUT3 = female pin header, 8 pins [form="♀ (female)"]
  LED49 = LED - 5mm [color="Red (633nm)" package="5 mm [THT]"]
  LED57 = LED - 5mm [color="Red (633nm)" package="5 mm [THT]"]
  LED58 = LED - 5mm [color="Red (633nm)" package="5 mm [THT]"]
  LED59 = LED - 5mm [color="Red (633nm)" package="5 mm [THT]"]
  LED60 = LED - 5mm [color="Red (633nm)" package="5 mm [THT]"]
  LED61 = LED - 5mm [color="Red (633nm)" package="5 mm [THT]"]
  LED62 = LED - 5mm [color="Red (633nm)" package="5 mm [THT]"]
  LED63 = LED - 5mm [color="Red (633nm)" package="5 mm [THT]"]

nets:
  N1: A.pin1, IC17.4A
  N2: A.pin2, IC17.3A
  N3: A.pin3, IC17.2A
  N4: A.pin4, IC17.1A
  N5: A.pin5, IC18.4A
  N6: A.pin6, IC18.3A
  N7: A.pin7, IC18.2A
  N8: A.pin8, IC18.1A
  N9: B.pin1, IC17.4B
  N10: B.pin2, IC17.3B
  N11: B.pin3, IC17.2B
  N12: B.pin4, IC17.1B
  N13: B.pin5, IC18.4B
  N14: B.pin6, IC18.3B
  N15: B.pin7, IC18.2B
  N16: B.pin8, IC18.1B
  N17: IC17._A/B, IC18._A/B
  N18: IC17.1Y, OUT3.pin4, LED60.anode
  N19: IC17.2Y, OUT3.pin3, LED61.anode
  GND: IC17.GND, IC18.GND, R72.Pin_0, R73.Pin_0, R74.Pin_0, R75.Pin_0, R76.Pin_0, R77.Pin_0, R78.Pin_0, R79.Pin_0
  N20: IC17.3Y, OUT3.pin2, LED63.anode
  N21: IC17.4Y, OUT3.pin1, LED62.anode
  N22: IC17._G, IC18._G
  VCC: IC17.VCC, IC18.VCC
  N23: IC18.1Y, OUT3.pin8, LED49.anode
  N24: IC18.2Y, OUT3.pin7, LED57.anode
  N25: IC18.3Y, OUT3.pin6, LED58.anode
  N26: IC18.4Y, OUT3.pin5, LED59.anode
  N27: R72.Pin_1, LED49.cathode
  N28: R73.Pin_1, LED57.cathode
  N29: R74.Pin_1, LED58.cathode
  N30: R75.Pin_1, LED59.cathode
  N31: R76.Pin_1, LED60.cathode
  N32: R77.Pin_1, LED61.cathode
  N33: R78.Pin_1, LED63.cathode
  N34: R79.Pin_1, LED62.cathode

custom parts:
  DIP - 16 pins: Quad 2 line to one line data selectors
