# Fritzing sketch two_to_one_O_A_B (saved by Fritzing 0.9.3b)
breadboards: 1

parts:
  R64 = Resistor [tolerance=±5% resistance=1k package=THT]
  R65 = Resistor [tolerance=±5% resistance=1k package=THT]
  R66 = Resistor [tolerance=±5% resistance=1k package=THT]
  R67 = Resistor [tolerance=±5% resistance=1k package=THT]
  R68 = Resistor [tolerance=±5% resistance=1k package=THT]
  R69 = Resistor [tolerance=±5% resistance=1k package=THT]
  R70 = Resistor [tolerance=±5% resistance=1k package=THT]
  R71 = Resistor [tolerance=±5% resistance=1k package=THT]
  A = female pin header, 8 pins [form="♀ (female)"]
  OUT = female pin header, 8 pins [form="♀ (female)"]
  B = female pin header, 8 pins [form="♀ (female)"]
  IC15 = DIP - 16 pins [chip_label=74HCT157 package="DIP (Dual Inline) [THT]"]
  IC16 = DIP - 16 pins [chip_label=74HCT157 package="DIP (Dual Inline) [THT]"]
  LED1 = LED - 5mm [color="Red (633nm)" package="5 mm [THT]"]
  LED2 = LED - 5mm [color="Red (633nm)" package="5 mm [THT]"]
  LED3 = LED - 5mm [color="Red (633nm)" package="5 mm [THT]"]
  LED4 = LED - 5mm [color="Red (633nm)" package="5 mm [THT]"]
  LED5 = LED - 5mm [color="Red (633nm)" package="5 mm [THT]"]
  LED6 = LED - 5mm [color="Red (633nm)" package="5 mm [THT]"]
  LED7 = LED - 5mm [color="Red (633nm)" package="5 mm [THT]"]
  LED8 = LED - 5mm [color="Red (633nm)" package="5 mm [THT]"]
  C1 = Ceramic Capacitor [capacitance=100nF package="100 mil [THT, multilayer]"]
  C2 = Ceramic Capacitor [capacitance=100nF package="100 mil [THT, multilayer]"]

nets:
  VCC: R64.Pin_0, R65.Pin_0, R66.Pin_0, R67.Pin_0, R68.Pin_0, R69.Pin_0, R70.Pin_0, R71.Pin_0, IC15.VCC, IC16.VCC, C1.1, C2.0
  N1: R64.Pin_1, LED7.cathode
  N2: R65.Pin_1, LED8.cathode
  N3: R66.Pin_1, LED6.cathode
  N4: R67.Pin_1, LED5.cathode
  N5: R68.Pin_1, LED4.cathode
  N6: R69.Pin_1, LED3.cathode
  N7: R70.Pin_1, LED2.cathode
  N8: R71.Pin_1, LED1.cathode
  N9: A.pin1, IC15.4A
  N10: A.pin2, IC15.3A
  N11: A.pin3, IC15.2A
  N12: A.pin4, IC15.1A
  N13: A.pin5, IC16.4A
  N14: A.pin6, IC16.3A
  N15: A.pin7, IC16.2A
  N16: A.pin8, IC16.1A
  N17: OUT.pin1, IC15.4Y, LED1.anode
  N18: OUT.pin2, IC15.3Y, LED2.anode
  N19: OUT.pin3, IC15.2Y, LED3.anode
  N20: OUT.pin4, IC15.1Y, LED4.anode
  N21: OUT.pin5, IC16.4Y, LED5.anode
  N22: OUT.pin6, IC16.3Y, LED6.anode
  N23: OUT.pin7, IC16.2Y, LED8.anode
  N24: OUT.pin8, IC16.1Y, LED7.anode
  N25: B.pin1, IC15.4B
  N26: B.pin2, IC15.3B
  N27: B.pin3, IC15.2B
  N28: B.pin4, IC15.1B
  N29: B.pin5, IC16.4B
  N30: B.pin6, IC16.3B
  N31: B.pin7, IC16.2B
  N32: B.pin8, IC16.1B
  N33: IC15._A/B, IC16._A/B
  GND: IC15.GND, IC15._G, IC16.GND, IC16._G, C1.0, C2.1

notes:
  A
  B
  output
  A/B

custom parts:
  DIP - 16 pins: Quad 2 line to one line data selectors
