# Fritzing sketch user_control (saved by Fritzing 0.9.3b)
breadboards: 1

parts:
  S1 = Pushbutton [package="[THT]"]
  R1 = Rotary Potentiometer (Small) [maximum_resistance=100kΩ package=THT]
  S2 = Pushbutton [package="[THT]"]
  S3 = Pushbutton [package="[THT]"]
  S4 = Pushbutton [package="[THT]"]
  S5 = Pushbutton [package="[THT]"]
  S6 = Pushbutton [package="[THT]"]
  S7 = Pushbutton [package="[THT]"]
  S8 = Pushbutton [package="[THT]"]
  LED1 = LED - 5mm [color="Red (633nm)" package="5 mm [THT]"]
  R2 = Resistor [tolerance=±5% resistance=2k package=THT]  # not connected
  R3 = Resistor [tolerance=±5% resistance=2k package=THT]
  LED2 = LED - 5mm [color="Red (633nm)" package="5 mm [THT]"]
  R4 = Resistor [tolerance=±5% resistance=10k package=THT]
  C1 = Ceramic Capacitor [capacitance=100nF package="100 mil [THT, multilayer]"]
  R5 = Resistor [tolerance=±5% resistance=10k package=THT]
  R6 = Resistor [tolerance=±5% resistance=220 package=THT]
  C2 = Ceramic Capacitor [capacitance=100nF package="100 mil [THT, multilayer]"]
  R7 = Resistor [tolerance=±5% resistance=10k package=THT]
  R8 = Resistor [tolerance=±5% resistance=10k package=THT]
  R9 = Resistor [tolerance=±5% resistance=10k package=THT]
  R10 = Resistor [tolerance=±5% resistance=10k package=THT]
  C3 = Ceramic Capacitor [capacitance=100nF package="100 mil [THT, multilayer]"]
  LED3 = LED - 5mm [color="Red (633nm)" package="5 mm [THT]"]
  LED4 = LED - 5mm [color="Red (633nm)" package="5 mm [THT]"]
  R12 = Resistor [tolerance=±5% resistance=2k package=THT]
  R13 = Resistor [tolerance=±5% resistance=2k package=THT]
  R14 = Resistor [tolerance=±5% resistance=2k package=THT]
  R15 = Resistor [tolerance=±5% resistance=2k package=THT]
  LED5 = LED - 5mm [color="Red (633nm)" package="5 mm [THT]"]
  LED6 = LED - 5mm [color="Red (633nm)" package="5 mm [THT]"]
  R16 = Resistor [tolerance=±5% resistance=10k package=THT]
  C4 = Ceramic Capacitor [capacitance=100nF package="100 mil [THT, multilayer]"]
  R17 = Resistor [tolerance=±5% resistance=10k package=THT]
  R18 = Resistor [tolerance=±5% resistance=10k package=THT]
  C5 = Ceramic Capacitor [capacitance=100nF package="100 mil [THT, multilayer]"]
  J1 = female pin header, 9 pins [form="♀ (female)"]
  C6 = Ceramic Capacitor [capacitance=100nF package="100 mil [THT, multilayer]"]

nets:
  N1: S1.Pin_1, S1.Pin_2, LED2.anode, R4.Pin_0
  N2: S1.Pin_3, S1.Pin_4, LED1.cathode
  N3: R1.wiper, J1.pin2
  N4: R1.leg2, J1.pin3
  N5: S2.Pin_1, S2.Pin_2, S5.Pin_1, S5.Pin_2, S8.Pin_1, S8.Pin_2, R3.Pin_0, R12.Pin_0, R13.Pin_0, R14.Pin_0, R15.Pin_0
  N6: S2.Pin_3, S2.Pin_4, S4.Pin_1, S4.Pin_2
  N7: S3.Pin_1, S3.Pin_2
  N8: S3.Pin_3, S3.Pin_4
  N9: S4.Pin_3, S4.Pin_4
  N10: S5.Pin_3, S5.Pin_4
  N11: S6.Pin_1, S6.Pin_2, LED4.anode, R16.Pin_0
  N12: S6.Pin_3, S6.Pin_4, LED3.cathode
  N13: S7.Pin_1, S7.Pin_2, LED5.anode
  N14: S7.Pin_3, S7.Pin_4, LED6.cathode
  N15: S8.Pin_3, S8.Pin_4
  N16: R3.Pin_1, LED2.cathode
  N17: R4.Pin_1, C1.1, J1.pin1
  N18: C1.0, R7.Pin_1, C4.0, C6.0
  N19: R5.Pin_0, C2.0, R10.Pin_0, C3.0, R17.Pin_0, C5.0
  N20: R5.Pin_1, R6.Pin_0
  N21: R6.Pin_1, C2.1, J1.pin4
  N22: R7.Pin_0, R8.Pin_0
  N23: R8.Pin_1, J1.pin5, C6.1
  N24: R9.Pin_0, R10.Pin_1
  N25: R9.Pin_1, C3.1, J1.pin6
  N26: LED3.anode, R13.Pin_1
  N27: LED4.cathode, R12.Pin_1
  N28: R14.Pin_1, LED5.cathode, J1.pin8
  N29: R15.Pin_1, LED6.anode
  N30: R16.Pin_1, C4.1, J1.pin7
  N31: R17.Pin_1, R18.Pin_0
  N32: R18.Pin_1, C5.1, J1.pin9

notes:
  _auto/manual
  1/4 step
  1/2 step
  full step
  reset
  sel _prog/data mem
  write
  _run/setup
  _auto/man
  variable_res
  1/4 and 1/2 step
  _prog/data mem
  left to right:
