# Fritzing sketch user_control_debounce (saved by Fritzing 0.9.3b)
breadboards: 1

parts:
  J1 = female pin header, 9 pins [form="♀ (female)"]
  IC1 = DIP - 14 pins [chip_label=74HCT14 package="DIP (Dual Inline) [THT]"]
  IC2 = DIP - 14 pins [chip_label=74HCT04 package="DIP (Dual Inline) [THT]"]
  IC3 = 74HCT123 [chip_label=74HCT123 package="DIP (Dual Inline) [THT]"]
  IC4 = DIP - 14 pins [chip_label=74HCT32 package="DIP (Dual Inline) [THT]"]
  IC5 = DIP - 14 pins [chip_label=74HCT86 package="DIP (Dual Inline) [THT]"]
  R1 = Resistor [tolerance=±5% resistance=220 package=THT]
  C1 = Ceramic Capacitor [capacitance=100nF package="100 mil [THT, multilayer]"]
  R2 = Resistor [tolerance=±5% resistance=220 package=THT]
  C2 = Ceramic Capacitor [capacitance=100nF package="100 mil [THT, multilayer]"]
  C3 = Ceramic Capacitor [capacitance=100nF package="100 mil [THT, multilayer]"]
  C4 = Ceramic Capacitor [capacitance=100nF package="100 mil [THT, multilayer]"]

nets:
  N1: J1.pin1, IC1.1A
  N2: J1.pin4, IC1.2A
  N3: J1.pin5, IC1.3A
  N4: J1.pin6, IC1.6A
  N5: J1.pin7, IC1.5A
  N6: J1.pin9, IC1.4A
  N7: IC1.2Y, IC2.1A
  N8: IC1.3Y, IC2.2A
  GND: IC1.GND, IC2.3A, IC2.GND, IC2.4A, IC3.1_A, IC3.2CEXT, IC3.GND, IC3.1CEXT, IC4.2A, IC4.2B, IC4.GND, IC4.3A, IC4.3B, IC5.2A, IC5.2B, IC5.GND, IC5.3A, IC5.3B, IC5.4A, IC5.4B, C1.1, C2.1, C3.0, C4.1
  N9: IC1.4Y, IC2.5A
  N10: IC1.5Y, IC4.4A
  N11: IC1.6Y, IC2.6A
  VCC: IC1.VCC, IC2.VCC, IC3.1_RD, IC3.2B, IC3.2_RD, IC3.VCC, IC4.VCC, IC5.VCC, R1.Pin_0, R2.Pin_1, C3.1, C4.0
  N12: IC2.1Y, IC5.1B
  N13: IC2.2Y, IC3.1B, IC3.2_A
  N14: IC2.6Y, IC4.4B
  N15: IC3.2Q, IC4.1B
  N16: IC3.2REXTCEXT, R2.Pin_0, C2.0
  N17: IC3.1Q, IC4.1A
  N18: IC3.1REXTCEXT, R1.Pin_1, C1.0
  N19: IC4.1Y, IC5.1A

notes:
  _auto/man
  man_clock
  reset or _run/setup
  setup_write
  _prog/data
  reset
  _run/setup
  write
  _prog/data mem
  variable_res
  full step
  1/4 and 1/2 step
  left to right:

custom parts:
  DIP - 14 pins: Hex Schmitt trigger inverters
  DIP - 14 pins: Hex Inverter
  74HCT123: Dual retriggerable monostable multivibrator with reset
  DIP - 14 pins: Quad OR gate
  DIP - 14 pins: Quad XOR
