// Logisim project 8bit_74LS_computer.circ as structural Verilog: 20 circuits, main circuit main
module main (
  input  in_1,
  input  in_2,
  input  [7:0] in_3
);

  wire ALU_add_sub, ALU_output_enable, button_1_out, carry, clear, clock, CLOCK_clock_out,
       finished_user_input, halt, instruction_register_input_enable, manual_clock_pulse,
       memory_address_register_input_enable, program_counter_increment, program_counter_input_enable,
       program_counter_output_enable, ram_input_enable, ram_output_enable, register_A_input_enable,
       register_A_output_enable, register_B_input_enable, register_B_output_enable, undriven, undriven_2;
  wire [2:0] microcode_step;
  wire [7:0] A_register_contents, ALU_result, B_register_contents, bus, C_register_contents,
       D_register_contents, display_content, instruction_register_contents, memory_address_register_contents,
       program_counter_contents;

  Button button_1 (.out(button_1_out));
  Button button_2 (.out(clear));
  Button button_3 (.out(finished_user_input));
  or or_1 (manual_clock_pulse, in_1, button_1_out);
  // Probe on register_A_input_enable
  // Probe on register_A_output_enable
  // Probe on register_B_input_enable
  // Probe on register_B_output_enable
  // Probe on ALU_output_enable
  // Probe on ALU_add_sub
  // Probe on memory_address_register_input_enable
  // Probe on ram_input_enable
  // Probe on ram_output_enable
  // Probe on program_counter_input_enable
  // Probe on program_counter_output_enable
  // Probe on program_counter_increment
  // Probe on instruction_register_input_enable
  // Probe on halt
  // Probe on clock
  // Probe on carry
  // Probe on bus
  // Probe on program_counter_contents
  // Probe on A_register_contents
  // Probe on ALU_result
  // Probe on B_register_contents
  // Probe on memory_address_register_contents
  // Probe on instruction_register_contents
  // Probe on microcode_step
  // Probe on microcode_step
  // Probe on bus
  // Probe on program_counter_contents
  // Probe on A_register_contents
  // Probe on ALU_result
  // Probe on B_register_contents
  // Probe on memory_address_register_contents
  // Probe on instruction_register_contents
  // Probe on microcode_step
  // Probe on bus
  // Probe on program_counter_contents
  // Probe on A_register_contents
  // Probe on ALU_result
  // Probe on B_register_contents
  // Probe on memory_address_register_contents
  // Probe on instruction_register_contents
  // OR_Gate or_2 is placed but not wired
  instruction_decoder instruction_decoder_1 ();  // open: register_A_input_enable, register_A_output_enable, register_B_input_enable, register_B_output_enable, alu_output_enable, alu_op_0, memory_address_register_input_enable, ram_input_enable, ram_output_enable, program_counter_input_enable, program_counter_output_enable, program_counter_increment, instruction_register_input_enable, halt, clock, clear, alu_signal, instruction_byte, microcode_step, register_C_input_enable, register_C_output_enable, register_D_input_enable, register_D_output_enable, alu_op_1, alu_op_2, alu_op_3
  clock u_CLOCK (
    .manual_clock(manual_clock_pulse), .clock_out(CLOCK_clock_out), .auto_manual_step(in_2));  // open: halt
  register_L INSTRUCTION_REGISTER (
    .\input (bus), .buffered_output(bus), .content(instruction_register_contents), .clock(undriven_2),
    .clear(undriven));  // open: input_enable, output_enable
  program_counter PROGRAM_COUNTER (
    .buffered_input(bus), .clock(undriven_2), .clear(undriven), .buffered_output(bus),
    .contents(program_counter_contents));  // open: increment, output_enable, input_enable
  register_L A_REGISTER (
    .\input (bus), .buffered_output(bus), .content(A_register_contents), .clock(undriven_2), .clear(undriven));  // open: input_enable, output_enable
  register_L B_REGISTER (
    .\input (bus), .buffered_output(bus), .content(B_register_contents), .clock(undriven_2), .clear(undriven));  // open: input_enable, output_enable
  register_L C_REGISTER (
    .\input (bus), .buffered_output(bus), .content(C_register_contents), .clock(undriven_2), .clear(undriven));  // open: input_enable, output_enable
  register_L D_REGISTER (
    .\input (bus), .buffered_output(bus), .content(D_register_contents), .clock(undriven_2), .clear(undriven));  // open: input_enable, output_enable
  Pull_Resistor pull_resistor_1 (.node(bus));
  user_input USER_INPUT (.buffered_output(bus));  // open: user_input, output_enable
  register_R MEMORY_ADDRESS_REGISTER (
    .\input (bus), .buffered_output(bus), .content(memory_address_register_contents));  // open: input_enable, clock, clear, output_enable
  RAM RAM (
    .address(memory_address_register_contents), .buffered_input(bus), .buffered_output(bus));  // open: input_enable, output_enable, clock
  request_user_input REQUEST_USER_INPUT (
    .\input (bus), .buffered_output(bus));  // open: user_finished, input_enable, clear, output_enable, waiting_for_user_input
  register_R DISPLAY (
    .\input (bus), .buffered_output(bus), .content(display_content));  // open: input_enable, clock, clear, output_enable
  memory_map_controller memory_map_controller_1 ();  // open: input_ram_input_enable, input_ram_output_enable, address, output_ram_input_enable, output_ram_output_enable, MMD_0_input_enable, MMD_0_output_enable, MMD_1_input_enable, MMD_1_output_enable, MMD_2_input_enable, MMD_2_output_enable

  // Other names for the same wires on the sheet: auto_manual_clock = in_2; user_input[7:0] = in_3

  // Notes on the sheet:
  //   this is needed for getting rid of strange startup error condiitions in logisim
endmodule

module ALU (
  input  [3:0] operation,
  input  [7:0] A_input,
  input  [7:0] B_input,
  input  output_enable,
  output signal,
  output [7:0] buffered_output
);

  wire adder_subtractor_1_carry_out, bit_shift_left_1_overflow, bit_shift_right_1_overflow, decoder_1_out0,
       decoder_1_out1, decoder_1_out2, decoder_1_out3, decoder_1_out4, or_1_out, or_2_out,
       zero_check_1_is_zero;
  wire [7:0] adder_subtractor_1_buffered_output, adder_subtractor_1_unbuffered_output,
       bit_shift_left_1_output, buffer_1_out, buffer_2_out;

  Decoder #(.select(4)) decoder_1 (
    .out0(decoder_1_out0), .out1(decoder_1_out1), .out2(decoder_1_out2), .out3(decoder_1_out3),
    .out4(decoder_1_out4), .sel(operation), .en(1'b1));  // open: out5, out6, out7, out8, out9, out10, out11, out12, out13, out14, out15
  or or_1 (or_1_out, decoder_1_out2, decoder_1_out1);
  or or_2 (or_2_out, bit_shift_right_1_overflow, bit_shift_left_1_overflow, adder_subtractor_1_carry_out, zero_check_1_is_zero);
  zero_check zero_check_1 (.\input (buffer_1_out), .is_zero(zero_check_1_is_zero), .enable(decoder_1_out0));
  adder_subtractor adder_subtractor_1 (
    .add_sub(decoder_1_out2), .buffered_output(adder_subtractor_1_buffered_output), .A_input(buffer_1_out),
    .enable(or_1_out), .B_input(buffer_2_out), .carry_out(adder_subtractor_1_carry_out),
    .unbuffered_output(adder_subtractor_1_unbuffered_output));
  bit_shift_left bit_shift_left_1 (
    .\input (buffer_1_out), .\output (bit_shift_left_1_output),
    .buffered_output(adder_subtractor_1_buffered_output), .overflow(bit_shift_left_1_overflow),
    .enable(decoder_1_out3));
  bit_shift_right bit_shift_right_1 (
    .\input (buffer_1_out), .buffered_output(adder_subtractor_1_buffered_output),
    .overflow(bit_shift_right_1_overflow), .enable(decoder_1_out4));  // open: output
  \and  and_1 ();  // open: A_input, B_input, buffered_output, enable, output
  \or  or_3 ();  // open: enable, A_input, buffered_output, B_input, output
  \not  not_1 ();  // open: buffered_output, input, enable, output
  \xor  xor_1 ();  // open: enable, A_input, buffered_output, B_input, output
  assign buffer_1_out = A_input;  // Buffer buffer_1, 8 bits wide
  assign buffer_2_out = B_input;  // Buffer buffer_2, 8 bits wide
  assign buffered_output = output_enable ? adder_subtractor_1_buffered_output : 8'bz;  // Controlled_Buffer controlled_buffer_1
endmodule

module zero_check (
  input  [7:0] \input ,
  input  enable,
  output is_zero
);

  wire nor_1_out;

  nor nor_1 (nor_1_out, \input [0], \input [1], \input [2], \input [3], \input [4], \input [5], \input [6], \input [7]);
  and and_1 (is_zero, nor_1_out, enable);
endmodule

module adder_subtractor (
  input  [7:0] A_input,
  input  enable,
  input  add_sub,
  input  [7:0] B_input,
  output [7:0] buffered_output,
  output [7:0] unbuffered_output,
  output carry_out
);

  wire adder_1_cout;
  wire [7:0] xor_1_out;

  assign xor_1_out = {8{add_sub}} ^ B_input;  // XOR_Gate xor_1, 8 bits wide
  Adder adder_1 (.a(A_input), .b(xor_1_out), .out(unbuffered_output), .cin(add_sub), .cout(adder_1_cout));
  and and_1 (carry_out, adder_1_cout, enable);
  assign buffered_output = enable ? unbuffered_output : 8'bz;  // Controlled_Buffer controlled_buffer_1
endmodule

module bit_shift_left (
  input  [7:0] \input ,
  input  enable,
  output [7:0] \output ,
  output [7:0] buffered_output,
  output overflow
);

  and and_1 (overflow, \input [7], enable);
  assign buffered_output = enable ? {\input [6:0], 1'b0} : 8'bz;  // Controlled_Buffer controlled_buffer_1

  assign \output  = {\input [6:0], 1'b0};
endmodule

module bit_shift_right (
  input  [7:0] \input ,
  input  enable,
  output [7:0] \output ,
  output [7:0] buffered_output,
  output overflow
);

  and and_1 (overflow, \input [0], enable);
  assign buffered_output = enable ? {1'b0, \input [7:1]} : 8'bz;  // Controlled_Buffer controlled_buffer_1

  assign \output  = {1'b0, \input [7:1]};
endmodule

module \and  (
  input  enable,
  input  [7:0] A_input,
  input  [7:0] B_input,
  output [7:0] buffered_output,
  output [7:0] \output 
);

  assign \output  = A_input & B_input;  // AND_Gate and_1, 8 bits wide
  assign buffered_output = enable ? \output  : 8'bz;  // Controlled_Buffer controlled_buffer_1
endmodule

module \or  (
  input  enable,
  input  [7:0] A_input,
  input  [7:0] B_input,
  output [7:0] buffered_output,
  output [7:0] \output 
);

  assign \output  = A_input | B_input;  // OR_Gate or_1, 8 bits wide
  assign buffered_output = enable ? \output  : 8'bz;  // Controlled_Buffer controlled_buffer_1
endmodule

module \not  (
  input  enable,
  input  [7:0] \input ,
  output [7:0] buffered_output,
  output [7:0] \output 
);

  assign \output  = ~\input ;  // NOT_Gate not_1, 8 bits wide
  assign buffered_output = enable ? \output  : 8'bz;  // Controlled_Buffer controlled_buffer_1
endmodule

module \xor  (
  input  enable,
  input  [7:0] A_input,
  input  [7:0] B_input,
  output [7:0] buffered_output,
  output [7:0] \output 
);

  assign \output  = A_input ^ B_input;  // XOR_Gate xor_1, 8 bits wide
  assign buffered_output = enable ? \output  : 8'bz;  // Controlled_Buffer controlled_buffer_1
endmodule

module register_L (
  input  [7:0] \input ,
  input  input_enable,
  input  clock,
  input  clear,
  input  output_enable,
  output [7:0] content,
  output [7:0] buffered_output
);

  wire and_1_out;

  Register register_1 (.D(\input ), .en(1'b1), .Q(content), .clk(and_1_out), .clr(clear));
  and and_1 (and_1_out, input_enable, clock);
  assign buffered_output = output_enable ? content : 8'bz;  // Controlled_Buffer controlled_buffer_1
endmodule

module register_R (
  input  [7:0] \input ,
  input  input_enable,
  input  clock,
  input  clear,
  input  output_enable,
  output [7:0] content,
  output [7:0] buffered_output
);

  wire and_1_out;

  Register register_1 (.D(\input ), .en(1'b1), .Q(content), .clk(and_1_out), .clr(clear));
  and and_1 (and_1_out, input_enable, clock);
  assign buffered_output = output_enable ? content : 8'bz;  // Controlled_Buffer controlled_buffer_1
endmodule

module clock (
  input  manual_clock,
  input  auto_manual_step,
  input  halt,
  output clock_out
);

  wire auto_clock_out, multiplexer_1_out, not_1_out;

  Clock auto_clock (.out(auto_clock_out));
  Multiplexer multiplexer_1 (
    .in0(auto_clock_out), .in1(manual_clock), .out(multiplexer_1_out), .sel(auto_manual_step), .en(1'b1));
  not not_1 (not_1_out, halt);
  and and_1 (clock_out, multiplexer_1_out, not_1_out);
endmodule

module RAM (
  input  [7:0] buffered_input,
  input  input_enable,
  input  [7:0] address,
  input  clock,
  input  output_enable,
  output [7:0] buffered_output
);

  wire not_1_out;
  wire [7:0] ram_1_data;

  RAM_part ram_1 (.addr(address), .data(ram_1_data), .sel(1'b1), .clk(clock), .ld(not_1_out), .clr(1'b0));
  not not_1 (not_1_out, input_enable);
  assign ram_1_data = input_enable ? buffered_input : 8'bz;  // Controlled_Buffer controlled_buffer_1
  assign buffered_output = output_enable ? ram_1_data : 8'bz;  // Controlled_Buffer controlled_buffer_2
endmodule

module program_counter (
  input  input_enable,
  input  output_enable,
  input  [7:0] buffered_input,
  input  increment,
  input  clock,
  input  clear,
  output [7:0] buffered_output,
  output [7:0] contents
);

  wire [7:0] controlled_buffer_1_out;

  assign controlled_buffer_1_out = input_enable ? buffered_input : 8'bz;  // Controlled_Buffer controlled_buffer_1
  Counter counter_1 (
    .load(input_enable), .D(controlled_buffer_1_out), .count(increment), .Q(contents), .clk(clock),
    .clr(clear));  // open: carry
  assign buffered_output = output_enable ? contents : 8'bz;  // Controlled_Buffer controlled_buffer_2
endmodule

module instruction_decoder (
  input  [7:0] instruction_byte,
  input  clock,
  input  clear,
  input  alu_signal,
  output register_A_input_enable,
  output register_A_output_enable,
  output register_B_input_enable,
  output register_B_output_enable,
  output register_C_input_enable,
  output register_C_output_enable,
  output [2:0] microcode_step,
  output register_D_input_enable,
  output register_D_output_enable,
  output alu_output_enable,
  output alu_op_0,
  output alu_op_1,
  output alu_op_2,
  output alu_op_3,
  output memory_address_register_input_enable,
  output ram_input_enable,
  output ram_output_enable,
  output program_counter_input_enable,
  output program_counter_output_enable,
  output program_counter_increment,
  output instruction_register_input_enable,
  output halt
);

  wire not_1_out, or_1_out;
  wire [7:5] rom_3_data;

  not not_1 (not_1_out, clock);
  or or_1 (or_1_out, clear, rom_3_data[5]);
  Counter #(.width(3), .max('h7)) counter_1 (
    .load(1'b0), .D(3'b000), .count(1'b1), .Q(microcode_step), .clk(not_1_out), .clr(or_1_out));  // open: carry
  ROM #(.addrWidth(13)) rom_1 (
    .addr({1'b0, alu_signal, microcode_step, instruction_byte}),
    .data({register_D_output_enable, register_D_input_enable, register_C_output_enable, register_C_input_enable, register_B_output_enable, register_B_input_enable, register_A_output_enable, register_A_input_enable}),
    .sel(1'b1));
  ROM #(.addrWidth(13)) rom_2 (
    .addr({1'b0, alu_signal, microcode_step, instruction_byte}),
    .data({ram_output_enable, ram_input_enable, memory_address_register_input_enable, alu_op_3, alu_op_2, alu_op_1, alu_op_0, alu_output_enable}),
    .sel(1'b1));
  ROM #(.addrWidth(13)) rom_3 (
    .addr({1'b0, alu_signal, microcode_step, instruction_byte}),
    .data({rom_3_data, halt, instruction_register_input_enable, program_counter_increment, program_counter_output_enable, program_counter_input_enable}),
    .sel(1'b1));

  // Notes on the sheet:
  //   microcode 0
  //   microcode 1
  //   microcode 2
  //   contents of rom_1 (hex, n*v repeats v):
  //   4*10 4*c 4*10 4*8 4*0 4*2 72*0 4*10 4*c 4*0 4*2 16*0 4*10 4*c 4*0 4*2 80*0 4*10 4*c 4*10 4*8 4*0 4*2
  //   200*0 4*10 4*c 8 10 8 10 2 20 2 20 0 2 0 2 108*0 4*10 4*c 4*2 20*0 4*10 4*c 4*1
  //   contents of rom_2 (hex, n*v repeats v):
  //   4*4 4*1 4*4 4*5 4*1 76*0 4*4 4*1 4*20 20*0 4*4 4*1 4*10 84*0 4*4 4*1 4*4 4*5 4*81 204*0 4*4 4*1 0 4
  //   0 4 0 1 0 1 112*0 4*4 4*1 24*0 4*4 4*1
  //   contents of rom_3 (hex, n*v repeats v):
  //   16*0 4*2 84*0 4*1 28*0 4*2
endmodule

module memory_map_controller (
  input  input_ram_input_enable,
  input  input_ram_output_enable,
  input  [7:0] address,
  output output_ram_input_enable,
  output output_ram_output_enable,
  output MMD_0_input_enable,
  output MMD_0_output_enable,
  output MMD_1_input_enable,
  output MMD_1_output_enable,
  output MMD_2_input_enable,
  output MMD_2_output_enable
);

  ROM #(.addrWidth(10)) rom_1 (
    .addr({input_ram_input_enable, input_ram_output_enable, address}),
    .data({MMD_2_output_enable, MMD_2_input_enable, MMD_1_output_enable, MMD_1_input_enable, MMD_0_output_enable, MMD_0_input_enable, output_ram_output_enable, output_ram_input_enable}),
    .sel(1'b1));
endmodule

module request_user_input (
  input  user_finished,
  input  clear,
  input  output_enable,
  input  [7:0] \input ,
  input  input_enable,
  output waiting_for_user_input,
  output [7:0] buffered_output
);

  wire and_1_out, and_2_out, or_1_out;
  wire [0:0] not_1_out;

  and and_1 (and_1_out, waiting_for_user_input, user_finished);
  and and_2 (and_2_out, \input [0], input_enable);
  or or_1 (or_1_out, and_1_out, and_2_out);
  J_K_Flip_Flop j_k_ff_1 (
    .J(1'b1), .clk(or_1_out), .K(1'b1), .Q(waiting_for_user_input), .preset(1'b0), .en(1'b1), .reset(clear));  // open: Qn
  not not_1 (not_1_out[0], waiting_for_user_input);
  assign buffered_output = output_enable ? {{7{1'b0}}, not_1_out[0]} : 8'bz;  // Controlled_Buffer controlled_buffer_1
endmodule

module user_input (
  input  [7:0] user_input,
  input  output_enable,
  output [7:0] buffered_output
);

  assign buffered_output = output_enable ? user_input : 8'bz;  // Controlled_Buffer controlled_buffer_1
endmodule

module _74LS181 (
  input  in_1,
  input  in_2,
  input  in_3,
  input  in_4,
  input  B3,
  input  A3,
  input  B2,
  input  A2,
  input  B1,
  input  A1,
  input  B0,
  input  A0,
  input  M,
  input  carry_in_bar,
  input  in_15,
  output Y,
  output carry_out_bar,
  output X,
  output F3,
  output F2,
  output A_B,
  output F1,
  output F0
);

  wire and_1_out, and_2_out, and_3_out, and_4_out, and_5_out, and_6_out, and_7_out, and_8_out, and_9_out,
       and_10_out, and_11_out, and_12_out, and_13_out, and_14_out, and_15_out, and_16_out, and_17_out,
       and_18_out, and_19_out, and_20_out, and_22_out, and_23_out, and_24_out, and_25_out, and_26_out,
       and_27_out, and_28_out, and_29_out, and_30_out, nand_1_out, nor_1_out, nor_2_out, nor_3_out,
       nor_4_out, nor_5_out, nor_6_out, nor_7_out, nor_8_out, nor_10_out, nor_11_out, nor_12_out, not_1_out,
       not_2_out, not_3_out, not_4_out, not_5_out, xor_1_out, xor_2_out, xor_3_out, xor_4_out;

  not not_1 (not_1_out, B3);
  not not_2 (not_2_out, B2);
  not not_3 (not_3_out, B1);
  not not_4 (not_4_out, B0);
  not not_5 (not_5_out, M);
  and and_1 (and_1_out, B3, in_4, A3);
  and and_2 (and_2_out, A3, in_3, not_1_out);
  and and_3 (and_3_out, not_1_out, in_2);
  and and_4 (and_4_out, in_1, B3);
  and and_5 (and_5_out, B2, in_4, A2);
  and and_6 (and_6_out, A2, in_3, not_2_out);
  and and_7 (and_7_out, not_2_out, in_2);
  and and_8 (and_8_out, in_1, B2);
  and and_9 (and_9_out, B1, in_4, A1);
  and and_10 (and_10_out, A1, in_3, not_3_out);
  and and_11 (and_11_out, not_3_out, in_2);
  and and_12 (and_12_out, in_1, B1);
  and and_13 (and_13_out, B0, in_4, A0);
  and and_14 (and_14_out, A0, in_3, not_4_out);
  and and_15 (and_15_out, not_4_out, in_2);
  and and_16 (and_16_out, in_1, B0);
  nor nor_1 (nor_1_out, and_1_out, and_2_out);
  nor nor_2 (nor_2_out, and_3_out, and_4_out, A3);
  nor nor_3 (nor_3_out, and_5_out, and_6_out);
  nor nor_4 (nor_4_out, and_7_out, and_8_out, A2);
  nor nor_5 (nor_5_out, and_9_out, and_10_out);
  nor nor_6 (nor_6_out, and_11_out, and_12_out, A1);
  nor nor_7 (nor_7_out, and_13_out, and_14_out);
  nor nor_8 (nor_8_out, and_15_out, and_16_out, A0);
  xor xor_1 (xor_1_out, nor_1_out, nor_2_out);
  xor xor_2 (xor_2_out, nor_3_out, nor_4_out);
  xor xor_3 (xor_3_out, nor_5_out, nor_6_out);
  xor xor_4 (xor_4_out, nor_7_out, nor_8_out);
  and and_17 (and_17_out, nor_1_out, nor_4_out);
  and and_18 (and_18_out, nor_1_out, nor_3_out, nor_6_out);
  and and_19 (and_19_out, nor_1_out, nor_3_out, nor_5_out, nor_8_out);
  and and_20 (and_20_out, nor_1_out, nor_3_out, nor_5_out, nor_7_out, carry_in_bar);
  and and_21 (X, nor_1_out, nor_3_out, nor_5_out, nor_7_out);
  and and_22 (and_22_out, carry_in_bar, nor_7_out, nor_5_out, nor_3_out, not_5_out);
  and and_23 (and_23_out, nor_5_out, nor_3_out, nor_8_out, not_5_out);
  and and_24 (and_24_out, nor_3_out, nor_6_out, not_5_out);
  and and_25 (and_25_out, nor_4_out, not_5_out);
  and and_26 (and_26_out, carry_in_bar, nor_7_out, nor_5_out, not_5_out);
  and and_27 (and_27_out, nor_5_out, nor_8_out, not_5_out);
  and and_28 (and_28_out, nor_6_out, not_5_out);
  and and_29 (and_29_out, carry_in_bar, nor_7_out, not_5_out);
  and and_30 (and_30_out, nor_8_out, not_5_out);
  nand nand_1 (nand_1_out, carry_in_bar, not_5_out);
  nor nor_9 (Y, nor_2_out, and_17_out, and_18_out, and_19_out);
  nor nor_10 (nor_10_out, and_22_out, and_23_out, and_24_out, and_25_out);
  nor nor_11 (nor_11_out, and_26_out, and_27_out, and_28_out);
  nor nor_12 (nor_12_out, and_29_out, and_30_out);
  or or_1 (carry_out_bar, ~Y, ~and_20_out);  // OR_Gate
  xor xor_5 (F3, xor_1_out, nor_10_out);
  xor xor_6 (F2, xor_2_out, nor_11_out);
  xor xor_7 (F1, xor_3_out, nor_12_out);
  xor xor_8 (F0, xor_4_out, nand_1_out);
  and and_31 (A_B, F3, F2, F1, F0);
endmodule
