// Logisim project sixteen-bit-computer.circ as structural Verilog: 22 circuits, main circuit main
module main_8 (
  input  [7:0] in_1,
  input  in_2,
  input  in_3,
  input  in_4,
  input  [7:0] in_5,
  input  in_6,
  input  in_7
);

  wire A_IN, A_OUT, ACC_IN, ACC_OUT, ALU_A_IS_BUS, ALU_C_IN, ALU_CARRYBORROW_FLAG_CLOCKED,
       ALU_CARRYBORROW_FLAG_IMM, ALU_EQUAL_FLAG_CLOCKED, ALU_EQUAL_FLAG_IMM, ALU_M,
       ALU_NEGATIVE_FLAG_CLOCKED, ALU_NEGATIVE_FLAG_IMM, ALU_OUT, ALU_S0, ALU_S1, ALU_S2, ALU_S3,
       ALU_STORE_FLAGS, ALU_STORE_RESULT, ALU_ZERO_FLAG_CLOCKED, ALU_ZERO_FLAG_IMM, and_1_out, B_IN, B_OUT,
       C_IN, C_OUT, clock_1_clock, CLOCK_HALT, CONTROL_CLOCK, cpu_8_1_out_55, cpu_8_1_out_57, cpu_8_1_out_59,
       cpu_8_1_out_61, CU_CARRYBORROW_MIRROR, CU_EQUAL_MIRROR, CU_NEGATIVE_MIRROR, CU_STEP_RESET,
       CU_ZERO_MIRROR, DATA_CLOCK, IR_IN, MAR_IN, not_1_out, PC_COUNT, PC_IN, PC_OUT, PROG_DATA_MEM,
       READ_FROM_MEM, RESET, SINGLE_STEP_ADVANCE, SP_IN, SP_OUT, WRITE_SETUP_DATA, WRITE_TO_MEM;
  wire [2:0] CU_MICROCODE_STEP;
  wire [7:0] A, ACC, ADDRESS, ALU_RESULT_CLOCKED, ALU_RESULT_IMM, B, BUS, C, CU_INSTRUCTION_MIRROR,
       CURRENT_RAM_DATA, DATA, DEVICE_AT_FF, IR, PC, SP;

  Button button_1 (.out(RESET));
  Button button_2 (.out(SINGLE_STEP_ADVANCE));
  Button button_3 (.out(WRITE_SETUP_DATA));
  LED led_1 (.in(ACC_IN));
  LED led_2 (.in(ACC_OUT));
  LED led_3 (.in(A_IN));
  LED led_4 (.in(A_OUT));
  LED led_5 (.in(B_IN));
  LED led_6 (.in(B_OUT));
  LED led_7 (.in(C_IN));
  LED led_8 (.in(C_OUT));
  LED led_9 (.in(ALU_STORE_RESULT));
  LED led_10 (.in(ALU_STORE_FLAGS));
  LED led_11 (.in(ALU_OUT));
  LED led_12 (.in(ALU_A_IS_BUS));
  LED led_13 (.in(ALU_S0));
  LED led_14 (.in(ALU_S1));
  LED led_15 (.in(ALU_S2));
  LED led_16 (.in(ALU_S3));
  LED led_17 (.in(ALU_M));
  LED led_18 (.in(ALU_C_IN));
  not not_1 (not_1_out, in_4);
  and and_1 (and_1_out, not_1_out, in_2);
  LED led_19 (.in(MAR_IN));
  LED led_20 (.in(WRITE_TO_MEM));
  LED led_21 (.in(READ_FROM_MEM));
  LED led_22 (.in(PROG_DATA_MEM));
  LED led_23 (.in(SP_IN));
  LED led_24 (.in(SP_OUT));
  LED led_25 (.in(PC_IN));
  LED led_26 (.in(PC_OUT));
  LED led_27 (.in(PC_COUNT));
  LED led_28 (.in(IR_IN));
  LED led_29 (.in(CU_STEP_RESET));
  LED led_30 (.in(CLOCK_HALT));
  LED led_31 (.in(DATA_CLOCK));
  LED led_32 (.in(CONTROL_CLOCK));
  LED led_33 (.in(DEVICE_AT_FF[6]));
  LED led_34 (.in(DEVICE_AT_FF[7]));
  Clock clock_1 (
    .enable(and_1_out), .Arduino_Crystal(in_3), .Arduino_clock(SINGLE_STEP_ADVANCE), .clock(clock_1_clock));
  // Probe on in_1
  // Probe on in_1
  // Probe on in_5
  // Probe on in_5
  // Probe on CURRENT_RAM_DATA
  // Probe on CURRENT_RAM_DATA
  LED led_35 (.in(DEVICE_AT_FF[4]));
  LED led_36 (.in(DEVICE_AT_FF[2]));
  LED led_37 (.in(DEVICE_AT_FF[5]));
  LED led_38 (.in(DEVICE_AT_FF[3]));
  LED led_39 (.in(in_1[6]));
  LED led_40 (.in(in_1[7]));
  LED led_41 (.in(in_1[5]));
  LED led_42 (.in(in_5[7]));
  LED led_43 (.in(in_5[5]));
  LED led_44 (.in(in_5[6]));
  LED led_45 (.in(CURRENT_RAM_DATA[7]));
  LED led_46 (.in(CURRENT_RAM_DATA[5]));
  LED led_47 (.in(CURRENT_RAM_DATA[6]));
  // Probe on DEVICE_AT_FF
  LED led_48 (.in(DEVICE_AT_FF[0]));
  LED led_49 (.in(DEVICE_AT_FF[1]));
  LED led_50 (.in(in_1[1]));
  LED led_51 (.in(in_1[2]));
  LED led_52 (.in(in_1[4]));
  LED led_53 (.in(in_1[3]));
  LED led_54 (.in(in_5[2]));
  LED led_55 (.in(in_5[3]));
  LED led_56 (.in(in_5[1]));
  LED led_57 (.in(in_5[4]));
  LED led_58 (.in(CURRENT_RAM_DATA[4]));
  LED led_59 (.in(CURRENT_RAM_DATA[3]));
  LED led_60 (.in(CURRENT_RAM_DATA[1]));
  LED led_61 (.in(CURRENT_RAM_DATA[2]));
  // Probe on DEVICE_AT_FF
  // Probe on DEVICE_AT_FF
  LED led_62 (.in(in_1[0]));
  LED led_63 (.in(in_5[0]));
  LED led_64 (.in(CURRENT_RAM_DATA[0]));
  LED led_65 (.in(BUS[7]));
  LED led_66 (.in(PC[7]));
  LED led_67 (.in(IR[7]));
  LED led_68 (.in(SP[7]));
  LED led_69 (.in(ACC[7]));
  LED led_70 (.in(A[7]));
  LED led_71 (.in(B[7]));
  LED led_72 (.in(C[7]));
  LED led_73 (.in(ADDRESS[7]));
  LED led_74 (.in(DATA[7]));
  CPU_8 cpu_8_1 (
    .in_2(clock_1_clock), .in_1(RESET), .DATA(DATA), .ADDRESS(ADDRESS), .out_62(DATA_CLOCK), .DATA_2(DATA),
    .out_6(ACC_OUT), .out_9(A_IN), .out_4(ACC_IN), .out_11(A_OUT), .out_13(B_IN), .out_16(B_OUT),
    .out_18(C_IN), .out_20(C_OUT), .out_25(ALU_STORE_RESULT), .out_28(ALU_STORE_FLAGS), .out_31(ALU_OUT),
    .out_35(ALU_A_IS_BUS), .out_37(ALU_S0), .out_40(ALU_S1), .out_42(ALU_S2), .out_45(ALU_S3),
    .out_46(ALU_M), .out_49(ALU_C_IN), .out_5(MAR_IN), .out_10(WRITE_TO_MEM), .out_12(READ_FROM_MEM),
    .out_14(PROG_DATA_MEM), .out_19(SP_IN), .out_21(SP_OUT), .out_26(PC_IN), .out_29(PC_OUT),
    .out_32(PC_COUNT), .out_38(IR_IN), .out_43(CU_STEP_RESET), .out_47(CLOCK_HALT), .out_7(BUS), .out_17(PC),
    .out_24(IR), .out_33(SP), .out_44(ACC), .out_50(A), .out_52(B), .out_54(C), .out_8(ALU_RESULT_IMM),
    .out_15(ALU_RESULT_CLOCKED), .out_22(ALU_ZERO_FLAG_IMM), .out_23(ALU_NEGATIVE_FLAG_IMM),
    .out_27(ALU_CARRYBORROW_FLAG_IMM), .out_30(ALU_EQUAL_FLAG_IMM), .out_34(ALU_ZERO_FLAG_CLOCKED),
    .out_36(ALU_NEGATIVE_FLAG_CLOCKED), .out_39(ALU_CARRYBORROW_FLAG_CLOCKED),
    .out_41(ALU_EQUAL_FLAG_CLOCKED), .out_48(CU_INSTRUCTION_MIRROR), .out_51(CU_MICROCODE_STEP),
    .out_53(CU_ZERO_MIRROR), .out_56(CU_NEGATIVE_MIRROR), .out_58(CU_CARRYBORROW_MIRROR),
    .out_60(CU_EQUAL_MIRROR), .out_63(CONTROL_CLOCK), .out_55(cpu_8_1_out_55), .out_57(cpu_8_1_out_57),
    .out_59(cpu_8_1_out_59), .out_61(cpu_8_1_out_61));
  RAM_8 ram_8_1 (
    .tristate_data_output(DATA), .current_data(CURRENT_RAM_DATA), .CPU_write_to_mem(cpu_8_1_out_55),
    .CPU_read_from_mem(cpu_8_1_out_57), .run_setup(in_4), .CPU_clock(cpu_8_1_out_61),
    .setup_clock(WRITE_SETUP_DATA), .cpu_address(ADDRESS), .setup_address(in_1), .cpu_data(DATA),
    .CPU_prog_data_mem(cpu_8_1_out_59), .setup_prog_data_mem(in_6), .setup_data(in_5), .examine_write(in_7));
  io_device io_device_1 (
    .in_2(ADDRESS), .Prog_data_sel(cpu_8_1_out_59), .Write_to_mem(cpu_8_1_out_55), .Clock(cpu_8_1_out_61),
    .out_6(DEVICE_AT_FF), .in_1(DATA));
  LED led_75 (.in(BUS[6]));
  LED led_76 (.in(BUS[3]));
  LED led_77 (.in(BUS[5]));
  LED led_78 (.in(BUS[4]));
  LED led_79 (.in(PC[6]));
  LED led_80 (.in(PC[5]));
  LED led_81 (.in(PC[4]));
  LED led_82 (.in(PC[3]));
  LED led_83 (.in(IR[4]));
  LED led_84 (.in(IR[3]));
  LED led_85 (.in(IR[6]));
  LED led_86 (.in(IR[5]));
  LED led_87 (.in(SP[4]));
  LED led_88 (.in(SP[3]));
  LED led_89 (.in(SP[5]));
  LED led_90 (.in(SP[6]));
  LED led_91 (.in(ACC[4]));
  LED led_92 (.in(ACC[6]));
  LED led_93 (.in(ACC[5]));
  LED led_94 (.in(ACC[3]));
  LED led_95 (.in(A[3]));
  LED led_96 (.in(A[4]));
  LED led_97 (.in(A[5]));
  LED led_98 (.in(A[6]));
  LED led_99 (.in(B[6]));
  LED led_100 (.in(B[5]));
  LED led_101 (.in(B[3]));
  LED led_102 (.in(B[4]));
  LED led_103 (.in(C[4]));
  LED led_104 (.in(C[5]));
  LED led_105 (.in(C[6]));
  LED led_106 (.in(C[3]));
  LED led_107 (.in(ADDRESS[5]));
  LED led_108 (.in(ADDRESS[3]));
  LED led_109 (.in(ADDRESS[4]));
  LED led_110 (.in(ADDRESS[6]));
  LED led_111 (.in(DATA[6]));
  LED led_112 (.in(DATA[5]));
  LED led_113 (.in(DATA[4]));
  LED led_114 (.in(DATA[3]));
  LED led_115 (.in(BUS[2]));
  LED led_116 (.in(BUS[1]));
  LED led_117 (.in(BUS[0]));
  LED led_118 (.in(PC[1]));
  LED led_119 (.in(PC[2]));
  LED led_120 (.in(PC[0]));
  LED led_121 (.in(IR[1]));
  LED led_122 (.in(IR[2]));
  LED led_123 (.in(IR[0]));
  LED led_124 (.in(SP[1]));
  LED led_125 (.in(SP[2]));
  LED led_126 (.in(SP[0]));
  LED led_127 (.in(ACC[2]));
  LED led_128 (.in(ACC[1]));
  LED led_129 (.in(ACC[0]));
  LED led_130 (.in(A[1]));
  LED led_131 (.in(A[0]));
  LED led_132 (.in(A[2]));
  LED led_133 (.in(B[0]));
  LED led_134 (.in(B[2]));
  LED led_135 (.in(B[1]));
  LED led_136 (.in(C[1]));
  LED led_137 (.in(C[2]));
  LED led_138 (.in(C[0]));
  LED led_139 (.in(ADDRESS[0]));
  LED led_140 (.in(ADDRESS[1]));
  LED led_141 (.in(ADDRESS[2]));
  LED led_142 (.in(DATA[2]));
  LED led_143 (.in(DATA[0]));
  LED led_144 (.in(DATA[1]));
  // Probe on BUS
  // Probe on BUS
  // Probe on BUS
  // Probe on PC
  // Probe on PC
  // Probe on PC
  // Probe on IR
  // Probe on IR
  // Probe on IR
  // Probe on SP
  // Probe on SP
  // Probe on SP
  // Probe on ACC
  // Probe on ACC
  // Probe on ACC
  // Probe on A
  // Probe on A
  // Probe on A
  // Probe on B
  // Probe on B
  // Probe on B
  // Probe on C
  // Probe on C
  // Probe on C
  // Probe on ADDRESS
  // Probe on ADDRESS
  // Probe on ADDRESS
  // Probe on DATA
  // Probe on DATA
  // Probe on DATA
  LED led_145 (.in(ALU_RESULT_IMM[6]));
  LED led_146 (.in(ALU_RESULT_IMM[7]));
  LED led_147 (.in(ALU_RESULT_CLOCKED[7]));
  LED led_148 (.in(ALU_RESULT_CLOCKED[6]));
  LED led_149 (.in(CU_INSTRUCTION_MIRROR[7]));
  LED led_150 (.in(CU_MICROCODE_STEP[2]));
  LED led_151 (.in(ALU_RESULT_IMM[3]));
  LED led_152 (.in(ALU_RESULT_IMM[5]));
  LED led_153 (.in(ALU_RESULT_IMM[2]));
  LED led_154 (.in(ALU_RESULT_IMM[4]));
  LED led_155 (.in(ALU_RESULT_CLOCKED[2]));
  LED led_156 (.in(ALU_RESULT_CLOCKED[5]));
  LED led_157 (.in(ALU_RESULT_CLOCKED[4]));
  LED led_158 (.in(ALU_RESULT_CLOCKED[3]));
  LED led_159 (.in(CU_INSTRUCTION_MIRROR[3]));
  LED led_160 (.in(CU_INSTRUCTION_MIRROR[4]));
  LED led_161 (.in(CU_INSTRUCTION_MIRROR[5]));
  LED led_162 (.in(CU_INSTRUCTION_MIRROR[6]));
  LED led_163 (.in(CU_MICROCODE_STEP[1]));
  LED led_164 (.in(CU_MICROCODE_STEP[0]));
  Pull_Resistor pull_resistor_1 (.node(DATA));
  // Probe on ALU_RESULT_IMM
  LED led_165 (.in(ALU_RESULT_IMM[1]));
  LED led_166 (.in(ALU_RESULT_IMM[0]));
  // Probe on ALU_RESULT_CLOCKED
  LED led_167 (.in(ALU_RESULT_CLOCKED[1]));
  LED led_168 (.in(ALU_RESULT_CLOCKED[0]));
  LED led_169 (.in(CU_INSTRUCTION_MIRROR[1]));
  LED led_170 (.in(CU_INSTRUCTION_MIRROR[0]));
  LED led_171 (.in(CU_INSTRUCTION_MIRROR[2]));
  // Probe on ALU_RESULT_IMM
  // Probe on ALU_RESULT_IMM
  // Probe on ALU_RESULT_CLOCKED
  // Probe on ALU_RESULT_CLOCKED
  LED led_172 (.in(ALU_ZERO_FLAG_IMM));
  LED led_173 (.in(ALU_NEGATIVE_FLAG_IMM));
  LED led_174 (.in(ALU_CARRYBORROW_FLAG_IMM));
  LED led_175 (.in(ALU_EQUAL_FLAG_IMM));
  LED led_176 (.in(ALU_ZERO_FLAG_CLOCKED));
  LED led_177 (.in(ALU_NEGATIVE_FLAG_CLOCKED));
  LED led_178 (.in(ALU_CARRYBORROW_FLAG_CLOCKED));
  LED led_179 (.in(ALU_EQUAL_FLAG_CLOCKED));
  LED led_180 (.in(CU_ZERO_MIRROR));
  LED led_181 (.in(CU_NEGATIVE_MIRROR));
  LED led_182 (.in(CU_CARRYBORROW_MIRROR));
  LED led_183 (.in(CU_EQUAL_MIRROR));
  // Probe on CU_INSTRUCTION_MIRROR
  // Probe on CU_INSTRUCTION_MIRROR
  // Probe on CU_INSTRUCTION_MIRROR
  // Probe on CU_MICROCODE_STEP
  // Probe on CU_MICROCODE_STEP
  // Probe on CU_MICROCODE_STEP

  // Other names for the same wires on the sheet: CLOCK_ENABLE = in_2; EXAMINE_WRITE = in_7;
  //   EXTERNAL_INTERNAL_CLOCK = in_3; RUN_SETUP_MODE = in_4; SETUP_ADDRESS[7:0] = in_1; SETUP_DATA[7:0] = in_5;
  //   SETUP_PROG_DATA_MEM = in_6

  // Notes on the sheet:
  //   Only necessary in sim - arduino takes care of this
  //   DEC
  //   HEX
  //   DEC
  //   HEX
  //   DEC
  //   HEX
  //   BIN
  //   HEX
  //   DEC
  //   BIN
  //   HEX
  //   DEC
  //   BIN
  //   HEX
  //   DEC
  //   BIN
  //   HEX
  //   DEC
  //   BIN
  //   HEX
  //   DEC
  //   BIN
  //   HEX
  //   DEC
  //   BIN
  //   HEX
  //   DEC
  //   BIN
  //   HEX
  //   DEC
  //   BIN
  //   HEX
  //   DEC
  //   BIN
  //   HEX
  //   DEC
  //   BIN
  //   HEX
  //   DEC
  //   BIN
  //   HEX
  //   BIN
  //   HEX
  //   DEC
  //   DEC
  //   BIN
  //   HEX
  //   DEC
  //   BIN
  //   HEX
  //   DEC
endmodule

module Clock (
  input  enable,
  input  Arduino_Crystal,
  input  Arduino_clock,
  output clock
);

  wire Crystal_clock_out, multiplexer_1_out;

  Clock_part Crystal_clock (.out(Crystal_clock_out));
  Multiplexer #(.enable("false")) multiplexer_1 (
    .in0(Arduino_clock), .in1(Crystal_clock_out), .out(multiplexer_1_out), .sel(Arduino_Crystal));
  safe_clock_enable safe_clock_enable_1 (.clock_enable(enable), .clock_in(multiplexer_1_out), .clock_out(clock));
endmodule

module RAM_8 (
  input  run_setup,
  input  [7:0] cpu_data,
  input  [7:0] setup_data,
  input  [7:0] cpu_address,
  input  [7:0] setup_address,
  input  CPU_prog_data_mem,
  input  setup_prog_data_mem,
  input  CPU_write_to_mem,
  input  examine_write,
  input  CPU_read_from_mem,
  input  CPU_clock,
  input  setup_clock,
  output [7:0] current_data,
  output [7:0] tristate_data_output
);

  wire multiplexer_1_out, multiplexer_2_out, multiplexer_6_out, multiplexer_7_out, multiplexer_8_out,
       nand_1_out, not_1_out, safe_clock_enable_1_clock_out;
  wire [7:0] multiplexer_3_out, multiplexer_4_out;
  wire [8:8] multiplexer_5_out;

  nand nand_1 (nand_1_out, CPU_prog_data_mem, cpu_address[3], cpu_address[4], cpu_address[5], cpu_address[6], cpu_address[7]);
  Multiplexer #(.enable("false")) multiplexer_1 (
    .in0(1'b0), .in1(CPU_write_to_mem), .out(multiplexer_1_out), .sel(nand_1_out));
  Multiplexer #(.enable("false")) multiplexer_2 (
    .in0(1'b0), .in1(CPU_read_from_mem), .out(multiplexer_2_out), .sel(nand_1_out));
  Multiplexer #(.width(8), .enable("false")) multiplexer_3 (
    .in0(cpu_data), .in1(setup_data), .out(multiplexer_3_out), .sel(run_setup));
  Multiplexer #(.width(8), .enable("false")) multiplexer_4 (
    .in0(cpu_address), .in1(setup_address), .out(multiplexer_4_out), .sel(run_setup));
  Multiplexer #(.enable("false")) multiplexer_5 (
    .in0(CPU_prog_data_mem), .in1(setup_prog_data_mem), .out(multiplexer_5_out[8]), .sel(run_setup));
  Multiplexer #(.enable("false")) multiplexer_6 (
    .in0(multiplexer_1_out), .in1(examine_write), .out(multiplexer_6_out), .sel(run_setup));
  Multiplexer #(.enable("false")) multiplexer_7 (
    .in0(multiplexer_2_out), .in1(1'b0), .out(multiplexer_7_out), .sel(run_setup));
  Multiplexer #(.enable("false")) multiplexer_8 (
    .in0(CPU_clock), .in1(setup_clock), .out(multiplexer_8_out), .sel(run_setup));
  safe_clock_enable safe_clock_enable_1 (
    .clock_enable(multiplexer_6_out), .clock_in(multiplexer_8_out), .clock_out(safe_clock_enable_1_clock_out));
  RAM_part #(.addrWidth(9)) ram_1 (
    .addr({multiplexer_5_out[8], multiplexer_4_out}), .data(current_data), .sel(1'b1),
    .clk(safe_clock_enable_1_clock_out), .ld(not_1_out), .clr(1'b0));
  assign current_data = multiplexer_6_out ? multiplexer_3_out : 8'bz;  // Controlled_Buffer controlled_buffer_1
  not not_1 (not_1_out, multiplexer_6_out);
  assign tristate_data_output = multiplexer_7_out ? current_data : 8'bz;  // Controlled_Buffer controlled_buffer_2
endmodule

module CPU_8 (
  input  in_1,
  input  in_2,
  input  [7:0] DATA,
  output out_4,
  output out_5,
  output out_6,
  output [7:0] out_7,
  output [7:0] out_8,
  output out_9,
  output out_10,
  output out_11,
  output out_12,
  output out_13,
  output out_14,
  output [7:0] out_15,
  output out_16,
  output [7:0] out_17,
  output out_18,
  output out_19,
  output out_20,
  output out_21,
  output out_22,
  output out_23,
  output [7:0] out_24,
  output out_25,
  output out_26,
  output out_27,
  output out_28,
  output out_29,
  output out_30,
  output out_31,
  output out_32,
  output [7:0] out_33,
  output out_34,
  output out_35,
  output out_36,
  output out_37,
  output out_38,
  output out_39,
  output out_40,
  output out_41,
  output out_42,
  output out_43,
  output [7:0] out_44,
  output out_45,
  output out_46,
  output out_47,
  output [7:0] out_48,
  output out_49,
  output [7:0] out_50,
  output [2:0] out_51,
  output [7:0] out_52,
  output out_53,
  output [7:0] out_54,
  output out_55,
  output out_56,
  output out_57,
  output out_58,
  output out_59,
  output out_60,
  output out_61,
  output out_62,
  output out_63,
  output [7:0] DATA_2,
  output [7:0] ADDRESS
);

  wire j_k_ff_1_q, j_k_ff_1_qn, nor_1_out, safe_clock_enable_1_clock_out, SIM_ONLY_RESET;
  wire [7:0] multiplexer_1_out;

  Button button_1 (.out(SIM_ONLY_RESET));
  LED led_1 (.in(out_4));
  LED led_2 (.in(out_6));
  LED led_3 (.in(out_9));
  LED led_4 (.in(out_11));
  LED led_5 (.in(out_13));
  LED led_6 (.in(out_16));
  LED led_7 (.in(out_18));
  LED led_8 (.in(out_20));
  LED led_9 (.in(out_25));
  LED led_10 (.in(out_28));
  LED led_11 (.in(out_31));
  LED led_12 (.in(out_35));
  LED led_13 (.in(out_37));
  LED led_14 (.in(out_40));
  LED led_15 (.in(out_42));
  LED led_16 (.in(out_45));
  LED led_17 (.in(out_46));
  LED led_18 (.in(out_49));
  nor nor_1 (nor_1_out, in_1, out_47);
  safe_clock_enable safe_clock_enable_1 (
    .clock_enable(nor_1_out), .clock_in(in_2), .clock_out(safe_clock_enable_1_clock_out));
  LED led_19 (.in(out_5));
  LED led_20 (.in(out_10));
  LED led_21 (.in(out_12));
  LED led_22 (.in(out_14));
  LED led_23 (.in(out_19));
  LED led_24 (.in(out_21));
  LED led_25 (.in(out_26));
  LED led_26 (.in(out_29));
  LED led_27 (.in(out_32));
  LED led_28 (.in(out_38));
  LED led_29 (.in(out_43));
  LED led_30 (.in(out_47));
  J_K_Flip_Flop j_k_ff_1 (
    .J(1'b1), .clk(safe_clock_enable_1_clock_out), .K(1'b1), .Q(j_k_ff_1_q), .Qn(j_k_ff_1_qn), .preset(1'b0),
    .en(1'b1), .reset(in_1));
  Control_unit_8 control_unit_8_1 (
    .ACC_IN(out_4), .ACC_OUT(out_6), .A_IN(out_9), .A_OUT(out_11), .ALU_STORE_RESULT(out_25),
    .ALU_STORE_FLAGS(out_28), .ALU_S1(out_40), .ALU_S2(out_42), .ALU_S3(out_45), .ALU_M(out_46),
    .ALU_C_IN(out_49), .MAR_IN(out_5), .WRITE_TO_MEM(out_10), .IR_IN(out_38), .control_clock(out_63),
    .clear(in_1), .zero_flag(out_34), .instruction(out_24), .microcode_step(out_51), .B_IN(out_13),
    .B_OUT(out_16), .C_IN(out_18), .C_OUT(out_20), .ALU_OUT(out_31), .ALU_A_IS_BUS(out_35), .ALU_S0(out_37),
    .negative_flag(out_36), .carryborrow_flag(out_39), .READ_FROM_MEM(out_12), .PROG_DATA_MEM(out_14),
    .SP_IN(out_19), .SP_OUT(out_21), .PC_IN(out_26), .PC_OUT(out_29), .PC_COUNT(out_32),
    .mirror_instruction(out_48), .sim_only_clear(SIM_ONLY_RESET), .equal_flag(out_41),
    .mirror_zero_flag(out_53), .mirror_negative_flag(out_56), .mirror_carryborrow_flag(out_58),
    .mirror_equal_flag(out_60), .CU_STEP_RESET(out_43), .CLOCK_HALT(out_47));
  register_bus_R_8 MAR (
    .\input (out_7), .content(ADDRESS), .input_enable(out_5), .clock(out_61), .output_enable(1'b0),
    .sim_only_reset(SIM_ONLY_RESET));  // open: buffered_output
  register_bus_R_8 IR (
    .\input (out_7), .buffered_output(out_7), .content(out_24), .input_enable(out_38), .clock(out_61),
    .output_enable(1'b0), .sim_only_reset(SIM_ONLY_RESET));
  J_K_Flip_Flop j_k_ff_2 (
    .J(1'b1), .clk(j_k_ff_1_q), .K(1'b1), .Q(out_61), .preset(1'b0), .en(1'b1), .reset(in_1));  // open: Qn
  LED led_31 (.in(out_7[4]));
  LED led_32 (.in(out_7[7]));
  LED led_33 (.in(out_7[6]));
  LED led_34 (.in(out_7[5]));
  LED led_35 (.in(out_17[6]));
  LED led_36 (.in(out_17[4]));
  LED led_37 (.in(out_17[7]));
  LED led_38 (.in(out_17[5]));
  LED led_39 (.in(out_24[4]));
  LED led_40 (.in(out_24[5]));
  LED led_41 (.in(out_24[7]));
  LED led_42 (.in(out_24[6]));
  LED led_43 (.in(out_33[7]));
  LED led_44 (.in(out_33[6]));
  LED led_45 (.in(out_33[5]));
  LED led_46 (.in(out_33[4]));
  LED led_47 (.in(out_44[5]));
  LED led_48 (.in(out_44[4]));
  LED led_49 (.in(out_44[7]));
  LED led_50 (.in(out_44[6]));
  LED led_51 (.in(out_50[6]));
  LED led_52 (.in(out_50[7]));
  LED led_53 (.in(out_50[5]));
  LED led_54 (.in(out_50[4]));
  LED led_55 (.in(out_52[5]));
  LED led_56 (.in(out_52[6]));
  LED led_57 (.in(out_52[4]));
  LED led_58 (.in(out_52[7]));
  LED led_59 (.in(out_54[4]));
  LED led_60 (.in(out_54[5]));
  LED led_61 (.in(out_54[7]));
  LED led_62 (.in(out_54[6]));
  LED led_63 (.in(ADDRESS[6]));
  LED led_64 (.in(ADDRESS[5]));
  LED led_65 (.in(ADDRESS[7]));
  LED led_66 (.in(ADDRESS[4]));
  J_K_Flip_Flop j_k_ff_3 (
    .J(1'b1), .clk(j_k_ff_1_qn), .K(1'b1), .Q(out_63), .preset(1'b0), .en(1'b1), .reset(in_1));  // open: Qn
  LED led_67 (.in(out_7[3]));
  LED led_68 (.in(out_7[2]));
  LED led_69 (.in(out_7[1]));
  LED led_70 (.in(out_7[0]));
  LED led_71 (.in(out_17[1]));
  LED led_72 (.in(out_17[2]));
  LED led_73 (.in(out_17[0]));
  LED led_74 (.in(out_17[3]));
  LED led_75 (.in(out_24[2]));
  LED led_76 (.in(out_24[0]));
  LED led_77 (.in(out_24[1]));
  LED led_78 (.in(out_24[3]));
  LED led_79 (.in(out_33[3]));
  LED led_80 (.in(out_33[1]));
  LED led_81 (.in(out_33[0]));
  LED led_82 (.in(out_33[2]));
  LED led_83 (.in(out_44[3]));
  LED led_84 (.in(out_44[2]));
  LED led_85 (.in(out_44[1]));
  LED led_86 (.in(out_44[0]));
  LED led_87 (.in(out_50[0]));
  LED led_88 (.in(out_50[1]));
  LED led_89 (.in(out_50[3]));
  LED led_90 (.in(out_50[2]));
  LED led_91 (.in(out_52[0]));
  LED led_92 (.in(out_52[2]));
  LED led_93 (.in(out_52[3]));
  LED led_94 (.in(out_52[1]));
  LED led_95 (.in(out_54[0]));
  LED led_96 (.in(out_54[3]));
  LED led_97 (.in(out_54[2]));
  LED led_98 (.in(out_54[1]));
  LED led_99 (.in(ADDRESS[0]));
  LED led_100 (.in(ADDRESS[3]));
  LED led_101 (.in(ADDRESS[1]));
  LED led_102 (.in(ADDRESS[2]));
  // Probe on out_7
  // Probe on out_17
  // Probe on out_24
  // Probe on out_33
  // Probe on out_44
  // Probe on out_50
  // Probe on out_52
  // Probe on out_54
  // Probe on ADDRESS
  // Probe on out_7
  // Probe on out_7
  // Probe on out_17
  // Probe on out_17
  // Probe on out_24
  // Probe on out_24
  // Probe on out_33
  // Probe on out_33
  // Probe on out_44
  // Probe on out_44
  // Probe on out_50
  // Probe on out_50
  // Probe on out_52
  // Probe on out_52
  // Probe on out_54
  // Probe on out_54
  // Probe on ADDRESS
  // Probe on ADDRESS
  assign DATA_2 = out_10 ? out_7 : 8'bz;  // Controlled_Buffer controlled_buffer_1
  assign out_7 = out_12 ? DATA : 8'bz;  // Controlled_Buffer controlled_buffer_2
  Pull_Resistor pull_resistor_1 (.node(out_7));
  Multiplexer #(.width(8), .enable("false")) multiplexer_1 (
    .in0(out_44), .in1(out_7), .out(multiplexer_1_out), .sel(out_35));
  LED led_103 (.in(out_8[7]));
  LED led_104 (.in(out_8[5]));
  LED led_105 (.in(out_8[6]));
  LED led_106 (.in(out_15[6]));
  LED led_107 (.in(out_15[7]));
  LED led_108 (.in(out_15[5]));
  LED led_109 (.in(out_22));
  LED led_110 (.in(out_23));
  LED led_111 (.in(out_27));
  LED led_112 (.in(out_30));
  LED led_113 (.in(out_34));
  LED led_114 (.in(out_36));
  LED led_115 (.in(out_39));
  LED led_116 (.in(out_41));
  LED led_117 (.in(out_48[7]));
  LED led_118 (.in(out_48[6]));
  LED led_119 (.in(out_48[5]));
  LED led_120 (.in(out_51[1]));
  LED led_121 (.in(out_51[2]));
  LED led_122 (.in(out_53));
  LED led_123 (.in(out_56));
  LED led_124 (.in(out_58));
  LED led_125 (.in(out_60));
  LED led_126 (.in(out_61));
  LED led_127 (.in(out_63));
  program_counter_8 PC (
    .\input (out_7), .count(out_32), .clock(out_61), .output_enable(out_29), .tristate_output(out_7),
    .in(out_26), .contents(out_17), .reset(in_1));
  register_bus_L_8 ACC (
    .\input (out_7), .buffered_output(out_7), .content(out_44), .output_enable(out_6), .input_enable(out_4),
    .clock(out_61), .sim_only_reset(SIM_ONLY_RESET));
  ALU_8 alu_8_1 (
    .carry_in(out_49), .M(out_46), .S0(out_37), .S1(out_40), .S2(out_42), .S3(out_45), .store_result(out_25),
    .clock(out_61), .unclocked_carryborrow_out(out_27), .clocked_carryborrow_out(out_39),
    .unclocked_A___B(out_30), .clocked_A___B(out_41), .clocked_zero(out_34), .unclocked_zero(out_22),
    .tristate_clocked_result(out_7), .A(multiplexer_1_out), .B(out_7), .result_output_enable(out_31),
    .unclocked_result(out_8), .clocked_result(out_15), .unclocked_negative(out_23),
    .clocked_negative(out_36), .store_flags(out_28), .sim_only_reset(SIM_ONLY_RESET));
  register_bus_L_8 A (
    .\input (out_7), .buffered_output(out_7), .content(out_50), .output_enable(out_11), .input_enable(out_9),
    .clock(out_61), .sim_only_reset(SIM_ONLY_RESET));
  register_bus_L_8 B (
    .\input (out_7), .buffered_output(out_7), .content(out_52), .output_enable(out_16),
    .input_enable(out_13), .clock(out_61), .sim_only_reset(SIM_ONLY_RESET));
  register_bus_L_8 C (
    .\input (out_7), .buffered_output(out_7), .content(out_54), .output_enable(out_20),
    .input_enable(out_18), .clock(out_61), .sim_only_reset(SIM_ONLY_RESET));
  register_bus_L_8 SP (
    .\input (out_7), .buffered_output(out_7), .content(out_33), .output_enable(out_21),
    .input_enable(out_19), .clock(out_61), .sim_only_reset(SIM_ONLY_RESET));
  LED led_128 (.in(out_8[1]));
  LED led_129 (.in(out_8[4]));
  LED led_130 (.in(out_8[3]));
  LED led_131 (.in(out_8[2]));
  LED led_132 (.in(out_15[4]));
  LED led_133 (.in(out_15[3]));
  LED led_134 (.in(out_15[2]));
  LED led_135 (.in(out_15[1]));
  LED led_136 (.in(out_48[4]));
  LED led_137 (.in(out_48[3]));
  LED led_138 (.in(out_48[1]));
  LED led_139 (.in(out_48[2]));
  LED led_140 (.in(out_51[0]));
  // Probe on out_8
  LED led_141 (.in(out_8[0]));
  // Probe on out_15
  LED led_142 (.in(out_15[0]));
  // Probe on out_48
  LED led_143 (.in(out_48[0]));
  // Probe on out_51
  // Probe on out_51
  // Probe on out_51
  // Probe on out_8
  // Probe on out_8
  // Probe on out_15
  // Probe on out_15
  // Probe on out_48
  // Probe on out_48

  assign out_55 = out_10;
  assign out_57 = out_12;
  assign out_59 = out_14;
  assign out_62 = out_61;

  // Other names for the same wires on the sheet: A[7:0] = out_50; A_IN = out_9; A_OUT = out_11; ACC[7:0] = out_44;
  //   ACC_IN = out_4; ACC_OUT = out_6; ALU_A_IS_BUS = out_35; ALU_C_IN = out_49;
  //   ALU_CARRYBORROW_FLAG_CLOCKED = out_39; ALU_CARRYBORROW_FLAG_IMM = out_27; ALU_EQUAL_FLAG_CLOCKED = out_41;
  //   ALU_EQUAL_FLAG_IMM = out_30; ALU_M = out_46; ALU_NEGATIVE_FLAG_CLOCKED = out_36; ALU_NEGATIVE_FLAG_IMM = out_23;
  //   ALU_OUT = out_31; ALU_RESULT_CLOCKED[7:0] = out_15; ALU_RESULT_IMM[7:0] = out_8; ALU_S0 = out_37;
  //   ALU_S1 = out_40; ALU_S2 = out_42; ALU_S3 = out_45; ALU_STORE_FLAGS = out_28; ALU_STORE_RESULT = out_25;
  //   ALU_ZERO_FLAG_CLOCKED = out_34; ALU_ZERO_FLAG_IMM = out_22; B[7:0] = out_52; B_IN = out_13; B_OUT = out_16;
  //   BUS[7:0] = out_7; C[7:0] = out_54; C_IN = out_18; C_OUT = out_20; CLOCK_HALT = out_47; CONTROL_CLOCK = out_63;
  //   CU_CARRYBORROW_MIRROR = out_58; CU_EQUAL_MIRROR = out_60; CU_INSTRUCTION_MIRROR[7:0] = out_48;
  //   CU_MICROCODE_STEP[2:0] = out_51; CU_NEGATIVE_MIRROR = out_56; CU_STEP_RESET = out_43; CU_ZERO_MIRROR = out_53;
  //   DATA_CLOCK = out_61; EXT_CLOCK_PULSE = in_2; IR[7:0] = out_24; IR_IN = out_38; MAR_IN = out_5; PC[7:0] = out_17;
  //   PC_COUNT = out_32; PC_IN = out_26; PC_OUT = out_29; PROG_DATA_MEM = out_14; READ_FROM_MEM = out_12;
  //   RESET = in_1; SP[7:0] = out_33; SP_IN = out_19; SP_OUT = out_21; WRITE_TO_MEM = out_10

  // Notes on the sheet:
  //   BIN
  //   HEX
  //   DEC
  //   BIN
  //   HEX
  //   DEC
  //   BIN
  //   HEX
  //   DEC
  //   BIN
  //   HEX
  //   DEC
  //   BIN
  //   HEX
  //   DEC
  //   BIN
  //   HEX
  //   DEC
  //   BIN
  //   HEX
  //   DEC
  //   BIN
  //   HEX
  //   DEC
  //   BIN
  //   HEX
  //   DEC
  //   BIN
  //   HEX
  //   DEC
  //   BIN
  //   HEX
  //   DEC
  //   BIN
  //   HEX
  //   DEC
  //   BIN
  //   HEX
  //   DEC
endmodule

module Control_unit_8 (
  input  [7:0] instruction,
  input  equal_flag,
  input  carryborrow_flag,
  input  negative_flag,
  input  zero_flag,
  input  control_clock,
  input  clear,
  input  sim_only_clear,
  output CLOCK_HALT,
  output CU_STEP_RESET,
  output [7:0] mirror_instruction,
  output IR_IN,
  output PC_COUNT,
  output PC_OUT,
  output PC_IN,
  output SP_OUT,
  output SP_IN,
  output PROG_DATA_MEM,
  output mirror_equal_flag,
  output READ_FROM_MEM,
  output mirror_carryborrow_flag,
  output WRITE_TO_MEM,
  output mirror_negative_flag,
  output MAR_IN,
  output mirror_zero_flag,
  output ALU_C_IN,
  output ALU_M,
  output [2:0] microcode_step,
  output ALU_S3,
  output ALU_S2,
  output ALU_S1,
  output ALU_S0,
  output ALU_A_IS_BUS,
  output ALU_OUT,
  output ALU_STORE_FLAGS,
  output ALU_STORE_RESULT,
  output C_OUT,
  output C_IN,
  output B_OUT,
  output B_IN,
  output A_OUT,
  output A_IN,
  output ACC_OUT,
  output ACC_IN
);

  wire not_1_out;
  wire [7:6] rom_1_data;

  not not_1 (not_1_out, CU_STEP_RESET);
  Register u_mirror_instruction (
    .D(instruction), .en(1'b1), .Q(mirror_instruction), .clk(control_clock), .clr(sim_only_clear));
  Register #(.width(4)) mirror_flags (
    .D({equal_flag, carryborrow_flag, negative_flag, zero_flag}), .en(1'b1),
    .Q({mirror_equal_flag, mirror_carryborrow_flag, mirror_negative_flag, mirror_zero_flag}),
    .clk(control_clock), .clr(sim_only_clear));
  Counter #(.width(3), .max('h7)) microcode_step_counter (
    .load(CU_STEP_RESET), .D(3'b000), .count(not_1_out), .Q(microcode_step), .clk(control_clock), .clr(clear));  // open: carry
  ROM #(.addrWidth(15)) rom_1 (
    .addr({mirror_instruction, mirror_equal_flag, mirror_carryborrow_flag, mirror_negative_flag, mirror_zero_flag, microcode_step}),
    .data({rom_1_data, CLOCK_HALT, CU_STEP_RESET, IR_IN, PC_COUNT, PC_OUT, PC_IN}), .sel(1'b1));
  ROM #(.addrWidth(15)) rom_2 (
    .addr({mirror_instruction, mirror_equal_flag, mirror_carryborrow_flag, mirror_negative_flag, mirror_zero_flag, microcode_step}),
    .data({SP_OUT, SP_IN, PROG_DATA_MEM, READ_FROM_MEM, WRITE_TO_MEM, MAR_IN, ALU_C_IN, ALU_M}), .sel(1'b1));
  ROM #(.addrWidth(15)) rom_3 (
    .addr({mirror_instruction, mirror_equal_flag, mirror_carryborrow_flag, mirror_negative_flag, mirror_zero_flag, microcode_step}),
    .data({ALU_S3, ALU_S2, ALU_S1, ALU_S0, ALU_A_IS_BUS, ALU_OUT, ALU_STORE_FLAGS, ALU_STORE_RESULT}),
    .sel(1'b1));
  ROM #(.addrWidth(15)) rom_4 (
    .addr({mirror_instruction, mirror_equal_flag, mirror_carryborrow_flag, mirror_negative_flag, mirror_zero_flag, microcode_step}),
    .data({C_OUT, C_IN, B_OUT, B_IN, A_OUT, A_IN, ACC_OUT, ACC_IN}), .sel(1'b1));

  // Notes on the sheet:
  //   Common inputs to all EEPROMS
  //   microcode 3
  //   microcode 2
  //   microcode 1
  //   microcode 0
  //   contents of rom_1 (hex, n*v repeats v):
  //   2 c 14 5*0 2 c 2 11 4*0 2 c 14 5*0 2 c 2 11 4*0 2 c 14 5*0 2 c 2 11 4*0 2 c 14 5*0 2 c 2 11 4*0 2 c
  //   14 5*0 2 c 2 11 4*0 2 c 14 5*0 2 c 2 11 4*0 2 c 14 5*0 2 c 2 11 4*0 2 c 14 5*0 2 c 2 11 4*0 2 c 10
  //   5*0 2 c 10 5*0 2 c 10 5*0 2 c 10 5*0 2 c 10 5*0 2 c 10 5*0 2 c 10 5*0 2 c 10 5*0 2 c 10 5*0 2 c 10
  //   5*0 2 c 10 5*0 2 c 10 5*0 2 c 10 5*0 2 c 10 5*0 2 c 10 5*0 2 c 10 5*0 2 c 10 5*0 2 c 10 5*0 2 c 10
  //   5*0 2 c 10 5*0 2 c 10 5*0 2 c 10 5*0 2 c 10 5*0 2 c 10 5*0 2 c 10 5*0 2 c 10 5*0 2 c 10 5*0 2 c 10
  //   5*0 2 c 10 5*0 2 c 10 5*0 2 c 10 5*0 2 c 10 5*0 2 c 10 5*0 2 c 10 5*0 2 c 10 5*0 2 c 10 5*0 2 c 10
  //   5*0 2 c 10 5*0 2 c 10 5*0 2 c 10 5*0 2 c 10 5*0 2 c 10 5*0 2 c 10 5*0 2 c 10 5*0 2 c 10 5*0 2 c 10
  //   5*0 2 c 10 5*0 2 c 10 5*0 2 c 10 5*0 2 c 10 5*0 2 c 10 5*0 2 c 10 5*0 2 c 10 5*0 2 c 10 5*0 2 c 10
  //   5*0 2 c 10 5*0 2 c 10 5*0 2 c 10 5*0 2 c 10 5*0 2 c 10 5*0 2 c 10 5*0 2 c 10 5*0 2 c 10 5*0 2 c 10
  //   5*0 2 c 11 5*0 2 c 11 5*0 2 c 11 5*0 2 c 11 5*0 2 c 11 5*0 2 c 11 5*0 2 c 11 5*0 2 c 11 5*0 2 c 11
  //   5*0 2 c 11 5*0 2 c 11 5*0 2 c 11 5*0 2 c 11 5*0 2 c 11 5*0 2 c 11 5*0 2 c 11 5*0 2 c 6*0 2 c 6*0 2 c
  //   6*0 2 c 6*0 2 c 6*0 2 c 6*0 2 c 6*0 2 c 6*0 2 c 6*0 2 c 6*0 2 c 6*0 2 c 6*0 2 c 6*0 2 c 6*0 2 c 6*0
  //   2 c 6*0 2 c 2 4 14 0 0 0 2 c 2 4 14 0 0 0 2 c 2 4 14 0 0 0 2 c 2 4 14 0 0 0 2 c 2 4 14 0 0 0 2 c 2 4
  //   14 0 0 0 2 c 2 4 14 0 0 0 2 c 2 4 14 0 0 0 2 c 2 4 2 11 0 0 2 c 2 4 2 11 0 0 2 c 2 4 2 11 0 0 2 c 2
  //   4 2 11 0 0 2 c 2 4 2 11 0 0 2 c 2 4 2 11 0 0 2 c 2 4 2 11 0 0 2 c 2 4 2 11 0 0 2 c 10 5*0 2 c 10 5*0
  //   2 c 10 5*0 2 c 10 5*0 2 c 10 5*0 2 c 10 5*0 2 c 10 5*0 2 c 10 5*0 2 c 10 5*0 2 c 10 5*0 2 c 10 5*0 2
  //   c 10 5*0 2 c 10 5*0 2 c 10 5*0 2 c 10 5*0 2 c 10 5*0 2 c 2 11 4*0 2 c 14 5*0 2 c 2 11 4*0 2 c 14 5*0
  //   2 c 2 11 4*0 2 c 14 5*0 2 c 2 11 4*0 2 c 14 5*0 2 c 2 11 4*0 2 c 14 5*0 2 c 2 11 4*0 2 c 14 5*0 2 c
  //   2 11 4*0 2 c 14 5*0 2 c 2 11 4*0 2 c 14 5*0 2 c 10 5*0 2 c 10 5*0 2 c 10 5*0 2 c 10 5*0 2 c 10 5*0 2
  //   c 10 5*0 2 c 10 5*0 2 c 10 5*0 2 c 10 5*0 2 c 10 5*0 2 c 10 5*0 2 c 10 5*0 2 c 10 5*0 2 c 10 5*0 2 c
  //   10 5*0 2 c 10 5*0 2 c 10 5*0 2 c 10 5*0 2 c 10 5*0 2 c 10 5*0 2 c 10 5*0 2 c 10 5*0 2 c 10 5*0 2 c
  //   10 5*0 2 c 10 5*0 2 c 10 5*0 2 c 10 5*0 2 c 10 5*0 2 c 10 5*0 2 c 10 5*0 2 c 10 5*0 2 c 10 5*0 2 c
  //   10 5*0 2 c 10 5*0 2 c 10 5*0 2 c 10 5*0 2 c 10 5*0 2 c 10 5*0 2 c 10 5*0 2 c 10 5*0 2 c 10 5*0 2 c
  //   10 5*0 2 c 10 5*0 2 c 10 5*0 2 c 10 5*0 2 c 10 5*0 2 c 10 5*0 2 c 10 5*0 2 c 11 5*0 2 c 11 5*0 2 c
  //   11 5*0 2 c 11 5*0 2 c 11 5*0 2 c 11 5*0 2 c 11 5*0 2 c 11 5*0 2 c 11 5*0 2 c 11 5*0 2 c 11 5*0 2 c
  //   11 5*0 2 c 11 5*0 2 c 11 5*0 2 c 11 5*0 2 c 11 5*0 2 c 0 14 4*0 2 c 0 14 4*0 2 c 0 14 4*0 2 c 0 14
  //   4*0 2 c 0 2 11 0 0 0 2 c 0 2 11 0 0 0 2 c 0 2 11 0 0 0 2 c 0 2 11 0 0 0 2 c 0 14 4*0 2 c 0 14 4*0 2
  //   c 0 14 4*0 2 c 0 14 4*0 2 c 0 2 11 0 0 0 2 c 0 2 11 0 0 0 2 c 0 2 11 0 0 0 2 c 0 2 11 0 0 0 2 c 0 14
  //   4*0 2 c 0 14 4*0 2 c 0 14 4*0 2 c 0 14 4*0 2 c 0 14 4*0 2 c 0 14 4*0 2 c 0 14 4*0 2 c 0 14 4*0 2 c 0
  //   2 11 0 0 0 2 c 0 2 11 0 0 0 2 c 0 2 11 0 0 0 2 c 0 2 11 0 0 0 2 c 0 2 11 0 0 0 2 c 0 2 11 0 0 0 2 c
  //   0 2 11 0 0 0 2 c 0 2 11 0 0 0 2 c 10 5*0 2 c 10 5*0 2 c 10 5*0 2 c 10 5*0 2 c 10 5*0 2 c 10 5*0 2 c
  //   10 5*0 2 c 10 5*0 2 c 10 5*0 2 c 10 5*0 2 c 10 5*0 2 c 10 5*0 2 c 10 5*0 2 c 10 5*0 2 c 10 5*0 2 c
  //   10 5*0 2 c 10 5*0 2 c 10 5*0 2 c 10 5*0 2 c 10 5*0 2 c 10 5*0 2 c 10 5*0 2 c 10 5*0 2 c 10 5*0 2 c
  //   10 5*0 2 c 10 5*0 2 c 10 5*0 2 c 10 5*0 2 c 10 5*0 2 c 10 5*0 2 c 10 5*0 2 c 10 5*0 2 c 2 11 4*0 2 c
  //   2 11 4*0 2 c 14 5*0 2 c 14 5*0 2 c 2 11 4*0 2 c 2 11 4*0 2 c 14 5*0 2 c 14 5*0 2 c 2 11 4*0 2 c 2 11
  //   4*0 2 c 14 5*0 2 c 14 5*0 2 c 2 11 4*0 2 c 2 11 4*0 2 c 14 5*0 2 c 14 5*0 2 c 10 5*0 2 c 10 5*0 2 c
  //   10 5*0 2 c 10 5*0 2 c 10 5*0 2 c 10 5*0 2 c 10 5*0 2 c 10 5*0 2 c 10 5*0 2 c 10 5*0 2 c 10 5*0 2 c
  //   10 5*0 2 c 10 5*0 2 c 10 5*0 2 c 10 5*0 2 c 10 5*0 2 c 10 5*0 2 c 10 5*0 2 c 10 5*0 2 c 10 5*0 2 c
  //   10 5*0 2 c 10 5*0 2 c 10 5*0 2 c 10 5*0 2 c 10 5*0 2 c 10 5*0 2 c 10 5*0 2 c 10 5*0 2 c 10 5*0 2 c
  //   10 5*0 2 c 10 5*0 2 c 10 5*0 2 c 11 5*0 2 c 11 5*0 2 c 11 5*0 2 c 11 5*0 2 c 11 5*0 2 c 11 5*0 2 c
  //   11 5*0 2 c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
  //   contents of rom_2 (hex, n*v repeats v):
  //   4 10 6*0 4 10 4 10 4*0 4 10 6*0 4 10 4 10 4*0 4 10 6*0 4 10 4 10 4*0 4 10 6*0 4 10 4 10 4*0 4 10 6*0
  //   4 10 4 10 4*0 4 10 6*0 4 10 4 10 4*0 4 10 6*0 4 10 4 10 4*0 4 10 6*0 4 10 4 10 4*0 4 10 6*0 4 10 6*0
  //   4 10 6*0 4 10 6*0 4 10 6*0 4 10 6*0 4 10 6*0 4 10 6*0 4 10 6*0 4 10 6*0 4 10 6*0 4 10 6*0 4 10 6*0 4
  //   10 6*0 4 10 6*0 4 10 6*0 4 10 6*0 4 10 6*0 4 10 6*0 4 10 6*0 4 10 6*0 4 10 6*0 4 10 6*0 4 10 6*0 4
  //   10 6*0 4 10 6*0 4 10 6*0 4 10 6*0 4 10 6*0 4 10 6*0 4 10 6*0 4 10 6*0 4 10 6*0 4 10 6*0 4 10 6*0 4
  //   10 6*0 4 10 6*0 4 10 6*0 4 10 6*0 4 10 6*0 4 10 6*0 4 10 6*0 4 10 6*0 4 10 6*0 4 10 6*0 4 10 6*0 4
  //   10 6*0 4 10 6*0 4 10 40 5*0 4 10 40 5*0 4 10 40 5*0 4 10 40 5*0 4 10 40 5*0 4 10 40 5*0 4 10 40 5*0
  //   4 10 40 5*0 4 10 40 5*0 4 10 40 5*0 4 10 40 5*0 4 10 40 5*0 4 10 40 5*0 4 10 40 5*0 4 10 40 5*0 4 10
  //   40 5*0 4 10 6*0 4 10 6*0 4 10 6*0 4 10 6*0 4 10 6*0 4 10 6*0 4 10 6*0 4 10 6*0 4 10 6*0 4 10 6*0 4
  //   10 6*0 4 10 6*0 4 10 6*0 4 10 6*0 4 10 6*0 4 10 6*0 4 10 6*0 4 10 6*0 4 10 6*0 4 10 6*0 4 10 6*0 4
  //   10 6*0 4 10 6*0 4 10 6*0 4 10 6*0 4 10 6*0 4 10 6*0 4 10 6*0 4 10 6*0 4 10 6*0 4 10 6*0 4 10 6*0 4
  //   10 4 10 4*0 4 10 4 10 4*0 4 10 4 10 4*0 4 10 4 10 4*0 4 10 4 10 4*0 4 10 4 10 4*0 4 10 4 10 4*0 4 10
  //   4 10 4*0 4 10 4 10 4 10 0 0 4 10 4 10 4 10 0 0 4 10 4 10 4 10 0 0 4 10 4 10 4 10 0 0 4 10 4 10 4 10
  //   0 0 4 10 4 10 4 10 0 0 4 10 4 10 4 10 0 0 4 10 4 10 4 10 0 0 4 10 6*0 4 10 6*0 4 10 6*0 4 10 6*0 4
  //   10 6*0 4 10 6*0 4 10 6*0 4 10 6*0 4 10 6*0 4 10 6*0 4 10 6*0 4 10 6*0 4 10 6*0 4 10 6*0 4 10 6*0 4
  //   10 6*0 4 10 4 10 4*0 4 10 6*0 4 10 4 10 4*0 4 10 6*0 4 10 4 10 4*0 4 10 6*0 4 10 4 10 4*0 4 10 6*0 4
  //   10 4 10 4*0 4 10 6*0 4 10 4 10 4*0 4 10 6*0 4 10 4 10 4*0 4 10 6*0 4 10 4 10 4*0 4 10 6*0 4 10 6*0 4
  //   10 6*0 4 10 6*0 4 10 6*0 4 10 6*0 4 10 6*0 4 10 6*0 4 10 6*0 4 10 6*0 4 10 6*0 4 10 6*0 4 10 6*0 4
  //   10 6*0 4 10 6*0 4 10 6*0 4 10 6*0 4 10 6*0 4 10 6*0 4 10 6*0 4 10 6*0 4 10 6*0 4 10 6*0 4 10 6*0 4
  //   10 6*0 4 10 6*0 4 10 6*0 4 10 6*0 4 10 6*0 4 10 6*0 4 10 6*0 4 10 6*0 4 10 6*0 4 10 40 5*0 4 10 40
  //   5*0 4 10 40 5*0 4 10 40 5*0 4 10 40 5*0 4 10 40 5*0 4 10 40 5*0 4 10 40 5*0 4 10 40 5*0 4 10 40 5*0
  //   4 10 40 5*0 4 10 40 5*0 4 10 40 5*0 4 10 40 5*0 4 10 40 5*0 4 10 40 5*0 4 10 6*0 4 10 6*0 4 10 6*0 4
  //   10 6*0 4 10 6*0 4 10 6*0 4 10 6*0 4 10 6*0 4 10 6*0 4 10 6*0 4 10 6*0 4 10 6*0 4 10 6*0 4 10 6*0 4
  //   10 6*0 4 10 6*0 4 10 2 5*0 4 10 2 5*0 4 10 2 5*0 4 10 2 5*0 4 10 2 4 10 0 0 0 4 10 2 4 10 0 0 0 4 10
  //   2 4 10 0 0 0 4 10 2 4 10 0 0 0 4 10 2 5*0 4 10 2 5*0 4 10 2 5*0 4 10 2 5*0 4 10 2 4 10 0 0 0 4 10 2
  //   4 10 0 0 0 4 10 2 4 10 0 0 0 4 10 2 4 10 0 0 0 4 10 6*0 4 10 6*0 4 10 6*0 4 10 6*0 4 10 6*0 4 10 6*0
  //   4 10 6*0 4 10 6*0 4 10 0 4 10 0 0 0 4 10 0 4 10 0 0 0 4 10 0 4 10 0 0 0 4 10 0 4 10 0 0 0 4 10 0 4
  //   10 0 0 0 4 10 0 4 10 0 0 0 4 10 0 4 10 0 0 0 4 10 0 4 10 0 0 0 4 10 6*0 4 10 6*0 4 10 6*0 4 10 6*0 4
  //   10 6*0 4 10 6*0 4 10 6*0 4 10 6*0 4 10 6*0 4 10 6*0 4 10 6*0 4 10 6*0 4 10 6*0 4 10 6*0 4 10 6*0 4
  //   10 6*0 4 10 6*0 4 10 6*0 4 10 6*0 4 10 6*0 4 10 6*0 4 10 6*0 4 10 6*0 4 10 6*0 4 10 6*0 4 10 6*0 4
  //   10 6*0 4 10 6*0 4 10 6*0 4 10 6*0 4 10 6*0 4 10 6*0 4 10 4 10 4*0 4 10 4 10 4*0 4 10 6*0 4 10 6*0 4
  //   10 4 10 4*0 4 10 4 10 4*0 4 10 6*0 4 10 6*0 4 10 4 10 4*0 4 10 4 10 4*0 4 10 6*0 4 10 6*0 4 10 4 10
  //   4*0 4 10 4 10 4*0 4 10 6*0 4 10 6*0 4 10 6*0 4 10 6*0 4 10 6*0 4 10 6*0 4 10 6*0 4 10 6*0 4 10 6*0 4
  //   10 6*0 4 10 6*0 4 10 6*0 4 10 6*0 4 10 6*0 4 10 6*0 4 10 6*0 4 10 6*0 4 10 6*0 4 10 40 5*0 4 10 40
  //   5*0 4 10 40 5*0 4 10 40 5*0 4 10 40 5*0 4 10 40 5*0 4 10 40 5*0 4 10 40 5*0 4 10 40 5*0 4 10 40 5*0
  //   4 10 40 5*0 4 10 40 5*0 4 10 40 5*0 4 10 40 5*0 4 10 40 5*0 4 10 40 5*0 4 10 6*0 4 10 6*0 4 10 6*0 4
  //   10 6*0 4 10 6*0 4 10 6*0 4 10 6*0 4 10 6*0 4 10 6*0 4 10 6*0 4 10 6*0 4 10 6*0 4 10 6*0 4 10 6*0 4
  //   10 6*0 4 10 6*0 4 10 2 5*0 4 10 2 5*0 4 10 2 5*0 4 10 2 5*0 4 10 2 4 10 0 0 0 4 10 2 4 10 0 0 0 4 10
  //   2 4 10 0 0 0 4 10 2 4 10 0 0 0 4 10 2 5*0 4 10 2 5*0 4 10 2 5*0 4 10 2 5*0 4 10 2 4 10 0 0 0 4 10 2
  //   4 10 0 0 0 4 10 2 4 10 0 0 0 4 10 2 4 10 0 0 0 4 10 6*0 4 10 6*0 4 10 6*0 4 10 6*0 4 10 6*0 4 10 6*0
  //   4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
  //   contents of rom_3 (hex, n*v repeats v):
  //   899*0 62 7*0 62 7*0 62 7*0 62 7*0 62 7*0 62 7*0 62 7*0 62 7*0 62 7*0 62 7*0 62 7*0 62 7*0 62 7*0 62
  //   7*0 62 7*0 62 774*0 62 7*0 62 7*0 62 7*0 62 7*0 62 7*0 62 7*0 62 7*0 62 7*0 62 7*0 62 7*0 62 7*0 62
  //   7*0 62 7*0 62 7*0 62 7*0 62 7*0 62 7*0 62 7*0 62 7*0 62 7*0 62 7*0 62 7*0 62 7*0 62 7*0 62 7*0 62
  //   7*0 62 7*0 62 7*0 62 7*0 62 7*0 62 7*0 62 775*0 62 7*0 62 7*0 62 7*0 62 7*0 62 7*0 62 7*0 62 7*0 62
  //   7*0 62 7*0 62 7*0 62 7*0 62 7*0 62 7*0 62 7*0 62 7*0 62 7*0 62 7*0 62 7*0 62 7*0 62 7*0 62 7*0 62
  //   7*0 62 7*0 62 7*0 62 7*0 62 7*0 62 7*0 62 7*0 62 7*0 62 7*0 62 7*0 62 775*0 62 7*0 62 7*0 62 7*0 62
  //   7*0 62 7*0 62 7*0 62 7*0 62 7*0 62 7*0 62 7*0 62 7*0 62 7*0 62 7*0 62 7*0 62 7*0 62 7*0 62 7*0 62
  //   7*0 62 7*0 62 7*0 62 7*0 62 7*0 62 7*0 62 7*0 62 7*0 62 7*0 62 7*0 62 7*0 62 7*0 62 7*0 62 7*0 62
  //   775*0 62 7*0 62 7*0 62 7*0 62 7*0 62 7*0 62 7*0 62 7*0 62 7*0 62 7*0 62 7*0 62 7*0 62 7*0 62 7*0 62
  //   7*0 62 7*0 62 7*0 62 7*0 62 7*0 62 7*0 62 7*0 62 7*0 62 7*0 62 7*0 62 7*0 62 7*0 62 7*0 62 7*0 62
  //   7*0 62 7*0 62 7*0 62 7*0 62 775*0 62 7*0 62 7*0 62 7*0 62 7*0 62 7*0 62 7*0 62 7*0 62 7*0 62 7*0 62
  //   7*0 62 7*0 62 7*0 62 7*0 62 7*0 62 7*0 62 7*0 62 7*0 62 7*0 62 7*0 62 7*0 62 7*0 62 7*0 62 7*0 62
  //   7*0 62 7*0 62 7*0 62 7*0 62 7*0 62 7*0 62 7*0 62 7*0 62 135*0 62 7*0 62 7*0 62 7*0 62 7*0 62 7*0 62
  //   7*0 62 7*0 62 7*0 62 7*0 62 7*0 62 7*0 62 7*0 62 7*0 62 7*0 62 7*0 62 7*0 62 7*0 62 7*0 62 7*0 62
  //   7*0 62 7*0 62 7*0 62 7*0 62 7*0 62 7*0 62 7*0 62 7*0 62 7*0 62 7*0 62 7*0 62 7*0 62 7*0 62 7*0 62
  //   7*0 62 7*0 62 7*0 62 7*0 62 7*0 62 7*0 62 7*0 62 7*0 62 7*0 62 7*0 62 7*0 62 7*0 62 7*0 62 7*0 62
  //   7*0 62 7*0 62 7*0 62 7*0 62 7*0 62 7*0 62 7*0 62 7*0 62 7*0 62 7*0 62 7*0 62 7*0 62 7*0 62 7*0 62
  //   7*0 62 7*0 62 7*0 62 7*0 62 7*0 62 7*0 62 7*0 62 7*0 62 7*0 62 7*0 62 7*0 62 7*0 62 7*0 62 7*0 62
  //   7*0 62 7*0 62 7*0 62 7*0 62 136*0 62 7*0 62 7*0 62 7*0 62 7*0 62 7*0 62 7*0 62 7*0 62 7*0 62 7*0 62
  //   7*0 62 7*0 62 7*0 62 7*0 62 7*0 62 7*0 62 775*0 62 7*0 62 7*0 62 7*0 62 7*0 62 7*0 62 7*0 62 7*0 62
  //   7*0 62 7*0 62 7*0 62 7*0 62 7*0 62 7*0 62 7*0 62 7*0 62 902*0 f9 4 6*0 f9 4 6*0 f9 4 6*0 f9 4 6*0 f9
  //   4 6*0 f9 4 6*0 f9 4 6*0 f9 4 6*0 f9 4 6*0 f9 4 6*0 f9 4 6*0 f9 4 6*0 f9 4 6*0 f9 4 6*0 f9 4 6*0 f9 4
  //   646*0 62 7*0 62 7*0 62 7*0 62 7*0 62 7*0 62 7*0 62 7*0 62 7*0 62 7*0 62 7*0 62 7*0 62 7*0 62 7*0 62
  //   7*0 62 7*0 62 135*0 f9 4 6*0 f9 4 6*0 f9 4 6*0 f9 4 6*0 f9 4 6*0 f9 4 6*0 f9 4 6*0 f9 4 6*0 f9 4 6*0
  //   f9 4 6*0 f9 4 6*0 f9 4 6*0 f9 4 6*0 f9 4 6*0 f9 4 6*0 f9 4 646*0 62 7*0 62 7*0 62 7*0 62 7*0 62 7*0
  //   62 7*0 62 7*0 62 7*0 62 7*0 62 7*0 62 7*0 62 7*0 62 7*0 62 7*0 62 7*0 62 135*0 f9 4 6*0 f9 4 6*0 f9
  //   4 6*0 f9 4 6*0 f9 4 6*0 f9 4 6*0 f9 4 6*0 f9 4 6*0 f9 4 6*0 f9 4 6*0 f9 4 6*0 f9 4 6*0 f9 4 6*0 f9 4
  //   6*0 f9 4 6*0 f9 4 646*0 62 7*0 62 7*0 62 7*0 62 7*0 62 7*0 62 7*0 62 7*0 62 7*0 62 7*0 62 7*0 62 7*0
  //   62 7*0 62 7*0 62 7*0 62 7*0 62 135*0 f9 4 6*0 f9 4 6*0 f9 4 6*0 f9 4 6*0 f9 4 6*0 f9 4 6*0 f9 4 6*0
  //   f9 4 6*0 f9 4 6*0 f9 4 6*0 f9 4 6*0 f9 4 6*0 f9 4 6*0 f9 4 6*0 f9 4 6*0 f9 4 646*0 62 7*0 62 7*0 62
  //   7*0 62 7*0 62 7*0 62 7*0 62 7*0 62 7*0 62 7*0 62 7*0 62 7*0 62 7*0 62 7*0 62 7*0 62 7*0 62 903*0 62
  //   7*0 62 7*0 62 7*0 62 7*0 62 7*0 62 7*0 62 7*0 62 7*0 62 7*0 62 7*0 62 7*0 62 7*0 62 7*0 62 7*0 62
  //   7*0 62 393*0 9 4 6*0 9 4 6*0 9 4 6*0 9 4 6*0 9 4 6*0 9 4 6*0 9 4 6*0 9 4 6*0 9 4 6*0 9 4 6*0 9 4 6*0
  //   9 4 6*0 9 4 6*0 9 4 6*0 9 4 6*0 9 4 6*0 9 4 6*0 9 4 6*0 9 4 6*0 9 4 6*0 9 4 6*0 9 4 6*0 9 4 6*0 9 4
  //   6*0 9 4 6*0 9 4 6*0 9 4 6*0 9 4 6*0 9 4 6*0 9 4 6*0 9 4 6*0 9 4 6*0 9 4 6*0 9 4 6*0 9 4 6*0 9 4 6*0
  //   9 4 6*0 9 4 6*0 9 4 6*0 9 4 6*0 9 4 6*0 9 4 6*0 9 4 6*0 9 4 6*0 9 4 6*0 9 4 6*0 9 4 6*0 9 4 6*0 9 4
  //   6*0 9 4 6*0 9 4 6*0 9 4 6*0 9 4 6*0 9 4 6*0 9 4 6*0 9 4 6*0 9 4 6*0 9 4 6*0 9 4 6*0 9 4 6*0 9 4 6*0
  //   9 4 6*0 9 4 6*0 9 4 134*0 9 4 6*0 9 4 6*0 9 4 6*0 9 4 6*0 9 4 6*0 9 4 6*0 9 4 6*0 9 4 6*0 9 4 6*0 9
  //   4 6*0 9 4 6*0 9 4 6*0 9 4 6*0 9 4 6*0 9 4 6*0 9 4 773*0 62 7*0 62 7*0 62 7*0 62 7*0 62 7*0 62 7*0 62
  //   7*0 62 7*0 62 7*0 62 7*0 62 7*0 62 7*0 62 7*0 62 7*0 62 7*0 62 134*0 f9 4 0 f9 4 0 0 0 f9 4 0 f9 4 0
  //   0 0 f9 4 0 f9 4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
  //   contents of rom_4 (hex, n*v repeats v):
  //   130*0 6 7*0 6 7*0 6 7*0 6 7*0 6 7*0 6 7*0 6 7*0 6 7*0 6 7*0 6 7*0 6 7*0 6 7*0 6 7*0 6 7*0 6 7*0 6
  //   7*0 12 7*0 12 7*0 12 7*0 12 7*0 12 7*0 12 7*0 12 7*0 12 7*0 12 7*0 12 7*0 12 7*0 12 7*0 12 7*0 12
  //   7*0 12 7*0 12 7*0 42 7*0 42 7*0 42 7*0 42 7*0 42 7*0 42 7*0 42 7*0 42 7*0 42 7*0 42 7*0 42 7*0 42
  //   7*0 42 7*0 42 7*0 42 7*0 42 7*0 2 7*0 2 7*0 2 7*0 2 7*0 2 7*0 2 7*0 2 7*0 2 7*0 2 7*0 2 7*0 2 7*0 2
  //   7*0 2 7*0 2 7*0 2 7*0 2 7*0 2 7*0 2 7*0 2 7*0 2 7*0 2 7*0 2 7*0 2 7*0 2 7*0 2 7*0 2 7*0 2 7*0 2 7*0
  //   2 7*0 2 7*0 2 7*0 2 263*0 9 7*0 9 7*0 9 7*0 9 7*0 9 7*0 9 7*0 9 7*0 9 7*0 9 7*0 9 7*0 9 7*0 9 7*0 9
  //   7*0 9 7*0 9 7*0 9 135*0 18 7*0 18 7*0 18 7*0 18 7*0 18 7*0 18 7*0 18 7*0 18 7*0 18 7*0 18 7*0 18 7*0
  //   18 7*0 18 7*0 18 7*0 18 7*0 18 7*0 48 7*0 48 7*0 48 7*0 48 7*0 48 7*0 48 7*0 48 7*0 48 7*0 48 7*0 48
  //   7*0 48 7*0 48 7*0 48 7*0 48 7*0 48 7*0 48 7*0 8 7*0 8 7*0 8 7*0 8 7*0 8 7*0 8 7*0 8 7*0 8 7*0 8 7*0
  //   8 7*0 8 7*0 8 7*0 8 7*0 8 7*0 8 7*0 8 7*0 8 7*0 8 7*0 8 7*0 8 7*0 8 7*0 8 7*0 8 7*0 8 7*0 8 7*0 8
  //   7*0 8 7*0 8 7*0 8 7*0 8 7*0 8 7*0 8 7*0 8 7*0 8 7*0 8 7*0 8 7*0 8 7*0 8 7*0 8 7*0 8 7*0 8 7*0 8 7*0
  //   8 7*0 8 7*0 8 7*0 8 7*0 8 7*0 8 7*0 8 7*0 8 7*0 8 7*0 8 7*0 8 7*0 8 7*0 8 7*0 8 7*0 8 7*0 8 7*0 8
  //   7*0 8 7*0 8 7*0 8 7*0 8 7*0 8 7*0 21 7*0 21 7*0 21 7*0 21 7*0 21 7*0 21 7*0 21 7*0 21 7*0 21 7*0 21
  //   7*0 21 7*0 21 7*0 21 7*0 21 7*0 21 7*0 21 7*0 24 7*0 24 7*0 24 7*0 24 7*0 24 7*0 24 7*0 24 7*0 24
  //   7*0 24 7*0 24 7*0 24 7*0 24 7*0 24 7*0 24 7*0 24 7*0 24 135*0 60 7*0 60 7*0 60 7*0 60 7*0 60 7*0 60
  //   7*0 60 7*0 60 7*0 60 7*0 60 7*0 60 7*0 60 7*0 60 7*0 60 7*0 60 7*0 60 7*0 20 7*0 20 7*0 20 7*0 20
  //   7*0 20 7*0 20 7*0 20 7*0 20 7*0 20 7*0 20 7*0 20 7*0 20 7*0 20 7*0 20 7*0 20 7*0 20 7*0 20 7*0 20
  //   7*0 20 7*0 20 7*0 20 7*0 20 7*0 20 7*0 20 7*0 20 7*0 20 7*0 20 7*0 20 7*0 20 7*0 20 7*0 20 7*0 20
  //   7*0 20 7*0 20 7*0 20 7*0 20 7*0 20 7*0 20 7*0 20 7*0 20 7*0 20 7*0 20 7*0 20 7*0 20 7*0 20 7*0 20
  //   7*0 20 7*0 20 7*0 20 7*0 20 7*0 20 7*0 20 7*0 20 7*0 20 7*0 20 7*0 20 7*0 20 7*0 20 7*0 20 7*0 20
  //   7*0 20 7*0 20 7*0 20 7*0 20 7*0 81 7*0 81 7*0 81 7*0 81 7*0 81 7*0 81 7*0 81 7*0 81 7*0 81 7*0 81
  //   7*0 81 7*0 81 7*0 81 7*0 81 7*0 81 7*0 81 7*0 84 7*0 84 7*0 84 7*0 84 7*0 84 7*0 84 7*0 84 7*0 84
  //   7*0 84 7*0 84 7*0 84 7*0 84 7*0 84 7*0 84 7*0 84 7*0 84 7*0 90 7*0 90 7*0 90 7*0 90 7*0 90 7*0 90
  //   7*0 90 7*0 90 7*0 90 7*0 90 7*0 90 7*0 90 7*0 90 7*0 90 7*0 90 7*0 90 135*0 80 7*0 80 7*0 80 7*0 80
  //   7*0 80 7*0 80 7*0 80 7*0 80 7*0 80 7*0 80 7*0 80 7*0 80 7*0 80 7*0 80 7*0 80 7*0 80 7*0 80 7*0 80
  //   7*0 80 7*0 80 7*0 80 7*0 80 7*0 80 7*0 80 7*0 80 7*0 80 7*0 80 7*0 80 7*0 80 7*0 80 7*0 80 7*0 80
  //   7*0 80 7*0 80 7*0 80 7*0 80 7*0 80 7*0 80 7*0 80 7*0 80 7*0 80 7*0 80 7*0 80 7*0 80 7*0 80 7*0 80
  //   7*0 80 7*0 80 7*0 80 7*0 80 7*0 80 7*0 80 7*0 80 7*0 80 7*0 80 7*0 80 7*0 80 7*0 80 7*0 80 7*0 80
  //   7*0 80 7*0 80 7*0 80 7*0 80 7*0 1 7*0 1 7*0 1 7*0 1 7*0 1 7*0 1 7*0 1 7*0 1 7*0 1 7*0 1 7*0 1 7*0 1
  //   7*0 1 7*0 1 7*0 1 7*0 1 7*0 4 7*0 4 7*0 4 7*0 4 7*0 4 7*0 4 7*0 4 7*0 4 7*0 4 7*0 4 7*0 4 7*0 4 7*0
  //   4 7*0 4 7*0 4 7*0 4 7*0 10 7*0 10 7*0 10 7*0 10 7*0 10 7*0 10 7*0 10 7*0 10 7*0 10 7*0 10 7*0 10 7*0
  //   10 7*0 10 7*0 10 7*0 10 7*0 10 7*0 40 7*0 40 7*0 40 7*0 40 7*0 40 7*0 40 7*0 40 7*0 40 7*0 40 7*0 40
  //   7*0 40 7*0 40 7*0 40 7*0 40 7*0 40 7*0 40 519*0 1 7*0 1 7*0 1 7*0 1 7*0 1 7*0 1 7*0 1 7*0 1 7*0 1
  //   7*0 1 7*0 1 7*0 1 7*0 1 7*0 1 7*0 1 7*0 1 7*0 4 7*0 4 7*0 4 7*0 4 7*0 4 7*0 4 7*0 4 7*0 4 7*0 4 7*0
  //   4 7*0 4 7*0 4 7*0 4 7*0 4 7*0 4 7*0 4 7*0 10 7*0 10 7*0 10 7*0 10 7*0 10 7*0 10 7*0 10 7*0 10 7*0 10
  //   7*0 10 7*0 10 7*0 10 7*0 10 7*0 10 7*0 10 7*0 10 7*0 40 7*0 40 7*0 40 7*0 40 7*0 40 7*0 40 7*0 40
  //   7*0 40 7*0 40 7*0 40 7*0 40 7*0 40 7*0 40 7*0 40 7*0 40 7*0 40 647*0 8 7*0 8 7*0 8 7*0 8 7*0 8 7*0 8
  //   7*0 8 7*0 8 7*0 8 7*0 8 7*0 8 7*0 8 7*0 8 7*0 8 7*0 8 7*0 8 7*0 20 7*0 20 7*0 20 7*0 20 7*0 20 7*0
  //   20 7*0 20 7*0 20 7*0 20 7*0 20 7*0 20 7*0 20 7*0 20 7*0 20 7*0 20 7*0 20 7*0 80 7*0 80 7*0 80 7*0 80
  //   7*0 80 7*0 80 7*0 80 7*0 80 7*0 80 7*0 80 7*0 80 7*0 80 7*0 80 7*0 80 7*0 80 7*0 80 520*0 1 7*0 1
  //   7*0 1 7*0 1 7*0 1 7*0 1 7*0 1 7*0 1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
  //   And so on.
  //   And another slice.
  //   This is one 8 bit "slice" of the output control signals.
endmodule

module ALU_8 (
  input  [7:0] A,
  input  [7:0] B,
  input  carry_in,
  input  M,
  input  S0,
  input  S1,
  input  S2,
  input  S3,
  input  result_output_enable,
  input  clock,
  input  sim_only_reset,
  input  store_result,
  input  store_flags,
  output unclocked_zero,
  output clocked_zero,
  output unclocked_negative,
  output clocked_negative,
  output unclocked_carryborrow_out,
  output clocked_carryborrow_out,
  output unclocked_A___B,
  output clocked_A___B,
  output [7:0] tristate_clocked_result,
  output [7:0] unclocked_result,
  output [7:0] clocked_result
);

  wire n74ls181_1_a_b, n74ls181_1_carry_out_bar, n74ls181_2_a_b, n74ls181_2_carry_out_bar, not_2_out,
       or_1_out, or_2_out, or_3_out, or_4_out, or_5_out, or_6_out, or_7_out, safe_clock_enable_1_clock_out,
       safe_clock_enable_2_clock_out;

  and and_1 (unclocked_A___B, n74ls181_1_a_b, n74ls181_2_a_b);
  not not_1 (unclocked_carryborrow_out, n74ls181_2_carry_out_bar);
  not not_2 (not_2_out, carry_in);
  _74LS181 u_74ls181_1 (
    .B(B[3:0]), .A(A[3:0]), .M(M), .carry_in_bar(not_2_out), .carry_out_bar(n74ls181_1_carry_out_bar),
    .F(unclocked_result[3:0]), .A_B(n74ls181_1_a_b), .S0(S0), .S1(S1), .S2(S2), .S3(S3));  // open: Y, X
  _74LS181 u_74ls181_2 (
    .B(B[7:4]), .A(A[7:4]), .M(M), .carry_in_bar(n74ls181_1_carry_out_bar),
    .carry_out_bar(n74ls181_2_carry_out_bar), .F({unclocked_negative, unclocked_result[6:4]}),
    .A_B(n74ls181_2_a_b), .S0(S0), .S1(S1), .S2(S2), .S3(S3));  // open: Y, X
  or or_1 (or_1_out, unclocked_result[0], unclocked_result[1]);
  or or_2 (or_2_out, or_1_out, or_3_out);
  or or_3 (or_3_out, unclocked_result[2], unclocked_result[3]);
  or or_4 (or_4_out, unclocked_result[4], unclocked_result[5]);
  or or_5 (or_5_out, or_4_out, or_6_out);
  or or_6 (or_6_out, unclocked_result[6], unclocked_negative);
  safe_clock_enable safe_clock_enable_1 (
    .clock_enable(store_result), .clock_in(clock), .clock_out(safe_clock_enable_1_clock_out));
  safe_clock_enable safe_clock_enable_2 (
    .clock_enable(store_flags), .clock_in(clock), .clock_out(safe_clock_enable_2_clock_out));
  or or_7 (or_7_out, or_2_out, or_5_out);
  not not_3 (unclocked_zero, or_7_out);
  Register result (
    .D({unclocked_negative, unclocked_result[6:0]}), .en(1'b1), .Q(clocked_result),
    .clk(safe_clock_enable_1_clock_out), .clr(sim_only_reset));
  assign tristate_clocked_result = result_output_enable ? clocked_result : 8'bz;  // Controlled_Buffer controlled_buffer_1
  Register #(.width(4)) register_1 (
    .D({unclocked_A___B, unclocked_carryborrow_out, unclocked_negative, unclocked_zero}), .en(1'b1),
    .Q({clocked_A___B, clocked_carryborrow_out, clocked_negative, clocked_zero}),
    .clk(safe_clock_enable_2_clock_out), .clr(sim_only_reset));

  assign unclocked_result[7] = unclocked_negative;
endmodule

module register_bus_R_8 (
  input  [7:0] \input ,
  input  input_enable,
  input  output_enable,
  input  clock,
  input  sim_only_reset,
  output [7:0] content,
  output [7:0] buffered_output
);

  wire safe_clock_enable_1_clock_out;

  safe_clock_enable safe_clock_enable_1 (
    .clock_enable(input_enable), .clock_in(clock), .clock_out(safe_clock_enable_1_clock_out));
  Register register_1 (.D(\input ), .en(1'b1), .Q(content), .clk(safe_clock_enable_1_clock_out), .clr(sim_only_reset));
  assign buffered_output = output_enable ? content : 8'bz;  // Controlled_Buffer controlled_buffer_1
endmodule

module register_bus_L_8 (
  input  [7:0] \input ,
  input  output_enable,
  input  input_enable,
  input  clock,
  input  sim_only_reset,
  output [7:0] content,
  output [7:0] buffered_output
);

  wire safe_clock_enable_1_clock_out;

  safe_clock_enable safe_clock_enable_1 (
    .clock_enable(input_enable), .clock_in(clock), .clock_out(safe_clock_enable_1_clock_out));
  Register register_1 (.D(\input ), .en(1'b1), .Q(content), .clk(safe_clock_enable_1_clock_out), .clr(sim_only_reset));
  assign buffered_output = output_enable ? content : 8'bz;  // Controlled_Buffer controlled_buffer_1
endmodule

module program_counter_8 (
  input  in,
  input  output_enable,
  input  [7:0] \input ,
  input  count,
  input  clock,
  input  reset,
  output [7:0] tristate_output,
  output [7:0] contents
);

  Counter counter_1 (.load(in), .D(\input ), .count(count), .Q(contents), .clk(clock), .clr(reset));  // open: carry
  assign tristate_output = output_enable ? contents : 8'bz;  // Controlled_Buffer controlled_buffer_1
endmodule

module _74LS181 (
  input  S0,
  input  S1,
  input  S2,
  input  S3,
  input  [3:0] B,
  input  [3:0] A,
  input  M,
  input  carry_in_bar,
  output Y,
  output carry_out_bar,
  output X,
  output [3:0] F,
  output A_B
);

  wire and_1_out, and_2_out, and_3_out, and_4_out, and_5_out, and_6_out, and_7_out, and_8_out, and_9_out,
       and_10_out, and_11_out, and_12_out, and_13_out, and_14_out, and_15_out, and_16_out, and_17_out,
       and_18_out, and_19_out, and_20_out, and_21_out, and_22_out, and_23_out, and_24_out, and_25_out,
       and_26_out, and_27_out, and_28_out, nand_1_out, nand_3_out, nor_1_out, nor_2_out, nor_3_out,
       nor_4_out, nor_5_out, nor_6_out, nor_7_out, nor_8_out, nor_10_out, nor_11_out, nor_12_out, not_1_out,
       not_2_out, not_3_out, not_4_out, not_5_out, xor_1_out, xor_2_out, xor_3_out, xor_4_out;

  not not_1 (not_1_out, B[3]);
  not not_2 (not_2_out, B[2]);
  not not_3 (not_3_out, B[1]);
  not not_4 (not_4_out, B[0]);
  not not_5 (not_5_out, M);
  and and_1 (and_1_out, B[3], S3, A[3]);
  and and_2 (and_2_out, A[3], S2, not_1_out);
  and and_3 (and_3_out, not_1_out, S1);
  and and_4 (and_4_out, S0, B[3]);
  and and_5 (and_5_out, B[2], S3, A[2]);
  and and_6 (and_6_out, A[2], S2, not_2_out);
  and and_7 (and_7_out, not_2_out, S1);
  and and_8 (and_8_out, S0, B[2]);
  and and_9 (and_9_out, B[1], S3, A[1]);
  and and_10 (and_10_out, A[1], S2, not_3_out);
  and and_11 (and_11_out, not_3_out, S1);
  and and_12 (and_12_out, S0, B[1]);
  and and_13 (and_13_out, B[0], S3, A[0]);
  and and_14 (and_14_out, A[0], S2, not_4_out);
  and and_15 (and_15_out, not_4_out, S1);
  and and_16 (and_16_out, S0, B[0]);
  nor nor_1 (nor_1_out, and_1_out, and_2_out);
  nor nor_2 (nor_2_out, and_3_out, and_4_out, A[3]);
  nor nor_3 (nor_3_out, and_5_out, and_6_out);
  nor nor_4 (nor_4_out, and_7_out, and_8_out, A[2]);
  nor nor_5 (nor_5_out, and_9_out, and_10_out);
  nor nor_6 (nor_6_out, and_11_out, and_12_out, A[1]);
  nor nor_7 (nor_7_out, and_13_out, and_14_out);
  nor nor_8 (nor_8_out, and_15_out, and_16_out, A[0]);
  xor xor_1 (xor_1_out, nor_1_out, nor_2_out);
  xor xor_2 (xor_2_out, nor_3_out, nor_4_out);
  xor xor_3 (xor_3_out, nor_5_out, nor_6_out);
  xor xor_4 (xor_4_out, nor_7_out, nor_8_out);
  and and_17 (and_17_out, nor_1_out, nor_4_out);
  and and_18 (and_18_out, nor_1_out, nor_3_out, nor_6_out);
  and and_19 (and_19_out, nor_1_out, nor_3_out, nor_5_out, nor_8_out);
  nand nand_1 (nand_1_out, nor_1_out, nor_3_out, nor_5_out, nor_7_out, carry_in_bar);
  nand nand_2 (X, nor_1_out, nor_3_out, nor_5_out, nor_7_out);
  and and_20 (and_20_out, carry_in_bar, nor_7_out, nor_5_out, nor_3_out, not_5_out);
  and and_21 (and_21_out, nor_5_out, nor_3_out, nor_8_out, not_5_out);
  and and_22 (and_22_out, nor_3_out, nor_6_out, not_5_out);
  and and_23 (and_23_out, nor_4_out, not_5_out);
  and and_24 (and_24_out, carry_in_bar, nor_7_out, nor_5_out, not_5_out);
  and and_25 (and_25_out, nor_5_out, nor_8_out, not_5_out);
  and and_26 (and_26_out, nor_6_out, not_5_out);
  and and_27 (and_27_out, carry_in_bar, nor_7_out, not_5_out);
  and and_28 (and_28_out, nor_8_out, not_5_out);
  nand nand_3 (nand_3_out, carry_in_bar, not_5_out);
  nor nor_9 (Y, nor_2_out, and_17_out, and_18_out, and_19_out);
  nor nor_10 (nor_10_out, and_20_out, and_21_out, and_22_out, and_23_out);
  nor nor_11 (nor_11_out, and_24_out, and_25_out, and_26_out);
  nor nor_12 (nor_12_out, and_27_out, and_28_out);
  or or_1 (carry_out_bar, ~Y, ~nand_1_out);  // OR_Gate
  xor xor_5 (F[3], xor_1_out, nor_10_out);
  xor xor_6 (F[2], xor_2_out, nor_11_out);
  xor xor_7 (F[1], xor_3_out, nor_12_out);
  xor xor_8 (F[0], xor_4_out, nand_3_out);
  and and_29 (A_B, F[3], F[2], F[1], F[0]);
endmodule

module safe_clock_enable (
  input  clock_enable,
  input  clock_in,
  output clock_out
);

  wire nor_1_out, nor_2_out, not_1_out, not_2_out;

  not not_1 (not_1_out, clock_enable);
  not not_2 (not_2_out, clock_in);
  nor nor_1 (nor_1_out, not_1_out, nor_2_out);
  nor nor_2 (nor_2_out, nor_1_out, not_2_out);
  and and_1 (clock_out, nor_1_out, clock_in);
endmodule

module schem_export (
  input  Halt,
  input  Reset,
  input  Auto_Manual,
  input  Manual_clock,
  output Clock,
  output Control_Clock
);

  wire Auto_clock_out, nand_1_out, nand_2_out, nand_3_out, nand_4_out, nand_5_out, nand_6_out, nand_7_out,
       nand_8_out, nor_1_out, nor_2_out, nor_3_out, nor_4_out, not_1_out, not_2_out;

  Clock_part Auto_clock (.out(Auto_clock_out));
  nand nand_1 (nand_1_out, Auto_Manual, Auto_Manual);
  nor nor_1 (nor_1_out, Halt, Reset);
  nand nand_2 (nand_2_out, Auto_Manual, Manual_clock);
  nand nand_3 (nand_3_out, nand_1_out, Auto_clock_out);
  nand nand_4 (nand_4_out, nor_1_out, nor_1_out);
  nand nand_5 (nand_5_out, nand_2_out, nand_3_out);
  nor nor_2 (nor_2_out, nand_5_out, nand_5_out);
  nor nor_3 (nor_3_out, nand_4_out, nor_4_out);
  nor nor_4 (nor_4_out, nor_3_out, nor_2_out);
  nand nand_6 (nand_6_out, nor_3_out, nand_5_out);
  nand nand_7 (nand_7_out, nand_6_out, nand_6_out);
  nand nand_8 (nand_8_out, nand_7_out, nand_7_out);
  J_K_Flip_Flop j_k_ff_1 (
    .J(1'b1), .clk(nand_7_out), .K(1'b1), .Q(Clock), .preset(1'b0), .en(1'b1), .reset(not_1_out));  // open: Qn
  not not_1 (not_1_out, nor_1_out);
  J_K_Flip_Flop j_k_ff_2 (
    .J(1'b1), .clk(nand_8_out), .K(1'b1), .Q(Control_Clock), .preset(1'b0), .en(1'b1), .reset(not_2_out));  // open: Qn
  not not_2 (not_2_out, nor_1_out);

  // Notes on the sheet:
  //   Safe clock enable
endmodule

module clipboard (
  input  in_1,
  input  in_2,
  output out_3,
  output out_4,
  output out_5,
  output clock_out
);

  wire A_IN, A_OUT, ACC_IN, ACC_OUT, ALU_A_IS_BUS, ALU_C_IN, ALU_CARRYBORROW_FLAG_CLOCKED,
       ALU_CARRYBORROW_FLAG_IMM, ALU_EQUAL_FLAG_CLOCKED, ALU_EQUAL_FLAG_IMM, ALU_M,
       ALU_NEGATIVE_FLAG_CLOCKED, ALU_NEGATIVE_FLAG_IMM, ALU_OUT, ALU_S0, ALU_S1, ALU_S2, ALU_S3,
       ALU_STORE_FLAGS, ALU_STORE_RESULT, ALU_ZERO_FLAG_CLOCKED, ALU_ZERO_FLAG_IMM, B_IN, B_OUT, C_IN, C_OUT,
       CLOCK_HALT, CONTROL_CLOCK, CU_CARRYBORROW_MIRROR, CU_EQUAL_MIRROR, CU_NEGATIVE_MIRROR, CU_STEP_RESET,
       CU_ZERO_MIRROR, IR_IN, MAR_IN, PC_COUNT, PC_IN, PC_OUT, SIM_ONLY_RESET, SP_IN, SP_OUT;
  wire [2:0] CU_MICROCODE_STEP;
  wire [7:0] A, ACC, ADDRESS, ALU_RESULT_CLOCKED, ALU_RESULT_IMM, B, BUS, C, CU_INSTRUCTION_MIRROR, IR, PC,
       SP;

  Button button_1 (.out(SIM_ONLY_RESET));
  LED led_1 (.in(ACC_IN));
  LED led_2 (.in(ACC_OUT));
  LED led_3 (.in(A_IN));
  LED led_4 (.in(A_OUT));
  LED led_5 (.in(B_IN));
  LED led_6 (.in(B_OUT));
  LED led_7 (.in(C_IN));
  LED led_8 (.in(C_OUT));
  LED led_9 (.in(ALU_STORE_RESULT));
  LED led_10 (.in(ALU_STORE_FLAGS));
  LED led_11 (.in(ALU_OUT));
  LED led_12 (.in(ALU_A_IS_BUS));
  LED led_13 (.in(ALU_S0));
  LED led_14 (.in(ALU_S1));
  LED led_15 (.in(ALU_S2));
  LED led_16 (.in(ALU_S3));
  LED led_17 (.in(ALU_M));
  LED led_18 (.in(ALU_C_IN));
  LED led_19 (.in(MAR_IN));
  LED led_20 (.in(out_4));
  LED led_21 (.in(out_5));
  LED led_22 (.in(out_3));
  LED led_23 (.in(SP_IN));
  LED led_24 (.in(SP_OUT));
  LED led_25 (.in(PC_IN));
  LED led_26 (.in(PC_OUT));
  LED led_27 (.in(PC_COUNT));
  LED led_28 (.in(IR_IN));
  LED led_29 (.in(CU_STEP_RESET));
  LED led_30 (.in(CLOCK_HALT));
  LED led_31 (.in(BUS[7]));
  LED led_32 (.in(BUS[6]));
  LED led_33 (.in(PC[6]));
  LED led_34 (.in(PC[7]));
  LED led_35 (.in(IR[6]));
  LED led_36 (.in(IR[7]));
  LED led_37 (.in(SP[6]));
  LED led_38 (.in(SP[7]));
  LED led_39 (.in(ACC[7]));
  LED led_40 (.in(ACC[6]));
  LED led_41 (.in(A[6]));
  LED led_42 (.in(A[7]));
  LED led_43 (.in(B[6]));
  LED led_44 (.in(B[7]));
  LED led_45 (.in(C[7]));
  LED led_46 (.in(C[6]));
  LED led_47 (.in(ADDRESS[7]));
  LED led_48 (.in(ADDRESS[6]));
  LED led_49 (.in(BUS[5]));
  LED led_50 (.in(BUS[3]));
  LED led_51 (.in(BUS[4]));
  LED led_52 (.in(BUS[2]));
  LED led_53 (.in(PC[5]));
  LED led_54 (.in(PC[2]));
  LED led_55 (.in(PC[4]));
  LED led_56 (.in(PC[3]));
  LED led_57 (.in(IR[4]));
  LED led_58 (.in(IR[5]));
  LED led_59 (.in(IR[3]));
  LED led_60 (.in(IR[2]));
  LED led_61 (.in(SP[2]));
  LED led_62 (.in(SP[4]));
  LED led_63 (.in(SP[5]));
  LED led_64 (.in(SP[3]));
  LED led_65 (.in(ACC[3]));
  LED led_66 (.in(ACC[5]));
  LED led_67 (.in(ACC[4]));
  LED led_68 (.in(ACC[2]));
  LED led_69 (.in(A[3]));
  LED led_70 (.in(A[4]));
  LED led_71 (.in(A[2]));
  LED led_72 (.in(A[5]));
  LED led_73 (.in(B[3]));
  LED led_74 (.in(B[4]));
  LED led_75 (.in(B[5]));
  LED led_76 (.in(B[2]));
  LED led_77 (.in(C[3]));
  LED led_78 (.in(C[5]));
  LED led_79 (.in(C[2]));
  LED led_80 (.in(C[4]));
  LED led_81 (.in(ADDRESS[2]));
  LED led_82 (.in(ADDRESS[4]));
  LED led_83 (.in(ADDRESS[3]));
  LED led_84 (.in(ADDRESS[5]));
  // Probe on BUS
  LED led_85 (.in(BUS[1]));
  LED led_86 (.in(BUS[0]));
  // Probe on PC
  LED led_87 (.in(PC[1]));
  LED led_88 (.in(PC[0]));
  // Probe on IR
  LED led_89 (.in(IR[1]));
  LED led_90 (.in(IR[0]));
  // Probe on SP
  LED led_91 (.in(SP[1]));
  LED led_92 (.in(SP[0]));
  // Probe on ACC
  LED led_93 (.in(ACC[1]));
  LED led_94 (.in(ACC[0]));
  // Probe on A
  LED led_95 (.in(A[0]));
  LED led_96 (.in(A[1]));
  // Probe on B
  LED led_97 (.in(B[0]));
  LED led_98 (.in(B[1]));
  // Probe on C
  LED led_99 (.in(C[1]));
  LED led_100 (.in(C[0]));
  // Probe on ADDRESS
  LED led_101 (.in(ADDRESS[0]));
  LED led_102 (.in(ADDRESS[1]));
  // Probe on BUS
  // Probe on BUS
  // Probe on PC
  // Probe on PC
  // Probe on IR
  // Probe on IR
  // Probe on SP
  // Probe on SP
  // Probe on ACC
  // Probe on ACC
  // Probe on A
  // Probe on A
  // Probe on B
  // Probe on B
  // Probe on C
  // Probe on C
  // Probe on ADDRESS
  // Probe on ADDRESS
  LED led_103 (.in(ALU_RESULT_IMM[7]));
  LED led_104 (.in(ALU_RESULT_IMM[6]));
  LED led_105 (.in(ALU_RESULT_CLOCKED[6]));
  LED led_106 (.in(ALU_RESULT_CLOCKED[7]));
  LED led_107 (.in(ALU_ZERO_FLAG_IMM));
  LED led_108 (.in(ALU_NEGATIVE_FLAG_IMM));
  LED led_109 (.in(ALU_CARRYBORROW_FLAG_IMM));
  LED led_110 (.in(ALU_EQUAL_FLAG_IMM));
  LED led_111 (.in(ALU_ZERO_FLAG_CLOCKED));
  LED led_112 (.in(ALU_NEGATIVE_FLAG_CLOCKED));
  LED led_113 (.in(ALU_CARRYBORROW_FLAG_CLOCKED));
  LED led_114 (.in(ALU_EQUAL_FLAG_CLOCKED));
  LED led_115 (.in(CU_INSTRUCTION_MIRROR[7]));
  LED led_116 (.in(CU_MICROCODE_STEP[2]));
  LED led_117 (.in(CU_ZERO_MIRROR));
  LED led_118 (.in(CU_NEGATIVE_MIRROR));
  LED led_119 (.in(CU_CARRYBORROW_MIRROR));
  LED led_120 (.in(CU_EQUAL_MIRROR));
  LED led_121 (.in(clock_out));
  LED led_122 (.in(CONTROL_CLOCK));
  LED led_123 (.in(ALU_RESULT_IMM[4]));
  LED led_124 (.in(ALU_RESULT_IMM[2]));
  LED led_125 (.in(ALU_RESULT_IMM[3]));
  LED led_126 (.in(ALU_RESULT_IMM[5]));
  LED led_127 (.in(ALU_RESULT_CLOCKED[2]));
  LED led_128 (.in(ALU_RESULT_CLOCKED[3]));
  LED led_129 (.in(ALU_RESULT_CLOCKED[4]));
  LED led_130 (.in(ALU_RESULT_CLOCKED[5]));
  LED led_131 (.in(CU_INSTRUCTION_MIRROR[6]));
  LED led_132 (.in(CU_INSTRUCTION_MIRROR[5]));
  LED led_133 (.in(CU_INSTRUCTION_MIRROR[3]));
  LED led_134 (.in(CU_INSTRUCTION_MIRROR[4]));
  LED led_135 (.in(CU_MICROCODE_STEP[1]));
  LED led_136 (.in(CU_MICROCODE_STEP[0]));
  // Probe on ALU_RESULT_IMM
  LED led_137 (.in(ALU_RESULT_IMM[0]));
  LED led_138 (.in(ALU_RESULT_IMM[1]));
  // Probe on ALU_RESULT_CLOCKED
  LED led_139 (.in(ALU_RESULT_CLOCKED[1]));
  LED led_140 (.in(ALU_RESULT_CLOCKED[0]));
  LED led_141 (.in(CU_INSTRUCTION_MIRROR[0]));
  LED led_142 (.in(CU_INSTRUCTION_MIRROR[2]));
  LED led_143 (.in(CU_INSTRUCTION_MIRROR[1]));
  // Probe on ALU_RESULT_IMM
  // Probe on ALU_RESULT_IMM
  // Probe on ALU_RESULT_CLOCKED
  // Probe on ALU_RESULT_CLOCKED
  // Probe on CU_INSTRUCTION_MIRROR
  // Probe on CU_INSTRUCTION_MIRROR
  // Probe on CU_INSTRUCTION_MIRROR
  // Probe on CU_MICROCODE_STEP
  // Probe on CU_MICROCODE_STEP
  // Probe on CU_MICROCODE_STEP

  // Other names for the same wires on the sheet: DATA_CLOCK = clock_out; EXT_CLOCK_PULSE = in_2;
  //   PROG_DATA_MEM = out_3; READ_FROM_MEM = out_5; RESET = in_1; WRITE_TO_MEM = out_4

  // Notes on the sheet:
  //   BIN
  //   BIN
  //   HEX
  //   BIN
  //   HEX
  //   DEC
  //   BIN
  //   HEX
  //   DEC
  //   BIN
  //   HEX
  //   DEC
  //   HEX
  //   DEC
  //   BIN
  //   HEX
  //   DEC
  //   BIN
  //   HEX
  //   DEC
  //   BIN
  //   HEX
  //   DEC
  //   DEC
  //   BIN
  //   HEX
  //   DEC
  //   BIN
  //   HEX
  //   DEC
  //   BIN
  //   HEX
  //   DEC
  //   BIN
  //   HEX
  //   DEC
  //   BIN
  //   HEX
  //   DEC
endmodule

module io_device (
  input  [7:0] in_1,
  input  [7:0] in_2,
  input  Prog_data_sel,
  input  Write_to_mem,
  input  Clock,
  output [7:0] out_6
);

  wire and_1_out, and_2_out, nand_1_out, not_1_out;

  nand nand_1 (nand_1_out, in_2[0], in_2[1], in_2[2], in_2[3], in_2[4], in_2[5], in_2[6], in_2[7]);
  not not_1 (not_1_out, nand_1_out);
  and and_1 (and_1_out, not_1_out, Prog_data_sel);
  and and_2 (and_2_out, and_1_out, Write_to_mem);
  Register register_1 (.D(in_1), .en(and_2_out), .Q(out_6), .clk(Clock), .clr(1'b0));
endmodule

module register_bus_R (
  input  [15:0] \input ,
  input  input_enable,
  input  output_enable,
  input  clock,
  input  sim_only_reset,
  output [15:0] content,
  output [15:0] buffered_output
);

  wire safe_clock_enable_1_clock_out;

  safe_clock_enable safe_clock_enable_1 (
    .clock_enable(input_enable), .clock_in(clock), .clock_out(safe_clock_enable_1_clock_out));
  Register #(.width(16)) register_1 (
    .D(\input ), .en(1'b1), .Q(content), .clk(safe_clock_enable_1_clock_out), .clr(sim_only_reset));
  assign buffered_output = output_enable ? content : 16'bz;  // Controlled_Buffer controlled_buffer_1
endmodule

module register_bus_L (
  input  [15:0] \input ,
  input  input_enable,
  input  output_enable,
  input  clock,
  input  sim_only_reset,
  output [15:0] content,
  output [15:0] buffered_output
);

  wire safe_clock_enable_1_clock_out;

  safe_clock_enable safe_clock_enable_1 (
    .clock_enable(input_enable), .clock_in(clock), .clock_out(safe_clock_enable_1_clock_out));
  Register #(.width(16)) register_1 (
    .D(\input ), .en(1'b1), .Q(content), .clk(safe_clock_enable_1_clock_out), .clr(sim_only_reset));
  assign buffered_output = output_enable ? content : 16'bz;  // Controlled_Buffer controlled_buffer_1
endmodule

module RAM (
  input  [15:0] data_in,
  input  [15:0] address,
  input  chip_enable,
  input  output_enable,
  input  input_enable,
  input  clock,
  output [15:0] addressed_value,
  output [15:0] tristate_data_out
);

  wire multiplexer_1_out, multiplexer_2_out, not_1_out, safe_clock_enable_1_clock_out;

  Multiplexer multiplexer_1 (.in0(1'b0), .in1(input_enable), .out(multiplexer_1_out), .sel(chip_enable), .en(1'b1));
  safe_clock_enable safe_clock_enable_1 (
    .clock_enable(multiplexer_1_out), .clock_in(clock), .clock_out(safe_clock_enable_1_clock_out));
  Multiplexer multiplexer_2 (.in0(1'b0), .in1(output_enable), .out(multiplexer_2_out), .sel(chip_enable), .en(1'b1));
  RAM_part #(.addrWidth(16), .dataWidth(16)) ram_1 (
    .addr(address), .data(addressed_value), .sel(1'b1), .clk(safe_clock_enable_1_clock_out), .ld(not_1_out),
    .clr(1'b0));
  assign addressed_value = multiplexer_1_out ? data_in : 16'bz;  // Controlled_Buffer controlled_buffer_1
  not not_1 (not_1_out, multiplexer_1_out);
  assign tristate_data_out = multiplexer_2_out ? addressed_value : 16'bz;  // Controlled_Buffer controlled_buffer_2
endmodule

module control_unit (
  input  [15:0] instruction,
  input  equal_flag,
  input  carryborrow_flag,
  input  negative_flag,
  input  zero_flag,
  input  control_clock,
  input  reset,
  input  sim_only_clear,
  output [15:0] mirror_instruction,
  output CLOCK_HALT,
  output CU_STEP_RESET,
  output IR_IN,
  output PC_COUNT,
  output PC_OUT,
  output PC_IN,
  output SP_OUT,
  output SP_IN,
  output mirror_equal_flag,
  output READ_FROM_MEM,
  output mirror_carryborrow_flag,
  output WRITE_TO_MEM,
  output mirror_negative_flag,
  output MAR_IN,
  output mirror_zero_flag,
  output ALU_C_IN,
  output ALU_M,
  output [2:0] microcode_step,
  output ALU_S3,
  output ALU_S2,
  output ALU_S1,
  output ALU_S0,
  output ALU_A_IS_BUS,
  output ALU_OUT,
  output ALU_STORE_FLAGS,
  output ALU_STORE_RESULT,
  output C_OUT,
  output C_IN,
  output B_OUT,
  output B_IN,
  output A_OUT,
  output A_IN,
  output ACC_OUT,
  output ACC_IN
);

  wire not_1_out;
  wire [7:5] rom_1_data;

  not not_1 (not_1_out, CU_STEP_RESET);
  Register u_mirror_instruction (
    .D(instruction[7:0]), .en(1'b1), .Q(mirror_instruction[7:0]), .clk(control_clock), .clr(sim_only_clear));
  Register #(.width(4)) mirror_flags (
    .D({equal_flag, carryborrow_flag, negative_flag, zero_flag}), .en(1'b1),
    .Q({mirror_equal_flag, mirror_carryborrow_flag, mirror_negative_flag, mirror_zero_flag}),
    .clk(control_clock), .clr(sim_only_clear));
  Counter #(.width(3), .max('h7)) microcode_step_counter (
    .load(CU_STEP_RESET), .D(3'b000), .count(not_1_out), .Q(microcode_step), .clk(control_clock), .clr(reset));  // open: carry
  ROM #(.addrWidth(15)) rom_1 (
    .addr({mirror_instruction[7:0], mirror_equal_flag, mirror_carryborrow_flag, mirror_negative_flag, mirror_zero_flag, microcode_step}),
    .data({rom_1_data, CLOCK_HALT, CU_STEP_RESET, IR_IN, PC_COUNT, PC_OUT}), .sel(1'b1));
  ROM #(.addrWidth(15)) rom_2 (
    .addr({mirror_instruction[7:0], mirror_equal_flag, mirror_carryborrow_flag, mirror_negative_flag, mirror_zero_flag, microcode_step}),
    .data({PC_IN, SP_OUT, SP_IN, READ_FROM_MEM, WRITE_TO_MEM, MAR_IN, ALU_C_IN, ALU_M}), .sel(1'b1));
  ROM #(.addrWidth(15)) rom_3 (
    .addr({mirror_instruction[7:0], mirror_equal_flag, mirror_carryborrow_flag, mirror_negative_flag, mirror_zero_flag, microcode_step}),
    .data({ALU_S3, ALU_S2, ALU_S1, ALU_S0, ALU_A_IS_BUS, ALU_OUT, ALU_STORE_FLAGS, ALU_STORE_RESULT}),
    .sel(1'b1));
  ROM #(.addrWidth(15)) rom_4 (
    .addr({mirror_instruction[7:0], mirror_equal_flag, mirror_carryborrow_flag, mirror_negative_flag, mirror_zero_flag, microcode_step}),
    .data({C_OUT, C_IN, B_OUT, B_IN, A_OUT, A_IN, ACC_OUT, ACC_IN}), .sel(1'b1));

  assign mirror_instruction[15:8] = {8{1'b0}};

  // Notes on the sheet:
  //   Common inputs to all EEPROMS
  //   microcode 3
  //   microcode 2
  //   microcode 1
  //   microcode 0
  //   contents of rom_1 (hex, n*v repeats v):
  //   2 c 14 5*0 2 c 2 11 4*0 2 c 14 5*0 2 c 2 11 4*0 2 c 14 5*0 2 c 2 11 4*0 2 c 14 5*0 2 c 2 11 4*0 2 c
  //   14 5*0 2 c 2 11 4*0 2 c 14 5*0 2 c 2 11 4*0 2 c 14 5*0 2 c 2 11 4*0 2 c 14 5*0 2 c 2 11 4*0 2 c 10
  //   5*0 2 c 10 5*0 2 c 10 5*0 2 c 10 5*0 2 c 10 5*0 2 c 10 5*0 2 c 10 5*0 2 c 10 5*0 2 c 10 5*0 2 c 10
  //   5*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
  //   contents of rom_2 (hex, n*v repeats v):
  //   4 10 6*0 4 10 4 10 4*0 4 10 6*0 4 10 4 10 4*0 4 10 6*0 4 10 4 10 4*0 4 10 6*0 4 10 4 10 4*0 4 10 6*0
  //   4 10 4 10 4*0 4 10 6*0 4 10 4 10 4*0 4 10 6*0 4 10 4 10 4*0 4 10 6*0 4 10 4 10 4*0 4 10 6*0 4 10 6*0
  //   4 10 6*0 4 10 6*0 4 10 6*0 4 10 6*0 4 10 6*0 4 10 6*0 4 10 6*0 4 10 6*0 4 10 6*0 4 10 6*0 4 10 6*0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
  //   contents of rom_3 (hex, n*v repeats v):
  //   899*0 62 7*0 62 7*0 62 7*0 62 7*0 62 7*0 62 7*0 62 7*0 62 7*0 62 7*0 62 7*0 62 7*0 62 7*0 62 7*0 62
  //   7*0 62 7*0 62 774*0 62 7*0 62 7*0 62 7*0 62 7*0 62 7*0 62 7*0 62 7*0 62 7*0 62 7*0 62 7*0 62 7*0 62
  //   7*0 62 7*0 62 7*0 62 7*0 62 7*0 62 7*0 62 7*0 62 7*0 62 7*0 62 7*0 62 7*0 62 7*0 62 7*0 62 7*0 62 7*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
  //   contents of rom_4 (hex, n*v repeats v):
  //   2 c 10 5*0 2 c 10 5*0 2 c 10 5*0 2 c 10 5*0 2 c 10 5*0 2 c 10 5*0 2 c 10 5*0 2 c 10 5*0 2 c 10 5*0 2
  //   c 10 5*0 2 c 10 5*0 2 c 10 5*0 2 c 10 5*0 2 c 10 5*0 2 c 10 5*0 2 c 10 5*0 2 c 0 10 4*0 2 c 0 10 4*0
  //   2 c 0 10 4*0 2 c 0 10 4*0 2 c 0 10 4*0 2 c 0 10 4*0 2 c 0 10 4*0 2 c 0 10 4*0 2 c 0 10 4*0 2 c 0 1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
  //   And so on.
  //   And another slice.
  //   This is one 8 bit "slice" of the output control signals.
endmodule

module program_counter (
  input  in,
  input  output_enable,
  input  [15:0] \input ,
  input  count,
  input  clock,
  input  reset,
  output [15:0] tristate_output,
  output [15:0] contents
);

  Counter #(.width(16), .max('hffff)) counter_1 (
    .load(in), .D(\input ), .count(count), .Q(contents), .clk(clock), .clr(reset));  // open: carry
  assign tristate_output = output_enable ? contents : 16'bz;  // Controlled_Buffer controlled_buffer_1
endmodule

module ALU (
  input  [15:0] A,
  input  [15:0] B,
  input  carry_in,
  input  M,
  input  S0,
  input  S1,
  input  S2,
  input  S3,
  input  result_output_enable,
  input  clock,
  input  sim_only_reset,
  input  store_result,
  input  store_flags,
  output unclocked_zero,
  output clocked_zero,
  output unclocked_negative,
  output clocked_negative,
  output unclocked_carryborrow_out,
  output clocked_carryborrow_out,
  output unclocked_A___B,
  output clocked_A___B,
  output [15:0] tristate_clocked_result,
  output [15:0] unclocked_result,
  output [15:0] clocked_result
);

  wire n74ls181_1_a_b, n74ls181_1_carry_out_bar, n74ls181_2_a_b, n74ls181_2_carry_out_bar, n74ls181_3_a_b,
       n74ls181_3_carry_out_bar, n74ls181_4_a_b, n74ls181_4_carry_out_bar, not_2_out, or_1_out,
       safe_clock_enable_1_clock_out, safe_clock_enable_2_clock_out;

  not not_1 (unclocked_carryborrow_out, n74ls181_4_carry_out_bar);
  not not_2 (not_2_out, carry_in);
  and and_1 (unclocked_A___B, n74ls181_1_a_b, n74ls181_2_a_b, n74ls181_3_a_b, n74ls181_4_a_b);
  _74LS181 u_74ls181_1 (
    .B(B[3:0]), .A(A[3:0]), .M(M), .carry_in_bar(not_2_out), .carry_out_bar(n74ls181_1_carry_out_bar),
    .F(unclocked_result[3:0]), .A_B(n74ls181_1_a_b), .S0(S0), .S1(S1), .S2(S2), .S3(S3));  // open: Y, X
  _74LS181 u_74ls181_2 (
    .B(B[7:4]), .A(A[7:4]), .M(M), .carry_in_bar(n74ls181_1_carry_out_bar),
    .carry_out_bar(n74ls181_2_carry_out_bar), .F(unclocked_result[7:4]), .A_B(n74ls181_2_a_b), .S0(S0),
    .S1(S1), .S2(S2), .S3(S3));  // open: Y, X
  _74LS181 u_74ls181_3 (
    .B(B[11:8]), .A(A[11:8]), .M(M), .carry_in_bar(n74ls181_2_carry_out_bar),
    .carry_out_bar(n74ls181_3_carry_out_bar), .F(unclocked_result[11:8]), .A_B(n74ls181_3_a_b), .S0(S0),
    .S1(S1), .S2(S2), .S3(S3));  // open: Y, X
  _74LS181 u_74ls181_4 (
    .B(B[15:12]), .A(A[15:12]), .M(M), .carry_in_bar(n74ls181_3_carry_out_bar),
    .carry_out_bar(n74ls181_4_carry_out_bar), .F({unclocked_negative, unclocked_result[14:12]}),
    .A_B(n74ls181_4_a_b), .S0(S0), .S1(S1), .S2(S2), .S3(S3));  // open: Y, X
  or or_1 (or_1_out, unclocked_result[0], unclocked_result[1], unclocked_result[2], unclocked_result[3], unclocked_result[4], unclocked_result[5], unclocked_result[6], unclocked_result[7], unclocked_result[8], unclocked_result[9], unclocked_result[10], unclocked_result[11], unclocked_result[12], unclocked_result[13], unclocked_result[14], unclocked_negative);
  safe_clock_enable safe_clock_enable_1 (
    .clock_enable(store_result), .clock_in(clock), .clock_out(safe_clock_enable_1_clock_out));
  safe_clock_enable safe_clock_enable_2 (
    .clock_enable(store_flags), .clock_in(clock), .clock_out(safe_clock_enable_2_clock_out));
  not not_3 (unclocked_zero, or_1_out);
  Register #(.width(16)) result (
    .D({unclocked_negative, unclocked_result[14:0]}), .en(1'b1), .Q(clocked_result),
    .clk(safe_clock_enable_1_clock_out), .clr(sim_only_reset));
  assign tristate_clocked_result = result_output_enable ? clocked_result : 16'bz;  // Controlled_Buffer controlled_buffer_1
  Register #(.width(4)) register_1 (
    .D({unclocked_A___B, unclocked_carryborrow_out, unclocked_negative, unclocked_zero}), .en(1'b1),
    .Q({clocked_A___B, clocked_carryborrow_out, clocked_negative, clocked_zero}),
    .clk(safe_clock_enable_2_clock_out), .clr(sim_only_reset));

  assign unclocked_result[15] = unclocked_negative;
endmodule

module CPU (
  input  in_1,
  input  in_2,
  input  [15:0] DATA,
  output out_4,
  output out_5,
  output out_6,
  output [15:0] out_7,
  output out_8,
  output out_9,
  output out_10,
  output [15:0] out_11,
  output out_12,
  output out_13,
  output out_14,
  output out_15,
  output [15:0] out_16,
  output out_17,
  output out_18,
  output [15:0] out_19,
  output out_20,
  output out_21,
  output out_22,
  output out_23,
  output out_24,
  output [15:0] out_25,
  output out_26,
  output out_27,
  output out_28,
  output out_29,
  output out_30,
  output out_31,
  output out_32,
  output out_33,
  output out_34,
  output [15:0] out_35,
  output out_36,
  output out_37,
  output out_38,
  output out_39,
  output out_40,
  output out_41,
  output out_42,
  output out_43,
  output [15:0] out_44,
  output out_45,
  output out_46,
  output out_47,
  output out_48,
  output [15:0] out_49,
  output out_50,
  output [15:0] out_51,
  output [2:0] out_52,
  output [15:0] out_53,
  output out_54,
  output [15:0] out_55,
  output out_56,
  output out_57,
  output out_58,
  output [15:0] out_59,
  output out_60,
  output out_61,
  output out_62,
  output [15:0] DATA_2
);

  wire j_k_ff_1_q, j_k_ff_1_qn, nor_1_out, safe_clock_enable_1_clock_out, SIM_ONLY_RESET;
  wire [15:0] multiplexer_1_out;

  Button button_1 (.out(SIM_ONLY_RESET));
  LED led_1 (.in(out_4));
  LED led_2 (.in(out_6));
  LED led_3 (.in(out_8));
  LED led_4 (.in(out_12));
  LED led_5 (.in(out_15));
  LED led_6 (.in(out_17));
  LED led_7 (.in(out_20));
  LED led_8 (.in(out_22));
  LED led_9 (.in(out_27));
  LED led_10 (.in(out_30));
  LED led_11 (.in(out_32));
  LED led_12 (.in(out_36));
  LED led_13 (.in(out_38));
  LED led_14 (.in(out_41));
  LED led_15 (.in(out_43));
  LED led_16 (.in(out_46));
  LED led_17 (.in(out_47));
  LED led_18 (.in(out_50));
  nor nor_1 (nor_1_out, in_1, out_48);
  LED led_19 (.in(out_5));
  LED led_20 (.in(out_9));
  LED led_21 (.in(out_13));
  LED led_22 (.in(out_18));
  LED led_23 (.in(out_23));
  LED led_24 (.in(out_28));
  LED led_25 (.in(out_31));
  LED led_26 (.in(out_34));
  LED led_27 (.in(out_40));
  LED led_28 (.in(out_45));
  LED led_29 (.in(out_48));
  safe_clock_enable safe_clock_enable_1 (
    .clock_enable(nor_1_out), .clock_in(in_2), .clock_out(safe_clock_enable_1_clock_out));
  J_K_Flip_Flop j_k_ff_1 (
    .J(1'b1), .clk(safe_clock_enable_1_clock_out), .K(1'b1), .Q(j_k_ff_1_q), .Qn(j_k_ff_1_qn), .preset(1'b0),
    .en(1'b1), .reset(in_1));
  DotMatrix #(.matrixcols(16), .matrixrows(1)) dotmatrix_1 (
    .col0(out_11[15]), .col1(out_11[14]), .col2(out_11[13]), .col3(out_11[12]), .col4(out_11[11]),
    .col5(out_11[10]), .col6(out_11[9]), .col7(out_11[8]), .col8(out_11[7]), .col9(out_11[6]),
    .col10(out_11[5]), .col11(out_11[4]), .col12(out_11[3]), .col13(out_11[2]), .col14(out_11[1]),
    .col15(out_11[0]));
  DotMatrix #(.matrixcols(16), .matrixrows(1)) dotmatrix_2 (
    .col0(out_19[15]), .col1(out_19[14]), .col2(out_19[13]), .col3(out_19[12]), .col4(out_19[11]),
    .col5(out_19[10]), .col6(out_19[9]), .col7(out_19[8]), .col8(out_19[7]), .col9(out_19[6]),
    .col10(out_19[5]), .col11(out_19[4]), .col12(out_19[3]), .col13(out_19[2]), .col14(out_19[1]),
    .col15(out_19[0]));
  DotMatrix #(.matrixcols(16), .matrixrows(1)) dotmatrix_3 (
    .col0(out_25[15]), .col1(out_25[14]), .col2(out_25[13]), .col3(out_25[12]), .col4(out_25[11]),
    .col5(out_25[10]), .col6(out_25[9]), .col7(out_25[8]), .col8(out_25[7]), .col9(out_25[6]),
    .col10(out_25[5]), .col11(out_25[4]), .col12(out_25[3]), .col13(out_25[2]), .col14(out_25[1]),
    .col15(out_25[0]));
  DotMatrix #(.matrixcols(16), .matrixrows(1)) dotmatrix_4 (
    .col0(out_35[15]), .col1(out_35[14]), .col2(out_35[13]), .col3(out_35[12]), .col4(out_35[11]),
    .col5(out_35[10]), .col6(out_35[9]), .col7(out_35[8]), .col8(out_35[7]), .col9(out_35[6]),
    .col10(out_35[5]), .col11(out_35[4]), .col12(out_35[3]), .col13(out_35[2]), .col14(out_35[1]),
    .col15(out_35[0]));
  DotMatrix #(.matrixcols(16), .matrixrows(1)) dotmatrix_5 (
    .col0(out_44[15]), .col1(out_44[14]), .col2(out_44[13]), .col3(out_44[12]), .col4(out_44[11]),
    .col5(out_44[10]), .col6(out_44[9]), .col7(out_44[8]), .col8(out_44[7]), .col9(out_44[6]),
    .col10(out_44[5]), .col11(out_44[4]), .col12(out_44[3]), .col13(out_44[2]), .col14(out_44[1]),
    .col15(out_44[0]));
  DotMatrix #(.matrixcols(16), .matrixrows(1)) dotmatrix_6 (
    .col0(out_51[15]), .col1(out_51[14]), .col2(out_51[13]), .col3(out_51[12]), .col4(out_51[11]),
    .col5(out_51[10]), .col6(out_51[9]), .col7(out_51[8]), .col8(out_51[7]), .col9(out_51[6]),
    .col10(out_51[5]), .col11(out_51[4]), .col12(out_51[3]), .col13(out_51[2]), .col14(out_51[1]),
    .col15(out_51[0]));
  DotMatrix #(.matrixcols(16), .matrixrows(1)) dotmatrix_7 (
    .col0(out_53[15]), .col1(out_53[14]), .col2(out_53[13]), .col3(out_53[12]), .col4(out_53[11]),
    .col5(out_53[10]), .col6(out_53[9]), .col7(out_53[8]), .col8(out_53[7]), .col9(out_53[6]),
    .col10(out_53[5]), .col11(out_53[4]), .col12(out_53[3]), .col13(out_53[2]), .col14(out_53[1]),
    .col15(out_53[0]));
  DotMatrix #(.matrixcols(16), .matrixrows(1)) dotmatrix_8 (
    .col0(out_55[15]), .col1(out_55[14]), .col2(out_55[13]), .col3(out_55[12]), .col4(out_55[11]),
    .col5(out_55[10]), .col6(out_55[9]), .col7(out_55[8]), .col8(out_55[7]), .col9(out_55[6]),
    .col10(out_55[5]), .col11(out_55[4]), .col12(out_55[3]), .col13(out_55[2]), .col14(out_55[1]),
    .col15(out_55[0]));
  DotMatrix #(.matrixcols(16), .matrixrows(1)) dotmatrix_9 (
    .col0(out_59[15]), .col1(out_59[14]), .col2(out_59[13]), .col3(out_59[12]), .col4(out_59[11]),
    .col5(out_59[10]), .col6(out_59[9]), .col7(out_59[8]), .col8(out_59[7]), .col9(out_59[6]),
    .col10(out_59[5]), .col11(out_59[4]), .col12(out_59[3]), .col13(out_59[2]), .col14(out_59[1]),
    .col15(out_59[0]));
  control_unit control_unit_1 (
    .mirror_instruction(out_49), .instruction(out_25), .equal_flag(out_42), .carryborrow_flag(out_39),
    .negative_flag(out_37), .zero_flag(out_33), .mirror_equal_flag(out_58), .mirror_carryborrow_flag(out_57),
    .mirror_negative_flag(out_56), .mirror_zero_flag(out_54), .microcode_step(out_52),
    .control_clock(out_62), .reset(in_1), .sim_only_clear(SIM_ONLY_RESET), .CLOCK_HALT(out_48),
    .CU_STEP_RESET(out_45), .IR_IN(out_40), .PC_COUNT(out_34), .PC_OUT(out_31), .PC_IN(out_28),
    .SP_OUT(out_23), .SP_IN(out_18), .READ_FROM_MEM(out_13), .WRITE_TO_MEM(out_9), .MAR_IN(out_5),
    .ALU_C_IN(out_50), .ALU_M(out_47), .ALU_S3(out_46), .ALU_S2(out_43), .ALU_S1(out_41), .ALU_S0(out_38),
    .ALU_A_IS_BUS(out_36), .ALU_OUT(out_32), .ALU_STORE_FLAGS(out_30), .ALU_STORE_RESULT(out_27),
    .C_OUT(out_22), .C_IN(out_20), .B_OUT(out_17), .B_IN(out_15), .A_OUT(out_12), .A_IN(out_8),
    .ACC_OUT(out_6), .ACC_IN(out_4));
  register_bus_R register_bus_r_1 (
    .\input (out_11), .input_enable(out_40), .clock(out_60), .buffered_output(out_11), .content(out_25),
    .sim_only_reset(SIM_ONLY_RESET), .output_enable(1'b0));
  register_bus_R register_bus_r_2 (
    .\input (out_11), .input_enable(out_5), .clock(out_60), .content(out_59),
    .sim_only_reset(SIM_ONLY_RESET), .output_enable(1'b0));  // open: buffered_output
  J_K_Flip_Flop j_k_ff_2 (
    .J(1'b1), .clk(j_k_ff_1_q), .K(1'b1), .Q(out_60), .preset(1'b0), .en(1'b1), .reset(in_1));  // open: Qn
  // Probe on out_11
  // Probe on out_19
  // Probe on out_25
  // Probe on out_35
  // Probe on out_44
  // Probe on out_51
  // Probe on out_53
  // Probe on out_55
  // Probe on out_59
  // Probe on out_11
  // Probe on out_11
  // Probe on out_19
  // Probe on out_19
  // Probe on out_25
  // Probe on out_25
  // Probe on out_35
  // Probe on out_35
  // Probe on out_44
  // Probe on out_44
  // Probe on out_51
  // Probe on out_51
  // Probe on out_53
  // Probe on out_53
  // Probe on out_55
  // Probe on out_55
  // Probe on out_59
  // Probe on out_59
  J_K_Flip_Flop j_k_ff_3 (
    .J(1'b1), .clk(j_k_ff_1_qn), .K(1'b1), .Q(out_62), .preset(1'b0), .en(1'b1), .reset(in_1));  // open: Qn
  assign DATA_2 = out_9 ? out_11 : 16'bz;  // Controlled_Buffer controlled_buffer_1
  assign out_11 = out_13 ? DATA : 16'bz;  // Controlled_Buffer controlled_buffer_2
  DotMatrix #(.matrixcols(16), .matrixrows(1)) dotmatrix_10 (
    .col0(out_7[15]), .col1(out_7[14]), .col2(out_7[13]), .col3(out_7[12]), .col4(out_7[11]),
    .col5(out_7[10]), .col6(out_7[9]), .col7(out_7[8]), .col8(out_7[7]), .col9(out_7[6]), .col10(out_7[5]),
    .col11(out_7[4]), .col12(out_7[3]), .col13(out_7[2]), .col14(out_7[1]), .col15(out_7[0]));
  DotMatrix #(.matrixcols(16), .matrixrows(1)) dotmatrix_11 (
    .col0(out_16[15]), .col1(out_16[14]), .col2(out_16[13]), .col3(out_16[12]), .col4(out_16[11]),
    .col5(out_16[10]), .col6(out_16[9]), .col7(out_16[8]), .col8(out_16[7]), .col9(out_16[6]),
    .col10(out_16[5]), .col11(out_16[4]), .col12(out_16[3]), .col13(out_16[2]), .col14(out_16[1]),
    .col15(out_16[0]));
  DotMatrix #(.matrixcols(16), .matrixrows(1)) dotmatrix_12 (
    .col0(out_49[15]), .col1(out_49[14]), .col2(out_49[13]), .col3(out_49[12]), .col4(out_49[11]),
    .col5(out_49[10]), .col6(out_49[9]), .col7(out_49[8]), .col8(out_49[7]), .col9(out_49[6]),
    .col10(out_49[5]), .col11(out_49[4]), .col12(out_49[3]), .col13(out_49[2]), .col14(out_49[1]),
    .col15(out_49[0]));
  LED led_30 (.in(out_52[2]));
  LED led_31 (.in(out_54));
  LED led_32 (.in(out_56));
  LED led_33 (.in(out_57));
  LED led_34 (.in(out_58));
  LED led_35 (.in(out_60));
  LED led_36 (.in(out_62));
  Pull_Resistor pull_resistor_1 (.node(out_11));
  LED led_37 (.in(out_21));
  LED led_38 (.in(out_24));
  LED led_39 (.in(out_26));
  LED led_40 (.in(out_29));
  LED led_41 (.in(out_33));
  LED led_42 (.in(out_37));
  LED led_43 (.in(out_39));
  LED led_44 (.in(out_42));
  LED led_45 (.in(out_52[0]));
  LED led_46 (.in(out_52[1]));
  Multiplexer #(.width(16), .enable("false")) multiplexer_1 (
    .in0(out_44), .in1(out_11), .out(multiplexer_1_out), .sel(out_36));
  ALU alu_1 (
    .carry_in(out_50), .M(out_47), .S0(out_38), .S1(out_41), .S2(out_43), .S3(out_46), .clock(out_60),
    .store_result(out_27), .store_flags(out_30), .unclocked_zero(out_21), .clocked_zero(out_33),
    .unclocked_negative(out_24), .clocked_negative(out_37), .unclocked_carryborrow_out(out_26),
    .clocked_carryborrow_out(out_39), .unclocked_A___B(out_29), .clocked_A___B(out_42),
    .tristate_clocked_result(out_11), .sim_only_reset(SIM_ONLY_RESET), .A(multiplexer_1_out), .B(out_11),
    .result_output_enable(out_32), .unclocked_result(out_7), .clocked_result(out_16));
  // Probe on out_7
  // Probe on out_7
  // Probe on out_7
  // Probe on out_16
  // Probe on out_16
  // Probe on out_16
  // Probe on out_49
  // Probe on out_49
  // Probe on out_49
  // Probe on out_52
  // Probe on out_52
  // Probe on out_52
  program_counter program_counter_1 (
    .\input (out_11), .count(out_34), .clock(out_60), .reset(in_1), .output_enable(out_31),
    .tristate_output(out_11), .contents(out_19), .in(out_28));
  register_bus_L register_bus_l_1 (
    .\input (out_11), .input_enable(out_4), .clock(out_60), .buffered_output(out_11), .content(out_44),
    .sim_only_reset(SIM_ONLY_RESET), .output_enable(out_6));
  register_bus_L register_bus_l_2 (
    .\input (out_11), .input_enable(out_8), .clock(out_60), .buffered_output(out_11), .content(out_51),
    .sim_only_reset(SIM_ONLY_RESET), .output_enable(out_12));
  register_bus_L register_bus_l_3 (
    .\input (out_11), .input_enable(out_15), .clock(out_60), .buffered_output(out_11), .content(out_53),
    .sim_only_reset(SIM_ONLY_RESET), .output_enable(out_17));
  register_bus_L register_bus_l_4 (
    .\input (out_11), .input_enable(out_20), .clock(out_60), .buffered_output(out_11), .content(out_55),
    .sim_only_reset(SIM_ONLY_RESET), .output_enable(out_22));
  register_bus_L register_bus_l_5 (
    .\input (out_11), .input_enable(out_18), .clock(out_60), .buffered_output(out_11), .content(out_35),
    .sim_only_reset(SIM_ONLY_RESET), .output_enable(out_23));

  assign out_10 = out_9;
  assign out_14 = out_13;
  assign out_61 = out_60;

  // Other names for the same wires on the sheet: A[15:0] = out_51; A_IN = out_8; A_OUT = out_12; ACC[15:0] = out_44;
  //   ACC_IN = out_4; ACC_OUT = out_6; ADDRESS[15:0] = out_59; ALU_A_IS_BUS = out_36; ALU_C_IN = out_50;
  //   ALU_CARRYBORROW_FLAG_CLOCKED = out_39; ALU_CARRYBORROW_FLAG_IMM = out_26; ALU_EQUAL_FLAG_CLOCKED = out_42;
  //   ALU_EQUAL_FLAG_IMM = out_29; ALU_M = out_47; ALU_NEGATIVE_FLAG_CLOCKED = out_37; ALU_NEGATIVE_FLAG_IMM = out_24;
  //   ALU_OUT = out_32; ALU_RESULT_CLOCKED[15:0] = out_16; ALU_RESULT_IMM[15:0] = out_7; ALU_S0 = out_38;
  //   ALU_S1 = out_41; ALU_S2 = out_43; ALU_S3 = out_46; ALU_STORE_FLAGS = out_30; ALU_STORE_RESULT = out_27;
  //   ALU_ZERO_FLAG_CLOCKED = out_33; ALU_ZERO_FLAG_IMM = out_21; B[15:0] = out_53; B_IN = out_15; B_OUT = out_17;
  //   BUS[15:0] = out_11; C[15:0] = out_55; C_IN = out_20; C_OUT = out_22; CLOCK_HALT = out_48;
  //   CONTROL_CLOCK = out_62; CU_CARRYBORROW_MIRROR = out_57; CU_EQUAL_MIRROR = out_58;
  //   CU_INSTRUCTION_MIRROR[15:0] = out_49; CU_MICROCODE_STEP[2:0] = out_52; CU_NEGATIVE_MIRROR = out_56;
  //   CU_STEP_RESET = out_45; CU_ZERO_MIRROR = out_54; DATA_CLOCK = out_60; EXT_CLOCK_PULSE = in_2; IR[15:0] = out_25;
  //   IR_IN = out_40; MAR_IN = out_5; PC[15:0] = out_19; PC_COUNT = out_34; PC_IN = out_28; PC_OUT = out_31;
  //   READ_FROM_MEM = out_13; RESET = in_1; SP[15:0] = out_35; SP_IN = out_18; SP_OUT = out_23; WRITE_TO_MEM = out_9

  // Notes on the sheet:
  //   BIN
  //   HEX
  //   DEC
  //   BIN
  //   HEX
  //   DEC
  //   BIN
  //   HEX
  //   DEC
  //   BIN
  //   HEX
  //   DEC
  //   BIN
  //   HEX
  //   DEC
  //   BIN
  //   HEX
  //   DEC
  //   BIN
  //   HEX
  //   DEC
  //   BIN
  //   HEX
  //   DEC
  //   BIN
  //   HEX
  //   DEC
  //   BIN
  //   HEX
  //   DEC
  //   BIN
  //   HEX
  //   DEC
  //   BIN
  //   HEX
  //   DEC
  //   BIN
  //   HEX
  //   DEC
endmodule
module main (
  input  in_1,
  input  in_2,
  input  in_3,
  output out_4,
  output out_5,
  output out_6,
  output [15:0] out_7,
  output out_8,
  output out_9,
  output [15:0] out_10,
  output out_11,
  output out_12,
  output out_13,
  output [15:0] out_14,
  output out_15,
  output out_16,
  output [15:0] out_17,
  output out_18,
  output out_19,
  output out_20,
  output out_21,
  output out_22,
  output [15:0] out_23,
  output out_24,
  output out_25,
  output out_26,
  output out_27,
  output out_28,
  output out_29,
  output out_30,
  output out_31,
  output out_32,
  output [15:0] out_33,
  output out_34,
  output out_35,
  output out_36,
  output out_37,
  output out_38,
  output out_39,
  output out_40,
  output out_41,
  output [15:0] out_42,
  output out_43,
  output out_44,
  output out_45,
  output out_46,
  output [15:0] out_47,
  output out_48,
  output [15:0] out_49,
  output [2:0] out_50,
  output [15:0] out_51,
  output out_52,
  output [15:0] out_53,
  output out_54,
  output out_55,
  output out_56,
  output [15:0] out_57,
  output out_58,
  output out_59
);

  wire clock_1_clock, cpu_1_out_10, cpu_1_out_14, cpu_1_out_61, RESET, SIM_ONLY_RESET, SINGLE_STEP_ADVANCE;
  wire [15:0] DATA;

  Button button_1 (.out(SIM_ONLY_RESET));
  Button button_2 (.out(RESET));
  Button button_3 (.out(SINGLE_STEP_ADVANCE));
  LED led_1 (.in(out_4));
  LED led_2 (.in(out_6));
  LED led_3 (.in(out_8));
  LED led_4 (.in(out_11));
  LED led_5 (.in(out_13));
  LED led_6 (.in(out_15));
  LED led_7 (.in(out_18));
  LED led_8 (.in(out_20));
  LED led_9 (.in(out_25));
  LED led_10 (.in(out_28));
  LED led_11 (.in(out_30));
  LED led_12 (.in(out_34));
  LED led_13 (.in(out_36));
  LED led_14 (.in(out_39));
  LED led_15 (.in(out_41));
  LED led_16 (.in(out_44));
  LED led_17 (.in(out_45));
  LED led_18 (.in(out_48));
  LED led_19 (.in(out_5));
  LED led_20 (.in(out_9));
  LED led_21 (.in(out_12));
  LED led_22 (.in(out_16));
  LED led_23 (.in(out_21));
  LED led_24 (.in(out_26));
  LED led_25 (.in(out_29));
  LED led_26 (.in(out_32));
  LED led_27 (.in(out_38));
  LED led_28 (.in(out_43));
  LED led_29 (.in(out_46));
  Clock clock_1 (.enable(in_1), .Arduino_Crystal(in_2), .Arduino_clock(SINGLE_STEP_ADVANCE), .clock(clock_1_clock));
  DotMatrix #(.matrixcols(16), .matrixrows(1)) dotmatrix_1 (
    .col0(out_10[15]), .col1(out_10[14]), .col2(out_10[13]), .col3(out_10[12]), .col4(out_10[11]),
    .col5(out_10[10]), .col6(out_10[9]), .col7(out_10[8]), .col8(out_10[7]), .col9(out_10[6]),
    .col10(out_10[5]), .col11(out_10[4]), .col12(out_10[3]), .col13(out_10[2]), .col14(out_10[1]),
    .col15(out_10[0]));
  DotMatrix #(.matrixcols(16), .matrixrows(1)) dotmatrix_2 (
    .col0(out_17[15]), .col1(out_17[14]), .col2(out_17[13]), .col3(out_17[12]), .col4(out_17[11]),
    .col5(out_17[10]), .col6(out_17[9]), .col7(out_17[8]), .col8(out_17[7]), .col9(out_17[6]),
    .col10(out_17[5]), .col11(out_17[4]), .col12(out_17[3]), .col13(out_17[2]), .col14(out_17[1]),
    .col15(out_17[0]));
  DotMatrix #(.matrixcols(16), .matrixrows(1)) dotmatrix_3 (
    .col0(out_23[15]), .col1(out_23[14]), .col2(out_23[13]), .col3(out_23[12]), .col4(out_23[11]),
    .col5(out_23[10]), .col6(out_23[9]), .col7(out_23[8]), .col8(out_23[7]), .col9(out_23[6]),
    .col10(out_23[5]), .col11(out_23[4]), .col12(out_23[3]), .col13(out_23[2]), .col14(out_23[1]),
    .col15(out_23[0]));
  DotMatrix #(.matrixcols(16), .matrixrows(1)) dotmatrix_4 (
    .col0(out_33[15]), .col1(out_33[14]), .col2(out_33[13]), .col3(out_33[12]), .col4(out_33[11]),
    .col5(out_33[10]), .col6(out_33[9]), .col7(out_33[8]), .col8(out_33[7]), .col9(out_33[6]),
    .col10(out_33[5]), .col11(out_33[4]), .col12(out_33[3]), .col13(out_33[2]), .col14(out_33[1]),
    .col15(out_33[0]));
  DotMatrix #(.matrixcols(16), .matrixrows(1)) dotmatrix_5 (
    .col0(out_42[15]), .col1(out_42[14]), .col2(out_42[13]), .col3(out_42[12]), .col4(out_42[11]),
    .col5(out_42[10]), .col6(out_42[9]), .col7(out_42[8]), .col8(out_42[7]), .col9(out_42[6]),
    .col10(out_42[5]), .col11(out_42[4]), .col12(out_42[3]), .col13(out_42[2]), .col14(out_42[1]),
    .col15(out_42[0]));
  DotMatrix #(.matrixcols(16), .matrixrows(1)) dotmatrix_6 (
    .col0(out_49[15]), .col1(out_49[14]), .col2(out_49[13]), .col3(out_49[12]), .col4(out_49[11]),
    .col5(out_49[10]), .col6(out_49[9]), .col7(out_49[8]), .col8(out_49[7]), .col9(out_49[6]),
    .col10(out_49[5]), .col11(out_49[4]), .col12(out_49[3]), .col13(out_49[2]), .col14(out_49[1]),
    .col15(out_49[0]));
  DotMatrix #(.matrixcols(16), .matrixrows(1)) dotmatrix_7 (
    .col0(out_51[15]), .col1(out_51[14]), .col2(out_51[13]), .col3(out_51[12]), .col4(out_51[11]),
    .col5(out_51[10]), .col6(out_51[9]), .col7(out_51[8]), .col8(out_51[7]), .col9(out_51[6]),
    .col10(out_51[5]), .col11(out_51[4]), .col12(out_51[3]), .col13(out_51[2]), .col14(out_51[1]),
    .col15(out_51[0]));
  DotMatrix #(.matrixcols(16), .matrixrows(1)) dotmatrix_8 (
    .col0(out_53[15]), .col1(out_53[14]), .col2(out_53[13]), .col3(out_53[12]), .col4(out_53[11]),
    .col5(out_53[10]), .col6(out_53[9]), .col7(out_53[8]), .col8(out_53[7]), .col9(out_53[6]),
    .col10(out_53[5]), .col11(out_53[4]), .col12(out_53[3]), .col13(out_53[2]), .col14(out_53[1]),
    .col15(out_53[0]));
  DotMatrix #(.matrixcols(16), .matrixrows(1)) dotmatrix_9 (
    .col0(out_57[15]), .col1(out_57[14]), .col2(out_57[13]), .col3(out_57[12]), .col4(out_57[11]),
    .col5(out_57[10]), .col6(out_57[9]), .col7(out_57[8]), .col8(out_57[7]), .col9(out_57[6]),
    .col10(out_57[5]), .col11(out_57[4]), .col12(out_57[3]), .col13(out_57[2]), .col14(out_57[1]),
    .col15(out_57[0]));
  // Probe on out_10
  // Probe on out_17
  // Probe on out_23
  // Probe on out_33
  // Probe on out_42
  // Probe on out_49
  // Probe on out_51
  // Probe on out_53
  // Probe on out_57
  CPU cpu_1 (
    .out_7(out_7), .out_11(out_10), .out_16(out_14), .out_19(out_17), .out_25(out_23), .out_35(out_33),
    .out_44(out_42), .out_49(out_47), .out_51(out_49), .out_52(out_50), .in_1(RESET), .out_53(out_51),
    .in_2(clock_1_clock), .out_55(out_53), .DATA_2(DATA), .out_4(out_4), .out_5(out_5), .out_6(out_6),
    .out_8(out_8), .out_9(out_9), .out_12(out_11), .out_13(out_12), .out_15(out_13), .out_17(out_15),
    .out_20(out_18), .out_18(out_16), .out_22(out_20), .out_23(out_21), .out_21(out_19), .out_24(out_22),
    .out_27(out_25), .out_28(out_26), .out_26(out_24), .out_30(out_28), .out_31(out_29), .out_29(out_27),
    .out_32(out_30), .out_34(out_32), .out_33(out_31), .out_36(out_34), .out_37(out_35), .out_38(out_36),
    .out_40(out_38), .out_39(out_37), .out_41(out_39), .out_42(out_40), .out_43(out_41), .out_45(out_43),
    .out_46(out_44), .out_47(out_45), .out_48(out_46), .out_50(out_48), .out_54(out_52), .out_56(out_54),
    .out_57(out_55), .out_58(out_56), .out_60(out_58), .out_62(out_59), .DATA(DATA), .out_59(out_57),
    .out_61(cpu_1_out_61), .out_10(cpu_1_out_10), .out_14(cpu_1_out_14));
  // Probe on out_10
  // Probe on out_10
  // Probe on out_17
  // Probe on out_17
  // Probe on out_23
  // Probe on out_23
  // Probe on out_33
  // Probe on out_33
  // Probe on out_42
  // Probe on out_42
  // Probe on out_49
  // Probe on out_49
  // Probe on out_51
  // Probe on out_51
  // Probe on out_53
  // Probe on out_53
  // Probe on out_57
  // Probe on out_57
  RAM ram_1 (
    .data_in(DATA), .address(out_57), .output_enable(cpu_1_out_14), .input_enable(cpu_1_out_10),
    .clock(cpu_1_out_61), .tristate_data_out(DATA), .chip_enable(in_3));  // open: addressed_value
  DotMatrix #(.matrixcols(16), .matrixrows(1)) dotmatrix_10 (
    .col0(out_7[15]), .col1(out_7[14]), .col2(out_7[13]), .col3(out_7[12]), .col4(out_7[11]),
    .col5(out_7[10]), .col6(out_7[9]), .col7(out_7[8]), .col8(out_7[7]), .col9(out_7[6]), .col10(out_7[5]),
    .col11(out_7[4]), .col12(out_7[3]), .col13(out_7[2]), .col14(out_7[1]), .col15(out_7[0]));
  DotMatrix #(.matrixcols(16), .matrixrows(1)) dotmatrix_11 (
    .col0(out_14[15]), .col1(out_14[14]), .col2(out_14[13]), .col3(out_14[12]), .col4(out_14[11]),
    .col5(out_14[10]), .col6(out_14[9]), .col7(out_14[8]), .col8(out_14[7]), .col9(out_14[6]),
    .col10(out_14[5]), .col11(out_14[4]), .col12(out_14[3]), .col13(out_14[2]), .col14(out_14[1]),
    .col15(out_14[0]));
  DotMatrix #(.matrixcols(16), .matrixrows(1)) dotmatrix_12 (
    .col0(out_47[15]), .col1(out_47[14]), .col2(out_47[13]), .col3(out_47[12]), .col4(out_47[11]),
    .col5(out_47[10]), .col6(out_47[9]), .col7(out_47[8]), .col8(out_47[7]), .col9(out_47[6]),
    .col10(out_47[5]), .col11(out_47[4]), .col12(out_47[3]), .col13(out_47[2]), .col14(out_47[1]),
    .col15(out_47[0]));
  LED led_30 (.in(out_50[2]));
  LED led_31 (.in(out_52));
  LED led_32 (.in(out_54));
  LED led_33 (.in(out_55));
  LED led_34 (.in(out_56));
  LED led_35 (.in(out_58));
  LED led_36 (.in(out_59));
  LED led_37 (.in(out_19));
  LED led_38 (.in(out_22));
  LED led_39 (.in(out_24));
  LED led_40 (.in(out_27));
  LED led_41 (.in(out_31));
  LED led_42 (.in(out_35));
  LED led_43 (.in(out_37));
  LED led_44 (.in(out_40));
  LED led_45 (.in(out_50[1]));
  LED led_46 (.in(out_50[0]));
  // Probe on out_7
  // Probe on out_7
  // Probe on out_7
  // Probe on out_14
  // Probe on out_14
  // Probe on out_14
  // Probe on out_47
  // Probe on out_47
  // Probe on out_47
  // Probe on out_50
  // Probe on out_50
  // Probe on out_50

  // Other names for the same wires on the sheet: A[15:0] = out_49; A_IN = out_8; A_OUT = out_11; ACC[15:0] = out_42;
  //   ACC_IN = out_4; ACC_OUT = out_6; ADDRESS[15:0] = out_57; ALU_A_IS_BUS = out_34; ALU_C_IN = out_48;
  //   ALU_CARRYBORROW_FLAG_CLOCKED = out_37; ALU_CARRYBORROW_FLAG_IMM = out_24; ALU_EQUAL_FLAG_CLOCKED = out_40;
  //   ALU_EQUAL_FLAG_IMM = out_27; ALU_M = out_45; ALU_NEGATIVE_FLAG_CLOCKED = out_35; ALU_NEGATIVE_FLAG_IMM = out_22;
  //   ALU_OUT = out_30; ALU_RESULT_CLOCKED[15:0] = out_14; ALU_RESULT_IMM[15:0] = out_7; ALU_S0 = out_36;
  //   ALU_S1 = out_39; ALU_S2 = out_41; ALU_S3 = out_44; ALU_STORE_FLAGS = out_28; ALU_STORE_RESULT = out_25;
  //   ALU_ZERO_FLAG_CLOCKED = out_31; ALU_ZERO_FLAG_IMM = out_19; B[15:0] = out_51; B_IN = out_13; B_OUT = out_15;
  //   BUS[15:0] = out_10; C[15:0] = out_53; C_IN = out_18; C_OUT = out_20; CLOCK_ENABLE = in_1; CLOCK_HALT = out_46;
  //   CONTROL_CLOCK = out_59; CU_CARRYBORROW_MIRROR = out_55; CU_EQUAL_MIRROR = out_56;
  //   CU_INSTRUCTION_MIRROR[15:0] = out_47; CU_MICROCODE_STEP[2:0] = out_50; CU_NEGATIVE_MIRROR = out_54;
  //   CU_STEP_RESET = out_43; CU_ZERO_MIRROR = out_52; DATA_CLOCK = out_58; EXTERNAL_INTERNAL_CLOCK = in_2;
  //   IR[15:0] = out_23; IR_IN = out_38; MAR_IN = out_5; PC[15:0] = out_17; PC_COUNT = out_32; PC_IN = out_26;
  //   PC_OUT = out_29; READ_FROM_MEM = out_12; SP[15:0] = out_33; SP_IN = out_16; SP_OUT = out_21;
  //   WRITE_TO_MEM = out_9

  // Notes on the sheet:
  //   BIN
  //   HEX
  //   DEC
  //   BIN
  //   HEX
  //   DEC
  //   BIN
  //   HEX
  //   DEC
  //   BIN
  //   HEX
  //   DEC
  //   BIN
  //   HEX
  //   DEC
  //   BIN
  //   HEX
  //   DEC
  //   BIN
  //   HEX
  //   DEC
  //   BIN
  //   HEX
  //   DEC
  //   BIN
  //   HEX
  //   DEC
  //   BIN
  //   HEX
  //   DEC
  //   BIN
  //   HEX
  //   DEC
  //   BIN
  //   HEX
  //   DEC
  //   BIN
  //   HEX
  //   DEC
endmodule
