// Logisim project sixteen-bit-computer_test.circ as structural Verilog: 17 circuits, main circuit main
module main (
  input  in_1,
  input  in_2,
  input  in_3,
  input  in_4
);

  wire A_IN, A_OUT, ACC_IN, ACC_OUT, ALU_A_IS_BUS, ALU_C_IN, ALU_CARRYBORROW_FLAG_CLOCKED,
       ALU_CARRYBORROW_FLAG_IMM, ALU_EQUAL_FLAG_CLOCKED, ALU_EQUAL_FLAG_IMM, ALU_M,
       ALU_NEGATIVE_FLAG_CLOCKED, ALU_NEGATIVE_FLAG_IMM, ALU_OUT, ALU_S0, ALU_S1, ALU_S2, ALU_S3,
       ALU_STORE_FLAGS, ALU_STORE_RESULT, ALU_ZERO_FLAG_CLOCKED, ALU_ZERO_FLAG_IMM, AUTO_CLOCK, B_IN, B_OUT,
       button_2_out, button_3_out, C_IN, C_OUT, CLOCK_HALT, CONTROL_CLOCK, cpu_1_p34, cpu_1_p35, cpu_1_p39,
       cpu_1_p40, CU_CARRYBORROW_MIRROR, CU_EQUAL_MIRROR, CU_NEGATIVE_MIRROR, CU_STEP_RESET, CU_ZERO_MIRROR,
       DATA_CLOCK, IR_IN, MANUAL_CLOCK, MAR_IN, multiplexer_1_out, PC_COUNT, PC_IN, PC_OUT, READ_FROM_MEM,
       RESET, SIM_ONLY_RESET, SP_IN, SP_OUT, WRITE_TO_MEM;
  wire [2:0] CU_MICROCODE_STEP;
  wire [15:0] A, ACC, ADDRESS, ALU_RESULT_CLOCKED, ALU_RESULT_IMM, B, BUS, C, cpu_1_p37, cpu_1_p38,
       CU_INSTRUCTION_MIRROR, IR, PC, SP;

  Button button_1 (.out(SIM_ONLY_RESET));
  Button button_2 (.out(button_2_out));
  Button button_3 (.out(button_3_out));
  Clock_part clock_1 (.out(AUTO_CLOCK));
  LED led_1 (.in(ACC_IN));
  LED led_2 (.in(ACC_OUT));
  LED led_3 (.in(A_IN));
  LED led_4 (.in(A_OUT));
  LED led_5 (.in(B_IN));
  LED led_6 (.in(B_OUT));
  LED led_7 (.in(C_IN));
  LED led_8 (.in(C_OUT));
  LED led_9 (.in(ALU_STORE_RESULT));
  LED led_10 (.in(ALU_STORE_FLAGS));
  LED led_11 (.in(ALU_OUT));
  LED led_12 (.in(ALU_A_IS_BUS));
  LED led_13 (.in(ALU_S0));
  LED led_14 (.in(ALU_S1));
  LED led_15 (.in(ALU_S2));
  LED led_16 (.in(ALU_S3));
  LED led_17 (.in(ALU_M));
  LED led_18 (.in(ALU_C_IN));
  xor xor_1 (RESET, button_2_out, in_1);
  xor xor_2 (MANUAL_CLOCK, in_3, button_3_out);
  LED led_19 (.in(MAR_IN));
  LED led_20 (.in(WRITE_TO_MEM));
  LED led_21 (.in(READ_FROM_MEM));
  LED led_22 (.in(SP_IN));
  LED led_23 (.in(SP_OUT));
  LED led_24 (.in(PC_IN));
  LED led_25 (.in(PC_OUT));
  LED led_26 (.in(PC_COUNT));
  LED led_27 (.in(IR_IN));
  LED led_28 (.in(CU_STEP_RESET));
  LED led_29 (.in(CLOCK_HALT));
  Multiplexer #(.enable("false")) multiplexer_1 (
    .in0(MANUAL_CLOCK), .in1(AUTO_CLOCK), .out(multiplexer_1_out), .sel(in_4));
  DotMatrix #(.matrixcols(16), .matrixrows(1)) dotmatrix_1 (
    .col0(BUS[15]), .col1(BUS[14]), .col2(BUS[13]), .col3(BUS[12]), .col4(BUS[11]), .col5(BUS[10]),
    .col6(BUS[9]), .col7(BUS[8]), .col8(BUS[7]), .col9(BUS[6]), .col10(BUS[5]), .col11(BUS[4]),
    .col12(BUS[3]), .col13(BUS[2]), .col14(BUS[1]), .col15(BUS[0]));
  DotMatrix #(.matrixcols(16), .matrixrows(1)) dotmatrix_2 (
    .col0(PC[15]), .col1(PC[14]), .col2(PC[13]), .col3(PC[12]), .col4(PC[11]), .col5(PC[10]), .col6(PC[9]),
    .col7(PC[8]), .col8(PC[7]), .col9(PC[6]), .col10(PC[5]), .col11(PC[4]), .col12(PC[3]), .col13(PC[2]),
    .col14(PC[1]), .col15(PC[0]));
  DotMatrix #(.matrixcols(16), .matrixrows(1)) dotmatrix_3 (
    .col0(IR[15]), .col1(IR[14]), .col2(IR[13]), .col3(IR[12]), .col4(IR[11]), .col5(IR[10]), .col6(IR[9]),
    .col7(IR[8]), .col8(IR[7]), .col9(IR[6]), .col10(IR[5]), .col11(IR[4]), .col12(IR[3]), .col13(IR[2]),
    .col14(IR[1]), .col15(IR[0]));
  DotMatrix #(.matrixcols(16), .matrixrows(1)) dotmatrix_4 (
    .col0(SP[15]), .col1(SP[14]), .col2(SP[13]), .col3(SP[12]), .col4(SP[11]), .col5(SP[10]), .col6(SP[9]),
    .col7(SP[8]), .col8(SP[7]), .col9(SP[6]), .col10(SP[5]), .col11(SP[4]), .col12(SP[3]), .col13(SP[2]),
    .col14(SP[1]), .col15(SP[0]));
  DotMatrix #(.matrixcols(16), .matrixrows(1)) dotmatrix_5 (
    .col0(ACC[15]), .col1(ACC[14]), .col2(ACC[13]), .col3(ACC[12]), .col4(ACC[11]), .col5(ACC[10]),
    .col6(ACC[9]), .col7(ACC[8]), .col8(ACC[7]), .col9(ACC[6]), .col10(ACC[5]), .col11(ACC[4]),
    .col12(ACC[3]), .col13(ACC[2]), .col14(ACC[1]), .col15(ACC[0]));
  DotMatrix #(.matrixcols(16), .matrixrows(1)) dotmatrix_6 (
    .col0(A[15]), .col1(A[14]), .col2(A[13]), .col3(A[12]), .col4(A[11]), .col5(A[10]), .col6(A[9]),
    .col7(A[8]), .col8(A[7]), .col9(A[6]), .col10(A[5]), .col11(A[4]), .col12(A[3]), .col13(A[2]),
    .col14(A[1]), .col15(A[0]));
  DotMatrix #(.matrixcols(16), .matrixrows(1)) dotmatrix_7 (
    .col0(B[15]), .col1(B[14]), .col2(B[13]), .col3(B[12]), .col4(B[11]), .col5(B[10]), .col6(B[9]),
    .col7(B[8]), .col8(B[7]), .col9(B[6]), .col10(B[5]), .col11(B[4]), .col12(B[3]), .col13(B[2]),
    .col14(B[1]), .col15(B[0]));
  DotMatrix #(.matrixcols(16), .matrixrows(1)) dotmatrix_8 (
    .col0(C[15]), .col1(C[14]), .col2(C[13]), .col3(C[12]), .col4(C[11]), .col5(C[10]), .col6(C[9]),
    .col7(C[8]), .col8(C[7]), .col9(C[6]), .col10(C[5]), .col11(C[4]), .col12(C[3]), .col13(C[2]),
    .col14(C[1]), .col15(C[0]));
  DotMatrix #(.matrixcols(16), .matrixrows(1)) dotmatrix_9 (
    .col0(ADDRESS[15]), .col1(ADDRESS[14]), .col2(ADDRESS[13]), .col3(ADDRESS[12]), .col4(ADDRESS[11]),
    .col5(ADDRESS[10]), .col6(ADDRESS[9]), .col7(ADDRESS[8]), .col8(ADDRESS[7]), .col9(ADDRESS[6]),
    .col10(ADDRESS[5]), .col11(ADDRESS[4]), .col12(ADDRESS[3]), .col13(ADDRESS[2]), .col14(ADDRESS[1]),
    .col15(ADDRESS[0]));
  // Probe on BUS
  // Probe on PC
  // Probe on IR
  // Probe on SP
  // Probe on ACC
  // Probe on A
  // Probe on B
  // Probe on C
  // Probe on ADDRESS
  // CPU cpu_1: pin names not known; wires that end beside it: multiplexer_1_out, in_2, RESET, 1'b1, 1'b1, ACC_IN, ACC_OUT, A_IN, A_OUT, B_IN, B_OUT, C_IN, C_OUT, ALU_STORE_RESULT, ALU_STORE_FLAGS, ALU_OUT, ALU_A_IS_BUS, ALU_S0, ALU_S1, ALU_S2, ALU_S3, ALU_M, ALU_C_IN, ALU_RESULT_IMM, ALU_RESULT_CLOCKED, ALU_ZERO_FLAG_IMM, ALU_NEGATIVE_FLAG_IMM, ALU_CARRYBORROW_FLAG_IMM, ALU_EQUAL_FLAG_IMM, ALU_ZERO_FLAG_CLOCKED, ALU_NEGATIVE_FLAG_CLOCKED, ALU_CARRYBORROW_FLAG_CLOCKED, ALU_EQUAL_FLAG_CLOCKED, cpu_1_p34, cpu_1_p35, ADDRESS, cpu_1_p37, cpu_1_p38, cpu_1_p39, cpu_1_p40, MAR_IN, WRITE_TO_MEM, READ_FROM_MEM, SP_IN, SP_OUT, PC_IN, PC_OUT, PC_COUNT, IR_IN, CU_STEP_RESET, CLOCK_HALT, CU_INSTRUCTION_MIRROR, CU_MICROCODE_STEP, CU_ZERO_MIRROR, CU_NEGATIVE_MIRROR, CU_CARRYBORROW_MIRROR, CU_EQUAL_MIRROR, BUS, PC, IR, SP, ACC, A, B, C, DATA_CLOCK, CONTROL_CLOCK
  // Probe on BUS
  // Probe on BUS
  // Probe on PC
  // Probe on PC
  // Probe on IR
  // Probe on IR
  // Probe on SP
  // Probe on SP
  // Probe on ACC
  // Probe on ACC
  // Probe on A
  // Probe on A
  // Probe on B
  // Probe on B
  // Probe on C
  // Probe on C
  // Probe on ADDRESS
  // Probe on ADDRESS
  RAM ram_1 (
    .data_in(cpu_1_p38), .address(ADDRESS), .output_enable(cpu_1_p40), .input_enable(cpu_1_p39),
    .clock(cpu_1_p34), .tristate_data_out(cpu_1_p37), .chip_enable(1'b1));  // open: addressed_value
  DotMatrix #(.matrixcols(16), .matrixrows(1)) dotmatrix_10 (
    .col0(ALU_RESULT_IMM[15]), .col1(ALU_RESULT_IMM[14]), .col2(ALU_RESULT_IMM[13]),
    .col3(ALU_RESULT_IMM[12]), .col4(ALU_RESULT_IMM[11]), .col5(ALU_RESULT_IMM[10]),
    .col6(ALU_RESULT_IMM[9]), .col7(ALU_RESULT_IMM[8]), .col8(ALU_RESULT_IMM[7]), .col9(ALU_RESULT_IMM[6]),
    .col10(ALU_RESULT_IMM[5]), .col11(ALU_RESULT_IMM[4]), .col12(ALU_RESULT_IMM[3]),
    .col13(ALU_RESULT_IMM[2]), .col14(ALU_RESULT_IMM[1]), .col15(ALU_RESULT_IMM[0]));
  DotMatrix #(.matrixcols(16), .matrixrows(1)) dotmatrix_11 (
    .col0(ALU_RESULT_CLOCKED[15]), .col1(ALU_RESULT_CLOCKED[14]), .col2(ALU_RESULT_CLOCKED[13]),
    .col3(ALU_RESULT_CLOCKED[12]), .col4(ALU_RESULT_CLOCKED[11]), .col5(ALU_RESULT_CLOCKED[10]),
    .col6(ALU_RESULT_CLOCKED[9]), .col7(ALU_RESULT_CLOCKED[8]), .col8(ALU_RESULT_CLOCKED[7]),
    .col9(ALU_RESULT_CLOCKED[6]), .col10(ALU_RESULT_CLOCKED[5]), .col11(ALU_RESULT_CLOCKED[4]),
    .col12(ALU_RESULT_CLOCKED[3]), .col13(ALU_RESULT_CLOCKED[2]), .col14(ALU_RESULT_CLOCKED[1]),
    .col15(ALU_RESULT_CLOCKED[0]));
  DotMatrix #(.matrixcols(16), .matrixrows(1)) dotmatrix_12 (
    .col0(CU_INSTRUCTION_MIRROR[15]), .col1(CU_INSTRUCTION_MIRROR[14]), .col2(CU_INSTRUCTION_MIRROR[13]),
    .col3(CU_INSTRUCTION_MIRROR[12]), .col4(CU_INSTRUCTION_MIRROR[11]), .col5(CU_INSTRUCTION_MIRROR[10]),
    .col6(CU_INSTRUCTION_MIRROR[9]), .col7(CU_INSTRUCTION_MIRROR[8]), .col8(CU_INSTRUCTION_MIRROR[7]),
    .col9(CU_INSTRUCTION_MIRROR[6]), .col10(CU_INSTRUCTION_MIRROR[5]), .col11(CU_INSTRUCTION_MIRROR[4]),
    .col12(CU_INSTRUCTION_MIRROR[3]), .col13(CU_INSTRUCTION_MIRROR[2]), .col14(CU_INSTRUCTION_MIRROR[1]),
    .col15(CU_INSTRUCTION_MIRROR[0]));
  LED led_30 (.in(CU_MICROCODE_STEP[2]));
  LED led_31 (.in(CU_ZERO_MIRROR));
  LED led_32 (.in(CU_NEGATIVE_MIRROR));
  LED led_33 (.in(CU_CARRYBORROW_MIRROR));
  LED led_34 (.in(CU_EQUAL_MIRROR));
  LED led_35 (.in(DATA_CLOCK));
  LED led_36 (.in(CONTROL_CLOCK));
  LED led_37 (.in(ALU_ZERO_FLAG_IMM));
  LED led_38 (.in(ALU_NEGATIVE_FLAG_IMM));
  LED led_39 (.in(ALU_CARRYBORROW_FLAG_IMM));
  LED led_40 (.in(ALU_EQUAL_FLAG_IMM));
  LED led_41 (.in(ALU_ZERO_FLAG_CLOCKED));
  LED led_42 (.in(ALU_NEGATIVE_FLAG_CLOCKED));
  LED led_43 (.in(ALU_CARRYBORROW_FLAG_CLOCKED));
  LED led_44 (.in(ALU_EQUAL_FLAG_CLOCKED));
  LED led_45 (.in(CU_MICROCODE_STEP[0]));
  LED led_46 (.in(CU_MICROCODE_STEP[1]));
  Pull_Resistor pull_resistor_1 (.node(cpu_1_p37));
  Pull_Resistor pull_resistor_2 (.node(cpu_1_p38));
  // Probe on ALU_RESULT_IMM
  // Probe on ALU_RESULT_IMM
  // Probe on ALU_RESULT_IMM
  // Probe on ALU_RESULT_CLOCKED
  // Probe on ALU_RESULT_CLOCKED
  // Probe on ALU_RESULT_CLOCKED
  // Probe on CU_INSTRUCTION_MIRROR
  // Probe on CU_INSTRUCTION_MIRROR
  // Probe on CU_INSTRUCTION_MIRROR
  // Probe on CU_MICROCODE_STEP
  // Probe on CU_MICROCODE_STEP
  // Probe on CU_MICROCODE_STEP

  // Other names for the same wires on the sheet: CLOCK_ENABLE = in_2; MANUAL_AUTO_CLOCK_SEL = in_4

  // Notes on the sheet:
  //   BIN
  //   HEX
  //   DEC
  //   BIN
  //   HEX
  //   DEC
  //   BIN
  //   HEX
  //   DEC
  //   BIN
  //   HEX
  //   DEC
  //   BIN
  //   HEX
  //   DEC
  //   BIN
  //   HEX
  //   DEC
  //   BIN
  //   HEX
  //   DEC
  //   BIN
  //   HEX
  //   DEC
  //   BIN
  //   HEX
  //   DEC
  //   BIN
  //   HEX
  //   DEC
  //   BIN
  //   HEX
  //   DEC
  //   BIN
  //   HEX
  //   DEC
  //   BIN
  //   HEX
  //   DEC
endmodule

module CPU (
  input  in_1,
  input  in_2,
  input  in_3,
  input  in_4,
  input  in_5,
  input  [15:0] in_6,
  output out_7,
  output out_8,
  output out_9,
  output [15:0] out_10,
  output out_11,
  output out_12,
  output out_13,
  output [15:0] out_14,
  output out_15,
  output out_16,
  output out_17,
  output out_18,
  output [15:0] out_19,
  output out_20,
  output out_21,
  output [15:0] out_22,
  output out_23,
  output out_24,
  output out_25,
  output out_26,
  output out_27,
  output [15:0] out_28,
  output out_29,
  output out_30,
  output out_31,
  output out_32,
  output out_33,
  output out_34,
  output out_35,
  output out_36,
  output out_37,
  output [15:0] out_38,
  output out_39,
  output out_40,
  output out_41,
  output out_42,
  output out_43,
  output out_44,
  output out_45,
  output out_46,
  output [15:0] out_47,
  output out_48,
  output out_49,
  output out_50,
  output out_51,
  output [15:0] out_52,
  output out_53,
  output [15:0] out_54,
  output [2:0] out_55,
  output [15:0] out_56,
  output out_57,
  output [15:0] out_58,
  output out_59,
  output out_60,
  output out_61,
  output [15:0] out_62,
  output out_63,
  output out_64,
  output out_65,
  output out_66,
  output [15:0] DATA_OUT
);

  wire and_1_out, and_2_out, and_3_out, buffer_2_out, j_k_ff_1_q, j_k_ff_1_qn, j_k_ff_2_q, j_k_ff_3_q,
       nor_1_out, nor_2_out, not_1_out, not_2_out, not_4_out, not_5_out, safe_clock_enable_1_clock_out,
       SIM_ONLY_RESET;
  wire [15:0] buffer_3_out, controlled_buffer_2_out, multiplexer_1_out, register_bus_r_2_content;

  Button button_1 (.out(SIM_ONLY_RESET));
  Pull_Resistor #(.pull(1)) pull_resistor_1 (.node(in_4));
  Pull_Resistor #(.pull(1)) pull_resistor_2 (.node(in_5));
  LED led_1 (.in(out_7));
  LED led_2 (.in(out_9));
  LED led_3 (.in(out_11));
  LED led_4 (.in(out_15));
  LED led_5 (.in(out_18));
  LED led_6 (.in(out_20));
  LED led_7 (.in(out_23));
  LED led_8 (.in(out_25));
  LED led_9 (.in(out_30));
  LED led_10 (.in(out_33));
  LED led_11 (.in(out_35));
  LED led_12 (.in(out_39));
  LED led_13 (.in(out_41));
  LED led_14 (.in(out_44));
  LED led_15 (.in(out_46));
  LED led_16 (.in(out_49));
  LED led_17 (.in(out_50));
  LED led_18 (.in(out_53));
  Pull_Resistor pull_resistor_3 (.node(out_62));
  assign out_62 = in_4 ? register_bus_r_2_content : 16'bz;  // Controlled_Buffer controlled_buffer_1
  nor nor_1 (nor_1_out, in_1, out_51);
  not not_1 (not_1_out, out_51);
  not not_2 (not_2_out, in_1);
  LED led_19 (.in(out_8));
  LED led_20 (.in(out_12));
  LED led_21 (.in(out_16));
  LED led_22 (.in(out_21));
  LED led_23 (.in(out_26));
  LED led_24 (.in(out_31));
  LED led_25 (.in(out_34));
  LED led_26 (.in(out_37));
  LED led_27 (.in(out_43));
  LED led_28 (.in(out_48));
  LED led_29 (.in(out_51));
  safe_clock_enable safe_clock_enable_1 (
    .clock_enable(nor_1_out), .clock_in(in_2), .clock_out(safe_clock_enable_1_clock_out));
  and and_1 (and_1_out, not_1_out, in_3);
  and and_2 (and_2_out, and_1_out, not_2_out);
  J_K_Flip_Flop j_k_ff_1 (
    .J(1'b1), .clk(safe_clock_enable_1_clock_out), .K(1'b1), .Q(j_k_ff_1_q), .Qn(j_k_ff_1_qn), .preset(1'b0),
    .en(1'b1), .reset(in_1));
  safe_clock_enable_disable safe_clock_enable_disable_1 (.clock_enable(and_2_out), .clock_in(in_2), .clock_out(out_63));
  DotMatrix #(.matrixcols(16), .matrixrows(1)) dotmatrix_1 (
    .col0(out_14[15]), .col1(out_14[14]), .col2(out_14[13]), .col3(out_14[12]), .col4(out_14[11]),
    .col5(out_14[10]), .col6(out_14[9]), .col7(out_14[8]), .col8(out_14[7]), .col9(out_14[6]),
    .col10(out_14[5]), .col11(out_14[4]), .col12(out_14[3]), .col13(out_14[2]), .col14(out_14[1]),
    .col15(out_14[0]));
  DotMatrix #(.matrixcols(16), .matrixrows(1)) dotmatrix_2 (
    .col0(out_22[15]), .col1(out_22[14]), .col2(out_22[13]), .col3(out_22[12]), .col4(out_22[11]),
    .col5(out_22[10]), .col6(out_22[9]), .col7(out_22[8]), .col8(out_22[7]), .col9(out_22[6]),
    .col10(out_22[5]), .col11(out_22[4]), .col12(out_22[3]), .col13(out_22[2]), .col14(out_22[1]),
    .col15(out_22[0]));
  DotMatrix #(.matrixcols(16), .matrixrows(1)) dotmatrix_3 (
    .col0(out_28[15]), .col1(out_28[14]), .col2(out_28[13]), .col3(out_28[12]), .col4(out_28[11]),
    .col5(out_28[10]), .col6(out_28[9]), .col7(out_28[8]), .col8(out_28[7]), .col9(out_28[6]),
    .col10(out_28[5]), .col11(out_28[4]), .col12(out_28[3]), .col13(out_28[2]), .col14(out_28[1]),
    .col15(out_28[0]));
  DotMatrix #(.matrixcols(16), .matrixrows(1)) dotmatrix_4 (
    .col0(out_38[15]), .col1(out_38[14]), .col2(out_38[13]), .col3(out_38[12]), .col4(out_38[11]),
    .col5(out_38[10]), .col6(out_38[9]), .col7(out_38[8]), .col8(out_38[7]), .col9(out_38[6]),
    .col10(out_38[5]), .col11(out_38[4]), .col12(out_38[3]), .col13(out_38[2]), .col14(out_38[1]),
    .col15(out_38[0]));
  DotMatrix #(.matrixcols(16), .matrixrows(1)) dotmatrix_5 (
    .col0(out_47[15]), .col1(out_47[14]), .col2(out_47[13]), .col3(out_47[12]), .col4(out_47[11]),
    .col5(out_47[10]), .col6(out_47[9]), .col7(out_47[8]), .col8(out_47[7]), .col9(out_47[6]),
    .col10(out_47[5]), .col11(out_47[4]), .col12(out_47[3]), .col13(out_47[2]), .col14(out_47[1]),
    .col15(out_47[0]));
  DotMatrix #(.matrixcols(16), .matrixrows(1)) dotmatrix_6 (
    .col0(out_54[15]), .col1(out_54[14]), .col2(out_54[13]), .col3(out_54[12]), .col4(out_54[11]),
    .col5(out_54[10]), .col6(out_54[9]), .col7(out_54[8]), .col8(out_54[7]), .col9(out_54[6]),
    .col10(out_54[5]), .col11(out_54[4]), .col12(out_54[3]), .col13(out_54[2]), .col14(out_54[1]),
    .col15(out_54[0]));
  DotMatrix #(.matrixcols(16), .matrixrows(1)) dotmatrix_7 (
    .col0(out_56[15]), .col1(out_56[14]), .col2(out_56[13]), .col3(out_56[12]), .col4(out_56[11]),
    .col5(out_56[10]), .col6(out_56[9]), .col7(out_56[8]), .col8(out_56[7]), .col9(out_56[6]),
    .col10(out_56[5]), .col11(out_56[4]), .col12(out_56[3]), .col13(out_56[2]), .col14(out_56[1]),
    .col15(out_56[0]));
  DotMatrix #(.matrixcols(16), .matrixrows(1)) dotmatrix_8 (
    .col0(out_58[15]), .col1(out_58[14]), .col2(out_58[13]), .col3(out_58[12]), .col4(out_58[11]),
    .col5(out_58[10]), .col6(out_58[9]), .col7(out_58[8]), .col8(out_58[7]), .col9(out_58[6]),
    .col10(out_58[5]), .col11(out_58[4]), .col12(out_58[3]), .col13(out_58[2]), .col14(out_58[1]),
    .col15(out_58[0]));
  DotMatrix #(.matrixcols(16), .matrixrows(1)) dotmatrix_9 (
    .col0(out_62[15]), .col1(out_62[14]), .col2(out_62[13]), .col3(out_62[12]), .col4(out_62[11]),
    .col5(out_62[10]), .col6(out_62[9]), .col7(out_62[8]), .col8(out_62[7]), .col9(out_62[6]),
    .col10(out_62[5]), .col11(out_62[4]), .col12(out_62[3]), .col13(out_62[2]), .col14(out_62[1]),
    .col15(out_62[0]));
  control_unit control_unit_1 (
    .mirror_instruction(out_52), .instruction(out_28), .equal_flag(out_45), .carryborrow_flag(out_42),
    .negative_flag(out_40), .zero_flag(out_36), .mirror_equal_flag(out_61), .mirror_carryborrow_flag(out_60),
    .mirror_negative_flag(out_59), .mirror_zero_flag(out_57), .microcode_step(out_55),
    .control_clock(out_65), .reset(in_1), .sim_only_clear(SIM_ONLY_RESET), .CLOCK_HALT(out_51),
    .CU_STEP_RESET(out_48), .IR_IN(out_43), .PC_COUNT(out_37), .PC_OUT(out_34), .PC_IN(out_31),
    .SP_OUT(out_26), .SP_IN(out_21), .READ_FROM_MEM(out_16), .WRITE_TO_MEM(out_12), .MAR_IN(out_8),
    .ALU_C_IN(out_53), .ALU_M(out_50), .ALU_S3(out_49), .ALU_S2(out_46), .ALU_S1(out_44), .ALU_S0(out_41),
    .ALU_A_IS_BUS(out_39), .ALU_OUT(out_35), .ALU_STORE_FLAGS(out_33), .ALU_STORE_RESULT(out_30),
    .C_OUT(out_25), .C_IN(out_23), .B_OUT(out_20), .B_IN(out_18), .A_OUT(out_15), .A_IN(out_11),
    .ACC_OUT(out_9), .ACC_IN(out_7));
  nor nor_2 (nor_2_out, out_16, and_3_out);
  and and_3 (and_3_out, out_12, in_5);
  register_bus_R register_bus_r_1 (
    .\input (out_14), .input_enable(out_43), .clock(out_63), .buffered_output(out_14), .content(out_28),
    .sim_only_reset(SIM_ONLY_RESET), .output_enable(1'b0));
  register_bus_R register_bus_r_2 (
    .\input (out_14), .input_enable(out_8), .clock(out_63), .content(register_bus_r_2_content),
    .sim_only_reset(SIM_ONLY_RESET), .output_enable(1'b0));  // open: buffered_output
  J_K_Flip_Flop j_k_ff_2 (
    .J(1'b1), .clk(j_k_ff_1_q), .K(1'b1), .Q(j_k_ff_2_q), .preset(1'b0), .en(1'b1), .reset(in_1));  // open: Qn
  not not_3 (out_65, out_63);
  // Probe on out_14
  // Probe on out_22
  // Probe on out_28
  // Probe on out_38
  // Probe on out_47
  // Probe on out_54
  // Probe on out_56
  // Probe on out_58
  // Probe on out_62
  not not_4 (not_4_out, nor_2_out);
  // Probe on out_14
  // Probe on out_14
  // Probe on out_22
  // Probe on out_22
  // Probe on out_28
  // Probe on out_28
  // Probe on out_38
  // Probe on out_38
  // Probe on out_47
  // Probe on out_47
  // Probe on out_54
  // Probe on out_54
  // Probe on out_56
  // Probe on out_56
  // Probe on out_58
  // Probe on out_58
  // Probe on out_62
  // Probe on out_62
  J_K_Flip_Flop j_k_ff_3 (
    .J(1'b1), .clk(j_k_ff_1_qn), .K(1'b1), .Q(j_k_ff_3_q), .preset(1'b0), .en(1'b1), .reset(in_1));  // open: Qn
  not not_5 (not_5_out, out_12);
  Pull_Resistor pull_resistor_4 (.node(DATA_OUT));
  assign DATA_OUT = controlled_buffer_2_out;  // Buffer buffer_1, 16 bits wide
  buf buffer_2 (buffer_2_out, not_5_out);
  assign controlled_buffer_2_out = out_12 ? out_14 : 16'bz;  // Controlled_Buffer controlled_buffer_2
  // AND_Gate and_4 has open pins: in0=out_12, in1=not_4_out, out=open
  Pull_Resistor pull_resistor_5 (.node(in_6));
  assign buffer_3_out = in_6;  // Buffer buffer_3, 16 bits wide
  assign out_14 = out_16 ? buffer_3_out : 16'bz;  // Controlled_Buffer controlled_buffer_3
  DotMatrix #(.matrixcols(16), .matrixrows(1)) dotmatrix_10 (
    .col0(out_10[15]), .col1(out_10[14]), .col2(out_10[13]), .col3(out_10[12]), .col4(out_10[11]),
    .col5(out_10[10]), .col6(out_10[9]), .col7(out_10[8]), .col8(out_10[7]), .col9(out_10[6]),
    .col10(out_10[5]), .col11(out_10[4]), .col12(out_10[3]), .col13(out_10[2]), .col14(out_10[1]),
    .col15(out_10[0]));
  DotMatrix #(.matrixcols(16), .matrixrows(1)) dotmatrix_11 (
    .col0(out_19[15]), .col1(out_19[14]), .col2(out_19[13]), .col3(out_19[12]), .col4(out_19[11]),
    .col5(out_19[10]), .col6(out_19[9]), .col7(out_19[8]), .col8(out_19[7]), .col9(out_19[6]),
    .col10(out_19[5]), .col11(out_19[4]), .col12(out_19[3]), .col13(out_19[2]), .col14(out_19[1]),
    .col15(out_19[0]));
  DotMatrix #(.matrixcols(16), .matrixrows(1)) dotmatrix_12 (
    .col0(out_52[15]), .col1(out_52[14]), .col2(out_52[13]), .col3(out_52[12]), .col4(out_52[11]),
    .col5(out_52[10]), .col6(out_52[9]), .col7(out_52[8]), .col8(out_52[7]), .col9(out_52[6]),
    .col10(out_52[5]), .col11(out_52[4]), .col12(out_52[3]), .col13(out_52[2]), .col14(out_52[1]),
    .col15(out_52[0]));
  LED led_30 (.in(out_55[2]));
  LED led_31 (.in(out_57));
  LED led_32 (.in(out_59));
  LED led_33 (.in(out_60));
  LED led_34 (.in(out_61));
  LED led_35 (.in(out_63));
  LED led_36 (.in(out_65));
  // AND_Gate and_5 has open pins: in0=buffer_2_out, in1=not_4_out, out=open
  Pull_Resistor pull_resistor_6 (.node(out_14));
  LED led_37 (.in(out_24));
  LED led_38 (.in(out_27));
  LED led_39 (.in(out_29));
  LED led_40 (.in(out_32));
  LED led_41 (.in(out_36));
  LED led_42 (.in(out_40));
  LED led_43 (.in(out_42));
  LED led_44 (.in(out_45));
  LED led_45 (.in(out_55[1]));
  LED led_46 (.in(out_55[0]));
  Multiplexer #(.width(16), .enable("false")) multiplexer_1 (
    .in0(out_47), .in1(out_14), .out(multiplexer_1_out), .sel(out_39));
  ALU alu_1 (
    .carry_in(out_53), .M(out_50), .S0(out_41), .S1(out_44), .S2(out_46), .S3(out_49), .clock(out_63),
    .store_result(out_30), .store_flags(out_33), .unclocked_zero(out_24), .clocked_zero(out_36),
    .unclocked_negative(out_27), .clocked_negative(out_40), .unclocked_carryborrow_out(out_29),
    .clocked_carryborrow_out(out_42), .unclocked_A___B(out_32), .clocked_A___B(out_45),
    .tristate_clocked_result(out_14), .sim_only_reset(SIM_ONLY_RESET), .A(multiplexer_1_out), .B(out_14),
    .result_output_enable(out_35), .unclocked_result(out_10), .clocked_result(out_19));
  // Probe on out_10
  // Probe on out_10
  // Probe on out_10
  // Probe on out_19
  // Probe on out_19
  // Probe on out_19
  // Probe on out_52
  // Probe on out_52
  // Probe on out_52
  // Probe on out_55
  // Probe on out_55
  // Probe on out_55
  program_counter program_counter_1 (
    .\input (out_14), .count(out_37), .clock(out_63), .reset(in_1), .output_enable(out_34),
    .tristate_output(out_14), .contents(out_22), .in(out_31));
  register_bus_L register_bus_l_1 (
    .\input (out_14), .input_enable(out_7), .clock(out_63), .buffered_output(out_14), .content(out_47),
    .sim_only_reset(SIM_ONLY_RESET), .output_enable(out_9));
  register_bus_L register_bus_l_2 (
    .\input (out_14), .input_enable(out_11), .clock(out_63), .content(out_54),
    .sim_only_reset(SIM_ONLY_RESET), .output_enable(out_15));  // open: buffered_output
  register_bus_L register_bus_l_3 (
    .\input (out_14), .input_enable(out_18), .clock(out_63), .buffered_output(out_14), .content(out_56),
    .sim_only_reset(SIM_ONLY_RESET), .output_enable(out_20));
  register_bus_L register_bus_l_4 (
    .\input (out_14), .input_enable(out_23), .clock(out_63), .buffered_output(out_14), .content(out_58),
    .sim_only_reset(SIM_ONLY_RESET), .output_enable(out_25));
  register_bus_L register_bus_l_5 (
    .\input (out_14), .input_enable(out_21), .clock(out_63), .buffered_output(out_14), .content(out_38),
    .sim_only_reset(SIM_ONLY_RESET), .output_enable(out_26));

  assign out_13 = out_12;
  assign out_17 = out_16;
  assign out_64 = out_63;
  assign out_66 = out_65;

  // Other names for the same wires on the sheet: A[15:0] = out_54; A_IN = out_11; A_OUT = out_15; ACC[15:0] = out_47;
  //   ACC_IN = out_7; ACC_OUT = out_9; ADDR_BUS_OUTPUT_ENABLE = in_4; ADDRESS[15:0] = out_62; ALU_A_IS_BUS = out_39;
  //   ALU_C_IN = out_53; ALU_CARRYBORROW_FLAG_CLOCKED = out_42; ALU_CARRYBORROW_FLAG_IMM = out_29;
  //   ALU_EQUAL_FLAG_CLOCKED = out_45; ALU_EQUAL_FLAG_IMM = out_32; ALU_M = out_50;
  //   ALU_NEGATIVE_FLAG_CLOCKED = out_40; ALU_NEGATIVE_FLAG_IMM = out_27; ALU_OUT = out_35;
  //   ALU_RESULT_CLOCKED[15:0] = out_19; ALU_RESULT_IMM[15:0] = out_10; ALU_S0 = out_41; ALU_S1 = out_44;
  //   ALU_S2 = out_46; ALU_S3 = out_49; ALU_STORE_FLAGS = out_33; ALU_STORE_RESULT = out_30;
  //   ALU_ZERO_FLAG_CLOCKED = out_36; ALU_ZERO_FLAG_IMM = out_24; B[15:0] = out_56; B_IN = out_18; B_OUT = out_20;
  //   BUS[15:0] = out_14; C[15:0] = out_58; C_IN = out_23; C_OUT = out_25; CLOCK_ENABLE = in_3; CLOCK_HALT = out_51;
  //   CONTROL_CLOCK = out_65; CU_CARRYBORROW_MIRROR = out_60; CU_EQUAL_MIRROR = out_61;
  //   CU_INSTRUCTION_MIRROR[15:0] = out_52; CU_MICROCODE_STEP[2:0] = out_55; CU_NEGATIVE_MIRROR = out_59;
  //   CU_STEP_RESET = out_48; CU_ZERO_MIRROR = out_57; DATA_BUS_OUTPUT_ENABLE = in_5; DATA_CLOCK = out_63;
  //   EXT_CLOCK_PULSE = in_2; IR[15:0] = out_28; IR_IN = out_43; MAR_IN = out_8; PC[15:0] = out_22; PC_COUNT = out_37;
  //   PC_IN = out_31; PC_OUT = out_34; READ_FROM_MEM = out_16; RESET = in_1; SP[15:0] = out_38; SP_IN = out_21;
  //   SP_OUT = out_26; WRITE_TO_MEM = out_12

  // Notes on the sheet:
  //   BIN
  //   HEX
  //   DEC
  //   BIN
  //   HEX
  //   DEC
  //   BIN
  //   HEX
  //   DEC
  //   BIN
  //   HEX
  //   DEC
  //   BIN
  //   HEX
  //   DEC
  //   BIN
  //   HEX
  //   DEC
  //   BIN
  //   HEX
  //   DEC
  //   BIN
  //   HEX
  //   DEC
  //   BIN
  //   HEX
  //   DEC
  //   BIN
  //   HEX
  //   DEC
  //   BIN
  //   HEX
  //   DEC
  //   BIN
  //   HEX
  //   DEC
  //   BIN
  //   HEX
  //   DEC
endmodule

module RAM (
  input  [15:0] data_in,
  input  [15:0] address,
  input  chip_enable,
  input  output_enable,
  input  input_enable,
  input  clock,
  output [15:0] addressed_value,
  output [15:0] tristate_data_out
);

  wire multiplexer_1_out, multiplexer_2_out, not_1_out, safe_clock_enable_1_clock_out;
  wire [15:0] buffer_1_out;

  Multiplexer multiplexer_1 (.in0(1'b0), .in1(input_enable), .out(multiplexer_1_out), .sel(chip_enable), .en(1'b1));
  safe_clock_enable safe_clock_enable_1 (
    .clock_enable(multiplexer_1_out), .clock_in(clock), .clock_out(safe_clock_enable_1_clock_out));
  Multiplexer multiplexer_2 (.in0(1'b0), .in1(output_enable), .out(multiplexer_2_out), .sel(chip_enable), .en(1'b1));
  not not_1 (not_1_out, multiplexer_1_out);
  RAM_part #(.addrWidth(16), .dataWidth(16)) ram_1 (
    .addr(address), .data(addressed_value), .sel(1'b1), .clk(safe_clock_enable_1_clock_out), .ld(not_1_out),
    .clr(1'b0));
  Pull_Resistor pull_resistor_1 (.node(data_in));
  assign buffer_1_out = data_in;  // Buffer buffer_1, 16 bits wide
  assign addressed_value = multiplexer_1_out ? buffer_1_out : 16'bz;  // Controlled_Buffer controlled_buffer_1
  Pull_Resistor pull_resistor_2 (.node(tristate_data_out));
  assign tristate_data_out = multiplexer_2_out ? addressed_value : 16'bz;  // Controlled_Buffer controlled_buffer_2
endmodule

module control_unit (
  input  [15:0] instruction,
  input  equal_flag,
  input  carryborrow_flag,
  input  negative_flag,
  input  zero_flag,
  input  control_clock,
  input  reset,
  input  sim_only_clear,
  output [15:0] mirror_instruction,
  output CLOCK_HALT,
  output CU_STEP_RESET,
  output IR_IN,
  output PC_COUNT,
  output PC_OUT,
  output PC_IN,
  output SP_OUT,
  output SP_IN,
  output mirror_equal_flag,
  output READ_FROM_MEM,
  output mirror_carryborrow_flag,
  output WRITE_TO_MEM,
  output mirror_negative_flag,
  output MAR_IN,
  output mirror_zero_flag,
  output ALU_C_IN,
  output ALU_M,
  output [2:0] microcode_step,
  output ALU_S3,
  output ALU_S2,
  output ALU_S1,
  output ALU_S0,
  output ALU_A_IS_BUS,
  output ALU_OUT,
  output ALU_STORE_FLAGS,
  output ALU_STORE_RESULT,
  output C_OUT,
  output C_IN,
  output B_OUT,
  output B_IN,
  output A_OUT,
  output A_IN,
  output ACC_OUT,
  output ACC_IN
);

  wire not_1_out;
  wire [7:5] rom_1_data;

  not not_1 (not_1_out, CU_STEP_RESET);
  Register u_mirror_instruction (
    .D(instruction[7:0]), .en(1'b1), .Q(mirror_instruction[7:0]), .clk(control_clock), .clr(sim_only_clear));
  Register #(.width(4)) mirror_flags (
    .D({equal_flag, carryborrow_flag, negative_flag, zero_flag}), .en(1'b1),
    .Q({mirror_equal_flag, mirror_carryborrow_flag, mirror_negative_flag, mirror_zero_flag}),
    .clk(control_clock), .clr(sim_only_clear));
  Counter #(.width(3), .max('h7)) microcode_step_counter (
    .load(CU_STEP_RESET), .D(3'b000), .count(not_1_out), .Q(microcode_step), .clk(control_clock), .clr(reset));  // open: carry
  ROM #(.addrWidth(15)) rom_1 (
    .addr({mirror_instruction[7:0], mirror_equal_flag, mirror_carryborrow_flag, mirror_negative_flag, mirror_zero_flag, microcode_step}),
    .data({rom_1_data, CLOCK_HALT, CU_STEP_RESET, IR_IN, PC_COUNT, PC_OUT}), .sel(1'b1));
  ROM #(.addrWidth(15)) rom_2 (
    .addr({mirror_instruction[7:0], mirror_equal_flag, mirror_carryborrow_flag, mirror_negative_flag, mirror_zero_flag, microcode_step}),
    .data({PC_IN, SP_OUT, SP_IN, READ_FROM_MEM, WRITE_TO_MEM, MAR_IN, ALU_C_IN, ALU_M}), .sel(1'b1));
  ROM #(.addrWidth(15)) rom_3 (
    .addr({mirror_instruction[7:0], mirror_equal_flag, mirror_carryborrow_flag, mirror_negative_flag, mirror_zero_flag, microcode_step}),
    .data({ALU_S3, ALU_S2, ALU_S1, ALU_S0, ALU_A_IS_BUS, ALU_OUT, ALU_STORE_FLAGS, ALU_STORE_RESULT}),
    .sel(1'b1));
  ROM #(.addrWidth(15)) rom_4 (
    .addr({mirror_instruction[7:0], mirror_equal_flag, mirror_carryborrow_flag, mirror_negative_flag, mirror_zero_flag, microcode_step}),
    .data({C_OUT, C_IN, B_OUT, B_IN, A_OUT, A_IN, ACC_OUT, ACC_IN}), .sel(1'b1));

  assign mirror_instruction[15:8] = {8{1'b0}};

  // Notes on the sheet:
  //   Common inputs to all EEPROMS
  //   microcode 3
  //   microcode 2
  //   microcode 1
  //   microcode 0
  //   contents of rom_1 (hex, n*v repeats v):
  //   1 6 0 8 4*0 1 6 0 8 4*0 1 6 0 8 4*0 1 6 0 8 4*0 1 6 0 8 4*0 1 6 0 8 4*0 1 6 0 8 4*0 1 6 0 8 4*0 1 6
  //   0 8 4*0 1 6 0 8 4*0 1 6 0 8 4*0 1 6 0 8 4*0 1 6 0 8 4*0 1 6 0 8 4*0 1 6 0 8 4*0 1 6 0 8 4*0 1 6 0 8
  //   4*0 1 6 0 8 4*0 1 6 0 8 4*0 1 6 0 8 4*0 1 6 0 8 4*0 1 6 0 8 4*0 1 6 0 8 4*0 1 6 0 8 4*0 1 6 0 8 4*0
  //   1 6 0 8 4*0 1 6 0 8 4*0 1 6 0 8 4*0 1 6 0 8 4*0 1 6 0 8 4*0 1 6 0 8 4*0 1 6 0 8 4*0 1 6 0 8 4*0 1 6
  //   0 8 4*0 1 6 0 8 4*0 1 6 0 8 4*0 1 6 0 8 4*0 1 6 0 8 4*0 1 6 0 8 4*0 1 6 0 8 4*0 1 6 0 8 4*0 1 6 0 8
  //   4*0 1 6 0 8 4*0 1 6 0 8 4*0 1 6 0 8 4*0 1 6 0 8 4*0 1 6 0 8 4*0 1 6 0 8 4*0 1 6 1 2 8 0 0 0 1 6 1 2
  //   8 0 0 0 1 6 1 2 8 0 0 0 1 6 1 2 8 0 0 0 1 6 1 2 8 0 0 0 1 6 1 2 8 0 0 0 1 6 1 2 8 0 0 0 1 6 1 2 8 0
  //   0 0 1 6 1 2 8 0 0 0 1 6 1 2 8 0 0 0 1 6 1 2 8 0 0 0 1 6 1 2 8 0 0 0 1 6 1 2 8 0 0 0 1 6 1 2 8 0 0 0
  //   1 6 1 2 8 0 0 0 1 6 1 2 8 0 0 0 1 6 1 2 0 0 8 0 1 6 1 2 0 0 8 0 1 6 1 2 0 0 8 0 1 6 1 2 0 0 8 0 1 6
  //   1 2 0 0 8 0 1 6 1 2 0 0 8 0 1 6 1 2 0 0 8 0 1 6 1 2 0 0 8 0 1 6 1 2 0 0 8 0 1 6 1 2 0 0 8 0 1 6 1 2
  //   0 0 8 0 1 6 1 2 0 0 8 0 1 6 1 2 0 0 8 0 1 6 1 2 0 0 8 0 1 6 1 2 0 0 8 0 1 6 1 2 0 0 8 0 1 6 0 8 4*0
  //   1 6 0 8 4*0 1 6 0 8 4*0 1 6 0 8 4*0 1 6 0 8 4*0 1 6 0 8 4*0 1 6 0 8 4*0 1 6 0 8 4*0 1 6 0 8 4*0 1 6
  //   0 8 4*0 1 6 0 8 4*0 1 6 0 8 4*0 1 6 0 8 4*0 1 6 0 8 4*0 1 6 0 8 4*0 1 6 0 8 4*0 1 6 0 8 4*0 1 6 0 8
  //   4*0 1 6 0 8 4*0 1 6 0 8 4*0 1 6 0 8 4*0 1 6 0 8 4*0 1 6 0 8 4*0 1 6 0 8 4*0 1 6 0 8 4*0 1 6 0 8 4*0
  //   1 6 0 8 4*0 1 6 0 8 4*0 1 6 0 8 4*0 1 6 0 8 4*0 1 6 0 8 4*0 1 6 0 8 4*0 1 6 0 8 4*0 1 6 0 8 4*0 1 6
  //   0 8 4*0 1 6 0 8 4*0 1 6 0 8 4*0 1 6 0 8 4*0 1 6 0 8 4*0 1 6 0 8 4*0 1 6 0 8 4*0 1 6 0 8 4*0 1 6 0 8
  //   4*0 1 6 0 8 4*0 1 6 0 8 4*0 1 6 0 8 4*0 1 6 0 8 4*0 1 6 0 8 4*0 1 6 1 2 8 0 0 0 1 6 1 2 8 0 0 0 1 6
  //   1 2 8 0 0 0 1 6 1 2 8 0 0 0 1 6 1 2 8 0 0 0 1 6 1 2 8 0 0 0 1 6 1 2 8 0 0 0 1 6 1 2 8 0 0 0 1 6 1 2
  //   8 0 0 0 1 6 1 2 8 0 0 0 1 6 1 2 8 0 0 0 1 6 1 2 8 0 0 0 1 6 1 2 8 0 0 0 1 6 1 2 8 0 0 0 1 6 1 2 8 0
  //   0 0 1 6 1 2 8 0 0 0 1 6 1 2 0 0 8 0 1 6 1 2 0 0 8 0 1 6 1 2 0 0 8 0 1 6 1 2 0 0 8 0 1 6 1 2 0 0 8 0
  //   1 6 1 2 0 0 8 0 1 6 1 2 0 0 8 0 1 6 1 2 0 0 8 0 1 6 1 2 0 0 8 0 1 6 1 2 0 0 8 0 1 6 1 2 0 0 8 0 1 6
  //   1 2 0 0 8 0 1 6 1 2 0 0 8 0 1 6 1 2 0 0 8 0 1 6 1 2 0 0 8 0 1 6 1 2 0 0 8 0 1 6 0 8 4*0 1 6 0 8 4*0
  //   1 6 0 8 4*0 1 6 0 8 4*0 1 6 0 8 4*0 1 6 0 8 4*0 1 6 0 8 4*0 1 6 0 8 4*0 1 6 0 8 4*0 1 6 0 8 4*0 1 6
  //   0 8 4*0 1 6 0 8 4*0 1 6 0 8 4*0 1 6 0 8 4*0 1 6 0 8 4*0 1 6 0 8 4*0 1 6 0 8 4*0 1 6 0 8 4*0 1 6 0 8
  //   4*0 1 6 0 8 4*0 1 6 0 8 4*0 1 6 0 8 4*0 1 6 0 8 4*0 1 6 0 8 4*0 1 6 0 8 4*0 1 6 0 8 4*0 1 6 0 8 4*0
  //   1 6 0 8 4*0 1 6 0 8 4*0 1 6 0 8 4*0 1 6 0 8 4*0 1 6 0 8 4*0 1 6 0 8 4*0 1 6 0 8 4*0 1 6 0 8 4*0 1 6
  //   0 8 4*0 1 6 0 8 4*0 1 6 0 8 4*0 1 6 0 8 4*0 1 6 0 8 4*0 1 6 0 8 4*0 1 6 0 8 4*0 1 6 0 8 4*0 1 6 0 8
  //   4*0 1 6 0 8 4*0 1 6 0 8 4*0 1 6 0 8 4*0 1 6 0 8 4*0 1 6 0 8 4*0 1 6 0 8 4*0 1 6 0 8 4*0 1 6 0 8 4*0
  //   1 6 0 8 4*0 1 6 0 8 4*0 1 6 0 8 4*0 1 6 0 8 4*0 1 6 0 8 4*0 1 6 0 8 4*0 1 6 0 8 4*0 1 6 0 8 4*0 1 6
  //   0 8 4*0 1 6 0 8 4*0 1 6 0 8 4*0 1 6 0 8 4*0 1 6 0 8 4*0 1 6 0 8 4*0 1 6 0 8 4*0 1 6 0 8 4*0 1 6 0 8
  //   4*0 1 6 0 8 4*0 1 6 0 8 4*0 1 6 0 8 4*0 1 6 0 8 4*0 1 6 0 8 4*0 1 6 0 8 4*0 1 6 0 8 4*0 1 6 0 8 4*0
  //   1 6 0 8 4*0 1 6 0 8 4*0 1 6 0 8 4*0 1 6 0 8 4*0 1 6 0 8 4*0 1 6 0 8 4*0 1 6 0 8 4*0 1 6 0 8 4*0 1 6
  //   0 8 4*0 1 6 0 8 4*0 1 6 0 8 4*0 1 6 0 8 4*0 1 6 0 8 4*0 1 6 0 8 4*0 1 6 0 8 4*0 1 6 0 8 4*0 1 6 0 8
  //   4*0 1 6 0 8 4*0 1 6 0 8 4*0 1 6 0 8 4*0 1 6 0 8 4*0 1 6 0 8 4*0 1 6 0 8 4*0 1 6 0 8 4*0 1 6 0 8 4*0
  //   1 6 0 8 4*0 1 6 0 8 4*0 1 6 0 8 4*0 1 6 0 8 4*0 1 6 0 8 4*0 1 6 0 8 4*0 1 6 0 8 4*0 1 6 0 8 4*0 1 6
  //   0 8 4*0 1 6 0 8 4*0 1 6 0 8 4*0 1 6 0 8 4*0 1 6 0 8 4*0 1 6 0 8 4*0 1 6 0 8 4*0 1 6 0 8 4*0 1 6 0 8
  //   4*0 1 6 0 8 4*0 1 6 0 8 4*0 1 6 0 8 4*0 1 6 0 8 4*0 1 6 0 8 4*0 1 6 0 8 4*0 1 6 0 8 4*0 1 6 0 8 4*0
  //   1 6 0 8 4*0 1 6 0 8 4*0 1 6 0 8 4*0 1 6 0 8 4*0 1 6 0 8 4*0 1 6 0 8 4*0 1 6 0 8 4*0 1 6 0 8 4*0 1 6
  //   0 8 4*0 1 6 0 8 4*0 1 6 0 8 4*0 1 6 0 8 4*0 1 6 0 8 4*0 1 6 0 8 4*0 1 6 0 8 4*0 1 6 0 8 4*0 1 6 0 8
  //   4*0 1 6 0 8 4*0 1 6 0 8 4*0 1 6 0 8 4*0 1 6 0 8 4*0 1 6 0 8 4*0 1 6 0 8 4*0 1 6 0 8 4*0 1 6 0 8 4*0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
  //   contents of rom_2 (hex, n*v repeats v):
  //   4 10 6*0 4 10 6*0 4 10 6*0 4 10 6*0 4 10 6*0 4 10 6*0 4 10 6*0 4 10 6*0 4 10 6*0 4 10 6*0 4 10 6*0 4
  //   10 6*0 4 10 6*0 4 10 6*0 4 10 6*0 4 10 6*0 4 10 6*0 4 10 6*0 4 10 6*0 4 10 6*0 4 10 6*0 4 10 6*0 4
  //   10 6*0 4 10 6*0 4 10 6*0 4 10 6*0 4 10 6*0 4 10 6*0 4 10 6*0 4 10 6*0 4 10 6*0 4 10 6*0 4 10 6*0 4
  //   10 6*0 4 10 6*0 4 10 6*0 4 10 6*0 4 10 6*0 4 10 6*0 4 10 6*0 4 10 6*0 4 10 6*0 4 10 6*0 4 10 6*0 4
  //   10 6*0 4 10 6*0 4 10 6*0 4 10 6*0 4 10 4 10 4*0 4 10 4 10 4*0 4 10 4 10 4*0 4 10 4 10 4*0 4 10 4 10
  //   4*0 4 10 4 10 4*0 4 10 4 10 4*0 4 10 4 10 4*0 4 10 4 10 4*0 4 10 4 10 4*0 4 10 4 10 4*0 4 10 4 10
  //   4*0 4 10 4 10 4*0 4 10 4 10 4*0 4 10 4 10 4*0 4 10 4 10 4*0 4 10 4 10 4 10 0 0 4 10 4 10 4 10 0 0 4
  //   10 4 10 4 10 0 0 4 10 4 10 4 10 0 0 4 10 4 10 4 10 0 0 4 10 4 10 4 10 0 0 4 10 4 10 4 10 0 0 4 10 4
  //   10 4 10 0 0 4 10 4 10 4 10 0 0 4 10 4 10 4 10 0 0 4 10 4 10 4 10 0 0 4 10 4 10 4 10 0 0 4 10 4 10 4
  //   10 0 0 4 10 4 10 4 10 0 0 4 10 4 10 4 10 0 0 4 10 4 10 4 10 0 0 4 10 2 5*0 4 10 2 5*0 4 10 2 5*0 4
  //   10 2 5*0 4 10 2 5*0 4 10 2 5*0 4 10 2 5*0 4 10 2 5*0 4 10 2 5*0 4 10 2 5*0 4 10 2 5*0 4 10 2 5*0 4
  //   10 2 5*0 4 10 2 5*0 4 10 2 5*0 4 10 2 5*0 4 10 2 5*0 4 10 2 5*0 4 10 2 5*0 4 10 2 5*0 4 10 2 5*0 4
  //   10 2 5*0 4 10 2 5*0 4 10 2 5*0 4 10 2 5*0 4 10 2 5*0 4 10 2 5*0 4 10 2 5*0 4 10 2 5*0 4 10 2 5*0 4
  //   10 2 5*0 4 10 2 5*0 4 10 2 5*0 4 10 2 5*0 4 10 2 5*0 4 10 2 5*0 4 10 2 5*0 4 10 2 5*0 4 10 2 5*0 4
  //   10 2 5*0 4 10 2 5*0 4 10 2 5*0 4 10 2 5*0 4 10 2 5*0 4 10 2 5*0 4 10 2 5*0 4 10 2 5*0 4 10 2 5*0 4
  //   10 4 12 4*0 4 10 4 12 4*0 4 10 4 12 4*0 4 10 4 12 4*0 4 10 4 12 4*0 4 10 4 12 4*0 4 10 4 12 4*0 4 10
  //   4 12 4*0 4 10 4 12 4*0 4 10 4 12 4*0 4 10 4 12 4*0 4 10 4 12 4*0 4 10 4 12 4*0 4 10 4 12 4*0 4 10 4
  //   12 4*0 4 10 4 12 4*0 4 10 4 10 4 12 0 0 4 10 4 10 4 12 0 0 4 10 4 10 4 12 0 0 4 10 4 10 4 12 0 0 4
  //   10 4 10 4 12 0 0 4 10 4 10 4 12 0 0 4 10 4 10 4 12 0 0 4 10 4 10 4 12 0 0 4 10 4 10 4 12 0 0 4 10 4
  //   10 4 12 0 0 4 10 4 10 4 12 0 0 4 10 4 10 4 12 0 0 4 10 4 10 4 12 0 0 4 10 4 10 4 12 0 0 4 10 4 10 4
  //   12 0 0 4 10 4 10 4 12 0 0 4 10 6*0 4 10 6*0 4 10 6*0 4 10 6*0 4 10 6*0 4 10 6*0 4 10 6*0 4 10 6*0 4
  //   10 6*0 4 10 6*0 4 10 6*0 4 10 6*0 4 10 6*0 4 10 6*0 4 10 6*0 4 10 6*0 4 10 6*0 4 10 6*0 4 10 6*0 4
  //   10 6*0 4 10 6*0 4 10 6*0 4 10 6*0 4 10 6*0 4 10 6*0 4 10 6*0 4 10 6*0 4 10 6*0 4 10 6*0 4 10 6*0 4
  //   10 6*0 4 10 6*0 4 10 6*0 4 10 6*0 4 10 6*0 4 10 6*0 4 10 6*0 4 10 6*0 4 10 6*0 4 10 6*0 4 10 6*0 4
  //   10 6*0 4 10 6*0 4 10 6*0 4 10 6*0 4 10 6*0 4 10 6*0 4 10 6*0 4 10 6*0 4 10 6*0 4 10 6*0 4 10 6*0 4
  //   10 6*0 4 10 6*0 4 10 6*0 4 10 6*0 4 10 6*0 4 10 6*0 4 10 6*0 4 10 6*0 4 10 6*0 4 10 6*0 4 10 6*0 4
  //   10 6*0 4 10 2 5*0 4 10 2 5*0 4 10 2 5*0 4 10 2 5*0 4 10 2 5*0 4 10 2 5*0 4 10 2 5*0 4 10 2 5*0 4 10
  //   2 5*0 4 10 2 5*0 4 10 2 5*0 4 10 2 5*0 4 10 2 5*0 4 10 2 5*0 4 10 2 5*0 4 10 2 5*0 4 10 2 5*0 4 10 2
  //   5*0 4 10 2 5*0 4 10 2 5*0 4 10 2 5*0 4 10 2 5*0 4 10 2 5*0 4 10 2 5*0 4 10 2 5*0 4 10 2 5*0 4 10 2
  //   5*0 4 10 2 5*0 4 10 2 5*0 4 10 2 5*0 4 10 2 5*0 4 10 2 5*0 4 10 2 5*0 4 10 2 5*0 4 10 2 5*0 4 10 2
  //   5*0 4 10 2 5*0 4 10 2 5*0 4 10 2 5*0 4 10 2 5*0 4 10 2 5*0 4 10 2 5*0 4 10 2 5*0 4 10 2 5*0 4 10 2
  //   5*0 4 10 2 5*0 4 10 2 5*0 4 10 2 5*0 4 10 2 5*0 4 10 2 5*0 4 10 2 5*0 4 10 2 5*0 4 10 2 5*0 4 10 2
  //   5*0 4 10 2 5*0 4 10 2 5*0 4 10 2 5*0 4 10 2 5*0 4 10 2 5*0 4 10 2 5*0 4 10 2 5*0 4 10 2 5*0 4 10 2
  //   5*0 4 10 2 5*0 4 10 6*0 4 10 6*0 4 10 6*0 4 10 6*0 4 10 6*0 4 10 6*0 4 10 6*0 4 10 6*0 4 10 6*0 4 10
  //   6*0 4 10 6*0 4 10 6*0 4 10 6*0 4 10 6*0 4 10 6*0 4 10 6*0 4 10 6*0 4 10 6*0 4 10 6*0 4 10 6*0 4 10
  //   6*0 4 10 6*0 4 10 6*0 4 10 6*0 4 10 6*0 4 10 6*0 4 10 6*0 4 10 6*0 4 10 6*0 4 10 6*0 4 10 6*0 4 10
  //   6*0 4 10 6*0 4 10 6*0 4 10 6*0 4 10 6*0 4 10 6*0 4 10 6*0 4 10 6*0 4 10 6*0 4 10 6*0 4 10 6*0 4 10
  //   6*0 4 10 6*0 4 10 6*0 4 10 6*0 4 10 6*0 4 10 6*0 4 10 6*0 4 10 6*0 4 10 6*0 4 10 6*0 4 10 6*0 4 10
  //   6*0 4 10 6*0 4 10 6*0 4 10 6*0 4 10 6*0 4 10 6*0 4 10 6*0 4 10 6*0 4 10 6*0 4 10 6*0 4 10 6*0 4 10
  //   6*0 4 10 6*0 4 10 6*0 4 10 6*0 4 10 6*0 4 10 6*0 4 10 6*0 4 10 6*0 4 10 6*0 4 10 6*0 4 10 6*0 4 10
  //   6*0 4 10 6*0 4 10 6*0 4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
  //   contents of rom_3 (hex, n*v repeats v):
  //   0 0 93 4 6*0 93 4 6*0 93 4 6*0 93 4 6*0 93 4 6*0 93 4 6*0 93 4 6*0 93 4 6*0 93 4 6*0 93 4 6*0 93 4
  //   6*0 93 4 6*0 93 4 6*0 93 4 6*0 93 4 6*0 93 4 6*0 93 4 6*0 93 4 6*0 93 4 6*0 93 4 6*0 93 4 6*0 93 4
  //   6*0 93 4 6*0 93 4 6*0 93 4 6*0 93 4 6*0 93 4 6*0 93 4 6*0 93 4 6*0 93 4 6*0 93 4 6*0 93 4 6*0 93 4
  //   6*0 93 4 6*0 93 4 6*0 93 4 6*0 93 4 6*0 93 4 6*0 93 4 6*0 93 4 6*0 93 4 6*0 93 4 6*0 93 4 6*0 93 4
  //   6*0 93 4 6*0 93 4 6*0 93 4 6*0 93 4 7*0 93 4 6*0 93 4 6*0 93 4 6*0 93 4 6*0 93 4 6*0 93 4 6*0 93 4
  //   6*0 93 4 6*0 93 4 6*0 93 4 6*0 93 4 6*0 93 4 6*0 93 4 6*0 93 4 6*0 93 4 6*0 93 4 6*0 9 4 93 4 4*0 9
  //   4 93 4 4*0 9 4 93 4 4*0 9 4 93 4 4*0 9 4 93 4 4*0 9 4 93 4 4*0 9 4 93 4 4*0 9 4 93 4 4*0 9 4 93 4
  //   4*0 9 4 93 4 4*0 9 4 93 4 4*0 9 4 93 4 4*0 9 4 93 4 4*0 9 4 93 4 4*0 9 4 93 4 4*0 9 4 93 4 0 0 0 63
  //   4 6*0 63 4 6*0 63 4 6*0 63 4 6*0 63 4 6*0 63 4 6*0 63 4 6*0 63 4 6*0 63 4 6*0 63 4 6*0 63 4 6*0 63 4
  //   6*0 63 4 6*0 63 4 6*0 63 4 6*0 63 4 6*0 63 4 6*0 63 4 6*0 63 4 6*0 63 4 6*0 63 4 6*0 63 4 6*0 63 4
  //   6*0 63 4 6*0 63 4 6*0 63 4 6*0 63 4 6*0 63 4 6*0 63 4 6*0 63 4 6*0 63 4 6*0 63 4 6*0 63 4 6*0 63 4
  //   6*0 63 4 6*0 63 4 6*0 63 4 6*0 63 4 6*0 63 4 6*0 63 4 6*0 63 4 6*0 63 4 6*0 63 4 6*0 63 4 6*0 63 4
  //   6*0 63 4 6*0 63 4 6*0 63 4 7*0 63 4 6*0 63 4 6*0 63 4 6*0 63 4 6*0 63 4 6*0 63 4 6*0 63 4 6*0 63 4
  //   6*0 63 4 6*0 63 4 6*0 63 4 6*0 63 4 6*0 63 4 6*0 63 4 6*0 63 4 6*0 63 4 6*0 9 4 63 4 4*0 9 4 63 4
  //   4*0 9 4 63 4 4*0 9 4 63 4 4*0 9 4 63 4 4*0 9 4 63 4 4*0 9 4 63 4 4*0 9 4 63 4 4*0 9 4 63 4 4*0 9 4
  //   63 4 4*0 9 4 63 4 4*0 9 4 63 4 4*0 9 4 63 4 4*0 9 4 63 4 4*0 9 4 63 4 4*0 9 4 63 4 0 0 0 cb 4 6*0 cb
  //   4 6*0 cb 4 6*0 cb 4 6*0 cb 4 6*0 cb 4 6*0 cb 4 6*0 cb 4 6*0 cb 4 6*0 cb 4 6*0 cb 4 6*0 cb 4 6*0 cb 4
  //   6*0 cb 4 6*0 cb 4 6*0 cb 4 6*0 cb 4 6*0 cb 4 6*0 cb 4 6*0 cb 4 6*0 cb 4 6*0 cb 4 6*0 cb 4 6*0 cb 4
  //   6*0 cb 4 6*0 cb 4 6*0 cb 4 6*0 cb 4 6*0 cb 4 6*0 cb 4 6*0 cb 4 6*0 cb 4 6*0 cb 4 6*0 cb 4 6*0 cb 4
  //   6*0 cb 4 6*0 cb 4 6*0 cb 4 6*0 cb 4 6*0 cb 4 6*0 cb 4 6*0 cb 4 6*0 cb 4 6*0 cb 4 6*0 cb 4 6*0 cb 4
  //   6*0 cb 4 6*0 cb 4 6*0 cb 4 6*0 cb 4 6*0 cb 4 6*0 cb 4 6*0 cb 4 6*0 cb 4 6*0 cb 4 6*0 cb 4 6*0 cb 4
  //   6*0 cb 4 6*0 cb 4 6*0 cb 4 6*0 cb 4 6*0 cb 4 6*0 cb 4 6*0 cb 4 6*0 b 4 6*0 b 4 6*0 b 4 6*0 b 4 6*0 b
  //   4 6*0 b 4 6*0 b 4 6*0 b 4 6*0 b 4 6*0 b 4 6*0 b 4 6*0 b 4 6*0 b 4 6*0 b 4 6*0 b 4 6*0 b 4 6*0 b 4
  //   6*0 b 4 6*0 b 4 6*0 b 4 6*0 b 4 6*0 b 4 6*0 b 4 6*0 b 4 6*0 b 4 6*0 b 4 6*0 b 4 6*0 b 4 6*0 b 4 6*0
  //   b 4 6*0 b 4 6*0 b 4 6*0 b 4 6*0 b 4 6*0 b 4 6*0 b 4 6*0 b 4 6*0 b 4 6*0 b 4 6*0 b 4 6*0 b 4 6*0 b 4
  //   6*0 b 4 6*0 b 4 6*0 b 4 6*0 b 4 6*0 b 4 6*0 b 4 6*0 b 4 6*0 b 4 6*0 b 4 6*0 b 4 6*0 b 4 6*0 b 4 6*0
  //   b 4 6*0 b 4 6*0 b 4 6*0 b 4 6*0 b 4 6*0 b 4 6*0 b 4 6*0 b 4 6*0 b 4 6*0 b 4 6*0 fb 4 6*0 fb 4 6*0 fb
  //   4 6*0 fb 4 6*0 fb 4 6*0 fb 4 6*0 fb 4 6*0 fb 4 6*0 fb 4 6*0 fb 4 6*0 fb 4 6*0 fb 4 6*0 fb 4 6*0 fb 4
  //   6*0 fb 4 6*0 fb 4 6*0 fb 4 6*0 fb 4 6*0 fb 4 6*0 fb 4 6*0 fb 4 6*0 fb 4 6*0 fb 4 6*0 fb 4 6*0 fb 4
  //   6*0 fb 4 6*0 fb 4 6*0 fb 4 6*0 fb 4 6*0 fb 4 6*0 fb 4 6*0 fb 4 6*0 fb 4 6*0 fb 4 6*0 fb 4 6*0 fb 4
  //   6*0 fb 4 6*0 fb 4 6*0 fb 4 6*0 fb 4 6*0 fb 4 6*0 fb 4 6*0 fb 4 6*0 fb 4 6*0 fb 4 6*0 fb 4 6*0 fb 4
  //   6*0 fb 4 6*0 fb 4 6*0 fb 4 6*0 fb 4 6*0 fb 4 6*0 fb 4 6*0 fb 4 6*0 fb 4 6*0 fb 4 6*0 fb 4 6*0 fb 4
  //   6*0 fb 4 6*0 fb 4 6*0 fb 4 6*0 fb 4 6*0 fb 4 6*0 fb 4 5767*0 9 4 6*0 9 4 6*0 9 4 6*0 9 4 6*0 9 4 6*0
  //   9 4 6*0 9 4 6*0 9 4 6*0 9 4 6*0 9 4 6*0 9 4 6*0 9 4 6*0 9 4 6*0 9 4 6*0 9 4 6*0 9 4 6*0 9 4 6*0 9 4
  //   6*0 9 4 6*0 9 4 6*0 9 4 6*0 9 4 6*0 9 4 6*0 9 4 6*0 9 4 6*0 9 4 6*0 9 4 6*0 9 4 6*0 9 4 6*0 9 4 6*0
  //   9 4 6*0 9 4 6*0 9 4 6*0 9 4 6*0 9 4 6*0 9 4 6*0 9 4 6*0 9 4 6*0 9 4 6*0 9 4 6*0 9 4 6*0 9 4 6*0 9 4
  //   6*0 9 4 6*0 9 4 6*0 9 4 6*0 9 4 6*0 9 4 6*0 9 4 6*0 9 4 6*0 9 4 6*0 9 4 6*0 9 4 6*0 9 4 6*0 9 4 6*0
  //   9 4 6*0 9 4 6*0 9 4 6*0 9 4 6*0 9 4 6*0 9 4 6*0 9 4 6*0 9 4 6*0 9 4 646*0 9 4 6*0 9 4 6*0 9 4 6*0 9
  //   4 6*0 9 4 6*0 9 4 6*0 9 4 6*0 9 4 6*0 9 4 6*0 9 4 6*0 9 4 6*0 9 4 6*0 9 4 6*0 9 4 6*0 9 4 6*0 9 4
  //   646*0 9 4 6*0 9 4 6*0 9 4 6*0 9 4 6*0 9 4 6*0 9 4 6*0 9 4 6*0 9 4 6*0 9 4 6*0 9 4 6*0 9 4 6*0 9 4
  //   6*0 9 4 6*0 9 4 6*0 9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
  //   contents of rom_4 (hex, n*v repeats v):
  //   0 0 8 1 6*0 8 1 6*0 8 1 6*0 8 1 6*0 8 1 6*0 8 1 6*0 8 1 6*0 8 1 6*0 8 1 6*0 8 1 6*0 8 1 6*0 8 1 6*0
  //   8 1 6*0 8 1 6*0 8 1 6*0 8 1 6*0 20 1 6*0 20 1 6*0 20 1 6*0 20 1 6*0 20 1 6*0 20 1 6*0 20 1 6*0 20 1
  //   6*0 20 1 6*0 20 1 6*0 20 1 6*0 20 1 6*0 20 1 6*0 20 1 6*0 20 1 6*0 20 1 6*0 80 1 6*0 80 1 6*0 80 1
  //   6*0 80 1 6*0 80 1 6*0 80 1 6*0 80 1 6*0 80 1 6*0 80 1 6*0 80 1 6*0 80 1 6*0 80 1 6*0 80 1 6*0 80 1
  //   6*0 80 1 6*0 80 1 8*0 1 7*0 1 7*0 1 7*0 1 7*0 1 7*0 1 7*0 1 7*0 1 7*0 1 7*0 1 7*0 1 7*0 1 7*0 1 7*0
  //   1 7*0 1 7*0 1 9*0 1 7*0 1 7*0 1 7*0 1 7*0 1 7*0 1 7*0 1 7*0 1 7*0 1 7*0 1 7*0 1 7*0 1 7*0 1 7*0 1
  //   7*0 1 7*0 1 0 0 0 8 1 6*0 8 1 6*0 8 1 6*0 8 1 6*0 8 1 6*0 8 1 6*0 8 1 6*0 8 1 6*0 8 1 6*0 8 1 6*0 8
  //   1 6*0 8 1 6*0 8 1 6*0 8 1 6*0 8 1 6*0 8 1 6*0 20 1 6*0 20 1 6*0 20 1 6*0 20 1 6*0 20 1 6*0 20 1 6*0
  //   20 1 6*0 20 1 6*0 20 1 6*0 20 1 6*0 20 1 6*0 20 1 6*0 20 1 6*0 20 1 6*0 20 1 6*0 20 1 6*0 80 1 6*0
  //   80 1 6*0 80 1 6*0 80 1 6*0 80 1 6*0 80 1 6*0 80 1 6*0 80 1 6*0 80 1 6*0 80 1 6*0 80 1 6*0 80 1 6*0
  //   80 1 6*0 80 1 6*0 80 1 6*0 80 1 8*0 1 7*0 1 7*0 1 7*0 1 7*0 1 7*0 1 7*0 1 7*0 1 7*0 1 7*0 1 7*0 1
  //   7*0 1 7*0 1 7*0 1 7*0 1 7*0 1 9*0 1 7*0 1 7*0 1 7*0 1 7*0 1 7*0 1 7*0 1 7*0 1 7*0 1 7*0 1 7*0 1 7*0
  //   1 7*0 1 7*0 1 7*0 1 7*0 1 0 0 0 2 1 6*0 2 1 6*0 2 1 6*0 2 1 6*0 2 1 6*0 2 1 6*0 2 1 6*0 2 1 6*0 2 1
  //   6*0 2 1 6*0 2 1 6*0 2 1 6*0 2 1 6*0 2 1 6*0 2 1 6*0 2 1 6*0 8 4 6*0 8 4 6*0 8 4 6*0 8 4 6*0 8 4 6*0
  //   8 4 6*0 8 4 6*0 8 4 6*0 8 4 6*0 8 4 6*0 8 4 6*0 8 4 6*0 8 4 6*0 8 4 6*0 8 4 6*0 8 4 6*0 20 10 6*0 20
  //   10 6*0 20 10 6*0 20 10 6*0 20 10 6*0 20 10 6*0 20 10 6*0 20 10 6*0 20 10 6*0 20 10 6*0 20 10 6*0 20
  //   10 6*0 20 10 6*0 20 10 6*0 20 10 6*0 20 10 6*0 80 40 6*0 80 40 6*0 80 40 6*0 80 40 6*0 80 40 6*0 80
  //   40 6*0 80 40 6*0 80 40 6*0 80 40 6*0 80 40 6*0 80 40 6*0 80 40 6*0 80 40 6*0 80 40 6*0 80 40 6*0 80
  //   40 6*0 2 1 6*0 2 1 6*0 2 1 6*0 2 1 6*0 2 1 6*0 2 1 6*0 2 1 6*0 2 1 6*0 2 1 6*0 2 1 6*0 2 1 6*0 2 1
  //   6*0 2 1 6*0 2 1 6*0 2 1 6*0 2 1 6*0 8 4 6*0 8 4 6*0 8 4 6*0 8 4 6*0 8 4 6*0 8 4 6*0 8 4 6*0 8 4 6*0
  //   8 4 6*0 8 4 6*0 8 4 6*0 8 4 6*0 8 4 6*0 8 4 6*0 8 4 6*0 8 4 6*0 20 10 6*0 20 10 6*0 20 10 6*0 20 10
  //   6*0 20 10 6*0 20 10 6*0 20 10 6*0 20 10 6*0 20 10 6*0 20 10 6*0 20 10 6*0 20 10 6*0 20 10 6*0 20 10
  //   6*0 20 10 6*0 20 10 6*0 80 40 6*0 80 40 6*0 80 40 6*0 80 40 6*0 80 40 6*0 80 40 6*0 80 40 6*0 80 40
  //   6*0 80 40 6*0 80 40 6*0 80 40 6*0 80 40 6*0 80 40 6*0 80 40 6*0 80 40 6*0 80 40 6*0 2 1 6*0 2 1 6*0
  //   2 1 6*0 2 1 6*0 2 1 6*0 2 1 6*0 2 1 6*0 2 1 6*0 2 1 6*0 2 1 6*0 2 1 6*0 2 1 6*0 2 1 6*0 2 1 6*0 2 1
  //   6*0 2 1 6*0 8 4 6*0 8 4 6*0 8 4 6*0 8 4 6*0 8 4 6*0 8 4 6*0 8 4 6*0 8 4 6*0 8 4 6*0 8 4 6*0 8 4 6*0
  //   8 4 6*0 8 4 6*0 8 4 6*0 8 4 6*0 8 4 6*0 20 10 6*0 20 10 6*0 20 10 6*0 20 10 6*0 20 10 6*0 20 10 6*0
  //   20 10 6*0 20 10 6*0 20 10 6*0 20 10 6*0 20 10 6*0 20 10 6*0 20 10 6*0 20 10 6*0 20 10 6*0 20 10 6*0
  //   80 40 6*0 80 40 6*0 80 40 6*0 80 40 6*0 80 40 6*0 80 40 6*0 80 40 6*0 80 40 6*0 80 40 6*0 80 40 6*0
  //   80 40 6*0 80 40 6*0 80 40 6*0 80 40 6*0 80 40 6*0 80 40 6*0 6 7*0 6 7*0 6 7*0 6 7*0 6 7*0 6 7*0 6
  //   7*0 6 7*0 6 7*0 6 7*0 6 7*0 6 7*0 6 7*0 6 7*0 6 7*0 6 7*0 12 7*0 12 7*0 12 7*0 12 7*0 12 7*0 12 7*0
  //   12 7*0 12 7*0 12 7*0 12 7*0 12 7*0 12 7*0 12 7*0 12 7*0 12 7*0 12 7*0 42 7*0 42 7*0 42 7*0 42 7*0 42
  //   7*0 42 7*0 42 7*0 42 7*0 42 7*0 42 7*0 42 7*0 42 7*0 42 7*0 42 7*0 42 7*0 42 7*0 2 7*0 2 7*0 2 7*0 2
  //   7*0 2 7*0 2 7*0 2 7*0 2 7*0 2 7*0 2 7*0 2 7*0 2 7*0 2 7*0 2 7*0 2 7*0 2 7*0 9 7*0 9 7*0 9 7*0 9 7*0
  //   9 7*0 9 7*0 9 7*0 9 7*0 9 7*0 9 7*0 9 7*0 9 7*0 9 7*0 9 7*0 9 7*0 9 7*0 18 7*0 18 7*0 18 7*0 18 7*0
  //   18 7*0 18 7*0 18 7*0 18 7*0 18 7*0 18 7*0 18 7*0 18 7*0 18 7*0 18 7*0 18 7*0 18 7*0 48 7*0 48 7*0 48
  //   7*0 48 7*0 48 7*0 48 7*0 48 7*0 48 7*0 48 7*0 48 7*0 48 7*0 48 7*0 48 7*0 48 7*0 48 7*0 48 7*0 8 7*0
  //   8 7*0 8 7*0 8 7*0 8 7*0 8 7*0 8 7*0 8 7*0 8 7*0 8 7*0 8 7*0 8 7*0 8 7*0 8 7*0 8 7*0 8 7*0 21 7*0 21
  //   7*0 21 7*0 21 7*0 21 7*0 21 7*0 21 7*0 21 7*0 21 7*0 21 7*0 21 7*0 21 7*0 21 7*0 21 7*0 21 7*0 21
  //   7*0 24 7*0 24 7*0 24 7*0 24 7*0 24 7*0 24 7*0 24 7*0 24 7*0 24 7*0 24 7*0 24 7*0 24 7*0 24 7*0 24
  //   7*0 24 7*0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
  //   And so on.
  //   And another slice.
  //   This is one 8 bit "slice" of the output control signals.
endmodule

module ALU (
  input  [15:0] A,
  input  [15:0] B,
  input  carry_in,
  input  M,
  input  S0,
  input  S1,
  input  S2,
  input  S3,
  input  result_output_enable,
  input  clock,
  input  sim_only_reset,
  input  store_result,
  input  store_flags,
  output unclocked_zero,
  output clocked_zero,
  output unclocked_negative,
  output clocked_negative,
  output unclocked_carryborrow_out,
  output clocked_carryborrow_out,
  output unclocked_A___B,
  output clocked_A___B,
  output [15:0] tristate_clocked_result,
  output [15:0] unclocked_result,
  output [15:0] clocked_result
);

  wire n74ls181_1_a_b, n74ls181_1_carry_out_bar, n74ls181_2_a_b, n74ls181_2_carry_out_bar, n74ls181_3_a_b,
       n74ls181_3_carry_out_bar, n74ls181_4_a_b, n74ls181_4_carry_out_bar, not_2_out, or_1_out,
       safe_clock_enable_1_clock_out, safe_clock_enable_2_clock_out;

  not not_1 (unclocked_carryborrow_out, n74ls181_4_carry_out_bar);
  not not_2 (not_2_out, carry_in);
  and and_1 (unclocked_A___B, n74ls181_1_a_b, n74ls181_2_a_b, n74ls181_3_a_b, n74ls181_4_a_b);
  _74LS181 u_74ls181_1 (
    .B(B[3:0]), .A(A[3:0]), .M(M), .carry_in_bar(not_2_out), .carry_out_bar(n74ls181_1_carry_out_bar),
    .F(unclocked_result[3:0]), .A_B(n74ls181_1_a_b), .S0(S0), .S1(S1), .S2(S2), .S3(S3));  // open: Y, X
  _74LS181 u_74ls181_2 (
    .B(B[7:4]), .A(A[7:4]), .M(M), .carry_in_bar(n74ls181_1_carry_out_bar),
    .carry_out_bar(n74ls181_2_carry_out_bar), .F(unclocked_result[7:4]), .A_B(n74ls181_2_a_b), .S0(S0),
    .S1(S1), .S2(S2), .S3(S3));  // open: Y, X
  _74LS181 u_74ls181_3 (
    .B(B[11:8]), .A(A[11:8]), .M(M), .carry_in_bar(n74ls181_2_carry_out_bar),
    .carry_out_bar(n74ls181_3_carry_out_bar), .F(unclocked_result[11:8]), .A_B(n74ls181_3_a_b), .S0(S0),
    .S1(S1), .S2(S2), .S3(S3));  // open: Y, X
  _74LS181 u_74ls181_4 (
    .B(B[15:12]), .A(A[15:12]), .M(M), .carry_in_bar(n74ls181_3_carry_out_bar),
    .carry_out_bar(n74ls181_4_carry_out_bar), .F({unclocked_negative, unclocked_result[14:12]}),
    .A_B(n74ls181_4_a_b), .S0(S0), .S1(S1), .S2(S2), .S3(S3));  // open: Y, X
  or or_1 (or_1_out, unclocked_result[0], unclocked_result[1], unclocked_result[2], unclocked_result[3], unclocked_result[4], unclocked_result[5], unclocked_result[6], unclocked_result[7], unclocked_result[8], unclocked_result[9], unclocked_result[10], unclocked_result[11], unclocked_result[12], unclocked_result[13], unclocked_result[14], unclocked_negative);
  safe_clock_enable safe_clock_enable_1 (
    .clock_enable(store_result), .clock_in(clock), .clock_out(safe_clock_enable_1_clock_out));
  safe_clock_enable safe_clock_enable_2 (
    .clock_enable(store_flags), .clock_in(clock), .clock_out(safe_clock_enable_2_clock_out));
  not not_3 (unclocked_zero, or_1_out);
  Register #(.width(16)) result (
    .D({unclocked_negative, unclocked_result[14:0]}), .en(1'b1), .Q(clocked_result),
    .clk(safe_clock_enable_1_clock_out), .clr(sim_only_reset));
  assign tristate_clocked_result = result_output_enable ? clocked_result : 16'bz;  // Controlled_Buffer controlled_buffer_1
  Register #(.width(4)) register_1 (
    .D({unclocked_A___B, unclocked_carryborrow_out, unclocked_negative, unclocked_zero}), .en(1'b1),
    .Q({clocked_A___B, clocked_carryborrow_out, clocked_negative, clocked_zero}),
    .clk(safe_clock_enable_2_clock_out), .clr(sim_only_reset));

  assign unclocked_result[15] = unclocked_negative;
endmodule

module Clock (
  input  enable,
  input  Arduino_Crystal,
  input  Arduino_clock,
  output clock
);

  wire Crystal_clock_out, multiplexer_1_out;

  Clock_part Crystal_clock (.out(Crystal_clock_out));
  Multiplexer #(.enable("false")) multiplexer_1 (
    .in0(Arduino_clock), .in1(Crystal_clock_out), .out(multiplexer_1_out), .sel(Arduino_Crystal));
  safe_clock_enable safe_clock_enable_1 (.clock_enable(enable), .clock_in(multiplexer_1_out), .clock_out(clock));
endmodule

module _74LS181 (
  input  S0,
  input  S1,
  input  S2,
  input  S3,
  input  [3:0] B,
  input  [3:0] A,
  input  M,
  input  carry_in_bar,
  output Y,
  output carry_out_bar,
  output X,
  output [3:0] F,
  output A_B
);

  wire and_1_out, and_2_out, and_3_out, and_4_out, and_5_out, and_6_out, and_7_out, and_8_out, and_9_out,
       and_10_out, and_11_out, and_12_out, and_13_out, and_14_out, and_15_out, and_16_out, and_17_out,
       and_18_out, and_19_out, and_20_out, and_21_out, and_22_out, and_23_out, and_24_out, and_25_out,
       and_26_out, and_27_out, and_28_out, nand_1_out, nand_3_out, nor_1_out, nor_2_out, nor_3_out,
       nor_4_out, nor_5_out, nor_6_out, nor_7_out, nor_8_out, nor_10_out, nor_11_out, nor_12_out, not_1_out,
       not_2_out, not_3_out, not_4_out, not_5_out, xor_1_out, xor_2_out, xor_3_out, xor_4_out;

  not not_1 (not_1_out, B[3]);
  not not_2 (not_2_out, B[2]);
  not not_3 (not_3_out, B[1]);
  not not_4 (not_4_out, B[0]);
  not not_5 (not_5_out, M);
  and and_1 (and_1_out, B[3], S3, A[3]);
  and and_2 (and_2_out, A[3], S2, not_1_out);
  and and_3 (and_3_out, not_1_out, S1);
  and and_4 (and_4_out, S0, B[3]);
  and and_5 (and_5_out, B[2], S3, A[2]);
  and and_6 (and_6_out, A[2], S2, not_2_out);
  and and_7 (and_7_out, not_2_out, S1);
  and and_8 (and_8_out, S0, B[2]);
  and and_9 (and_9_out, B[1], S3, A[1]);
  and and_10 (and_10_out, A[1], S2, not_3_out);
  and and_11 (and_11_out, not_3_out, S1);
  and and_12 (and_12_out, S0, B[1]);
  and and_13 (and_13_out, B[0], S3, A[0]);
  and and_14 (and_14_out, A[0], S2, not_4_out);
  and and_15 (and_15_out, not_4_out, S1);
  and and_16 (and_16_out, S0, B[0]);
  nor nor_1 (nor_1_out, and_1_out, and_2_out);
  nor nor_2 (nor_2_out, and_3_out, and_4_out, A[3]);
  nor nor_3 (nor_3_out, and_5_out, and_6_out);
  nor nor_4 (nor_4_out, and_7_out, and_8_out, A[2]);
  nor nor_5 (nor_5_out, and_9_out, and_10_out);
  nor nor_6 (nor_6_out, and_11_out, and_12_out, A[1]);
  nor nor_7 (nor_7_out, and_13_out, and_14_out);
  nor nor_8 (nor_8_out, and_15_out, and_16_out, A[0]);
  xor xor_1 (xor_1_out, nor_1_out, nor_2_out);
  xor xor_2 (xor_2_out, nor_3_out, nor_4_out);
  xor xor_3 (xor_3_out, nor_5_out, nor_6_out);
  xor xor_4 (xor_4_out, nor_7_out, nor_8_out);
  and and_17 (and_17_out, nor_1_out, nor_4_out);
  and and_18 (and_18_out, nor_1_out, nor_3_out, nor_6_out);
  and and_19 (and_19_out, nor_1_out, nor_3_out, nor_5_out, nor_8_out);
  nand nand_1 (nand_1_out, nor_1_out, nor_3_out, nor_5_out, nor_7_out, carry_in_bar);
  nand nand_2 (X, nor_1_out, nor_3_out, nor_5_out, nor_7_out);
  and and_20 (and_20_out, carry_in_bar, nor_7_out, nor_5_out, nor_3_out, not_5_out);
  and and_21 (and_21_out, nor_5_out, nor_3_out, nor_8_out, not_5_out);
  and and_22 (and_22_out, nor_3_out, nor_6_out, not_5_out);
  and and_23 (and_23_out, nor_4_out, not_5_out);
  and and_24 (and_24_out, carry_in_bar, nor_7_out, nor_5_out, not_5_out);
  and and_25 (and_25_out, nor_5_out, nor_8_out, not_5_out);
  and and_26 (and_26_out, nor_6_out, not_5_out);
  and and_27 (and_27_out, carry_in_bar, nor_7_out, not_5_out);
  and and_28 (and_28_out, nor_8_out, not_5_out);
  nand nand_3 (nand_3_out, carry_in_bar, not_5_out);
  nor nor_9 (Y, nor_2_out, and_17_out, and_18_out, and_19_out);
  nor nor_10 (nor_10_out, and_20_out, and_21_out, and_22_out, and_23_out);
  nor nor_11 (nor_11_out, and_24_out, and_25_out, and_26_out);
  nor nor_12 (nor_12_out, and_27_out, and_28_out);
  or or_1 (carry_out_bar, ~Y, ~nand_1_out);  // OR_Gate
  xor xor_5 (F[3], xor_1_out, nor_10_out);
  xor xor_6 (F[2], xor_2_out, nor_11_out);
  xor xor_7 (F[1], xor_3_out, nor_12_out);
  xor xor_8 (F[0], xor_4_out, nand_3_out);
  and and_29 (A_B, F[3], F[2], F[1], F[0]);
endmodule

module safe_clock_enable (
  input  clock_enable,
  input  clock_in,
  output clock_out
);

  wire nor_1_out, nor_2_out, not_1_out, not_2_out;

  not not_1 (not_1_out, clock_enable);
  not not_2 (not_2_out, clock_in);
  nor nor_1 (nor_1_out, not_1_out, nor_2_out);
  nor nor_2 (nor_2_out, nor_1_out, not_2_out);
  and and_1 (clock_out, nor_1_out, clock_in);
endmodule

module register_bus_R (
  input  [15:0] \input ,
  input  input_enable,
  input  output_enable,
  input  clock,
  input  sim_only_reset,
  output [15:0] content,
  output [15:0] buffered_output
);

  wire safe_clock_enable_1_clock_out;

  safe_clock_enable safe_clock_enable_1 (
    .clock_enable(input_enable), .clock_in(clock), .clock_out(safe_clock_enable_1_clock_out));
  Register #(.width(16)) register_1 (
    .D(\input ), .en(1'b1), .Q(content), .clk(safe_clock_enable_1_clock_out), .clr(sim_only_reset));
  assign buffered_output = output_enable ? content : 16'bz;  // Controlled_Buffer controlled_buffer_1
endmodule

module register_bus_L (
  input  [15:0] \input ,
  input  input_enable,
  input  output_enable,
  input  clock,
  input  sim_only_reset,
  output [15:0] content,
  output [15:0] buffered_output
);

  wire safe_clock_enable_1_clock_out;

  safe_clock_enable safe_clock_enable_1 (
    .clock_enable(input_enable), .clock_in(clock), .clock_out(safe_clock_enable_1_clock_out));
  Register #(.width(16)) register_1 (
    .D(\input ), .en(1'b1), .Q(content), .clk(safe_clock_enable_1_clock_out), .clr(sim_only_reset));
  assign buffered_output = output_enable ? content : 16'bz;  // Controlled_Buffer controlled_buffer_1
endmodule

module program_counter (
  input  in,
  input  output_enable,
  input  [15:0] \input ,
  input  count,
  input  clock,
  input  reset,
  output [15:0] tristate_output,
  output [15:0] contents
);

  Counter #(.width(16), .max('hffff)) counter_1 (
    .load(in), .D(\input ), .count(count), .Q(contents), .clk(clock), .clr(reset));  // open: carry
  assign tristate_output = output_enable ? contents : 16'bz;  // Controlled_Buffer controlled_buffer_1
endmodule

module io_device (
  input  [7:0] in_1,
  input  [7:0] in_2,
  input  Prog_data_sel,
  input  Write_to_mem,
  input  Clock,
  output [7:0] out_6
);

  wire and_1_out, and_2_out, nand_1_out, not_1_out;

  nand nand_1 (nand_1_out, in_2[0], in_2[1], in_2[2], in_2[3], in_2[4], in_2[5], in_2[6], in_2[7]);
  not not_1 (not_1_out, nand_1_out);
  and and_1 (and_1_out, not_1_out, Prog_data_sel);
  and and_2 (and_2_out, and_1_out, Write_to_mem);
  Register register_1 (.D(in_1), .en(and_2_out), .Q(out_6), .clk(Clock), .clr(1'b0));
endmodule

module clipboard (
  input  in_1,
  input  in_2,
  output out_3,
  output out_4,
  output out_5,
  output clock_out
);

  wire A_IN, A_OUT, ACC_IN, ACC_OUT, ALU_A_IS_BUS, ALU_C_IN, ALU_CARRYBORROW_FLAG_CLOCKED,
       ALU_CARRYBORROW_FLAG_IMM, ALU_EQUAL_FLAG_CLOCKED, ALU_EQUAL_FLAG_IMM, ALU_M,
       ALU_NEGATIVE_FLAG_CLOCKED, ALU_NEGATIVE_FLAG_IMM, ALU_OUT, ALU_S0, ALU_S1, ALU_S2, ALU_S3,
       ALU_STORE_FLAGS, ALU_STORE_RESULT, ALU_ZERO_FLAG_CLOCKED, ALU_ZERO_FLAG_IMM, B_IN, B_OUT, C_IN, C_OUT,
       CLOCK_HALT, CONTROL_CLOCK, CU_CARRYBORROW_MIRROR, CU_EQUAL_MIRROR, CU_NEGATIVE_MIRROR, CU_STEP_RESET,
       CU_ZERO_MIRROR, IR_IN, MAR_IN, PC_COUNT, PC_IN, PC_OUT, SIM_ONLY_RESET, SP_IN, SP_OUT;
  wire [2:0] CU_MICROCODE_STEP;
  wire [7:0] A, ACC, ADDRESS, ALU_RESULT_CLOCKED, ALU_RESULT_IMM, B, BUS, C, CU_INSTRUCTION_MIRROR, IR, PC,
       SP;

  Button button_1 (.out(SIM_ONLY_RESET));
  LED led_1 (.in(ACC_IN));
  LED led_2 (.in(ACC_OUT));
  LED led_3 (.in(A_IN));
  LED led_4 (.in(A_OUT));
  LED led_5 (.in(B_IN));
  LED led_6 (.in(B_OUT));
  LED led_7 (.in(C_IN));
  LED led_8 (.in(C_OUT));
  LED led_9 (.in(ALU_STORE_RESULT));
  LED led_10 (.in(ALU_STORE_FLAGS));
  LED led_11 (.in(ALU_OUT));
  LED led_12 (.in(ALU_A_IS_BUS));
  LED led_13 (.in(ALU_S0));
  LED led_14 (.in(ALU_S1));
  LED led_15 (.in(ALU_S2));
  LED led_16 (.in(ALU_S3));
  LED led_17 (.in(ALU_M));
  LED led_18 (.in(ALU_C_IN));
  LED led_19 (.in(MAR_IN));
  LED led_20 (.in(out_4));
  LED led_21 (.in(out_5));
  LED led_22 (.in(out_3));
  LED led_23 (.in(SP_IN));
  LED led_24 (.in(SP_OUT));
  LED led_25 (.in(PC_IN));
  LED led_26 (.in(PC_OUT));
  LED led_27 (.in(PC_COUNT));
  LED led_28 (.in(IR_IN));
  LED led_29 (.in(CU_STEP_RESET));
  LED led_30 (.in(CLOCK_HALT));
  LED led_31 (.in(BUS[6]));
  LED led_32 (.in(BUS[7]));
  LED led_33 (.in(PC[7]));
  LED led_34 (.in(PC[6]));
  LED led_35 (.in(IR[7]));
  LED led_36 (.in(IR[6]));
  LED led_37 (.in(SP[6]));
  LED led_38 (.in(SP[7]));
  LED led_39 (.in(ACC[6]));
  LED led_40 (.in(ACC[7]));
  LED led_41 (.in(A[6]));
  LED led_42 (.in(A[7]));
  LED led_43 (.in(B[7]));
  LED led_44 (.in(B[6]));
  LED led_45 (.in(C[6]));
  LED led_46 (.in(C[7]));
  LED led_47 (.in(ADDRESS[6]));
  LED led_48 (.in(ADDRESS[7]));
  LED led_49 (.in(BUS[5]));
  LED led_50 (.in(BUS[3]));
  LED led_51 (.in(BUS[2]));
  LED led_52 (.in(BUS[4]));
  LED led_53 (.in(PC[3]));
  LED led_54 (.in(PC[2]));
  LED led_55 (.in(PC[5]));
  LED led_56 (.in(PC[4]));
  LED led_57 (.in(IR[3]));
  LED led_58 (.in(IR[2]));
  LED led_59 (.in(IR[5]));
  LED led_60 (.in(IR[4]));
  LED led_61 (.in(SP[3]));
  LED led_62 (.in(SP[2]));
  LED led_63 (.in(SP[5]));
  LED led_64 (.in(SP[4]));
  LED led_65 (.in(ACC[4]));
  LED led_66 (.in(ACC[5]));
  LED led_67 (.in(ACC[3]));
  LED led_68 (.in(ACC[2]));
  LED led_69 (.in(A[4]));
  LED led_70 (.in(A[3]));
  LED led_71 (.in(A[5]));
  LED led_72 (.in(A[2]));
  LED led_73 (.in(B[5]));
  LED led_74 (.in(B[2]));
  LED led_75 (.in(B[3]));
  LED led_76 (.in(B[4]));
  LED led_77 (.in(C[5]));
  LED led_78 (.in(C[3]));
  LED led_79 (.in(C[4]));
  LED led_80 (.in(C[2]));
  LED led_81 (.in(ADDRESS[2]));
  LED led_82 (.in(ADDRESS[3]));
  LED led_83 (.in(ADDRESS[5]));
  LED led_84 (.in(ADDRESS[4]));
  // Probe on BUS
  LED led_85 (.in(BUS[0]));
  LED led_86 (.in(BUS[1]));
  // Probe on PC
  LED led_87 (.in(PC[1]));
  LED led_88 (.in(PC[0]));
  // Probe on IR
  LED led_89 (.in(IR[0]));
  LED led_90 (.in(IR[1]));
  // Probe on SP
  LED led_91 (.in(SP[0]));
  LED led_92 (.in(SP[1]));
  // Probe on ACC
  LED led_93 (.in(ACC[1]));
  LED led_94 (.in(ACC[0]));
  // Probe on A
  LED led_95 (.in(A[1]));
  LED led_96 (.in(A[0]));
  // Probe on B
  LED led_97 (.in(B[0]));
  LED led_98 (.in(B[1]));
  // Probe on C
  LED led_99 (.in(C[0]));
  LED led_100 (.in(C[1]));
  // Probe on ADDRESS
  LED led_101 (.in(ADDRESS[1]));
  LED led_102 (.in(ADDRESS[0]));
  // Probe on BUS
  // Probe on BUS
  // Probe on PC
  // Probe on PC
  // Probe on IR
  // Probe on IR
  // Probe on SP
  // Probe on SP
  // Probe on ACC
  // Probe on ACC
  // Probe on A
  // Probe on A
  // Probe on B
  // Probe on B
  // Probe on C
  // Probe on C
  // Probe on ADDRESS
  // Probe on ADDRESS
  LED led_103 (.in(ALU_RESULT_IMM[6]));
  LED led_104 (.in(ALU_RESULT_IMM[7]));
  LED led_105 (.in(ALU_RESULT_CLOCKED[7]));
  LED led_106 (.in(ALU_RESULT_CLOCKED[6]));
  LED led_107 (.in(ALU_ZERO_FLAG_IMM));
  LED led_108 (.in(ALU_NEGATIVE_FLAG_IMM));
  LED led_109 (.in(ALU_CARRYBORROW_FLAG_IMM));
  LED led_110 (.in(ALU_EQUAL_FLAG_IMM));
  LED led_111 (.in(ALU_ZERO_FLAG_CLOCKED));
  LED led_112 (.in(ALU_NEGATIVE_FLAG_CLOCKED));
  LED led_113 (.in(ALU_CARRYBORROW_FLAG_CLOCKED));
  LED led_114 (.in(ALU_EQUAL_FLAG_CLOCKED));
  LED led_115 (.in(CU_INSTRUCTION_MIRROR[7]));
  LED led_116 (.in(CU_MICROCODE_STEP[2]));
  LED led_117 (.in(CU_ZERO_MIRROR));
  LED led_118 (.in(CU_NEGATIVE_MIRROR));
  LED led_119 (.in(CU_CARRYBORROW_MIRROR));
  LED led_120 (.in(CU_EQUAL_MIRROR));
  LED led_121 (.in(clock_out));
  LED led_122 (.in(CONTROL_CLOCK));
  LED led_123 (.in(ALU_RESULT_IMM[3]));
  LED led_124 (.in(ALU_RESULT_IMM[5]));
  LED led_125 (.in(ALU_RESULT_IMM[4]));
  LED led_126 (.in(ALU_RESULT_IMM[2]));
  LED led_127 (.in(ALU_RESULT_CLOCKED[4]));
  LED led_128 (.in(ALU_RESULT_CLOCKED[5]));
  LED led_129 (.in(ALU_RESULT_CLOCKED[3]));
  LED led_130 (.in(ALU_RESULT_CLOCKED[2]));
  LED led_131 (.in(CU_INSTRUCTION_MIRROR[5]));
  LED led_132 (.in(CU_INSTRUCTION_MIRROR[4]));
  LED led_133 (.in(CU_INSTRUCTION_MIRROR[6]));
  LED led_134 (.in(CU_INSTRUCTION_MIRROR[3]));
  LED led_135 (.in(CU_MICROCODE_STEP[0]));
  LED led_136 (.in(CU_MICROCODE_STEP[1]));
  // Probe on ALU_RESULT_IMM
  LED led_137 (.in(ALU_RESULT_IMM[1]));
  LED led_138 (.in(ALU_RESULT_IMM[0]));
  // Probe on ALU_RESULT_CLOCKED
  LED led_139 (.in(ALU_RESULT_CLOCKED[1]));
  LED led_140 (.in(ALU_RESULT_CLOCKED[0]));
  LED led_141 (.in(CU_INSTRUCTION_MIRROR[2]));
  LED led_142 (.in(CU_INSTRUCTION_MIRROR[0]));
  LED led_143 (.in(CU_INSTRUCTION_MIRROR[1]));
  // Probe on ALU_RESULT_IMM
  // Probe on ALU_RESULT_IMM
  // Probe on ALU_RESULT_CLOCKED
  // Probe on ALU_RESULT_CLOCKED
  // Probe on CU_INSTRUCTION_MIRROR
  // Probe on CU_INSTRUCTION_MIRROR
  // Probe on CU_INSTRUCTION_MIRROR
  // Probe on CU_MICROCODE_STEP
  // Probe on CU_MICROCODE_STEP
  // Probe on CU_MICROCODE_STEP

  // Other names for the same wires on the sheet: DATA_CLOCK = clock_out; EXT_CLOCK_PULSE = in_2;
  //   PROG_DATA_MEM = out_3; READ_FROM_MEM = out_5; RESET = in_1; WRITE_TO_MEM = out_4

  // Notes on the sheet:
  //   BIN
  //   BIN
  //   HEX
  //   BIN
  //   HEX
  //   DEC
  //   BIN
  //   HEX
  //   DEC
  //   BIN
  //   HEX
  //   DEC
  //   HEX
  //   DEC
  //   BIN
  //   HEX
  //   DEC
  //   BIN
  //   HEX
  //   DEC
  //   BIN
  //   HEX
  //   DEC
  //   DEC
  //   BIN
  //   HEX
  //   DEC
  //   BIN
  //   HEX
  //   DEC
  //   BIN
  //   HEX
  //   DEC
  //   BIN
  //   HEX
  //   DEC
  //   BIN
  //   HEX
  //   DEC
endmodule

module schem_export (
  input  Halt,
  input  Reset,
  input  Auto_Manual,
  input  Manual_clock,
  output Clock,
  output Control_Clock
);

  wire Auto_clock_out, nand_1_out, nand_2_out, nand_3_out, nand_4_out, nand_5_out, nand_6_out, nand_7_out,
       nand_8_out, nor_1_out, nor_2_out, nor_3_out, nor_4_out, not_1_out, not_2_out;

  Clock_part Auto_clock (.out(Auto_clock_out));
  nand nand_1 (nand_1_out, Auto_Manual, Auto_Manual);
  nor nor_1 (nor_1_out, Halt, Reset);
  nand nand_2 (nand_2_out, Auto_Manual, Manual_clock);
  nand nand_3 (nand_3_out, nand_1_out, Auto_clock_out);
  nand nand_4 (nand_4_out, nor_1_out, nor_1_out);
  nand nand_5 (nand_5_out, nand_2_out, nand_3_out);
  nor nor_2 (nor_2_out, nand_5_out, nand_5_out);
  nor nor_3 (nor_3_out, nand_4_out, nor_4_out);
  nor nor_4 (nor_4_out, nor_3_out, nor_2_out);
  nand nand_6 (nand_6_out, nor_3_out, nand_5_out);
  nand nand_7 (nand_7_out, nand_6_out, nand_6_out);
  nand nand_8 (nand_8_out, nand_7_out, nand_7_out);
  J_K_Flip_Flop j_k_ff_1 (
    .J(1'b1), .clk(nand_7_out), .K(1'b1), .Q(Clock), .preset(1'b0), .en(1'b1), .reset(not_1_out));  // open: Qn
  not not_1 (not_1_out, nor_1_out);
  J_K_Flip_Flop j_k_ff_2 (
    .J(1'b1), .clk(nand_8_out), .K(1'b1), .Q(Control_Clock), .preset(1'b0), .en(1'b1), .reset(not_2_out));  // open: Qn
  not not_2 (not_2_out, nor_1_out);

  // Notes on the sheet:
  //   Safe clock enable
endmodule

module ALU_comparison_test (
  input  [7:0] in_1,
  input  [7:0] in_2,
  input  in_3,
  input  in_4,
  input  in_5,
  input  in_6,
  input  in_7,
  input  in_8,
  output out_9,
  output out_10,
  output [7:0] out_11
);

  wire n74ls181_1_a_b, n74ls181_1_carry_out_bar, n74ls181_2_a_b, n74ls181_2_carry_out_bar, not_2_out;

  not not_1 (out_10, n74ls181_2_carry_out_bar);
  not not_2 (not_2_out, in_3);
  and and_1 (out_9, n74ls181_1_a_b, n74ls181_2_a_b);
  _74LS181 u_74ls181_1 (
    .B(in_2[3:0]), .A(in_1[3:0]), .M(in_4), .carry_in_bar(not_2_out),
    .carry_out_bar(n74ls181_1_carry_out_bar), .F(out_11[3:0]), .A_B(n74ls181_1_a_b), .S0(in_5), .S1(in_6),
    .S2(in_7), .S3(in_8));  // open: Y, X
  _74LS181 u_74ls181_2 (
    .B(in_2[7:4]), .A(in_1[7:4]), .M(in_4), .carry_in_bar(n74ls181_1_carry_out_bar),
    .carry_out_bar(n74ls181_2_carry_out_bar), .F(out_11[7:4]), .A_B(n74ls181_2_a_b), .S0(in_5), .S1(in_6),
    .S2(in_7), .S3(in_8));  // open: Y, X
  // Probe on in_2[3:0]
  // Probe on in_1[3:0]
endmodule

module new_clock_test (
  input  clock_enable,
  input  R,
  input  clock_in,
  input  S,
  input  in_5,
  input  clock_enable_2,
  input  in_7,
  input  clock_in_2,
  input  in_9,
  input  in_10,
  input  in_11,
  input  in_12,
  input  in_13,
  input  in_14,
  output clock_out,
  output out_16,
  output out_17
);

  wire and_1_out, and_2_out, nor_1_out, nor_2_out, nor_3_out, nor_4_out, nor_5_out, nor_6_out, not_1_out,
       not_2_out;

  nor nor_1 (nor_1_out, R, nor_2_out);
  nor nor_2 (nor_2_out, nor_1_out, S);
  safe_clock_enable safe_clock_enable_1 (.clock_enable(in_5), .clock_in(in_7), .clock_out(out_16));
  safe_clock_enable_disable safe_clock_enable_disable_1 (.clock_enable(in_13), .clock_in(in_14), .clock_out(out_17));
  not not_1 (not_1_out, clock_enable);
  not not_2 (not_2_out, clock_in);
  nor nor_3 (nor_3_out, not_1_out, nor_4_out);
  nor nor_4 (nor_4_out, nor_3_out, not_2_out);
  and and_1 (and_1_out, nor_3_out, clock_in);
  J_K_Flip_Flop j_k_ff_1 (
    .J(clock_enable_2), .clk(clock_in_2), .K(in_9), .preset(in_10), .en(in_11), .reset(in_12));  // open: Q, Qn
  and and_2 (and_2_out, not_1_out, not_2_out);
  nor nor_5 (nor_5_out, and_2_out, nor_6_out);
  nor nor_6 (nor_6_out, nor_5_out, and_1_out);
  and and_3 (clock_out, nor_5_out, clock_in);

  // Notes on the sheet:
  //   Q
  //   Q'
  //   Reset
  //   Set
endmodule

module safe_clock_enable_disable (
  input  clock_enable,
  input  clock_in,
  output clock_out
);

  wire and_1_out, and_2_out, nor_1_out, nor_2_out, nor_3_out, nor_4_out, not_1_out, not_2_out;

  not not_1 (not_1_out, clock_enable);
  nor nor_1 (nor_1_out, not_1_out, nor_2_out);
  nor nor_2 (nor_2_out, nor_1_out, not_2_out);
  not not_2 (not_2_out, clock_in);
  and and_1 (and_1_out, nor_1_out, clock_in);
  and and_2 (and_2_out, not_1_out, not_2_out);
  nor nor_3 (nor_3_out, and_2_out, nor_4_out);
  nor nor_4 (nor_4_out, nor_3_out, and_1_out);
  and and_3 (clock_out, nor_3_out, clock_in);
  Pull_Resistor pull_resistor_1 (.node(nor_3_out));
  Pull_Resistor pull_resistor_2 (.node(nor_4_out));

  // Notes on the sheet:
  //   Reset
  //   Set
endmodule
